// Digital circuit 16xPrescaler.dig as structural Verilog
module _16xPrescaler (
  input  Clk,
  output ClockOut
);

  wire d_ff_1_nq, d_ff_1_q, d_ff_2_nq, d_ff_2_q, d_ff_3_nq, d_ff_3_q, d_ff_4_nq, d_ff_4_q, d_ff_5_nq;

  D_FF d_ff_1 (.D(d_ff_1_nq), .C(Clk), .Q(d_ff_1_q), .nQ(d_ff_1_nq));
  D_FF d_ff_2 (.D(d_ff_2_nq), .C(d_ff_1_q), .Q(d_ff_2_q), .nQ(d_ff_2_nq));
  D_FF d_ff_3 (.D(d_ff_3_nq), .C(d_ff_2_q), .Q(d_ff_3_q), .nQ(d_ff_3_nq));
  D_FF d_ff_4 (.D(d_ff_4_nq), .C(d_ff_3_q), .Q(d_ff_4_q), .nQ(d_ff_4_nq));
  D_FF d_ff_5 (.D(d_ff_5_nq), .C(d_ff_4_q), .Q(ClockOut), .nQ(d_ff_5_nq));

  // Notes on the sheet:
  //   Clk: Hz: 48
endmodule
