// Digital circuit CPUDesign - Copy.dig as structural Verilog
module CPUDesign___Copy (
  input  [3:0] SW,
  input  [4:0] BTN,
  input  mclk,
  output [7:0] LED,
  output Deg2,
  output DataClockOut,
  output RealClockOut,
  output Deg4,
  output Deg1,
  output Deg3,
  output SCL,
  output SDA
);

  wire _16xprescaler_1_clockout, _16xprescaler_2_clockout, _16xprescaler_3_clockout,
       _16xprescaler_4_clockout, _16xprescaler_5_clockout, _16xprescaler_6_clockout,
       _16xprescaler_7_clockout, abs, Activate_Debug_out, alu2D, alut_1_carry, alut_1_neg, alut_1_zero,
       and_1_out, and_2_out, and_4_out, and_5_out, and_6_out, and_7_out, and_8_out, and_10_out, and_11_out,
       and_12_out, and_13_out, and_14_out, and_15_out, and_16_out, and_18_out, and_19_out, and_20_out,
       and_21_out, and_22_out, and_23_out, and_24_out, and_25_out, and_27_out, comparator_1_eq,
       comparator_2_eq, comparator_3_eq, comparator_4_eq, comparator_5_eq, comparator_6_eq, comparator_7_eq,
       comparator_8_eq, comparator_9_eq, comparator_10_eq, comparator_11_eq, counter_7_ovf, d_ff_2_q,
       DataSel, demultiplexer_2_out_1, dipswitch_1_out, endCom, flagread, flagStr, I2CAck, I2CBusy, I2CDone,
       imm, instMem, inter, interEnable, InterLock, intr, ioR, ioW, isadrwrite, isEnable, isReading,
       isWriting, ld, multiplexer_6_out, multiplexer_7_out, multiplexer_9_out, multiplexer_10_out,
       multiplexer_11_out, multiplexer_12_out, multiplexer_14_out, multiplexer_15_out, multiplexer_17_out,
       multiplexer_18_out, muxA, not_1_out, not_2_out, not_3_out, not_4_out, not_5_out, not_6_out, or_1_out,
       or_2_out, or_3_out, or_4_out, or_5_out, or_6_out, or_7_out, or_8_out, or_10_out, or_11_out, or_12_out,
       pcReset, RandomNUMSel, rddataLeft, readReg, readSlave, register_1_q, register_2_q, Reti, sdain,
       sdaouy, Sel3, sf, src2D, st, stPC, u_i2c_master_isadrwriting, u_i2c_master_isstandby, WE, wrdataLeft,
       wrdataLessThen, xor_1_out, xor_2_out;
  wire [1:0] counter_7_out, I2CBR, iem;
  wire [2:0] br, muxB, WDmux;
  wire [3:0] FlagOut, u_i2c_master_statedebug;
  wire [3:3] selectorformultplx_1_out;
  wire [4:0] aluOp, counter_1_out, counter_2_out, counter_3_out, counter_4_out, multiplexer_13_out,
       multiplexer_16_out;
  wire [6:0] adrToWrite;
  wire [7:0] dataToi2c, demultiplexer_1_out_1, OPcode, OpcodeDebug, RedData;
  wire [15:0] Addr, Addr_q, bootrom_d, counter_5_out, counter_6_out, datain, demultiplexer_1_out_0, Din,
       DinI2C, imreg_1_p5, mem_d, multiplexer_3_out, multiplexer_4_out, multiplexer_5_out, PcDebug,
       pcte_1_nextpc, ramdualport_1_d, RandomNUM, rdln, registerblock_1_rdest, registerblock_1_rsrc,
       singextend_1__4d, singextend_1__4s, singextend_1__8sd, wrtln;
  wire [15:1] instruct_q, intEn_q;
  wire [15:8] demultiplexer_1_out_1_2;

  Comparator #(.Bits(16)) comparator_1 (.a(Addr), .b(16'h2), .eq(comparator_1_eq));  // open: gt, lt
  and and_1 (and_1_out, comparator_1_eq, ioW);
  Register #(.Bits(16)) instruct (.D(datain), .C(RealClockOut), .en(and_1_out), .Q({instruct_q, instMem}));
  and and_2 (and_2_out, ~instMem, register_1_q);  // And
  Register register_1 (.D(instMem), .C(RealClockOut), .en(or_1_out), .Q(register_1_q));
  or or_1 (or_1_out, and_2_out, not_1_out);
  not not_1 (not_1_out, register_1_q);
  and and_3 (pcReset, ~register_1_q, instMem);  // And
  Comparator #(.Bits(16)) comparator_2 (.a(Addr), .b(16'h3), .eq(comparator_2_eq));  // open: gt, lt
  and and_4 (and_4_out, comparator_2_eq, ioW);
  Register #(.Bits(16)) intEn (.D(datain), .C(RealClockOut), .en(and_4_out), .Q({intEn_q, interEnable}));
  Comparator #(.Bits(16)) comparator_3 (.a(Addr), .b(16'h1), .eq(comparator_3_eq));  // open: gt, lt
  pcTe pcte_1 (
    .ALU(Addr), .C(RealClockOut), .abs(abs), .intr(intr), .reti(Reti), .rel(xor_1_out), .Reset(pcReset),
    .interruptEnable(interEnable), .PC(PcDebug), .NextPC(pcte_1_nextpc));
  and and_5 (and_5_out, comparator_3_eq, ioW);
  Demultiplexer #(.Bits(16)) demultiplexer_1 (
    .sel(instMem), .in(PcDebug), .out_0(demultiplexer_1_out_0),
    .out_1({demultiplexer_1_out_1_2, demultiplexer_1_out_1}));
  _16bit_paralel_serial _16bit_paralel_serial_1 (.Data(datain), .Clk(DataClockOut), .Out(Deg4));
  _16bit_paralel_serial _16bit_paralel_serial_2 (.Data(Addr), .Clk(DataClockOut), .Out(Deg3));
  _16bit_paralel_serial _16bit_paralel_serial_3 (.Data(PcDebug), .Clk(DataClockOut), .Out(Deg2));
  _16bit_paralel_serial _16bit_paralel_serial_4 (.Data({OPcode, OpcodeDebug}), .Clk(DataClockOut), .Out(Deg1));
  Demultiplexer demultiplexer_2 (
    .sel(Activate_Debug_out), .in(mclk), .out_0(DataClockOut), .out_1(demultiplexer_2_out_1));
  DipSwitch #(.dipDefault("true")) Activate_Debug (.out(Activate_Debug_out));
  ROM #(.AddrBits(16), .isProgramMemory("true"), .Bits(16)) bootrom (
    .A(demultiplexer_1_out_0), .sel(1'b1), .D(bootrom_d));
  RAMDualPort #(.AddrBits(8), .Bits(16)) ramdualport_1 (
    .A(demultiplexer_1_out_1), .Din(datain), .str(and_5_out), .C(RealClockOut), .ld(instMem),
    .D(ramdualport_1_d));
  _16xPrescaler _16xprescaler_1 (.Clk(DataClockOut), .ClockOut(_16xprescaler_1_clockout));
  Multiplexer #(.Bits(16)) multiplexer_1 (
    .sel(instMem), .in_0(bootrom_d), .in_1(ramdualport_1_d), .out({OPcode, OpcodeDebug}));
  Register #(.Bits(16)) u_OPcode (.D({OPcode, OpcodeDebug}), .C(RealClockOut), .en(1'b1));  // open: Q
  Multiplexer multiplexer_2 (
    .sel(Activate_Debug_out), .in_0(_16xprescaler_1_clockout), .in_1(demultiplexer_2_out_1),
    .out(RealClockOut));
  Multiplexer #(.Selector_Bits(3), .Bits(16)) multiplexer_3 (
    .sel(WDmux), .in_0(Addr), .in_1(mem_d), .in_2(Din), .in_3(pcte_1_nextpc), .in_4({{12{1'b0}}, FlagOut}),
    .in_5(RandomNUM), .in_6(DinI2C), .in_7({16{1'b0}}), .out(multiplexer_3_out));
  OpDecoder opdecoder_1 (
    .OPcode(OPcode), .stPC(stPC), .WE(WE), .iem(iem), .absJmp(abs), .muxB(muxB), .src2D(src2D), .muxA(muxA),
    .alu2D(alu2D), .aluOp(aluOp), .storeFlags(sf), .branch(br), .ramSt(st), .ramLd(ld), .ioW(ioW), .ioR(ioR),
    .RetI(Reti), .flagR(flagread), .flagST(flagStr), .imm(imm), .RandomSel(RandomNUMSel), .dataSel(DataSel),
    .I2cSel(I2CBR));
  SelectorForMultplx selectorformultplx_1 (
    .in1(ld), .in2(ioR), .in3(stPC), .in4(flagread), .in5(RandomNUMSel), .in6(1'b0), .in7(1'b0), .in8(1'b0),
    .in9(1'b0), .in10(1'b0), .in11(1'b0), .in12(1'b0), .in13(1'b0), .in14(1'b0), .in15(1'b0),
    .out({selectorformultplx_1_out[3], WDmux}));
  RegisterBlock registerblock_1 (
    .DataIn(multiplexer_3_out), .WE(WE), .clk(RealClockOut), .src(OpcodeDebug[3:0]), .Dest(OpcodeDebug[7:4]),
    .RDest(registerblock_1_rdest), .Rsrc(registerblock_1_rsrc));  // open: rst
  singExtend singextend_1 (
    .inst({OPcode, OpcodeDebug}), ._4S(singextend_1__4s), ._8SD(singextend_1__8sd), ._4D(singextend_1__4d));
  // ImReg imreg_1: pin names not known; wires that end beside it: imm, iem, RealClockOut, {OPcode, OpcodeDebug}, imreg_1_p5
  xor xor_1 (xor_1_out, multiplexer_6_out, xor_2_out);
  // Probe randomNum on RandomNUM
  Multiplexer #(.Bits(16)) multiplexer_4 (
    .sel(muxA), .in_0(registerblock_1_rdest), .in_1(registerblock_1_rsrc), .out(multiplexer_4_out));
  Multiplexer #(.Selector_Bits(3), .Bits(16)) multiplexer_5 (
    .sel(muxB), .in_0(registerblock_1_rsrc), .in_1({16{1'b0}}), .in_2(imreg_1_p5), .in_3({16{1'b0}}),
    .in_4({16{1'b0}}), .in_5(singextend_1__4s), .in_6(singextend_1__8sd), .in_7(singextend_1__4d),
    .out(multiplexer_5_out));
  Multiplexer #(.Selector_Bits(2)) multiplexer_6 (
    .sel(I2CBR), .in_0(1'b0), .in_1(I2CBusy), .in_2(I2CAck), .in_3(I2CDone), .out(multiplexer_6_out));
  and and_6 (and_6_out, d_ff_2_q, ~Reti);  // And
  and and_7 (and_7_out, inter, interEnable);
  and and_8 (and_8_out, InterLock, ~Reti);  // And
  or or_2 (or_2_out, and_6_out, and_7_out);
  // randomNumberGen randomnumbergen_1: pin names not known; wires that end beside it: RandomNUM, ioW, RandomNUMSel, Addr, datain, RealClockOut
  xor xor_2 (xor_2_out, multiplexer_7_out, br[2]);
  or or_3 (or_3_out, and_8_out, intr);
  D_FF d_ff (.D(or_3_out), .C(~RealClockOut), .Q(InterLock));  // open: nQ
  D_FF d_ff_2 (.D(or_2_out), .C(~RealClockOut), .Q(d_ff_2_q));  // open: nQ
  Multiplexer #(.Selector_Bits(2)) multiplexer_7 (
    .sel(br[1:0]), .in_0(1'b0), .in_1(FlagOut[0]), .in_2(FlagOut[1]), .in_3(FlagOut[2]),
    .out(multiplexer_7_out));
  and and_9 (intr, ~InterLock, ~imm, d_ff_2_q, ~FlagOut[3]);  // And
  Multiplexer #(.Bits(16)) multiplexer_8 (
    .sel(DataSel), .in_0(registerblock_1_rsrc), .in_1(multiplexer_5_out), .out(datain));
  Alut alut_1 (
    .A(multiplexer_4_out), .B(multiplexer_5_out), .Aluop(aluOp), .CarryIn(FlagOut[0]), .Zero(alut_1_zero),
    .Neg(alut_1_neg), .Carry(alut_1_carry), .DataOut(Addr));
  Register inter1 (.D(intr), .C(RealClockOut), .en(sf), .Q(FlagOut[3]));
  Register Neg (.D(multiplexer_9_out), .C(RealClockOut), .en(sf), .Q(FlagOut[2]));
  Register Zero (.D(multiplexer_10_out), .C(RealClockOut), .en(sf), .Q(FlagOut[1]));
  Register Carry (.D(multiplexer_11_out), .C(RealClockOut), .en(sf), .Q(FlagOut[0]));
  Multiplexer multiplexer_9 (.sel(flagStr), .in_0(alut_1_neg), .in_1(datain[2]), .out(multiplexer_9_out));
  Multiplexer multiplexer_10 (.sel(flagStr), .in_0(alut_1_zero), .in_1(datain[1]), .out(multiplexer_10_out));
  Multiplexer multiplexer_11 (.sel(flagStr), .in_0(alut_1_carry), .in_1(datain[0]), .out(multiplexer_11_out));
  RAMDualPort #(.AddrBits(8), .Bits(16), .Addr_Bits(10)) mem (
    .A(Addr[7:0]), .Din(datain), .str(st), .C(RealClockOut), .ld(ld), .D(mem_d));
  // GPO outputio: pin names not known; wires that end beside it: datain, Addr, RealClockOut, ioW, LED[0], LED[1], LED[2], LED[3], LED[4], LED[5], LED[6], LED[7]
  GPI_HDL inputio (
    .A(Addr), .R(ioR), .In0(SW[0]), .In1(SW[1]), .In2(SW[2]), .In3(SW[3]), .In4(BTN[0]), .In5(BTN[1]),
    .In6(BTN[2]), .In7(BTN[3]), .In8(BTN[4]), .In9(1'b0), .In10(1'b0), .In11(1'b0), .In12(1'b0), .In13(1'b0),
    .In14(1'b0), .In15(1'b0), .clk(not_2_out), .inter_En(InterLock), .D(Din), .sel(Sel3), .Interrupt(inter));
  not not_2 (not_2_out, RealClockOut);
  or or_4 (or_4_out, isWriting, isadrwrite);
  // PinControl pincontrol_1: pin names not known; wires that end beside it: sdaouy, or_4_out, sdain, SDA
  _16xPrescaler _16xprescaler_2 (.Clk(RealClockOut), .ClockOut(_16xprescaler_2_clockout));
  _16xPrescaler _16xprescaler_3 (.Clk(_16xprescaler_2_clockout), .ClockOut(_16xprescaler_3_clockout));
  _16xPrescaler _16xprescaler_4 (.Clk(_16xprescaler_3_clockout), .ClockOut(_16xprescaler_4_clockout));
  _16xPrescaler _16xprescaler_5 (.Clk(_16xprescaler_4_clockout), .ClockOut(_16xprescaler_5_clockout));
  Comparator #(.Bits(16)) comparator_4 (.a(Addr), .b(16'ha), .eq(comparator_4_eq));  // open: gt, lt
  Comparator #(.Bits(16)) comparator_5 (.a(Addr), .b(16'hb), .eq(comparator_5_eq));  // open: gt, lt
  Register register_2 (.D(I2CDone), .C(RealClockOut), .en(or_5_out), .Q(register_2_q));
  or or_5 (or_5_out, ~isEnable, not_3_out);  // Or
  not not_3 (not_3_out, register_2_q);
  _16xPrescaler _16xprescaler_6 (.Clk(_16xprescaler_5_clockout), .ClockOut(_16xprescaler_6_clockout));
  Comparator #(.Bits(16)) comparator_6 (.a(Addr), .b(16'hd), .eq(comparator_6_eq));  // open: gt, lt
  and and_10 (and_10_out, register_2_q, isWriting);
  and and_11 (and_11_out, comparator_4_eq, ioW);
  and and_12 (and_12_out, comparator_5_eq, ioW);
  Comparator #(.Bits(16)) comparator_7 (.a(Addr), .b(16'he), .eq(comparator_7_eq));  // open: gt, lt
  Comparator #(.Bits(16)) comparator_8 (.a(Addr), .b(16'hf), .eq(comparator_8_eq));  // open: gt, lt
  Comparator #(.Bits(16)) comparator_9 (.a(Addr), .b(16'hc), .eq(comparator_9_eq));  // open: gt, lt
  not not_4 (not_4_out, isWriting);
  _16xPrescaler _16xprescaler_7 (.Clk(_16xprescaler_6_clockout), .ClockOut(_16xprescaler_7_clockout));
  and and_13 (and_13_out, comparator_6_eq, ioW);
  and and_14 (and_14_out, RealClockOut, ~isEnable);  // And
  Register #(.Bits(16)) writeLen (.D(datain), .C(RealClockOut), .en(and_11_out), .Q(wrtln));
  Register #(.Bits(16)) u_Addr (
    .D(datain), .C(RealClockOut), .en(and_12_out), .Q({Addr_q[15:8], adrToWrite, Addr_q[0]}));
  and and_15 (and_15_out, datain[0], and_13_out);
  and and_16 (and_16_out, comparator_7_eq, ioW);
  and and_17 (readReg, comparator_8_eq, ioR);
  and and_18 (and_18_out, comparator_9_eq, ioW);
  and and_19 (and_19_out, RealClockOut, not_4_out);
  or or_6 (or_6_out, I2CDone, and_19_out);
  not not_5 (not_5_out, isEnable);
  and and_20 (and_20_out, isEnable, ~and_13_out);  // And
  Multiplexer multiplexer_12 (.sel(and_20_out), .in_0(and_15_out), .in_1(1'b0), .out(multiplexer_12_out));
  or or_7 (or_7_out, and_13_out, endCom);
  Register #(.Bits(16)) readLen (.D(datain), .C(RealClockOut), .en(and_16_out), .Q(rdln));
  or or_8 (or_8_out, isWriting, and_18_out);
  and and_21 (and_21_out, ~and_18_out, isEnable);  // And
  and and_22 (and_22_out, isEnable, and_10_out);
  DipSwitch dipswitch_1 (.out(dipswitch_1_out));
  i2c_master #(.applicationType("GHDL"), .CodeFile("C:\\Users\\Berkant\\Desktop\\fpga\\CpuDesign\\Vhdl\\i2c.vhdl")) u_i2c_master (
    .enable(isEnable), .clk(_16xprescaler_7_clockout), .addr({adrToWrite, readSlave}), .data(dataToi2c),
    .rst(not_5_out), .sdain(sdain), .sclin(dipswitch_1_out), .endCon(endCom), .sdaout(sdaouy), .sclout(SCL),
    .dataOut(RedData), .ack(I2CAck), .busy(I2CBusy), .done(I2CDone), .isWriting(isWriting),
    .isReading(isReading), .isAdrWriting(u_i2c_master_isadrwriting), .isStandby(u_i2c_master_isstandby),
    .statedebug(u_i2c_master_statedebug));
  RAMDualPort #(.AddrBits(5), .Bits(8)) ramdualport_2 (
    .A(multiplexer_16_out), .Din(RedData), .str(multiplexer_14_out), .C(RealClockOut), .ld(readReg),
    .D(DinI2C[15:8]));
  RAMDualPort #(.AddrBits(5), .Bits(8)) ramdualport_3 (
    .A(multiplexer_16_out), .Din(RedData), .str(multiplexer_15_out), .C(RealClockOut), .ld(readReg),
    .D(DinI2C[7:0]));
  Register Enable (.D(multiplexer_12_out), .C(RealClockOut), .en(or_7_out), .Q(isEnable));
  Counter #(.Bits(5)) counter_1 (.en(or_8_out), .C(~and_14_out), .clr(and_21_out), .out(counter_1_out));  // open: ovf
  Counter #(.Bits(5)) counter_2 (.en(and_22_out), .C(~or_6_out), .clr(not_4_out), .out(counter_2_out));  // open: ovf
  Multiplexer #(.Bits(5)) multiplexer_13 (
    .sel(isEnable), .in_0(counter_1_out), .in_1(counter_2_out), .out(multiplexer_13_out));
  Multiplexer multiplexer_14 (.sel(not_6_out), .in_0(1'b0), .in_1(isReading), .out(multiplexer_14_out));
  Multiplexer multiplexer_15 (.sel(counter_7_out[0]), .in_0(1'b0), .in_1(isReading), .out(multiplexer_15_out));
  or or_9 (isadrwrite, u_i2c_master_isadrwriting, u_i2c_master_isstandby);
  RAMDualPort #(.AddrBits(5), .Bits(8)) DataToWrite (
    .A(multiplexer_13_out), .Din(datain[7:0]), .str(and_18_out), .C(RealClockOut), .ld(isEnable),
    .D(dataToi2c));
  not not_6 (not_6_out, counter_7_out[0]);
  Multiplexer #(.Bits(5)) multiplexer_16 (
    .sel(readReg), .in_0(counter_4_out), .in_1(counter_3_out), .out(multiplexer_16_out));
  Multiplexer multiplexer_17 (.sel(isEnable), .in_0(RealClockOut), .in_1(I2CDone), .out(multiplexer_17_out));
  Multiplexer multiplexer_18 (.sel(isEnable), .in_0(RealClockOut), .in_1(I2CDone), .out(multiplexer_18_out));
  Counter #(.Bits(5)) counter_3 (.en(1'b1), .C(and_23_out), .clr(~readReg), .out(counter_3_out));  // open: ovf
  Counter #(.Bits(5)) counter_4 (.en(1'b1), .C(and_25_out), .clr(~isEnable), .out(counter_4_out));  // open: ovf
  Counter #(.Bits(16)) counter_5 (
    .en(isWriting), .C(multiplexer_17_out), .clr(~isEnable), .out(counter_5_out));  // open: ovf
  Counter #(.Bits(16)) counter_6 (
    .en(isReading), .C(multiplexer_18_out), .clr(~isEnable), .out(counter_6_out));  // open: ovf
  and and_23 (and_23_out, readReg, RealClockOut);
  Comparator #(.Bits(16)) comparator_10 (
    .a(wrtln), .b(counter_5_out), .gt(wrdataLeft), .eq(comparator_10_eq), .lt(wrdataLessThen));
  Comparator #(.Bits(16)) comparator_11 (
    .a(rdln), .b(counter_6_out), .gt(rddataLeft), .eq(comparator_11_eq));  // open: lt
  and and_24 (and_24_out, ~counter_7_out[0], counter_7_out[1]);  // And
  and and_25 (and_25_out, I2CDone, and_24_out);
  or or_10 (or_10_out, wrdataLeft, rddataLeft);
  Counter #(.Bits(2)) counter_7 (.en(1'b1), .C(and_27_out), .clr(or_12_out), .out(counter_7_out), .ovf(counter_7_ovf));
  or or_11 (or_11_out, and_24_out, counter_7_ovf);
  not not_7 (endCom, or_10_out);
  and and_26 (readSlave, ~wrdataLeft, rddataLeft);  // And
  or or_12 (or_12_out, ~isEnable, or_11_out);  // Or
  and and_27 (and_27_out, isReading, I2CDone);

  // Other names for the same wires on the sheet: AddressDebug[15:0] = Addr; adrin[15:0] = Addr; Dout[15:0] = datain;
  //   DoutDebug[15:0] = datain; interEn = FlagOut[3]; ioread = ioR; iowrite = ioW; isDone = I2CDone; C = RealClockOut;
  //   Clk = RealClockOut; mclk_t = RealClockOut; OpcodeDebug[15:8] = OPcode; sclout = SCL

  // Notes on the sheet:
  //   mclk: Hz: 1000
  //   Debugger
  //   contents of bootrom (hex, n*v repeats v):
  //   a0f,3f30,4224,4223,8020,3e02,8020,4130,2087*0,1
  //   interrupt Logic
  //   RandomNumberGen
  //   FlagStore
  //   wroteLen ?= writeLen
  //   redLen ?= readLen
endmodule
