// Digital circuit FIFO.dig as structural Verilog
module FIFO (
  input  [7:0] datain,
  input  wr,
  input  clk,
  input  rst,
  input  rd,
  output [7:0] dataOut,
  output [4:0] Count,
  output Full,
  output Empty
);

  Fifo8 #(.applicationType("IVERILOG"), .CodeFile("C:\\Users\\Berkant\\Desktop\\fpga\\RemedyCpu\\verilog\\fifo-8.v")) u_Fifo8 (
    .clk(clk), .data(datain), .rst(rst), .writeEn(wr), .readEn(rd), .FIFOEmpty(Empty), .FIFOFull(Full),
    .FIFOCount(Count), .readData(dataOut));

  // Other names for the same wires on the sheet: empy = Empty; readdat[7:0] = dataOut; readEn = rd; writeEn = wr
endmodule
