// Digital circuit GPI_HDL.dig as structural Verilog
// Simple general input register.
// {{de Element für ein allgemeines Eingaberegister.}}
module GPI_HDL (
  input  [15:0] A,
  input  R,
  input  In0,
  input  In1,
  input  In2,
  input  In3,
  input  In4,
  input  In5,
  input  In6,
  input  In7,
  input  In8,
  input  In9,
  input  In10,
  input  In11,
  input  In12,
  input  In13,
  input  In14,
  input  In15,
  input  clk,
  input  inter_En,
  output [15:0] D,
  output sel,
  output Interrupt
);

  wire comparator_1_eq, comparator_2_gt, comparator_2_lt;
  wire [15:0] multiplexer_1_out, register_1_q;

  Comparator #(.Bits(16)) comparator_1 (.a(A), .b(16'h4), .eq(comparator_1_eq));  // open: gt, lt
  Multiplexer #(.Bits(16)) multiplexer_1 (
    .sel(inter_En),
    .in_0({In15, In14, In13, In12, In11, In10, In9, In8, In7, In6, In5, In4, In3, In2, In1, In0}),
    .in_1(register_1_q), .out(multiplexer_1_out));
  Register #(.Bits(16)) register_1 (.D(multiplexer_1_out), .C(clk), .en(Interrupt), .Q(register_1_q));
  and and_1 (sel, comparator_1_eq, R);
  Comparator #(.Bits(16)) comparator_2 (
    .a(multiplexer_1_out), .b(register_1_q), .gt(comparator_2_gt), .lt(comparator_2_lt));  // open: eq
  or or_1 (Interrupt, comparator_2_gt, comparator_2_lt);

  assign D = {In15, In14, In13, In12, In11, In10, In9, In8, In7, In6, In5, In4, In3, In2, In1, In0};

  // Notes on the sheet:
  //   D: Output
  //   {{de Ausgabe}}
  //   A: address bus
  //   {{de Addressbus}}
  //   R: Read Enable
  //   {{de Lesefreigabe}}
  //   clk: Hz: 2
endmodule
