// Digital circuit SelectorForMultplx.dig as structural Verilog
module SelectorForMultplx (
  input  in1,
  input  in2,
  input  in3,
  input  in4,
  input  in5,
  input  in6,
  input  in7,
  input  in8,
  input  in9,
  input  in10,
  input  in11,
  input  in12,
  input  in13,
  input  in14,
  input  in15,
  output [3:0] out
);

  wire or_1_out, or_2_out, or_3_out, or_4_out;

  or or_1 (or_1_out, in1, in3, in9, in5, in7);
  or or_2 (or_2_out, in2, in3, in10, in6, in7);
  or or_3 (or_3_out, in4, in5, in12, in6, in7);
  or or_4 (or_4_out, in8, in9, in10, in11, in12);
  or or_5 (out[0], or_1_out, in11, in13, in15);
  or or_6 (out[1], or_2_out, in11, in14, in15);
  or or_7 (out[2], or_3_out, in13, in14, in15);
  or or_8 (out[3], or_4_out, in13, in14, in15);
endmodule
