// Digital circuit denic - Copy.dig as structural Verilog
module denic___Copy (
  input  [15:0] Addr,
  input  [15:0] Datain,
  input  Clk,
  output [3:0] out_1,
  output sda_out,
  output scl_out,
  output done,
  output [15:0] Dout
);

  wire and_1_out, and_2_out, and_3_out, and_4_out, and_5_out, and_6_out, and_7_out, and_8_out, and_9_out,
       and_10_out, and_12_out, comparator_1_eq, comparator_2_eq, comparator_3_eq, comparator_4_eq,
       comparator_6_eq, comparator_7_eq, comparator_8_eq, counter_2_ovf, counter_9_ovf, dipswitch_1_out,
       dipswitch_2_out, endCom, isEnable, isReading, isWriting, multiplexer_1_out, multiplexer_2_out,
       multiplexer_4_out, multiplexer_5_out, multiplexer_7_out, multiplexer_8_out, not_1_out, not_2_out,
       not_3_out, not_4_out, or_1_out, or_2_out, or_3_out, or_4_out, or_5_out, or_6_out, or_7_out, or_8_out,
       rddataLeft, readReg, readSlave, register_1_q, u_i2c_master_ack, u_i2c_master_busy, V_out, wrdataLeft,
       wrdataLessThen;
  wire [1:0] counter_9_out;
  wire [2:0] counter_2_out;
  wire [4:0] counter_1_out, counter_3_out, counter_4_out, counter_5_out, counter_6_out, multiplexer_3_out,
       multiplexer_6_out;
  wire [6:0] adrToWrite;
  wire [7:0] dataToi2c, RedData, rom_1_d;
  wire [15:0] Addr_q, counter_7_out, counter_8_out, rdln, wrtln;

  ROM #(.AddrBits(5), .Bits(8)) rom_1 (.A(counter_1_out), .sel(1'b1), .D(rom_1_d));
  Counter #(.Bits(5)) counter_1 (
    .en(counter_2_ovf), .C(V_out), .clr(dipswitch_1_out), .out(counter_1_out));  // open: ovf
  Multiplexer #(.Selector_Bits(3)) multiplexer_1 (
    .sel(counter_2_out), .in_0(rom_1_d[7]), .in_1(rom_1_d[6]), .in_2(rom_1_d[5]), .in_3(rom_1_d[4]),
    .in_4(rom_1_d[3]), .in_5(rom_1_d[2]), .in_6(rom_1_d[1]), .in_7(rom_1_d[0]), .out(multiplexer_1_out));
  DipSwitch dipswitch_1 (.out(dipswitch_1_out));
  Counter #(.Bits(3)) counter_2 (.en(1'b1), .C(V_out), .clr(dipswitch_1_out), .out(counter_2_out), .ovf(counter_2_ovf));
  Register register_1 (.D(done), .C(Clk), .en(or_1_out), .Q(register_1_q));
  or or_1 (or_1_out, ~isEnable, not_1_out);  // Or
  Button V (.out(V_out));
  not not_1 (not_1_out, register_1_q);
  Comparator #(.Bits(16)) comparator_1 (.a(Addr), .b(16'ha), .eq(comparator_1_eq));  // open: gt, lt
  Comparator #(.Bits(16)) comparator_2 (.a(Addr), .b(16'hb), .eq(comparator_2_eq));  // open: gt, lt
  and and_1 (and_1_out, register_1_q, isWriting);
  Comparator #(.Bits(16)) comparator_3 (.a(Addr), .b(16'hd), .eq(comparator_3_eq));  // open: gt, lt
  and and_2 (and_2_out, Clk, ~isEnable);  // And
  not not_2 (not_2_out, isWriting);
  Comparator #(.Bits(16)) comparator_4 (.a(Addr), .b(16'he), .eq(comparator_4_eq));  // open: gt, lt
  Comparator #(.Bits(16)) comparator_5 (.a(Addr), .b(16'hf), .eq(readReg));  // open: gt, lt
  or or_2 (or_2_out, done, and_2_out);
  Comparator #(.Bits(16)) comparator_6 (.a(Addr), .b(16'hc), .eq(comparator_6_eq));  // open: gt, lt
  and and_3 (and_3_out, Clk, not_2_out);
  Register #(.Bits(16)) writeLen (.D(Datain), .C(Clk), .en(comparator_1_eq), .Q(wrtln));
  Register #(.Bits(16)) u_Addr (.D(Datain), .C(Clk), .en(comparator_2_eq), .Q({Addr_q[15:8], adrToWrite, Addr_q[0]}));
  and and_4 (and_4_out, Datain[0], comparator_3_eq);
  or or_3 (or_3_out, done, and_3_out);
  Multiplexer multiplexer_2 (.sel(and_5_out), .in_0(and_4_out), .in_1(1'b0), .out(multiplexer_2_out));
  not not_3 (not_3_out, isEnable);
  DipSwitch dipswitch_2 (.out(dipswitch_2_out));
  and and_5 (and_5_out, isEnable, ~comparator_3_eq);  // And
  or or_4 (or_4_out, comparator_3_eq, endCom);
  Register #(.Bits(16)) readLen (.D(Datain), .C(Clk), .en(comparator_4_eq), .Q(rdln));
  or or_5 (or_5_out, isWriting, comparator_6_eq);
  and and_6 (and_6_out, ~comparator_6_eq, ~isEnable);  // And
  and and_7 (and_7_out, isEnable, and_1_out);
  i2c_master #(.applicationType("GHDL"), .CodeFile("C:\\Users\\Berkant\\Desktop\\fpga\\RemedyCpu\\Vhdl\\i2c master.vhdl")) u_i2c_master (
    .enable(isEnable), .clk(Clk), .addr({adrToWrite, readSlave}), .data(dataToi2c), .rst(not_3_out),
    .sdain(multiplexer_1_out), .sclin(dipswitch_2_out), .endCon(endCom), .sdaout(sda_out), .sclout(scl_out),
    .dataOut(RedData), .ack(u_i2c_master_ack), .busy(u_i2c_master_busy), .done(done), .isWriting(isWriting),
    .isReading(isReading), .statedebug(out_1));
  RAMDualPort #(.AddrBits(5), .Bits(8)) ramdualport_1 (
    .A(multiplexer_6_out), .Din(RedData), .str(multiplexer_4_out), .C(Clk), .ld(readReg), .D(Dout[15:8]));
  RAMDualPort #(.AddrBits(5), .Bits(8)) ramdualport_2 (
    .A(multiplexer_6_out), .Din(RedData), .str(multiplexer_5_out), .C(Clk), .ld(readReg), .D(Dout[7:0]));
  Register Enable (.D(multiplexer_2_out), .C(Clk), .en(or_4_out), .Q(isEnable));
  Counter #(.Bits(5)) counter_3 (.en(or_5_out), .C(~or_2_out), .clr(and_6_out), .out(counter_3_out));  // open: ovf
  Counter #(.Bits(5)) counter_4 (.en(and_7_out), .C(~or_3_out), .clr(not_2_out), .out(counter_4_out));  // open: ovf
  Multiplexer #(.Bits(5)) multiplexer_3 (
    .sel(isEnable), .in_0(counter_3_out), .in_1(counter_4_out), .out(multiplexer_3_out));
  Multiplexer multiplexer_4 (.sel(not_4_out), .in_0(1'b0), .in_1(isReading), .out(multiplexer_4_out));
  Multiplexer multiplexer_5 (.sel(counter_9_out[0]), .in_0(1'b0), .in_1(isReading), .out(multiplexer_5_out));
  RAMDualPort #(.AddrBits(5), .Bits(8)) DataToWrite (
    .A(multiplexer_3_out), .Din(Datain[7:0]), .str(comparator_6_eq), .C(Clk), .ld(isEnable), .D(dataToi2c));
  not not_4 (not_4_out, counter_9_out[0]);
  Multiplexer #(.Bits(5)) multiplexer_6 (
    .sel(readReg), .in_0(counter_6_out), .in_1(counter_5_out), .out(multiplexer_6_out));
  Multiplexer multiplexer_7 (.sel(isEnable), .in_0(Clk), .in_1(done), .out(multiplexer_7_out));
  Multiplexer multiplexer_8 (.sel(isEnable), .in_0(Clk), .in_1(done), .out(multiplexer_8_out));
  Counter #(.Bits(5)) counter_5 (.en(1'b1), .C(and_8_out), .clr(~readReg), .out(counter_5_out));  // open: ovf
  Counter #(.Bits(5)) counter_6 (.en(1'b1), .C(and_9_out), .clr(~isEnable), .out(counter_6_out));  // open: ovf
  Counter #(.Bits(16)) counter_7 (
    .en(isWriting), .C(multiplexer_7_out), .clr(~isEnable), .out(counter_7_out));  // open: ovf
  Counter #(.Bits(16)) counter_8 (
    .en(isReading), .C(multiplexer_8_out), .clr(~isEnable), .out(counter_8_out));  // open: ovf
  and and_8 (and_8_out, readReg, Clk);
  Comparator #(.Bits(16)) comparator_7 (
    .a(wrtln), .b(counter_7_out), .gt(wrdataLeft), .eq(comparator_7_eq), .lt(wrdataLessThen));
  Comparator #(.Bits(16)) comparator_8 (
    .a(rdln), .b(counter_8_out), .gt(rddataLeft), .eq(comparator_8_eq));  // open: lt
  and and_9 (and_9_out, done, and_10_out);
  and and_10 (and_10_out, ~counter_9_out[0], counter_9_out[1]);  // And
  Counter #(.Bits(2)) counter_9 (.en(1'b1), .C(and_12_out), .clr(or_8_out), .out(counter_9_out), .ovf(counter_9_ovf));
  or or_6 (or_6_out, wrdataLeft, rddataLeft);
  or or_7 (or_7_out, and_10_out, counter_9_ovf);
  not not_5 (endCom, or_6_out);
  and and_11 (readSlave, ~wrdataLeft, rddataLeft);  // And
  or or_8 (or_8_out, ~isEnable, or_7_out);  // Or
  and and_12 (and_12_out, isReading, done);

  // Other names for the same wires on the sheet: adrin[15:0] = Addr; isDone = done; mclk = Clk

  // Notes on the sheet:
  //   contents of rom_1 (hex, n*v repeats v):
  //   fe,cb,6c
  //   wroteLen ?= writeLen
  //   redLen ?= readLen
endmodule
