// Digital circuit denic.dig as structural Verilog
module denic (
  input  [15:0] Addr,
  input  [15:0] Datain,
  input  Clk,
  input  sdain,
  input  ioW,
  input  ioR,
  output scl_out,
  output isWrite,
  output isAdrWrite,
  output sda_out,
  output done,
  output ack,
  output busy,
  output [15:0] Dout
);

  wire and_1_out, and_2_out, and_3_out, and_4_out, and_5_out, and_6_out, and_8_out, and_9_out, and_10_out,
       and_11_out, and_12_out, and_13_out, and_14_out, and_15_out, and_16_out, and_18_out, comparator_1_eq,
       comparator_2_eq, comparator_3_eq, comparator_4_eq, comparator_5_eq, comparator_6_eq, comparator_7_eq,
       comparator_8_eq, counter_7_ovf, dipswitch_1_out, endCom, isEnable, isReading, multiplexer_1_out,
       multiplexer_3_out, multiplexer_4_out, multiplexer_6_out, multiplexer_7_out, not_1_out, not_2_out,
       not_3_out, not_4_out, or_1_out, or_2_out, or_3_out, or_4_out, or_6_out, or_7_out, or_8_out,
       rddataLeft, readReg, readSlave, register_1_q, u_i2c_master_isadrwriting, u_i2c_master_isstandby,
       wrdataLeft, wrdataLessThen;
  wire [1:0] counter_7_out;
  wire [3:0] u_i2c_master_statedebug;
  wire [4:0] counter_1_out, counter_2_out, counter_3_out, counter_4_out, multiplexer_2_out, multiplexer_5_out;
  wire [6:0] adrToWrite;
  wire [7:0] dataToi2c, RedData;
  wire [15:0] Addr_q, counter_5_out, counter_6_out, rdln, wrtln;

  Register register_1 (.D(done), .C(Clk), .en(or_1_out), .Q(register_1_q));
  or or_1 (or_1_out, ~isEnable, not_1_out);  // Or
  Comparator #(.Bits(16)) comparator_1 (.a(Addr), .b(16'ha), .eq(comparator_1_eq));  // open: gt, lt
  Comparator #(.Bits(16)) comparator_2 (.a(Addr), .b(16'hb), .eq(comparator_2_eq));  // open: gt, lt
  not not_1 (not_1_out, register_1_q);
  Comparator #(.Bits(16)) comparator_3 (.a(Addr), .b(16'hd), .eq(comparator_3_eq));  // open: gt, lt
  and and_1 (and_1_out, comparator_1_eq, ioW);
  and and_2 (and_2_out, comparator_2_eq, ioW);
  Comparator #(.Bits(16)) comparator_4 (.a(Addr), .b(16'hf), .eq(comparator_4_eq));  // open: gt, lt
  and and_3 (and_3_out, register_1_q, isWrite);
  Comparator #(.Bits(16)) comparator_5 (.a(Addr), .b(16'he), .eq(comparator_5_eq));  // open: gt, lt
  and and_4 (and_4_out, Clk, ~isEnable);  // And
  Comparator #(.Bits(16)) comparator_6 (.a(Addr), .b(16'hc), .eq(comparator_6_eq));  // open: gt, lt
  not not_2 (not_2_out, isWrite);
  and and_5 (and_5_out, comparator_3_eq, ioW);
  and and_6 (and_6_out, comparator_5_eq, ioW);
  and and_7 (readReg, comparator_4_eq, ioR);
  and and_8 (and_8_out, comparator_6_eq, ioW);
  and and_9 (and_9_out, Clk, not_2_out);
  Register #(.Bits(16)) writeLen (.D(Datain), .C(Clk), .en(and_1_out), .Q(wrtln));
  Register #(.Bits(16)) u_Addr (.D(Datain), .C(Clk), .en(and_2_out), .Q({Addr_q[15:8], adrToWrite, Addr_q[0]}));
  and and_10 (and_10_out, Datain[0], and_5_out);
  or or_2 (or_2_out, done, and_9_out);
  Multiplexer multiplexer_1 (.sel(and_11_out), .in_0(and_10_out), .in_1(1'b0), .out(multiplexer_1_out));
  not not_3 (not_3_out, isEnable);
  DipSwitch dipswitch_1 (.out(dipswitch_1_out));
  and and_11 (and_11_out, isEnable, ~and_5_out);  // And
  or or_3 (or_3_out, and_5_out, endCom);
  Register #(.Bits(16)) readLen (.D(Datain), .C(Clk), .en(and_6_out), .Q(rdln));
  or or_4 (or_4_out, isWrite, and_8_out);
  and and_12 (and_12_out, ~and_8_out, isEnable);  // And
  and and_13 (and_13_out, isEnable, and_3_out);
  i2c_master #(.applicationType("GHDL"), .CodeFile("C:\\Users\\Berkant\\Desktop\\fpga\\CpuDesign\\Vhdl\\i2c.vhdl")) u_i2c_master (
    .enable(isEnable), .clk(Clk), .addr({adrToWrite, readSlave}), .data(dataToi2c), .rst(not_3_out),
    .sdain(sdain), .sclin(dipswitch_1_out), .endCon(endCom), .sdaout(sda_out), .sclout(scl_out),
    .dataOut(RedData), .ack(ack), .busy(busy), .done(done), .isWriting(isWrite), .isReading(isReading),
    .isAdrWriting(u_i2c_master_isadrwriting), .isStandby(u_i2c_master_isstandby),
    .statedebug(u_i2c_master_statedebug));
  RAMDualPort #(.AddrBits(5), .Bits(8)) ramdualport_1 (
    .A(multiplexer_5_out), .Din(RedData), .str(multiplexer_3_out), .C(Clk), .ld(readReg), .D(Dout[15:8]));
  RAMDualPort #(.AddrBits(5), .Bits(8)) ramdualport_2 (
    .A(multiplexer_5_out), .Din(RedData), .str(multiplexer_4_out), .C(Clk), .ld(readReg), .D(Dout[7:0]));
  Register Enable (.D(multiplexer_1_out), .C(Clk), .en(or_3_out), .Q(isEnable));
  Counter #(.Bits(5)) counter_1 (.en(or_4_out), .C(~and_4_out), .clr(and_12_out), .out(counter_1_out));  // open: ovf
  Counter #(.Bits(5)) counter_2 (.en(and_13_out), .C(~or_2_out), .clr(not_2_out), .out(counter_2_out));  // open: ovf
  Multiplexer #(.Bits(5)) multiplexer_2 (
    .sel(isEnable), .in_0(counter_1_out), .in_1(counter_2_out), .out(multiplexer_2_out));
  Multiplexer multiplexer_3 (.sel(not_4_out), .in_0(1'b0), .in_1(isReading), .out(multiplexer_3_out));
  Multiplexer multiplexer_4 (.sel(counter_7_out[0]), .in_0(1'b0), .in_1(isReading), .out(multiplexer_4_out));
  or or_5 (isAdrWrite, u_i2c_master_isadrwriting, u_i2c_master_isstandby);
  RAMDualPort #(.AddrBits(5), .Bits(8)) DataToWrite (
    .A(multiplexer_2_out), .Din(Datain[7:0]), .str(and_8_out), .C(Clk), .ld(isEnable), .D(dataToi2c));
  not not_4 (not_4_out, counter_7_out[0]);
  Multiplexer #(.Bits(5)) multiplexer_5 (
    .sel(readReg), .in_0(counter_4_out), .in_1(counter_3_out), .out(multiplexer_5_out));
  Multiplexer multiplexer_6 (.sel(isEnable), .in_0(Clk), .in_1(done), .out(multiplexer_6_out));
  Multiplexer multiplexer_7 (.sel(isEnable), .in_0(Clk), .in_1(done), .out(multiplexer_7_out));
  Counter #(.Bits(5)) counter_3 (.en(1'b1), .C(and_14_out), .clr(~readReg), .out(counter_3_out));  // open: ovf
  Counter #(.Bits(5)) counter_4 (.en(1'b1), .C(and_15_out), .clr(~isEnable), .out(counter_4_out));  // open: ovf
  Counter #(.Bits(16)) counter_5 (
    .en(isWrite), .C(multiplexer_6_out), .clr(~isEnable), .out(counter_5_out));  // open: ovf
  Counter #(.Bits(16)) counter_6 (
    .en(isReading), .C(multiplexer_7_out), .clr(~isEnable), .out(counter_6_out));  // open: ovf
  and and_14 (and_14_out, readReg, Clk);
  Comparator #(.Bits(16)) comparator_7 (
    .a(wrtln), .b(counter_5_out), .gt(wrdataLeft), .eq(comparator_7_eq), .lt(wrdataLessThen));
  Comparator #(.Bits(16)) comparator_8 (
    .a(rdln), .b(counter_6_out), .gt(rddataLeft), .eq(comparator_8_eq));  // open: lt
  and and_15 (and_15_out, done, and_16_out);
  and and_16 (and_16_out, ~counter_7_out[0], counter_7_out[1]);  // And
  Counter #(.Bits(2)) counter_7 (.en(1'b1), .C(and_18_out), .clr(or_8_out), .out(counter_7_out), .ovf(counter_7_ovf));
  or or_6 (or_6_out, wrdataLeft, rddataLeft);
  or or_7 (or_7_out, and_16_out, counter_7_ovf);
  not not_5 (endCom, or_6_out);
  and and_17 (readSlave, ~wrdataLeft, rddataLeft);  // And
  or or_8 (or_8_out, ~isEnable, or_7_out);  // Or
  and and_18 (and_18_out, isReading, done);

  // Other names for the same wires on the sheet: adrin[15:0] = Addr; ioread = ioR; iowrite = ioW; isDone = done;
  //   isWriting = isWrite; mclk = Clk

  // Notes on the sheet:
  //   wroteLen ?= writeLen
  //   redLen ?= readLen
endmodule
