// Digital circuit pcTe.dig as structural Verilog
module pcTe (
  input  [15:0] ALU,
  input  C,
  input  abs,
  input  intr,
  input  reti,
  input  rel,
  input  Reset,
  input  interruptEnable,
  output [15:0] PC,
  output [15:0] NextPC
);

  wire and_1_out, and_2_out;
  wire [15:0] Add_ALU_s, multiplexer_1_out, multiplexer_2_out, multiplexer_3_out, multiplexer_4_out,
       multiplexer_5_out, register_1_q;

  Register #(.Bits(16), .isProgramCounter("true")) u_PC (.D(multiplexer_5_out), .C(~C), .en(1'b1), .Q(PC));
  Add #(.Bits(16)) Add_One (.a(PC), .b(16'h1), .c_i(1'b0), .s(NextPC));  // open: c_o
  Add #(.Bits(16)) Add_ALU (.a(NextPC), .b(ALU), .c_i(1'b0), .s(Add_ALU_s));  // open: c_o
  Multiplexer #(.Bits(16)) multiplexer_1 (.sel(rel), .in_0(NextPC), .in_1(Add_ALU_s), .out(multiplexer_1_out));
  Multiplexer #(.Bits(16)) multiplexer_2 (.sel(abs), .in_0(multiplexer_1_out), .in_1(ALU), .out(multiplexer_2_out));
  Register #(.Bits(16)) register_1 (.D(multiplexer_2_out), .C(~C), .en(and_1_out), .Q(register_1_q));
  and and_1 (and_1_out, intr, interruptEnable);
  Multiplexer #(.Bits(16)) multiplexer_3 (
    .sel(and_1_out), .in_0(multiplexer_2_out), .in_1(16'h2), .out(multiplexer_3_out));
  Multiplexer #(.Bits(16)) multiplexer_4 (
    .sel(and_2_out), .in_0(multiplexer_3_out), .in_1(register_1_q), .out(multiplexer_4_out));
  and and_2 (and_2_out, interruptEnable, reti);
  Multiplexer #(.Bits(16)) multiplexer_5 (
    .sel(Reset), .in_0(multiplexer_4_out), .in_1({16{1'b0}}), .out(multiplexer_5_out));

  // Notes on the sheet:
  //   ALU: current ALU output
  //   {{de Aktuelle ALU-Ausgabe}}
  //   abs: triggers a absolute jump
  //   {{de absoluten Sprung auslösen}}
  //   intr: triggers an interrupt
  //   {{de Interrupt auslösen}}
  //   reti: triggers an interrupt
  //   {{de Interrupt auslösen}}
  //   rel: triggers a relative jump
  //   {{de relativen Spung auslösen}}
  //   PC: Programm Counter 
  //   {{de Programmzähler}}
  //   NextPC: Programm Counter 
  //   {{de Programmzähler}}
  //   Reset: triggers an interrupt
  //   {{de Interrupt auslösen}}
  //   interruptEnable: triggers an interrupt
  //   {{de Interrupt auslösen}}
endmodule
