// Digital circuit spi.dig as structural Verilog
module spi (
  input  [15:0] a,
  input  sdfsdfz,
  input  [15:0] b,
  output [15:0] dfdf,
  output [15:0] sdsd
);

  wire dipswitch_1_out, dipswitch_2_out, dipswitch_3_out, dipswitch_4_out, u_spi_master_busy,
       u_spi_master_mosi, u_spi_master_sclk, u_spi_master_ss_n, u_spi_slave_busy, u_spi_slave_miso;

  DipSwitch #(.dipDefault("true")) dipswitch_1 (.out(dipswitch_1_out));
  DipSwitch #(.dipDefault("true")) dipswitch_2 (.out(dipswitch_2_out));
  DipSwitch dipswitch_3 (.out(dipswitch_3_out));
  DipSwitch #(.dipDefault("true")) dipswitch_4 (.out(dipswitch_4_out));
  spi_master #(.applicationType("GHDL")) u_spi_master (
    .clk(sdfsdfz), .reset_n(dipswitch_4_out), .enable(dipswitch_2_out), .cpol(dipswitch_3_out),
    .cpha(dipswitch_1_out), .miso(u_spi_slave_miso), .tx(a), .sclk(u_spi_master_sclk),
    .ss_n(u_spi_master_ss_n), .mosi(u_spi_master_mosi), .busy(u_spi_master_busy), .rx(sdsd));
  spi_slave #(.applicationType("GHDL")) u_spi_slave (
    .reset_n(dipswitch_4_out), .cpol(dipswitch_3_out), .cpha(dipswitch_1_out), .sclk(u_spi_master_sclk),
    .ss_n(u_spi_master_ss_n), .mosi(u_spi_master_mosi), .rx_enable(dipswitch_2_out), .tx(b),
    .miso(u_spi_slave_miso), .rx(dfdf), .busy(u_spi_slave_busy));

  // Notes on the sheet:
  //   sdfsdfz: Hz: 5
endmodule

/* Code of spi_master:
LIBRARY ieee;
USE ieee.std_logic_1164.all;
USE ieee.std_logic_arith.all;
USE ieee.std_logic_unsigned.all;

ENTITY spi_master IS
  GENERIC(
    data_length : INTEGER := 16);     --data length in bits
  PORT(
    clk     : IN     STD_LOGIC;                             --system clock
    reset_n : IN     STD_LOGIC;                             --asynchronous active low reset
    enable  : IN     STD_LOGIC;                             --initiate communication
	 cpol    : IN     STD_LOGIC;  									--clock polarity mode
    cpha    : IN     STD_LOGIC;  									--clock phase mode
    miso    : IN     STD_LOGIC;                             --master in slave out
    sclk    : OUT    STD_LOGIC;                             --spi clock
    ss_n    : OUT    STD_LOGIC;                             --slave select
    mosi    : OUT    STD_LOGIC;                             --master out slave in
    busy    : OUT    STD_LOGIC;                             --master busy signal
    tx		: IN     STD_LOGIC_VECTOR(16-1 DOWNTO 0);  --data to transmit
    rx	   : OUT    STD_LOGIC_VECTOR(16-1 DOWNTO 0)); --data received
END spi_master;

ARCHITECTURE behavioural OF spi_master IS
  TYPE FSM IS(init, execute);                           		--state machine
  SIGNAL state       : FSM;                             
  SIGNAL receive_transmit : STD_LOGIC;                      --'1' for tx, '0' for rx 
  SIGNAL clk_toggles : INTEGER RANGE 0 TO data_length*2 + 1;    --clock toggle counter
  SIGNAL last_bit		: INTEGER RANGE 0 TO data_length*2;        --last bit indicator
  SIGNAL rxBuffer    : STD_LOGIC_VECTOR(data_length-1 DOWNTO 0) := (OTHERS => '0'); --receive data buffer
  SIGNAL txBuffer    : STD_LOGIC_VECTOR(data_length-1 DOWNTO 0) := (OTHERS => '0'); --transmit data buffer
  SIGNAL INT_ss_n    : STD_LOGIC;                            --Internal register for ss_n 
  SIGNAL INT_sclk    : STD_LOGIC;                            --Internal register for sclk 


BEGIN
	
  -- wire internal registers to outside	
  ss_n <= INT_ss_n;
  sclk <= INT_sclk;
  
  PROCESS(clk, reset_n)
  BEGIN

    IF(reset_n = '0') THEN        --reset everything
      busy <= '1';                
      INT_ss_n <= '1';            
      mosi <= 'Z';                
      rx <= (OTHERS => '0');      
      state <= init;              

    ELSIF(falling_edge(clk)) THEN
      CASE state IS               

        WHEN init =>					 -- bus is idle
          busy <= '0';             
          INT_ss_n <= '1'; 		  
          mosi <= 'Z';             
   
          IF(enable = '1') THEN       		--initiate communication
            busy <= '1';             
            INT_sclk <= cpol;        		--set spi clock polarity
            receive_transmit <= NOT cpha; --set spi clock phase
            txBuffer <= tx;    				--put data to buffer to transmit
            clk_toggles <= 0;        		--initiate clock toggle counter
            last_bit <= data_length*2 + conv_integer(cpha) - 1; --set last rx data bit
            state <= execute;        
          ELSE
            state <= init;          
          END IF;


        WHEN execute =>
          busy <= '1';               
          INT_ss_n <= '0';           						--pull the slave select signal down
			 receive_transmit <= NOT receive_transmit;   --change receive transmit mode
          
			 -- counter
			 IF(clk_toggles = data_length*2 + 1) THEN
				clk_toggles <= 0;               				--reset counter
          ELSE
				clk_toggles <= clk_toggles + 1; 				--increment counter
          END IF;
            
          -- toggle sclk
          IF(clk_toggles <= data_length*2 AND INT_ss_n = '0') THEN 
            INT_sclk <= NOT INT_sclk; --toggle spi clock
          END IF;
            
          --receive miso bit
          IF(receive_transmit = '0' AND clk_toggles < last_bit + 1 AND INT_ss_n = '0') THEN 
            rxBuffer <= rxBuffer(data_length-2 DOWNTO 0) & miso; 
          END IF;
            
          --transmit mosi bit
          IF(receive_transmit = '1' AND clk_toggles < last_bit) THEN 
            mosi <= txBuffer(data_length-1);                    
            txBuffer <= txBuffer(data_length-2 DOWNTO 0) & '0'; 
          END IF;
            
          -- Finish/ resume the communication
          IF(clk_toggles = data_length*2 + 1) THEN   
            busy <= '0';             
            INT_ss_n <= '1';         
            mosi <= 'Z';             
            rx <= rxBuffer;    
            state <= init;          
          ELSE                       
            state <= execute;        
          END IF;
      END CASE;
    END IF;
  END PROCESS; 
END behavioural;
*/

/* Code of spi_slave:
LIBRARY ieee;
USE ieee.std_logic_1164.all;
USE ieee.std_logic_arith.all;
--this is comment
ENTITY spi_slave IS
  PORT(
    reset_n      : IN     STD_LOGIC;  																	 --asynchronous active low reset
    cpol    	  : IN 	  STD_LOGIC;  																	 --clock polarity mode
    cpha    	  : IN 	  STD_LOGIC;  																	 --clock phase mode
    sclk         : IN     STD_LOGIC;  																	 --spi clk
    ss_n         : IN     STD_LOGIC;  																	 --slave select
    mosi         : IN     STD_LOGIC;  																	 --master out slave in
    miso         : OUT    STD_LOGIC;  																	 --master in slave out
    rx_enable    : IN     STD_LOGIC;  																	 --enable signal to wire rxBuffer to outside 
    tx		 : IN     STD_LOGIC_VECTOR(16-1 DOWNTO 0);  						 --data to transmit
    rx		 : OUT    STD_LOGIC_VECTOR(16-1 DOWNTO 0) := (OTHERS => '0');  --data received
    busy         : OUT    STD_LOGIC := '0');  														 --slave busy signal	 
END spi_slave;

ARCHITECTURE behavioural OF spi_slave IS
  SIGNAL mode    : STD_LOGIC;  																	  --according to CPOL and CPHA
  SIGNAL clk     : STD_LOGIC;  
  SIGNAL bit_counter : STD_LOGIC_VECTOR(16 DOWNTO 0); 						  --active bit indicator
  SIGNAL rxBuffer  : STD_LOGIC_VECTOR(16-1 DOWNTO 0) := (OTHERS => '0');  --receiver buffer
  SIGNAL txBuffer  : STD_LOGIC_VECTOR(16-1 DOWNTO 0) := (OTHERS => '0');  --transmit buffer
BEGIN
  busy <= NOT ss_n;  
  
  mode <= cpol XOR cpha;  

  PROCESS (mode, ss_n, sclk)
  BEGIN
  IF(ss_n = '1') then
     clk <= '0';
  ELSE
     IF (mode = '1') then
	     clk <= sclk;
	  ELSE
	     clk <= NOT sclk;
	  END IF;
  END IF;
  END PROCESS;

  --where is the active bit
  PROCESS(ss_n, clk)
  BEGIN
    IF(ss_n = '1' OR reset_n = '0') THEN                         
	   bit_counter <= (others => '0');
if cpha = '1' then
  bit_counter(0) <= '1';
else
  bit_counter(1) <= '1';
	end if; 
    ELSE                                                         
      IF(rising_edge(clk)) THEN                                  
        bit_counter <= bit_counter(16-1 DOWNTO 0) & '0';    --left shift active bit indicator
      END IF;
    END IF;
  END PROCESS;


  PROCESS(ss_n, clk, rx_enable, reset_n)
  BEGIN      
  
	 --receive mosi bit
    IF(cpha = '0') then
		 IF(reset_n = '0') THEN			--reset the buffer
			rxBuffer <= (OTHERS => '0');
		 ELSIF(bit_counter /= "00000000000000010" and falling_edge(clk)) THEN
			rxBuffer(16-1 DOWNTO 0) <= rxBuffer(16-2 DOWNTO 0) & mosi;  --shift in the received bit
		 END IF;
	 ELSE
		 IF(reset_n = '0') THEN       --reset the buffer
			rxBuffer <= (OTHERS => '0');
		 ELSIF(bit_counter /= "00000000000000001" and falling_edge(clk)) THEN
			rxBuffer(16-1 DOWNTO 0) <= rxBuffer(16-2 DOWNTO 0) & mosi;  --shift in the received bit
		 END IF;
	 END IF;

    --if user wants the received data output it
    IF(reset_n = '0') THEN
      rx <= (OTHERS => '0');
    ELSIF(ss_n = '1' AND rx_enable = '1') THEN  
      rx <= rxBuffer;
    END IF;

    --transmit registers
    IF(reset_n = '0') THEN
      txBuffer <= (OTHERS => '0');
    ELSIF(ss_n = '1') THEN  
      txBuffer <= tx;
    ELSIF(bit_counter(16) = '0' AND rising_edge(clk)) THEN
      txBuffer(16-1 DOWNTO 0) <= txBuffer(16-2 DOWNTO 0) & txBuffer(16-1);  --shift through tx data
    END IF;

    --transmit miso bit
    IF(ss_n = '1' OR reset_n = '0') THEN           
      miso <= 'Z';
    ELSIF(rising_edge(clk)) THEN
      miso <= txBuffer(16-1);               
    END IF;
    
  END PROCESS;
END behavioural;
*/
