// Digital circuit timer.dig as structural Verilog
module timer (
  input  [15:0] dOut,
  input  [15:0] Addr,
  input  ioW,
  input  ioR,
  input  C,
  input  InterLock,
  input  [15:0] timerConfigAddr,
  input  [15:0] timerTargetAddr,
  input  [15:0] timerResetAddr,
  input  [15:0] timerReadAddr,
  input  rst,
  output [15:0] TimerOut,
  output \timerİnterrupt 
);

  wire and_1_out, and_2_out, and_3_out, and_4_out, and_5_out, and_6_out, and_7_out, and_8_out, and_9_out,
       and_10_out, and_11_out, and_12_out, and_13_out, comparator_3_eq, comparator_5_eq, comparator_5_gt,
       comparator_6_eq, multiplexer_1_out, multiplexer_4_out, not_1_out, or_1_out, or_2_out, or_3_out,
       or_4_out, Reset_q, timerconf, timerreset, timertarget;
  wire [2:0] multiplexer_2_out, u_muxEncoder_q;
  wire [6:0] counter_1_out;
  wire [15:0] conf, counterpreset_1_out, multiplexer_3_out, multiplexer_5_out, target;

  not not_1 (not_1_out, C);
  Comparator #(.Signed("true"), .Bits(16)) comparator_1 (
    .a(Addr), .b(timerConfigAddr), .eq(timerconf));  // open: gt, lt
  Comparator #(.Signed("true"), .Bits(16)) comparator_2 (
    .a(Addr), .b(timerResetAddr), .eq(timerreset));  // open: gt, lt
  Comparator #(.Bits(16)) comparator_3 (.a(timerReadAddr), .b(Addr), .eq(comparator_3_eq));  // open: gt, lt
  and and_1 (and_1_out, timerconf, ioW);
  Comparator #(.Signed("true"), .Bits(16)) comparator_4 (
    .a(Addr), .b(timerTargetAddr), .eq(timertarget));  // open: gt, lt
  and and_2 (and_2_out, timerreset, ioW);
  Register #(.Bits(16)) Config (.D(dOut), .C(not_1_out), .en(and_1_out), .Q(conf));
  and and_3 (and_3_out, timertarget, ioW);
  Register #(.Bits(16)) u_target (.D(dOut), .C(not_1_out), .en(and_3_out), .Q(target));
  and and_4 (and_4_out, dOut[0], and_2_out);
  and and_5 (and_5_out, comparator_3_eq, ioR);
  JK_FF Reset (.J(and_4_out), .C(C), .K(1'b1), .Q(Reset_q));  // open: nQ
  and and_6 (and_6_out, comparator_6_eq, conf[4]);
  and and_7 (and_7_out, comparator_6_eq, ~comparator_5_eq);  // And
  or or_1 (or_1_out, and_6_out, Reset_q);
  Comparator #(.Bits(16)) comparator_5 (
    .a(target), .b({16{1'b0}}), .gt(comparator_5_gt), .eq(comparator_5_eq));  // open: lt
  Counter #(.Bits(7)) counter_1 (.en(conf[0]), .C(C), .clr(1'b0), .out(counter_1_out));  // open: ovf
  and and_8 (and_8_out, ~comparator_5_eq, or_1_out);  // And
  Multiplexer #(.Selector_Bits(3)) multiplexer_1 (
    .sel(multiplexer_2_out), .in_0(C), .in_1(counter_1_out[0]), .in_2(counter_1_out[1]),
    .in_3(counter_1_out[2]), .in_4(counter_1_out[3]), .in_5(counter_1_out[4]), .in_6(counter_1_out[5]),
    .in_7(counter_1_out[6]), .out(multiplexer_1_out));
  Multiplexer #(.Bits(3)) multiplexer_2 (.sel(and_8_out), .in_0(conf[3:1]), .in_1(3'b000), .out(multiplexer_2_out));
  Multiplexer #(.Bits(16)) multiplexer_3 (
    .sel(comparator_5_gt), .in_0({16{1'b0}}), .in_1(target), .out(multiplexer_3_out));
  and and_9 (and_9_out, and_7_out, ~and_8_out);  // And
  or or_2 (or_2_out, InterLock, and_9_out);
  Multiplexer multiplexer_4 (.sel(or_2_out), .in_0(multiplexer_1_out), .in_1(1'b1), .out(multiplexer_4_out));
  or or_3 (or_3_out, and_8_out, rst);
  CounterPreset #(.Bits(16)) counterpreset_1 (
    .en(conf[0]), .C(multiplexer_4_out), .dir(1'b0), .in({16{1'b0}}), .ld(or_3_out), .clr(1'b0),
    .out(counterpreset_1_out));  // open: ovf
  Comparator #(.Bits(16)) comparator_6 (
    .a(multiplexer_3_out), .b(counterpreset_1_out), .eq(comparator_6_eq));  // open: gt, lt
  and and_10 (and_10_out, timertarget, ioR);
  and and_11 (and_11_out, timerconf, ioR);
  and and_12 (and_12_out, timerreset, ioR);
  and and_13 (and_13_out, ~comparator_5_eq, comparator_6_eq);  // And
  muxEncoder #(.applicationType("IVERILOG"), .CodeFile("D:\\Desktop\\fpga\\RemedyCpu\\verilog\\multipleToMux.v")) u_muxEncoder (
    .a(1'b0), .b(and_10_out), .c(and_11_out), .d(and_12_out), .e(1'b0), .f(1'b0), .g(1'b0), .h(1'b0),
    .Q(u_muxEncoder_q));
  Multiplexer #(.Selector_Bits(3), .Bits(16)) multiplexer_5 (
    .sel(u_muxEncoder_q), .in_0(counterpreset_1_out), .in_1(target), .in_2(conf), .in_3({16{1'b0}}),
    .in_4({16{1'b0}}), .in_5({16{1'b0}}), .in_6({16{1'b0}}), .in_7({16{1'b0}}), .out(multiplexer_5_out));
  and and_14 (\timerİnterrupt , ~InterLock, conf[5], and_13_out);  // And
  assign TimerOut = or_4_out ? multiplexer_5_out : 16'bz;  // Driver driver_1
  or or_4 (or_4_out, and_10_out, and_11_out, and_12_out, and_5_out);

  // Other names for the same wires on the sheet: timer_en = conf[0]; timerPrescaler[2:0] = conf[3:1];
  //   timerReload = conf[4]; timerInter = conf[5]

  // Notes on the sheet:
  //   timerTargetAddr: default 1
  //   timerResetAddr: default 2
  //   timerReadAddr: default 3
  //   Timer
endmodule
