// Digital circuit Alu.dig as structural Verilog
module Alu (
  input  [15:0] A,
  input  [15:0] B,
  input  carryIn,
  input  [5:0] AluOp,
  output [15:0] Out,
  output Neg,
  output Zero,
  output CarryOut
);

  wire add_1_c_o, sub_1_c_o;
  wire [15:0] add_1_s, and_2_out, divs_1_bolum, divs_1_kalan, mul_1_mul, neg_1_out, not_1_out, or_1_out,
       sub_1_s, xor_1_out;
  wire [15:15] and_1_out;
  wire [31:16] mul_1_mul_2;

  and and_1 (and_1_out[15], AluOp[5], carryIn);
  divs divs_1 (.bolunen(A), .Bolen(B), .bolum(divs_1_bolum), .Kalan(divs_1_kalan));
  Add #(.Bits(16)) add_1 (.a(A), .b(B), .c_i(and_1_out[15]), .s(add_1_s), .c_o(add_1_c_o));
  Sub #(.Bits(16)) sub_1 (.a(A), .b(B), .c_i(and_1_out[15]), .s(sub_1_s), .c_o(sub_1_c_o));
  assign and_2_out = A & B;  // And and_2, 16 bits wide
  assign or_1_out = A | B;  // Or or_1, 16 bits wide
  assign xor_1_out = A ^ B;  // XOr xor_1, 16 bits wide
  assign not_1_out = ~A;  // Not not_1, 16 bits wide
  Neg #(.Bits(16)) neg_1 (.in(A), .out(neg_1_out));
  Mul #(.Bits(16)) mul_1 (.a(A), .b(B), .mul({mul_1_mul_2, mul_1_mul}));
  Multiplexer #(.Selector_Bits(5), .Bits(16)) multiplexer_1 (
    .sel(AluOp[4:0]), .in_0(B), .in_1(add_1_s), .in_2(sub_1_s), .in_3(and_2_out), .in_4(or_1_out),
    .in_5(xor_1_out), .in_6(not_1_out), .in_7(neg_1_out), .in_8({A[14:0], and_1_out[15]}),
    .in_9({and_1_out[15], A[15:1]}), .in_10({{2{A[15]}}, A[14:1]}), .in_11({A[7:0], A[15:8]}),
    .in_12({A[11:8], A[15:12], A[3:0], A[7:4]}), .in_13(mul_1_mul), .in_14(divs_1_bolum),
    .in_15(divs_1_kalan), .in_16(A), .in_17({16{1'b0}}), .in_18({16{1'b0}}), .in_19({16{1'b0}}),
    .in_20({16{1'b0}}), .in_21({16{1'b0}}), .in_22({16{1'b0}}), .in_23({16{1'b0}}), .in_24({16{1'b0}}),
    .in_25({16{1'b0}}), .in_26({16{1'b0}}), .in_27({16{1'b0}}), .in_28({16{1'b0}}), .in_29({16{1'b0}}),
    .in_30({16{1'b0}}), .in_31({16{1'b0}}), .out({Neg, Out[14:0]}));
  Multiplexer #(.Selector_Bits(5)) multiplexer_2 (
    .sel(AluOp[4:0]), .in_0(1'b0), .in_1(add_1_c_o), .in_2(sub_1_c_o), .in_3(1'b0), .in_4(1'b0), .in_5(1'b0),
    .in_6(1'b0), .in_7(1'b0), .in_8(A[15]), .in_9(A[0]), .in_10(A[0]), .in_11(1'b0), .in_12(1'b0),
    .in_13(1'b0), .in_14(1'b0), .in_15(1'b0), .in_16(1'b0), .in_17(1'b0), .in_18(1'b0), .in_19(1'b0),
    .in_20(1'b0), .in_21(1'b0), .in_22(1'b0), .in_23(1'b0), .in_24(1'b0), .in_25(1'b0), .in_26(1'b0),
    .in_27(1'b0), .in_28(1'b0), .in_29(1'b0), .in_30(1'b0), .in_31(1'b0), .out(CarryOut));
  Comparator #(.Signed("true"), .Bits(16)) comparator_1 (
    .a({Neg, Out[14:0]}), .b({16{1'b0}}), .eq(Zero));  // open: gt, lt

  assign Out[15] = Neg;

  // Other names for the same wires on the sheet: sel[4:0] = AluOp[4:0]

  // Notes on the sheet:
  //   logical shift left
  //   logical shift right
  //   arithmetic shift right
  //   swapBytes
  //   swapNibbles
  //   ALU
endmodule
