// Digital circuit Alut.dig as structural Verilog
module Alut (
  input  [15:0] A,
  input  [15:0] B,
  input  [4:0] Aluop,
  input  CarryIn,
  output Zero,
  output Neg,
  output Carry,
  output [15:0] DataOut
);

  wire add_1_c_o, and_1_out, asr_1_p2, lsl_1_p4, lsr_1_p4, sub_1_c_o;
  wire [15:0] add_1_s, and_2_out, asr_1_p3, lsl_1_p3, lsr_1_p3, neg_1_out, not_1_out, or_1_out, sub_1_s,
       swap_1_p2, swapn_1_p2, xor_1_out;
  wire [31:0] mul_1_mul;

  and and_1 (and_1_out, Aluop[4], CarryIn);
  Add #(.Bits(16)) add_1 (.a(A), .b(B), .c_i(and_1_out), .s(add_1_s), .c_o(add_1_c_o));
  Sub #(.Bits(16)) sub_1 (.a(A), .b(B), .c_i(and_1_out), .s(sub_1_s), .c_o(sub_1_c_o));
  assign and_2_out = A & B;  // And and_2, 16 bits wide
  assign or_1_out = A | B;  // Or or_1, 16 bits wide
  assign xor_1_out = A ^ B;  // XOr xor_1, 16 bits wide
  assign not_1_out = ~A;  // Not not_1, 16 bits wide
  Neg #(.Bits(16)) neg_1 (.in(A), .out(neg_1_out));
  // LSL lsl_1: pin names not known; wires that end beside it: A, and_1_out, lsl_1_p3, lsl_1_p4
  // LSR lsr_1: pin names not known; wires that end beside it: A, and_1_out, lsr_1_p3, lsr_1_p4
  // ASR asr_1: pin names not known; wires that end beside it: A, asr_1_p2, asr_1_p3
  // SWAP swap_1: pin names not known; wires that end beside it: A, swap_1_p2
  // SWAPN swapn_1: pin names not known; wires that end beside it: A, swapn_1_p2
  Mul #(.Bits(16)) mul_1 (.a(A), .b(B), .mul(mul_1_mul));
  Multiplexer #(.Selector_Bits(4), .Bits(16)) multiplexer_1 (
    .sel(Aluop[3:0]), .in_0(B), .in_1(add_1_s), .in_2(sub_1_s), .in_3(and_2_out), .in_4(or_1_out),
    .in_5(xor_1_out), .in_6(not_1_out), .in_7(neg_1_out), .in_8(lsl_1_p3), .in_9(lsr_1_p3), .in_10(asr_1_p3),
    .in_11(swap_1_p2), .in_12(swapn_1_p2), .in_13(mul_1_mul[15:0]), .in_14({16{1'b0}}), .in_15({16{1'b0}}),
    .out(DataOut));
  Multiplexer #(.Selector_Bits(4)) multiplexer_2 (
    .sel(Aluop[3:0]), .in_0(1'b0), .in_1(add_1_c_o), .in_2(sub_1_c_o), .in_3(1'b0), .in_4(1'b0), .in_5(1'b0),
    .in_6(1'b0), .in_7(1'b0), .in_8(lsl_1_p4), .in_9(lsr_1_p4), .in_10(asr_1_p2), .in_11(1'b0), .in_12(1'b0),
    .in_13(1'b0), .in_14(1'b0), .in_15(1'b0), .out(Carry));
  Comparator #(.Signed("true"), .Bits(16)) comparator_1 (.a(DataOut), .b({16{1'b0}}), .eq(Zero));  // open: gt, lt

  assign Neg = DataOut[15];

  // Other names for the same wires on the sheet: sel[3:0] = Aluop[3:0]
endmodule
