// Digital circuit ClockDiv.dig as structural Verilog
module ClockDiv (
  input  Clock,
  output S_in,
  output C_in,
  output C
);

  wire and_1_out, and_2_out, not_1_out, or_1_out, rs_ff_as_1_nq, rs_ff_as_1_q, t_ff_1_nq;
  wire [1:0] counter_1_out;

  Counter #(.Bits(2)) counter_1 (.en(1'b1), .C(Clock), .clr(and_1_out), .out(counter_1_out));  // open: ovf
  and and_1 (and_1_out, rs_ff_as_1_q, counter_1_out[0]);
  and and_2 (and_2_out, counter_1_out[0], rs_ff_as_1_q);
  RS_FF_AS rs_ff_as_1 (.S(counter_1_out[1]), .R(1'b0), .Q(rs_ff_as_1_q), .nQ(rs_ff_as_1_nq));
  or or_1 (or_1_out, and_2_out, counter_1_out[1]);
  not not_1 (not_1_out, or_1_out);
  T_FF #(.withEnable("false")) t_ff_1 (.C(not_1_out), .Q(S_in), .nQ(t_ff_1_nq));
  and and_3 (C_in, or_1_out, S_in);
  and and_4 (C, t_ff_1_nq, or_1_out);

  // Notes on the sheet:
  //   S_in: Signal to configure the processor for reading 
  //   the next instruction.
  //   {{de Signal welches den Prozessor für das Lesen 
  //   eines Befehlswortes konfiguriert.}}
  //   C_in: Clock signal to read the next instruction.
  //   {{de Taktsignal für das Lesen eines Befehlswortes}}
  //   C: Clock used to execute an instruction.
  //   {{de Takt der das Ausführen eines Befehlswortes 
  //   steuert.}}
endmodule
