// Digital circuit controllogic.dig as structural Verilog
module controllogic (
  input  A,
  input  B,
  input  C,
  input  D,
  input  E,
  input  F,
  input  G,
  output muxb0,
  output muxb1,
  output muxb2,
  output src2D,
  output aluop0,
  output aluop1,
  output aluop2,
  output aluop3,
  output aluop4,
  output WE,
  output sf,
  output alu2D,
  output iem0,
  output iem1,
  output br0,
  output br1,
  output br2,
  output muxA,
  output ld,
  output st,
  output abs,
  output ioW,
  output ioR,
  output stPC,
  output Reti,
  output randomSel,
  output timerSel
);

  wire nand_1_out, nand_2_out, nand_3_out, nand_4_out, nand_5_out, nand_6_out, nand_7_out, nand_8_out,
       nand_9_out, nand_10_out, nand_11_out, nand_12_out, nand_13_out, nand_14_out, nand_15_out, nand_16_out,
       nand_17_out, nand_18_out, nand_19_out, nand_20_out, nand_21_out, nand_22_out, nand_23_out,
       nand_24_out, nand_25_out, nand_26_out, nand_27_out, nand_28_out, nand_29_out, nand_30_out,
       nand_31_out, nand_32_out, nand_33_out, nand_34_out, nand_35_out, nand_36_out, nand_37_out,
       nand_38_out, nand_39_out, nand_40_out, nand_41_out, nand_42_out, nand_43_out, nand_44_out,
       nand_45_out, nand_46_out, nand_47_out, nand_48_out, nand_49_out, nand_50_out, nand_51_out,
       nand_52_out, nand_53_out, nand_54_out, nand_55_out, nand_56_out, nand_57_out, nand_58_out,
       nand_59_out, nand_60_out, nand_61_out, nand_62_out, nand_63_out, nand_64_out, nand_65_out,
       nand_66_out, nand_67_out, nand_68_out, nand_69_out, nand_70_out, nand_71_out, nand_72_out,
       nand_73_out, nand_74_out, nand_75_out, nand_76_out, nand_77_out, nand_78_out, nand_79_out,
       nand_80_out, nand_81_out, nand_82_out, nand_83_out, nand_84_out, nand_85_out, nand_86_out,
       nand_87_out, nand_88_out, nand_89_out, nand_90_out, nand_91_out, nand_92_out, nand_93_out,
       nand_94_out, nand_95_out, nand_96_out, nand_97_out, nand_98_out, nand_99_out, nand_100_out,
       nand_101_out, nand_102_out, nand_103_out, nand_104_out, nand_105_out, nand_106_out, nand_107_out,
       nand_108_out, nand_109_out, nand_110_out, nand_111_out, nand_112_out, nand_113_out, nand_114_out,
       nand_115_out, nand_116_out, nand_117_out, nand_118_out, nand_119_out, nand_120_out, nand_121_out,
       nand_122_out, nand_123_out, nand_124_out, nand_125_out, nand_126_out, nand_127_out, nand_128_out,
       nand_129_out, nand_130_out, nand_131_out, nand_132_out, nand_133_out, nand_134_out, nand_135_out,
       nand_136_out, nand_137_out, nand_138_out, nand_139_out, nand_140_out, nand_141_out, nand_142_out,
       nand_143_out, nand_144_out, nand_145_out, nand_146_out, nand_147_out, nand_148_out, nand_149_out,
       nand_150_out, nand_151_out, nand_152_out, nand_153_out, nand_154_out, nand_155_out, nand_156_out,
       nand_157_out, nand_158_out, nand_159_out, nand_160_out, nand_161_out, nand_162_out, nand_163_out,
       nand_164_out, nand_165_out, nand_166_out, nand_167_out, not_1_out, not_2_out, not_3_out, not_4_out,
       not_5_out, not_6_out, not_7_out;

  not not_1 (not_1_out, A);
  not not_2 (not_2_out, B);
  not not_3 (not_3_out, C);
  not not_4 (not_4_out, D);
  not not_5 (not_5_out, E);
  not not_6 (not_6_out, F);
  not not_7 (not_7_out, G);
  nand nand_1 (nand_1_out, A, not_2_out, not_3_out, not_4_out, not_5_out, F, not_7_out);
  nand nand_2 (nand_2_out, A, not_2_out, not_3_out, not_4_out, E, F, G);
  nand nand_3 (nand_3_out, A, not_2_out, not_3_out, D, not_5_out, not_6_out, not_7_out);
  nand nand_4 (nand_4_out, not_1_out, not_3_out, D, E, F, not_7_out);
  nand nand_5 (nand_5_out, not_1_out, B, C, not_5_out, not_6_out, not_7_out);
  nand nand_6 (nand_6_out, not_1_out, not_2_out, not_3_out, D, F, not_7_out);
  nand nand_7 (nand_7_out, not_1_out, not_2_out, not_3_out, D, E, not_7_out);
  nand nand_8 (nand_8_out, not_1_out, not_2_out, C, not_4_out, not_5_out, not_7_out);
  nand nand_9 (nand_9_out, not_1_out, B, not_3_out, not_4_out, not_5_out, G);
  nand nand_10 (nand_10_out, not_1_out, C, D, not_6_out, G);
  nand nand_11 (nand_11_out, not_1_out, C, not_4_out, E, G);
  nand nand_12 (nand_12_out, not_1_out, B, C, E, G);
  nand nand_13 (nand_13_out, not_1_out, B, C, not_4_out, E);
  nand nand_14 (nand_14_out, A, not_2_out, not_3_out, not_4_out, E, F, not_7_out);
  nand nand_15 (nand_15_out, not_1_out, C, not_4_out, not_5_out, not_6_out, G);
  nand nand_16 (nand_16_out, not_1_out, B, not_3_out, not_4_out, not_5_out, not_7_out);
  nand nand_17 (nand_17_out, A, not_2_out, not_3_out, not_4_out, not_5_out, G);
  nand nand_18 (nand_18_out, A, not_2_out, not_3_out, not_4_out, not_5_out, not_6_out);
  nand nand_19 (nand_19_out, not_1_out, not_3_out, D, F, G);
  nand nand_20 (nand_20_out, not_1_out, C, D, not_6_out, not_7_out);
  nand nand_21 (nand_21_out, not_1_out, B, C, not_6_out, G);
  nand nand_22 (nand_22_out, not_1_out, B, C, F, not_7_out);
  nand nand_23 (nand_23_out, not_1_out, C, not_4_out, E, not_7_out);
  nand nand_24 (nand_24_out, not_1_out, not_2_out, not_3_out, D, G);
  nand nand_25 (nand_25_out, not_1_out, B, D, E);
  nand nand_26 (nand_26_out, not_1_out, B, C, E);
  nand nand_27 (nand_27_out, not_1_out, B, C, D, E, F, G);
  nand nand_28 (nand_28_out, not_1_out, C, not_4_out, not_5_out, not_6_out, not_7_out);
  nand nand_29 (nand_29_out, not_1_out, B, not_4_out, not_5_out, F, G);
  nand nand_30 (nand_30_out, not_1_out, B, not_3_out, not_5_out, F, G);
  nand nand_31 (nand_31_out, A, not_2_out, not_3_out, not_5_out, not_6_out, not_7_out);
  nand nand_32 (nand_32_out, not_1_out, not_2_out, not_3_out, D, F, not_7_out);
  nand nand_33 (nand_33_out, not_1_out, not_2_out, C, D, not_6_out, G);
  nand nand_34 (nand_34_out, A, not_2_out, not_3_out, not_4_out, F, G);
  nand nand_35 (nand_35_out, not_1_out, not_2_out, C, not_4_out, not_5_out, not_7_out);
  nand nand_36 (nand_36_out, not_1_out, not_2_out, C, not_4_out, E, G);
  nand nand_37 (nand_37_out, not_1_out, B, not_3_out, not_4_out, not_5_out, G);
  nand nand_38 (nand_38_out, A, not_2_out, not_3_out, not_4_out, not_5_out, not_7_out);
  nand nand_39 (nand_39_out, not_1_out, not_3_out, D, E, not_7_out);
  nand nand_40 (nand_40_out, not_1_out, not_2_out, not_3_out, not_4_out, not_5_out, not_6_out, G);
  nand nand_41 (nand_41_out, not_1_out, B, not_3_out, D, not_5_out, F, G);
  nand nand_42 (nand_42_out, not_1_out, B, not_3_out, D, E, not_6_out, G);
  nand nand_43 (nand_43_out, not_1_out, B, C, not_4_out, not_5_out, not_6_out, G);
  nand nand_44 (nand_44_out, A, not_2_out, not_3_out, not_4_out, not_5_out, not_6_out, not_7_out);
  nand nand_45 (nand_45_out, not_1_out, B, D, E, F, not_7_out);
  nand nand_46 (nand_46_out, not_1_out, B, C, D, E, F);
  nand nand_47 (nand_47_out, not_1_out, not_2_out, not_3_out, D, E, F, not_7_out);
  nand nand_48 (nand_48_out, not_1_out, not_2_out, C, not_4_out, not_5_out, not_6_out, G);
  nand nand_49 (nand_49_out, not_1_out, not_2_out, C, not_4_out, not_5_out, F, not_7_out);
  nand nand_50 (nand_50_out, not_1_out, not_2_out, C, D, E, F, G);
  nand nand_51 (nand_51_out, not_1_out, not_3_out, not_4_out, not_5_out, F, G);
  nand nand_52 (nand_52_out, not_1_out, not_2_out, not_3_out, E, not_6_out, G);
  nand nand_53 (nand_53_out, not_1_out, B, not_3_out, not_4_out, F);
  nand nand_54 (nand_54_out, not_1_out, not_2_out, C, D, not_5_out, F, G);
  nand nand_55 (nand_55_out, A, not_2_out, not_3_out, not_4_out, E, not_6_out, G);
  nand nand_56 (nand_56_out, A, not_2_out, not_3_out, not_4_out, E, F, not_7_out);
  nand nand_57 (nand_57_out, not_1_out, B, not_3_out, D, not_5_out, not_7_out);
  nand nand_58 (nand_58_out, not_1_out, not_2_out, C, D, E, not_6_out);
  nand nand_59 (nand_59_out, not_1_out, B, not_3_out, D, not_5_out, not_6_out);
  nand nand_60 (nand_60_out, not_1_out, B, not_3_out, not_4_out, E);
  nand nand_61 (nand_61_out, not_1_out, B, not_3_out, D, not_5_out, F, not_7_out);
  nand nand_62 (nand_62_out, A, not_2_out, not_3_out, not_4_out, E, not_6_out, G);
  nand nand_63 (nand_63_out, A, not_2_out, not_3_out, not_4_out, E, F, not_7_out);
  nand nand_64 (nand_64_out, not_1_out, not_2_out, not_4_out, E, F, G);
  nand nand_65 (nand_65_out, not_1_out, not_2_out, D, not_5_out, not_6_out, not_7_out);
  nand nand_66 (nand_66_out, not_1_out, not_2_out, C, not_5_out, F, G);
  nand nand_67 (nand_67_out, not_1_out, not_2_out, C, not_4_out, E, F);
  nand nand_68 (nand_68_out, not_1_out, not_2_out, C, D, not_6_out);
  nand nand_69 (nand_69_out, not_1_out, not_2_out, C, D, not_5_out);
  nand nand_70 (nand_70_out, not_1_out, not_2_out, D, E, F, G);
  nand nand_71 (nand_71_out, not_1_out, not_2_out, C, D, F, not_7_out);
  nand nand_72 (nand_72_out, not_1_out, not_2_out, not_4_out, E, not_6_out);
  nand nand_73 (nand_73_out, not_1_out, B, not_3_out, not_5_out, not_6_out);
  nand nand_74 (nand_74_out, not_1_out, not_2_out, C, not_4_out, not_5_out);
  nand nand_75 (nand_75_out, not_1_out, B, not_3_out, not_4_out, not_5_out);
  nand nand_76 (nand_76_out, not_2_out, not_3_out, not_4_out, E, not_6_out, G);
  nand nand_77 (nand_77_out, not_2_out, not_3_out, not_4_out, E, F, not_7_out);
  nand nand_78 (nand_78_out, not_1_out, B, C, not_4_out, not_5_out, not_6_out, G);
  nand nand_79 (nand_79_out, not_1_out, B, C, not_4_out, not_5_out, F, not_7_out);
  nand nand_80 (nand_80_out, A, not_2_out, not_3_out, not_4_out, not_5_out, not_6_out, not_7_out);
  nand nand_81 (nand_81_out, not_1_out, not_3_out, D, E, not_6_out, not_7_out);
  nand nand_82 (nand_82_out, not_1_out, not_2_out, not_3_out, E, F, not_7_out);
  nand nand_83 (nand_83_out, not_1_out, not_2_out, not_3_out, not_4_out, F, not_7_out);
  nand nand_84 (nand_84_out, not_1_out, not_2_out, C, D, not_5_out, G);
  nand nand_85 (nand_85_out, not_1_out, B, not_3_out, not_4_out, E, G);
  nand nand_86 (nand_86_out, not_1_out, B, not_3_out, D, not_5_out, G);
  nand nand_87 (nand_87_out, not_1_out, not_2_out, not_5_out, F, G);
  nand nand_88 (nand_88_out, not_1_out, not_2_out, D, not_6_out, not_7_out);
  nand nand_89 (nand_89_out, not_1_out, not_2_out, D, E, not_6_out);
  nand nand_90 (nand_90_out, not_1_out, not_2_out, C, E, not_6_out);
  nand nand_91 (nand_91_out, not_2_out, not_3_out, not_4_out, not_5_out, F, G);
  nand nand_92 (nand_92_out, not_1_out, D, not_5_out, F, not_7_out);
  nand nand_93 (nand_93_out, not_1_out, not_3_out, E, not_6_out, not_7_out);
  nand nand_94 (nand_94_out, not_1_out, not_3_out, E, F, G);
  nand nand_95 (nand_95_out, not_1_out, C, not_4_out, not_5_out, not_7_out);
  nand nand_96 (nand_96_out, not_1_out, not_3_out, D, not_5_out, not_6_out);
  nand nand_97 (nand_97_out, not_1_out, C, not_4_out, not_5_out, F);
  nand nand_98 (nand_98_out, not_1_out, not_2_out, D, not_6_out);
  nand nand_99 (nand_99_out, not_1_out, not_3_out, not_4_out, E);
  nand nand_100 (nand_100_out, not_1_out, not_2_out, D, not_5_out);
  nand nand_101 (nand_101_out, not_1_out, not_2_out, not_3_out, D);
  nand nand_102 (nand_102_out, not_1_out, not_2_out, C, not_4_out);
  nand nand_103 (nand_103_out, not_2_out, not_3_out, D, not_5_out, not_6_out, not_7_out);
  nand nand_104 (nand_104_out, not_2_out, not_3_out, not_4_out, G);
  nand nand_105 (nand_105_out, not_2_out, not_3_out, not_4_out, F);
  nand nand_106 (nand_106_out, not_1_out, not_3_out, D, not_5_out, not_6_out, not_7_out);
  nand nand_107 (nand_107_out, not_1_out, not_2_out, not_4_out, F, not_7_out);
  nand nand_108 (nand_108_out, not_1_out, not_2_out, D, F, G);
  nand nand_109 (nand_109_out, not_1_out, not_2_out, not_3_out, F, G);
  nand nand_110 (nand_110_out, not_1_out, not_2_out, C, not_6_out);
  nand nand_111 (nand_111_out, not_1_out, B, not_3_out, not_4_out);
  nand nand_112 (nand_112_out, not_1_out, not_2_out, E);
  nand nand_113 (nand_113_out, not_2_out, not_3_out, not_4_out, E, not_6_out, G);
  nand nand_114 (nand_114_out, not_2_out, not_3_out, not_4_out, E, F, not_7_out);
  nand nand_115 (nand_115_out, not_1_out, C, not_4_out, not_5_out, F, G);
  nand nand_116 (nand_116_out, not_1_out, not_3_out, D, not_5_out, not_7_out);
  nand nand_117 (nand_117_out, not_1_out, not_3_out, D, not_5_out, not_6_out);
  nand nand_118 (nand_118_out, not_1_out, not_2_out, E, not_6_out);
  nand nand_119 (nand_119_out, not_1_out, not_2_out, not_4_out, F);
  nand nand_120 (nand_120_out, not_1_out, not_2_out, not_3_out, F);
  nand nand_121 (nand_121_out, not_1_out, not_3_out, not_4_out, E);
  nand nand_122 (nand_122_out, not_1_out, not_2_out, C, not_5_out);
  nand nand_123 (nand_123_out, not_2_out, not_3_out, not_4_out, E, not_6_out, G);
  nand nand_124 (nand_124_out, not_2_out, not_3_out, not_4_out, E, F, not_7_out);
  nand nand_125 (nand_125_out, not_1_out, not_2_out, C, not_4_out, not_5_out, not_6_out, G);
  nand nand_126 (nand_126_out, A, not_2_out, not_3_out, not_4_out, not_5_out, not_6_out, G);
  nand nand_127 (nand_127_out, A, not_2_out, not_3_out, not_4_out, E, F, not_7_out);
  nand nand_128 (nand_128_out, not_1_out, C, D, E, not_6_out, not_7_out);
  nand nand_129 (nand_129_out, not_1_out, not_2_out, C, D, not_6_out, not_7_out);
  nand nand_130 (nand_130_out, not_1_out, B, C, D, F, not_7_out);
  nand nand_131 (nand_131_out, not_1_out, not_2_out, C, not_4_out, E, not_7_out);
  nand nand_132 (nand_132_out, not_1_out, B, not_3_out, not_4_out, not_5_out, not_7_out);
  nand nand_133 (nand_133_out, not_1_out, not_3_out, D, E, G);
  nand nand_134 (nand_134_out, not_1_out, not_2_out, not_3_out, D, G);
  nand nand_135 (nand_135_out, not_1_out, B, not_3_out, D, E, not_6_out, G);
  nand nand_136 (nand_136_out, not_1_out, B, C, D, E, F, not_7_out);
  nand nand_137 (nand_137_out, not_1_out, B, C, not_4_out, E, F, G);
  nand nand_138 (nand_138_out, not_1_out, B, C, D, not_6_out, G);
  nand nand_139 (nand_139_out, not_1_out, B, C, D, not_5_out, not_6_out);
  nand nand_140 (nand_140_out, not_1_out, B, C, not_4_out, E, not_6_out, G);
  nand nand_141 (nand_141_out, not_1_out, B, C, not_4_out, E, F, not_7_out);
  nand nand_142 (nand_142_out, not_1_out, B, C, D, not_5_out, not_6_out);
  nand nand_143 (nand_143_out, not_1_out, B, C, D, not_5_out, not_6_out, G);
  nand nand_144 (nand_144_out, not_1_out, B, C, not_4_out, E, not_7_out);
  nand nand_145 (nand_145_out, not_1_out, B, C, not_4_out, E, F);
  nand nand_146 (nand_146_out, not_1_out, B, not_3_out, D, E, not_6_out, not_7_out);
  nand nand_147 (nand_147_out, not_1_out, B, C, not_4_out, not_5_out, F, not_7_out);
  nand nand_148 (nand_148_out, A, not_2_out, not_3_out, not_4_out, not_5_out, G);
  nand nand_149 (nand_149_out, A, not_2_out, not_3_out, not_4_out, not_5_out, F);
  nand nand_150 (nand_150_out, not_1_out, B, not_3_out, D, E, not_6_out, not_7_out);
  nand nand_151 (nand_151_out, not_1_out, B, not_3_out, D, E, F, G);
  nand nand_152 (nand_152_out, not_1_out, B, C, not_4_out, not_5_out, not_7_out);
  nand nand_153 (nand_153_out, not_1_out, B, not_3_out, D, not_5_out, F, G);
  nand nand_154 (nand_154_out, not_1_out, B, not_3_out, D, E, not_6_out, G);
  nand nand_155 (nand_155_out, not_1_out, B, not_3_out, D, E, F, not_7_out);
  nand nand_156 (nand_156_out, not_1_out, B, C, not_4_out, not_5_out, not_6_out, G);
  nand nand_157 (nand_157_out, not_1_out, B, C, D, E, not_6_out, not_7_out);
  nand nand_158 (nand_158_out, A, not_2_out, not_3_out, not_4_out, E, not_6_out, not_7_out);
  nand nand_159 (nand_159_out, not_1_out, B, C, D, not_5_out, F);
  nand nand_160 (nand_160_out, A, not_2_out, not_3_out, not_4_out, not_5_out, not_6_out, not_7_out);
  nand nand_161 (nand_161_out, not_1_out, B, C, D, E, F);
  nand nand_162 (nand_162_out, A, not_2_out, not_3_out, not_4_out, not_5_out, G);
  nand nand_163 (nand_163_out, A, not_2_out, not_3_out, not_4_out, not_5_out, F);
  nand nand_164 (nand_164_out, not_1_out, B, C, D, not_5_out, F, not_7_out);
  nand nand_165 (nand_165_out, A, not_2_out, not_3_out, not_4_out, E, not_6_out, not_7_out);
  nand nand_166 (nand_166_out, A, not_2_out, not_3_out, not_4_out, E, F, G);
  nand nand_167 (nand_167_out, A, not_2_out, not_3_out, D, not_5_out, not_6_out, not_7_out);
  nand nand_168 (src2D, nand_40_out, nand_41_out, nand_42_out, nand_43_out, nand_44_out, nand_45_out, nand_46_out);
  nand nand_169 (aluop0, nand_47_out, nand_48_out, nand_49_out, nand_50_out, nand_51_out, nand_52_out, nand_53_out);
  nand nand_170 (aluop1, nand_54_out, nand_55_out, nand_56_out, nand_57_out, nand_58_out, nand_59_out, nand_60_out);
  nand nand_171 (iem1, nand_135_out, nand_136_out);
  nand nand_172 (br0, nand_137_out, nand_138_out, nand_139_out);
  nand nand_173 (br1, nand_140_out, nand_141_out, nand_142_out);
  nand nand_174 (br2, nand_143_out, nand_144_out, nand_145_out);
  nand nand_175 (muxA, nand_146_out, nand_147_out, nand_148_out, nand_149_out);
  nand nand_176 (ld, nand_150_out, nand_151_out, nand_152_out);
  nand nand_177 (st, nand_153_out, nand_154_out, nand_155_out, nand_156_out);
  nand nand_178 (abs, nand_157_out, nand_158_out, nand_159_out);
  nand nand_179 (ioW, nand_160_out, nand_161_out);
  nand nand_180 (ioR, nand_162_out, nand_163_out);
  not not_8 (stPC, nand_164_out);
  not not_9 (Reti, nand_165_out);
  not not_10 (randomSel, nand_166_out);
  not not_11 (timerSel, nand_167_out);
  nand nand_181 (muxb0, nand_1_out, nand_2_out, nand_3_out, nand_4_out, nand_5_out, nand_6_out, nand_7_out, nand_8_out, nand_9_out, nand_10_out, nand_11_out, nand_12_out, nand_13_out);
  nand nand_182 (muxb1, nand_14_out, nand_15_out, nand_16_out, nand_17_out, nand_18_out, nand_19_out, nand_20_out, nand_21_out, nand_22_out, nand_23_out, nand_24_out, nand_25_out, nand_26_out);
  nand nand_183 (muxb2, nand_27_out, nand_28_out, nand_29_out, nand_30_out, nand_31_out, nand_32_out, nand_33_out, nand_34_out, nand_35_out, nand_36_out, nand_37_out, nand_38_out, nand_39_out);
  nand nand_184 (aluop2, nand_61_out, nand_62_out, nand_63_out, nand_64_out, nand_65_out, nand_66_out, nand_67_out, nand_68_out, nand_69_out);
  nand nand_185 (aluop3, nand_70_out, nand_71_out, nand_72_out, nand_73_out, nand_74_out, nand_75_out, nand_76_out, nand_77_out);
  nand nand_186 (aluop4, nand_78_out, nand_79_out, nand_80_out, nand_81_out, nand_82_out, nand_83_out, nand_84_out, nand_85_out, nand_86_out, nand_87_out, nand_88_out, nand_89_out, nand_90_out, nand_91_out);
  nand nand_187 (WE, nand_92_out, nand_93_out, nand_94_out, nand_95_out, nand_96_out, nand_97_out, nand_98_out, nand_99_out, nand_100_out, nand_101_out, nand_102_out, nand_103_out, nand_104_out, nand_105_out);
  nand nand_188 (sf, nand_106_out, nand_107_out, nand_108_out, nand_109_out, nand_110_out, nand_111_out, nand_112_out, nand_113_out, nand_114_out);
  nand nand_189 (alu2D, nand_115_out, nand_116_out, nand_117_out, nand_118_out, nand_119_out, nand_120_out, nand_121_out, nand_122_out, nand_123_out, nand_124_out);
  nand nand_190 (iem0, nand_125_out, nand_126_out, nand_127_out, nand_128_out, nand_129_out, nand_130_out, nand_131_out, nand_132_out, nand_133_out, nand_134_out);
endmodule
