// Digital circuit lfsr RandomNumberGen.dig as structural Verilog
module lfsr_RandomNumberGen (
  input  [15:0] adrrIn,
  input  [15:0] dataIn,
  input  ioW,
  input  clk,
  input  ioR,
  input  [15:0] SeedAdr,
  input  [15:0] RngAdr,
  output [15:0] Out
);

  wire and_1_out, and_2_out, and_3_out, and_4_out, and_5_out, comparator_2_eq, d_ff_as_1_nq, d_ff_as_1_q,
       jk_ff_1_q, not_1_out, or_1_out, or_2_out, RandomSeedflag, xor_1_out, xor_2_out, xor_3_out;
  wire [2:0] u_muxEncoder_q;
  wire [15:0] multiplexer_1_out, multiplexer_2_out, RandomNUM, sed;

  Comparator #(.Signed("true"), .Bits(16)) comparator_1 (.a(adrrIn), .b(SeedAdr), .eq(RandomSeedflag));  // open: gt, lt
  and and_1 (and_1_out, RandomSeedflag, ioW);
  Comparator #(.Signed("true"), .Bits(16)) comparator_2 (.a(adrrIn), .b(RngAdr), .eq(comparator_2_eq));  // open: gt, lt
  not not_1 (not_1_out, or_2_out);
  and and_2 (and_2_out, clk, and_1_out);
  and and_3 (and_3_out, and_1_out, not_1_out);
  and and_4 (and_4_out, comparator_2_eq, ioR);
  and and_5 (and_5_out, RandomSeedflag, ioR);
  JK_FF jk_ff_1 (.J(or_2_out), .C(clk), .K(or_2_out), .Q(jk_ff_1_q));  // open: nQ
  D_FF_AS d_ff_as_1 (.Set(1'b0), .D(d_ff_as_1_nq), .C(and_2_out), .Clr(jk_ff_1_q), .Q(d_ff_as_1_q), .nQ(d_ff_as_1_nq));
  Register #(.Bits(16)) seed (.D(dataIn), .C(clk), .en(and_1_out), .Q(sed));
  or or_1 (or_1_out, and_4_out, and_5_out);
  muxEncoder #(.applicationType("IVERILOG"), .CodeFile("D:\\Desktop\\fpga\\RemedyCpu\\verilog\\multipleToMux.v")) u_muxEncoder (
    .a(and_4_out), .b(and_5_out), .c(1'b0), .d(1'b0), .e(1'b0), .f(1'b0), .g(1'b0), .h(1'b0),
    .Q(u_muxEncoder_q));
  or or_2 (or_2_out, d_ff_as_1_q, jk_ff_1_q);
  Multiplexer #(.Bits(16)) multiplexer_1 (.sel(and_1_out), .in_0({16{1'b0}}), .in_1(sed), .out(multiplexer_1_out));
  assign Out = or_1_out ? multiplexer_2_out : 16'bz;  // Driver driver_1
  Multiplexer #(.Bits(16)) multiplexer_2 (
    .sel(u_muxEncoder_q[0]), .in_0(RandomNUM), .in_1(sed), .out(multiplexer_2_out));
  // Probe on RandomNUM
  D_FF_AS d_ff_as_2 (
    .Set(multiplexer_1_out[0]), .D(xor_1_out), .C(clk), .Clr(and_3_out), .Q(RandomNUM[0]));  // open: nQ
  D_FF_AS d_ff_as_3 (
    .Set(multiplexer_1_out[1]), .D(RandomNUM[0]), .C(clk), .Clr(and_3_out), .Q(RandomNUM[1]));  // open: nQ
  D_FF_AS d_ff_as_4 (
    .Set(multiplexer_1_out[2]), .D(RandomNUM[1]), .C(clk), .Clr(and_3_out), .Q(RandomNUM[2]));  // open: nQ
  D_FF_AS d_ff_as_5 (
    .Set(multiplexer_1_out[3]), .D(RandomNUM[2]), .C(clk), .Clr(and_3_out), .Q(RandomNUM[3]));  // open: nQ
  D_FF_AS d_ff_as_6 (
    .Set(multiplexer_1_out[4]), .D(RandomNUM[3]), .C(clk), .Clr(and_3_out), .Q(RandomNUM[4]));  // open: nQ
  D_FF_AS d_ff_as_7 (
    .Set(multiplexer_1_out[5]), .D(RandomNUM[4]), .C(clk), .Clr(and_3_out), .Q(RandomNUM[5]));  // open: nQ
  D_FF_AS d_ff_as_8 (
    .Set(multiplexer_1_out[6]), .D(RandomNUM[5]), .C(clk), .Clr(and_3_out), .Q(RandomNUM[6]));  // open: nQ
  D_FF_AS d_ff_as_9 (
    .Set(multiplexer_1_out[7]), .D(RandomNUM[6]), .C(clk), .Clr(and_3_out), .Q(RandomNUM[7]));  // open: nQ
  D_FF_AS d_ff_as_10 (
    .Set(multiplexer_1_out[8]), .D(RandomNUM[7]), .C(clk), .Clr(and_3_out), .Q(RandomNUM[8]));  // open: nQ
  D_FF_AS d_ff_as_11 (
    .Set(multiplexer_1_out[9]), .D(RandomNUM[8]), .C(clk), .Clr(and_3_out), .Q(RandomNUM[9]));  // open: nQ
  D_FF_AS d_ff_as_12 (
    .Set(multiplexer_1_out[10]), .D(RandomNUM[9]), .C(clk), .Clr(and_3_out), .Q(RandomNUM[10]));  // open: nQ
  xor xor_1 (xor_1_out, xor_2_out, RandomNUM[10]);
  D_FF_AS d_ff_as_13 (
    .Set(multiplexer_1_out[11]), .D(RandomNUM[10]), .C(clk), .Clr(and_3_out), .Q(RandomNUM[11]));  // open: nQ
  D_FF_AS d_ff_as_14 (
    .Set(multiplexer_1_out[12]), .D(RandomNUM[11]), .C(clk), .Clr(and_3_out), .Q(RandomNUM[12]));  // open: nQ
  xor xor_2 (xor_2_out, xor_3_out, RandomNUM[12]);
  xor xor_3 (xor_3_out, RandomNUM[13], RandomNUM[15]);
  D_FF_AS d_ff_as_15 (
    .Set(multiplexer_1_out[13]), .D(RandomNUM[12]), .C(clk), .Clr(and_3_out), .Q(RandomNUM[13]));  // open: nQ
  D_FF_AS d_ff_as_16 (
    .Set(multiplexer_1_out[14]), .D(RandomNUM[13]), .C(clk), .Clr(and_3_out), .Q(RandomNUM[14]));  // open: nQ
  D_FF_AS d_ff_as_17 (
    .Set(multiplexer_1_out[15]), .D(RandomNUM[14]), .C(clk), .Clr(and_3_out), .Q(RandomNUM[15]));  // open: nQ

  // Other names for the same wires on the sheet: AddrOut[15:0] = adrrIn; Clk_in = clk; DataOut[15:0] = dataIn;
  //   RandomReg[15:0] = RngAdr; RandomSeedReg[15:0] = SeedAdr

  // Notes on the sheet:
  //   RandomNumberGen
endmodule
