// Digital circuit 16bit paralel-serial.dig as structural Verilog
module _16bit_paralel_serial (
  input  [15:0] Data,
  input  Clk,
  output Out
);

  wire C, comparator_1_eq, d_ff_1_q, d_ff_2_q, d_ff_3_q, d_ff_4_q, d_ff_5_q, d_ff_6_q, d_ff_7_q, d_ff_8_q,
       d_ff_9_q, d_ff_10_q, d_ff_11_q, d_ff_12_q, d_ff_13_q, d_ff_14_q, d_ff_15_q, multiplexer_1_out,
       multiplexer_2_out, multiplexer_3_out, multiplexer_4_out, multiplexer_5_out, multiplexer_6_out,
       multiplexer_7_out, multiplexer_8_out, multiplexer_9_out, multiplexer_10_out, multiplexer_11_out,
       multiplexer_12_out, multiplexer_13_out, multiplexer_14_out, multiplexer_15_out, multiplexer_16_out,
       or_1_out;
  wire [3:0] counter_1_out;

  Multiplexer multiplexer_1 (.sel(C), .in_0(Data[15]), .in_1(1'b0), .out(multiplexer_1_out));
  D_FF d_ff_1 (.D(multiplexer_1_out), .C(Clk), .Q(d_ff_1_q));  // open: nQ
  Multiplexer multiplexer_2 (.sel(C), .in_0(Data[14]), .in_1(d_ff_1_q), .out(multiplexer_2_out));
  D_FF d_ff_2 (.D(multiplexer_2_out), .C(Clk), .Q(d_ff_2_q));  // open: nQ
  Multiplexer multiplexer_3 (.sel(C), .in_0(Data[13]), .in_1(d_ff_2_q), .out(multiplexer_3_out));
  D_FF d_ff_3 (.D(multiplexer_3_out), .C(Clk), .Q(d_ff_3_q));  // open: nQ
  Multiplexer multiplexer_4 (.sel(C), .in_0(Data[12]), .in_1(d_ff_3_q), .out(multiplexer_4_out));
  D_FF d_ff_4 (.D(multiplexer_4_out), .C(Clk), .Q(d_ff_4_q));  // open: nQ
  Multiplexer multiplexer_5 (.sel(C), .in_0(Data[11]), .in_1(d_ff_4_q), .out(multiplexer_5_out));
  D_FF d_ff_5 (.D(multiplexer_5_out), .C(Clk), .Q(d_ff_5_q));  // open: nQ
  Multiplexer multiplexer_6 (.sel(C), .in_0(Data[10]), .in_1(d_ff_5_q), .out(multiplexer_6_out));
  D_FF d_ff_6 (.D(multiplexer_6_out), .C(Clk), .Q(d_ff_6_q));  // open: nQ
  Multiplexer multiplexer_7 (.sel(C), .in_0(Data[9]), .in_1(d_ff_6_q), .out(multiplexer_7_out));
  D_FF d_ff_7 (.D(multiplexer_7_out), .C(Clk), .Q(d_ff_7_q));  // open: nQ
  Multiplexer multiplexer_8 (.sel(C), .in_0(Data[8]), .in_1(d_ff_7_q), .out(multiplexer_8_out));
  D_FF d_ff_8 (.D(multiplexer_8_out), .C(Clk), .Q(d_ff_8_q));  // open: nQ
  Multiplexer multiplexer_9 (.sel(C), .in_0(Data[7]), .in_1(d_ff_8_q), .out(multiplexer_9_out));
  D_FF d_ff_9 (.D(multiplexer_9_out), .C(Clk), .Q(d_ff_9_q));  // open: nQ
  Multiplexer multiplexer_10 (.sel(C), .in_0(Data[6]), .in_1(d_ff_9_q), .out(multiplexer_10_out));
  D_FF d_ff_10 (.D(multiplexer_10_out), .C(Clk), .Q(d_ff_10_q));  // open: nQ
  Multiplexer multiplexer_11 (.sel(C), .in_0(Data[5]), .in_1(d_ff_10_q), .out(multiplexer_11_out));
  D_FF d_ff_11 (.D(multiplexer_11_out), .C(Clk), .Q(d_ff_11_q));  // open: nQ
  Multiplexer multiplexer_12 (.sel(C), .in_0(Data[4]), .in_1(d_ff_11_q), .out(multiplexer_12_out));
  D_FF d_ff_12 (.D(multiplexer_12_out), .C(Clk), .Q(d_ff_12_q));  // open: nQ
  Multiplexer multiplexer_13 (.sel(C), .in_0(Data[3]), .in_1(d_ff_12_q), .out(multiplexer_13_out));
  D_FF d_ff_13 (.D(multiplexer_13_out), .C(Clk), .Q(d_ff_13_q));  // open: nQ
  Multiplexer multiplexer_14 (.sel(C), .in_0(Data[2]), .in_1(d_ff_13_q), .out(multiplexer_14_out));
  D_FF d_ff_14 (.D(multiplexer_14_out), .C(Clk), .Q(d_ff_14_q));  // open: nQ
  Multiplexer multiplexer_15 (.sel(C), .in_0(Data[1]), .in_1(d_ff_14_q), .out(multiplexer_15_out));
  D_FF d_ff_15 (.D(multiplexer_15_out), .C(Clk), .Q(d_ff_15_q));  // open: nQ
  Multiplexer multiplexer_16 (.sel(C), .in_0(Data[0]), .in_1(d_ff_15_q), .out(multiplexer_16_out));
  D_FF d_ff_16 (.D(multiplexer_16_out), .C(Clk), .Q(Out));  // open: nQ
  Counter #(.Bits(4)) counter_1 (.en(1'b1), .C(Clk), .clr(or_1_out), .out(counter_1_out));  // open: ovf
  or or_1 (or_1_out, comparator_1_eq, comparator_1_eq);
  Comparator #(.Bits(4)) comparator_1 (.a(counter_1_out), .b(4'b1111), .eq(comparator_1_eq));  // open: gt, lt
  not not_1 (C, comparator_1_eq);
endmodule
