// Digital circuit 16bit reverse serial-paralel.dig as structural Verilog
module _16bit_reverse_serial_paralel (
  input  Data,
  input  Clk,
  input  Reset,
  output [15:0] Out
);

  wire C, comparator_1_eq;
  wire [3:0] counter_1_out;
  wire [15:1] d_ff_as_1_q;

  D_FF_AS d_ff_as_1 (.Set(1'b0), .D(Data), .C(Clk), .Clr(Reset), .Q(d_ff_as_1_q[1]));  // open: nQ
  D_FF_AS d_ff_as_2 (.Set(1'b0), .D(d_ff_as_1_q[1]), .C(Clk), .Clr(Reset), .Q(d_ff_as_1_q[2]));  // open: nQ
  D_FF_AS d_ff_as_3 (.Set(1'b0), .D(d_ff_as_1_q[2]), .C(Clk), .Clr(Reset), .Q(d_ff_as_1_q[3]));  // open: nQ
  D_FF_AS d_ff_as_4 (.Set(1'b0), .D(d_ff_as_1_q[3]), .C(Clk), .Clr(Reset), .Q(d_ff_as_1_q[4]));  // open: nQ
  D_FF_AS d_ff_as_5 (.Set(1'b0), .D(d_ff_as_1_q[4]), .C(Clk), .Clr(Reset), .Q(d_ff_as_1_q[5]));  // open: nQ
  D_FF_AS d_ff_as_6 (.Set(1'b0), .D(d_ff_as_1_q[5]), .C(Clk), .Clr(Reset), .Q(d_ff_as_1_q[6]));  // open: nQ
  D_FF_AS d_ff_as_7 (.Set(1'b0), .D(d_ff_as_1_q[6]), .C(Clk), .Clr(Reset), .Q(d_ff_as_1_q[7]));  // open: nQ
  D_FF_AS d_ff_as_8 (.Set(1'b0), .D(d_ff_as_1_q[7]), .C(Clk), .Clr(Reset), .Q(d_ff_as_1_q[8]));  // open: nQ
  D_FF_AS d_ff_as_9 (.Set(1'b0), .D(d_ff_as_1_q[8]), .C(Clk), .Clr(Reset), .Q(d_ff_as_1_q[9]));  // open: nQ
  D_FF_AS d_ff_as_10 (.Set(1'b0), .D(d_ff_as_1_q[9]), .C(Clk), .Clr(Reset), .Q(d_ff_as_1_q[10]));  // open: nQ
  D_FF_AS d_ff_as_11 (.Set(1'b0), .D(d_ff_as_1_q[10]), .C(Clk), .Clr(Reset), .Q(d_ff_as_1_q[11]));  // open: nQ
  Register #(.Bits(16)) R0 (.D({d_ff_as_1_q, Data}), .C(Clk), .en(comparator_1_eq), .Q(Out));
  D_FF_AS d_ff_as_12 (.Set(1'b0), .D(d_ff_as_1_q[11]), .C(Clk), .Clr(Reset), .Q(d_ff_as_1_q[12]));  // open: nQ
  D_FF_AS d_ff_as_13 (.Set(1'b0), .D(d_ff_as_1_q[12]), .C(Clk), .Clr(Reset), .Q(d_ff_as_1_q[13]));  // open: nQ
  D_FF_AS d_ff_as_14 (.Set(1'b0), .D(d_ff_as_1_q[13]), .C(Clk), .Clr(Reset), .Q(d_ff_as_1_q[14]));  // open: nQ
  D_FF_AS d_ff_as_15 (.Set(1'b0), .D(d_ff_as_1_q[14]), .C(Clk), .Clr(Reset), .Q(d_ff_as_1_q[15]));  // open: nQ
  _16xPrescaler _16xprescaler_1 (.Clk(Clk), .ClockOut(C));
  Counter #(.Bits(4)) counter_1 (.en(C), .C(Clk), .clr(comparator_1_eq), .out(counter_1_out));  // open: ovf
  Comparator #(.Bits(4)) comparator_1 (.a(counter_1_out), .b(4'b1110), .eq(comparator_1_eq));  // open: gt, lt

  // Notes on the sheet:
  //   Clk: Hz: 16
endmodule
