// Digital circuit 16bit serial-paralel.dig as structural Verilog
module _16bit_serial_paralel (
  input  Data,
  input  Clk,
  input  Reset,
  output [15:0] Out
);

  wire comparator_1_eq, d_ff_1_q, or_1_out;
  wire [4:0] counter_1_out;
  wire [15:0] d_ff_as_16_q;

  D_FF_AS d_ff_as_1 (.Set(1'b0), .D(Data), .C(Clk), .Clr(Reset), .Q(d_ff_as_16_q[15]));  // open: nQ
  D_FF_AS d_ff_as_2 (.Set(1'b0), .D(d_ff_as_16_q[15]), .C(Clk), .Clr(Reset), .Q(d_ff_as_16_q[14]));  // open: nQ
  D_FF_AS d_ff_as_3 (.Set(1'b0), .D(d_ff_as_16_q[14]), .C(Clk), .Clr(Reset), .Q(d_ff_as_16_q[13]));  // open: nQ
  D_FF_AS d_ff_as_4 (.Set(1'b0), .D(d_ff_as_16_q[13]), .C(Clk), .Clr(Reset), .Q(d_ff_as_16_q[12]));  // open: nQ
  D_FF_AS d_ff_as_5 (.Set(1'b0), .D(d_ff_as_16_q[12]), .C(Clk), .Clr(Reset), .Q(d_ff_as_16_q[11]));  // open: nQ
  D_FF_AS d_ff_as_6 (.Set(1'b0), .D(d_ff_as_16_q[11]), .C(Clk), .Clr(Reset), .Q(d_ff_as_16_q[10]));  // open: nQ
  D_FF_AS d_ff_as_7 (.Set(1'b0), .D(d_ff_as_16_q[10]), .C(Clk), .Clr(Reset), .Q(d_ff_as_16_q[9]));  // open: nQ
  D_FF_AS d_ff_as_8 (.Set(1'b0), .D(d_ff_as_16_q[9]), .C(Clk), .Clr(Reset), .Q(d_ff_as_16_q[8]));  // open: nQ
  D_FF_AS d_ff_as_9 (.Set(1'b0), .D(d_ff_as_16_q[8]), .C(Clk), .Clr(Reset), .Q(d_ff_as_16_q[7]));  // open: nQ
  D_FF_AS d_ff_as_10 (.Set(1'b0), .D(d_ff_as_16_q[7]), .C(Clk), .Clr(Reset), .Q(d_ff_as_16_q[6]));  // open: nQ
  D_FF_AS d_ff_as_11 (.Set(1'b0), .D(d_ff_as_16_q[6]), .C(Clk), .Clr(Reset), .Q(d_ff_as_16_q[5]));  // open: nQ
  D_FF_AS d_ff_as_12 (.Set(1'b0), .D(d_ff_as_16_q[5]), .C(Clk), .Clr(Reset), .Q(d_ff_as_16_q[4]));  // open: nQ
  Register #(.Bits(16)) R0 (.D(d_ff_as_16_q), .C(~Clk), .en(d_ff_1_q), .Q(Out));
  D_FF_AS d_ff_as_13 (.Set(1'b0), .D(d_ff_as_16_q[4]), .C(Clk), .Clr(Reset), .Q(d_ff_as_16_q[3]));  // open: nQ
  D_FF_AS d_ff_as_14 (.Set(1'b0), .D(d_ff_as_16_q[3]), .C(Clk), .Clr(Reset), .Q(d_ff_as_16_q[2]));  // open: nQ
  D_FF_AS d_ff_as_15 (.Set(1'b0), .D(d_ff_as_16_q[2]), .C(Clk), .Clr(Reset), .Q(d_ff_as_16_q[1]));  // open: nQ
  D_FF_AS d_ff_as_16 (.Set(1'b0), .D(d_ff_as_16_q[1]), .C(Clk), .Clr(Reset), .Q(d_ff_as_16_q[0]));  // open: nQ
  Counter #(.Bits(5)) counter_1 (.en(1'b1), .C(Clk), .clr(or_1_out), .out(counter_1_out));  // open: ovf
  D_FF d_ff_1 (.D(comparator_1_eq), .C(Clk), .Q(d_ff_1_q));  // open: nQ
  Comparator #(.Bits(5)) comparator_1 (.a(counter_1_out), .b(5'b01110), .eq(comparator_1_eq));  // open: gt, lt
  or or_1 (or_1_out, Reset, comparator_1_eq);

  // Notes on the sheet:
  //   Clk: Hz: 16
endmodule
