// Digital circuit 8bit paralel-serial.dig as structural Verilog
module _8bit_paralel_serial (
  input  [7:0] Data,
  input  Clk,
  input  putData,
  output Out
);

  wire C, Clk_t, d_ff_1_q, d_ff_2_q, d_ff_3_q, d_ff_4_q, d_ff_5_q, d_ff_6_q, d_ff_7_q, d_ff_8_q, d_ff_9_q,
       multiplexer_1_out, multiplexer_2_out, multiplexer_3_out, multiplexer_4_out, multiplexer_5_out,
       multiplexer_6_out, multiplexer_7_out, multiplexer_8_out, multiplexer_9_out, not_1_out, not_2_out,
       register_1_q;
  wire [3:0] counter_1_out;

  Multiplexer multiplexer_1 (.sel(C), .in_0(Data[0]), .in_1(1'b0), .out(multiplexer_1_out));
  D_FF d_ff_1 (.D(multiplexer_1_out), .C(Clk_t), .Q(d_ff_1_q));  // open: nQ
  Multiplexer multiplexer_2 (.sel(C), .in_0(Data[1]), .in_1(d_ff_1_q), .out(multiplexer_2_out));
  D_FF d_ff_2 (.D(multiplexer_2_out), .C(Clk_t), .Q(d_ff_2_q));  // open: nQ
  Multiplexer multiplexer_3 (.sel(C), .in_0(Data[2]), .in_1(d_ff_2_q), .out(multiplexer_3_out));
  D_FF d_ff_3 (.D(multiplexer_3_out), .C(Clk_t), .Q(d_ff_3_q));  // open: nQ
  Multiplexer multiplexer_4 (.sel(C), .in_0(Data[3]), .in_1(d_ff_3_q), .out(multiplexer_4_out));
  D_FF d_ff_4 (.D(multiplexer_4_out), .C(Clk_t), .Q(d_ff_4_q));  // open: nQ
  Multiplexer multiplexer_5 (.sel(C), .in_0(Data[4]), .in_1(d_ff_4_q), .out(multiplexer_5_out));
  D_FF d_ff_5 (.D(multiplexer_5_out), .C(Clk_t), .Q(d_ff_5_q));  // open: nQ
  or or_1 (Clk_t, Clk, Clk);
  Multiplexer multiplexer_6 (.sel(C), .in_0(Data[5]), .in_1(d_ff_5_q), .out(multiplexer_6_out));
  D_FF d_ff_6 (.D(multiplexer_6_out), .C(Clk_t), .Q(d_ff_6_q));  // open: nQ
  or or_2 (C, putData, not_2_out);
  Multiplexer multiplexer_7 (.sel(C), .in_0(Data[6]), .in_1(d_ff_6_q), .out(multiplexer_7_out));
  D_FF d_ff_7 (.D(multiplexer_7_out), .C(Clk_t), .Q(d_ff_7_q));  // open: nQ
  Multiplexer multiplexer_8 (.sel(C), .in_0(Data[7]), .in_1(d_ff_7_q), .out(multiplexer_8_out));
  Counter #(.Bits(4)) counter_1 (.en(1'b1), .C(Clk_t), .clr(multiplexer_9_out), .out(counter_1_out));  // open: ovf
  D_FF d_ff_8 (.D(multiplexer_8_out), .C(Clk_t), .Q(d_ff_8_q));  // open: nQ
  D_FF d_ff_9 (.D(d_ff_8_q), .C(Clk_t), .Q(d_ff_9_q));  // open: nQ
  Multiplexer multiplexer_9 (.sel(register_1_q), .in_0(1'b1), .in_1(counter_1_out[3]), .out(multiplexer_9_out));
  and and_1 (Out, C, d_ff_9_q);
  not not_1 (not_1_out, register_1_q);
  Register register_1 (.D(multiplexer_9_out), .C(Clk_t), .en(not_1_out), .Q(register_1_q));
  not not_2 (not_2_out, multiplexer_9_out);
endmodule
