// Digital circuit 8bit serial-paralel.dig as structural Verilog
module _8bit_serial_paralel (
  input  Data,
  input  Clk,
  output [7:0] Out
);

  wire C, comparator_1_eq, counter_2_ovf, d_ff_1_q, multiplexer_1_out, not_1_out, not_2_out, register_1_q;
  wire [3:0] counter_1_out, counter_2_out;
  wire [7:0] d_ff_2_q;

  D_FF d_ff_1 (.D(Data), .C(Clk), .Q(d_ff_1_q));  // open: nQ
  D_FF d_ff_2 (.D(d_ff_1_q), .C(Clk), .Q(d_ff_2_q[7]));  // open: nQ
  D_FF d_ff_3 (.D(d_ff_2_q[7]), .C(Clk), .Q(d_ff_2_q[6]));  // open: nQ
  D_FF d_ff_4 (.D(d_ff_2_q[6]), .C(Clk), .Q(d_ff_2_q[5]));  // open: nQ
  D_FF d_ff_5 (.D(d_ff_2_q[5]), .C(Clk), .Q(d_ff_2_q[4]));  // open: nQ
  not not_1 (not_1_out, Clk);
  Register #(.Bits(8)) R0 (.D(d_ff_2_q), .C(not_1_out), .en(comparator_1_eq), .Q(Out));
  D_FF d_ff_6 (.D(d_ff_2_q[4]), .C(Clk), .Q(d_ff_2_q[3]));  // open: nQ
  D_FF d_ff_7 (.D(d_ff_2_q[3]), .C(Clk), .Q(d_ff_2_q[2]));  // open: nQ
  D_FF d_ff_8 (.D(d_ff_2_q[2]), .C(Clk), .Q(d_ff_2_q[1]));  // open: nQ
  D_FF d_ff_9 (.D(d_ff_2_q[1]), .C(Clk), .Q(d_ff_2_q[0]));  // open: nQ
  Counter #(.Bits(4)) counter_1 (.en(1'b1), .C(Clk), .clr(multiplexer_1_out), .out(counter_1_out));  // open: ovf
  Counter #(.Bits(4)) counter_2 (.en(C), .C(Clk), .clr(comparator_1_eq), .out(counter_2_out), .ovf(counter_2_ovf));
  Multiplexer multiplexer_1 (.sel(register_1_q), .in_0(1'b1), .in_1(counter_1_out[3]), .out(multiplexer_1_out));
  not not_2 (not_2_out, register_1_q);
  Register register_1 (.D(multiplexer_1_out), .C(Clk), .en(not_2_out), .Q(register_1_q));
  Comparator #(.Bits(4)) comparator_1 (.a(counter_2_out), .b(4'b1000), .eq(comparator_1_eq));  // open: gt, lt
  not not_3 (C, multiplexer_1_out);

  // Notes on the sheet:
  //   Clk: Hz: 16
endmodule
