// Digital circuit RegisterBlock.dig as structural Verilog
module RegisterBlock (
  input  [15:0] DataIn,
  input  WE,
  input  clk,
  input  [3:0] src,
  input  [3:0] Dest,
  input  rst,
  output [15:0] RDest,
  output [15:0] Rsrc
);

  wire demultiplexer_1_out_0, demultiplexer_1_out_1, demultiplexer_1_out_2, demultiplexer_1_out_3,
       demultiplexer_1_out_4, demultiplexer_1_out_5, demultiplexer_1_out_6, demultiplexer_1_out_7,
       demultiplexer_1_out_8, demultiplexer_1_out_9, demultiplexer_1_out_10, demultiplexer_1_out_11,
       demultiplexer_1_out_12, demultiplexer_1_out_13, demultiplexer_1_out_14, demultiplexer_1_out_15,
       not_1_out;
  wire [15:0] BranchPointer_q, R0_q, R1_q, R2_q, R3_q, R4_q, R5_q, R6_q, R7_q, R8_q, R9_q, R10_q, R11_q,
       R12_q, ReturnAddr_q, StackPointer_q;

  not not_1 (not_1_out, clk);
  Demultiplexer #(.Selector_Bits(4)) demultiplexer_1 (
    .sel(Dest), .in(WE), .out_0(demultiplexer_1_out_0), .out_1(demultiplexer_1_out_1),
    .out_2(demultiplexer_1_out_2), .out_3(demultiplexer_1_out_3), .out_4(demultiplexer_1_out_4),
    .out_5(demultiplexer_1_out_5), .out_6(demultiplexer_1_out_6), .out_7(demultiplexer_1_out_7),
    .out_8(demultiplexer_1_out_8), .out_9(demultiplexer_1_out_9), .out_10(demultiplexer_1_out_10),
    .out_11(demultiplexer_1_out_11), .out_12(demultiplexer_1_out_12), .out_13(demultiplexer_1_out_13),
    .out_14(demultiplexer_1_out_14), .out_15(demultiplexer_1_out_15));
  register_16bit R0 (.D(DataIn), .C(not_1_out), .en(demultiplexer_1_out_0), .rst(rst), .Q(R0_q));
  register_16bit R1 (.D(DataIn), .C(not_1_out), .en(demultiplexer_1_out_1), .rst(rst), .Q(R1_q));
  register_16bit R2 (.D(DataIn), .C(not_1_out), .en(demultiplexer_1_out_2), .rst(rst), .Q(R2_q));
  register_16bit R3 (.D(DataIn), .C(not_1_out), .en(demultiplexer_1_out_3), .rst(rst), .Q(R3_q));
  register_16bit R4 (.D(DataIn), .C(not_1_out), .en(demultiplexer_1_out_4), .rst(rst), .Q(R4_q));
  register_16bit R5 (.D(DataIn), .C(not_1_out), .en(demultiplexer_1_out_5), .rst(rst), .Q(R5_q));
  register_16bit R6 (.D(DataIn), .C(not_1_out), .en(demultiplexer_1_out_6), .rst(rst), .Q(R6_q));
  register_16bit R7 (.D(DataIn), .C(not_1_out), .en(demultiplexer_1_out_7), .rst(rst), .Q(R7_q));
  register_16bit R8 (.D(DataIn), .C(not_1_out), .en(demultiplexer_1_out_8), .rst(rst), .Q(R8_q));
  register_16bit R9 (.D(DataIn), .C(not_1_out), .en(demultiplexer_1_out_9), .rst(rst), .Q(R9_q));
  register_16bit R10 (.D(DataIn), .C(not_1_out), .en(demultiplexer_1_out_10), .rst(rst), .Q(R10_q));
  register_16bit R11 (.D(DataIn), .C(not_1_out), .en(demultiplexer_1_out_11), .rst(rst), .Q(R11_q));
  register_16bit R12 (.D(DataIn), .C(not_1_out), .en(demultiplexer_1_out_12), .rst(rst), .Q(R12_q));
  register_16bit BranchPointer (.D(DataIn), .C(not_1_out), .en(demultiplexer_1_out_13), .rst(rst), .Q(BranchPointer_q));
  register_16bit StackPointer (.D(DataIn), .C(not_1_out), .en(demultiplexer_1_out_14), .rst(rst), .Q(StackPointer_q));
  register_16bit ReturnAddr (.D(DataIn), .C(not_1_out), .en(demultiplexer_1_out_15), .rst(rst), .Q(ReturnAddr_q));
  // Probe r0 on R0_q
  // Probe r1 on R1_q
  // Probe r2 on R2_q
  // Probe r3 on R3_q
  Multiplexer #(.Selector_Bits(4), .Bits(16)) multiplexer_1 (
    .sel(Dest), .in_0(R0_q), .in_1(R1_q), .in_2(R2_q), .in_3(R3_q), .in_4(R4_q), .in_5(R5_q), .in_6(R6_q),
    .in_7(R7_q), .in_8(R8_q), .in_9(R9_q), .in_10(R10_q), .in_11(R11_q), .in_12(R12_q),
    .in_13(BranchPointer_q), .in_14(StackPointer_q), .in_15(ReturnAddr_q), .out(RDest));
  Multiplexer #(.Selector_Bits(4), .Bits(16)) multiplexer_2 (
    .sel(src), .in_0(R0_q), .in_1(R1_q), .in_2(R2_q), .in_3(R3_q), .in_4(R4_q), .in_5(R5_q), .in_6(R6_q),
    .in_7(R7_q), .in_8(R8_q), .in_9(R9_q), .in_10(R10_q), .in_11(R11_q), .in_12(R12_q),
    .in_13(BranchPointer_q), .in_14(StackPointer_q), .in_15(ReturnAddr_q), .out(Rsrc));
endmodule
