// Digital circuit register-16bit.dig as structural Verilog
module register_16bit (
  input  [15:0] D,
  input  C,
  input  en,
  input  rst,
  output [15:0] Q
);

  Register16 #(.applicationType("IVERILOG"), .CodeFile("C:\\Users\\Berkant\\Desktop\\fpga\\RemedyCpu\\verilog\\reg-16.v")) u_Register16 (
    .D(D), .C(C), .en(en), .rst(rst), .Q(Q));
endmodule
