// Digital circuit uartBlock.dig as structural Verilog
module uartBlock (
  input  RX,
  input  rst,
  input  [15:0] dataIn,
  input  [15:0] Addr,
  input  ioW,
  input  ioR,
  input  clk,
  input  localclk,
  input  [15:0] transmitAddr,
  input  [15:0] ReceiveAddr,
  output TX,
  output [15:0] DataOut
);

  wire and_1_out, and_2_out, and_3_out, and_4_out, and_5_out, comparator_1_eq, comparator_2_eq,
       comparator_3_gt, fifo_1_empty, fifo_2_empty, fifo_2_full, not_1_out, or_1_out,
       u_UART_Receiver_rx_valid, u_UART_Transmitter_tx_busy;
  wire [4:0] fifo_1_count, fifo_2_count;
  wire [7:0] fifo_1_dataout, u_UART_Receiver_data_out;

  Comparator #(.Signed("true"), .Bits(16)) comparator_1 (
    .a(Addr), .b(transmitAddr), .eq(comparator_1_eq));  // open: gt, lt
  and and_1 (and_1_out, comparator_1_eq, ioW);
  and and_2 (and_2_out, clk, and_1_out);
  or or_1 (or_1_out, and_5_out, and_2_out);
  FIFO fifo_1 (
    .datain(dataIn[7:0]), .clk(or_1_out), .wr(and_1_out), .dataOut(fifo_1_dataout), .Count(fifo_1_count),
    .rd(and_5_out), .rst(rst), .Empty(fifo_1_empty));  // open: Full
  UART_Receiver #(.applicationType("IVERILOG"), .CodeFile("C:\\Users\\Berkant\\Desktop\\fpga\\RemedyCpu\\verilog\\uartRc.v")) u_UART_Receiver (
    .clk(clk), .rst(rst), .rx(RX), .data_out(u_UART_Receiver_data_out), .rx_valid(u_UART_Receiver_rx_valid));
  and and_3 (and_3_out, ~fifo_1_empty, ~and_1_out);  // And
  Comparator #(.Signed("true"), .Bits(16)) comparator_2 (
    .a(Addr), .b(ReceiveAddr), .eq(comparator_2_eq));  // open: gt, lt
  // Probe on fifo_1_count
  Comparator #(.Signed("true"), .Bits(5)) comparator_3 (
    .a(fifo_1_count), .b({5{1'b0}}), .gt(comparator_3_gt));  // open: eq, lt
  and and_4 (and_4_out, comparator_2_eq, ioR);
  and and_5 (and_5_out, comparator_3_gt, and_3_out, not_1_out);
  FIFO fifo_2 (
    .datain(u_UART_Receiver_data_out), .clk(clk), .wr(u_UART_Receiver_rx_valid), .dataOut(DataOut[7:0]),
    .Full(fifo_2_full), .Count(fifo_2_count), .rd(and_4_out), .rst(rst), .Empty(fifo_2_empty));
  UART_Transmitter #(.applicationType("IVERILOG"), .CodeFile("C:\\Users\\Berkant\\Desktop\\fpga\\RemedyCpu\\verilog\\uartTr.v")) u_UART_Transmitter (
    .clk(localclk), .rst(rst), .data(fifo_1_dataout), .start(and_5_out), .tx(TX),
    .tx_busy(u_UART_Transmitter_tx_busy));
  not not_1 (not_1_out, u_UART_Transmitter_tx_busy);

  assign DataOut[15:8] = {8{1'b0}};

  // Other names for the same wires on the sheet: FifoIn[7:0] = dataIn[7:0]; FifoOut[7:0] = DataOut[7:0];
  //   Lclk = localclk; receivaddr[15:0] = ReceiveAddr; transaddr[15:0] = transmitAddr

  // Notes on the sheet:
  //   Addr: default 71
  //   clk: Hz: 10
  //   localclk: Hz: 10
  //   transmitAddr: default 71
endmodule
