// Digital circuit UartBlock.dig as structural Verilog
module UartBlock (
  input  rst,
  input  clk,
  input  iow,
  input  [15:0] datain,
  input  ior,
  input  [15:0] addr,
  input  interbusy,
  input  Rx,
  input  [15:0] uartRegAdr,
  input  [15:0] configRegAdr,
  input  [15:0] statusRegAdr,
  output tx,
  output busy,
  output interrupt,
  output [15:0] dataout
);

  wire and_1_out, not_1_out, not_2_out, not_3_out, rx_Full, rx_rd_en, rxEmpty, tick, tx_wrEn, txEmpty,
       txfull, u_tx_fsm_rd_en, u_tx_fsm_start_tx, u_uart_regs_outenable, u_uart_rx_data_ready,
       u_uart_rx_framing_error, u_uart_rx_fsm_data_read, u_uart_rx_fsm_fifo_wr_en;
  wire [7:0] rx_dataout, tx_data, u_tx_fifo_data_out, u_uart_rx_data_out;
  wire [15:0] baud_div, u_uart_regs_data_out;

  not not_1 (not_1_out, rx_Full);
  not not_2 (not_2_out, txfull);
  uart_regs #(.applicationType("IVERILOG"), .CodeFile("D:\\Desktop\\fpga\\RemedyCpu\\verilog\\uart\\uartRegs.v")) u_uart_regs (
    .clk(clk), .rst(rst), .iow(iow), .ior(ior), .addr(addr), .data_in(datain), .rx_data(rx_dataout),
    .rx_ready(not_1_out), .tx_ready(not_2_out), .rx_empty(rxEmpty), .tx_empty(txEmpty), .rx_full(rx_Full),
    .tx_full(txfull), .tx_busy(busy), .interrupt_busy(interbusy), .writeReadAddr(uartRegAdr),
    .configReg(configRegAdr), .statusReg(statusRegAdr), .data_out(u_uart_regs_data_out), .tx_wr_en(tx_wrEn),
    .rx_rd_en(rx_rd_en), .tx_data(tx_data), .baud_div(baud_div), .interrupt(interrupt),
    .outEnable(u_uart_regs_outenable));
  assign dataout = u_uart_regs_outenable ? u_uart_regs_data_out : 16'bz;  // Driver driver_1
  tx_fifo #(.applicationType("IVERILOG"), .CodeFile("D:\\Desktop\\fpga\\RemedyCpu\\verilog\\uart\\txFifo.v")) u_tx_fifo (
    .clk(clk), .rst(rst), .wr_en(tx_wrEn), .data_in(tx_data), .rd_en(u_tx_fsm_rd_en),
    .data_out(u_tx_fifo_data_out), .empty(txEmpty), .full(txfull));
  uart_rx #(.applicationType("IVERILOG"), .CodeFile("D:\\Desktop\\fpga\\RemedyCpu\\verilog\\uart\\uartRx.v")) u_uart_rx (
    .clk(clk), .rst(rst), .rx(Rx), .baud_tick(tick), .data_read(u_uart_rx_fsm_data_read),
    .data_out(u_uart_rx_data_out), .data_ready(u_uart_rx_data_ready), .framing_error(u_uart_rx_framing_error));
  baud_tick_generator #(.applicationType("IVERILOG"), .CodeFile("D:\\Desktop\\fpga\\RemedyCpu\\verilog\\uart\\baudTick.v")) u_baud_tick_generator (
    .clk(clk), .rst(rst), .clock_div(baud_div), .tick(tick));
  not not_3 (not_3_out, u_uart_rx_framing_error);
  and and_1 (and_1_out, u_uart_rx_data_ready, not_3_out);
  // Probe uart clock on tick
  tx_fsm #(.applicationType("IVERILOG"), .CodeFile("D:\\Desktop\\fpga\\RemedyCpu\\verilog\\uart\\uartStarter.v")) u_tx_fsm (
    .clk(clk), .rst(rst), .fifo_empty(txEmpty), .tx_busy(busy), .rd_en(u_tx_fsm_rd_en),
    .start_tx(u_tx_fsm_start_tx));
  uart_rx_fsm #(.applicationType("IVERILOG"), .CodeFile("D:\\Desktop\\fpga\\RemedyCpu\\verilog\\uart\\uartRxFsm.v")) u_uart_rx_fsm (
    .clk(clk), .rst(rst), .data_ready(and_1_out), .fifo_full(rx_Full), .data_read(u_uart_rx_fsm_data_read),
    .fifo_wr_en(u_uart_rx_fsm_fifo_wr_en));
  uart_tx #(.applicationType("IVERILOG"), .CodeFile("D:\\Desktop\\fpga\\RemedyCpu\\verilog\\uart\\transmitterFsm.v")) u_uart_tx (
    .clk(clk), .rst(rst), .baud_tick(tick), .start(u_tx_fsm_start_tx), .data_in(u_tx_fifo_data_out), .tx(tx),
    .busy(busy));
  rx_fifo #(.applicationType("IVERILOG"), .CodeFile("D:\\Desktop\\fpga\\RemedyCpu\\verilog\\uart\\rxFifo.v")) u_rx_fifo (
    .clk(clk), .rst(rst), .wr_en(u_uart_rx_fsm_fifo_wr_en), .data_in(u_uart_rx_data_out), .rd_en(rx_rd_en),
    .data_out(rx_dataout), .empty(rxEmpty), .full(rx_Full));

  // Other names for the same wires on the sheet: txbusy = busy

  // Notes on the sheet:
  //   iow: default 1
  //   datain: default 18
  //   addr: default 1
  //   interbusy: default 18
  //   Rx: default 18
  //   uartRegAdr: default 1
  //   configRegAdr: default 2
  //   statusRegAdr: default 3
endmodule
