// Digital circuit fpu.dig as structural Verilog
module fpu (
  input  [15:0] A,
  input  [15:0] B,
  input  [3:0] Aluop
);

  wire sign_a, sign_b, u_fpu_mult_sign, u_fpu_operator_signout;
  wire [4:0] expo_a, expo_b, u_fpu_align_commonexp, u_fpu_mult_exp;
  wire [10:0] mantisa_A, mantisa_b, u_fpu_align_aligneda, u_fpu_align_alignedb;
  wire [11:0] u_fpu_mult_manstisa, u_fpu_operator_mantout;
  wire [15:0] u_float16_to_int_out, u_fpu_div_fixed_result, u_fpu_normalize_pack_2_result,
       u_fpu_normalize_pack_result, u_int_to_float16_out;

  fpu_unpack #(.applicationType("IVERILOG"), .CodeFile("D:\\Desktop\\fpga\\RemedyCpu\\verilog\\fpu\\fpu Unpack.v")) u_fpu_unpack (
    .in(A), .sign(sign_a), .exp(expo_a), .mantissa(mantisa_A));
  fpu_unpack #(.applicationType("IVERILOG"), .CodeFile("D:\\Desktop\\fpga\\RemedyCpu\\verilog\\fpu\\fpu Unpack.v")) u_fpu_unpack_2 (
    .in(B), .sign(sign_b), .exp(expo_b), .mantissa(mantisa_b));
  fpu_align #(.applicationType("IVERILOG"), .CodeFile("D:\\Desktop\\fpga\\RemedyCpu\\verilog\\fpu\\fpuAlign.v")) u_fpu_align (
    .expA(expo_a), .expB(expo_b), .mantA(mantisa_A), .mantB(mantisa_b), .alignedA(u_fpu_align_aligneda),
    .alignedB(u_fpu_align_alignedb), .commonExp(u_fpu_align_commonexp));
  fpu_operator #(.applicationType("IVERILOG"), .CodeFile("D:\\Desktop\\fpga\\RemedyCpu\\verilog\\fpu\\fpuAddSub.v")) u_fpu_operator (
    .mantA(u_fpu_align_aligneda), .mantB(u_fpu_align_alignedb), .signA(sign_a), .signB(sign_b),
    .mantOut(u_fpu_operator_mantout), .signOut(u_fpu_operator_signout));
  fpu_mult #(.applicationType("IVERILOG"), .CodeFile("D:\\Desktop\\fpga\\RemedyCpu\\verilog\\fpu\\fpumult.v")) u_fpu_mult (
    .a(A), .b(B), .manstisa(u_fpu_mult_manstisa), .exp(u_fpu_mult_exp), .sign(u_fpu_mult_sign));
  fpu_div_fixed #(.applicationType("IVERILOG"), .CodeFile("D:\\Desktop\\fpga\\RemedyCpu\\verilog\\fpu\\div.v")) u_fpu_div_fixed (
    .a(A), .b(B), .result(u_fpu_div_fixed_result));
  float16_to_int #(.applicationType("IVERILOG"), .CodeFile("D:\\Desktop\\fpga\\RemedyCpu\\verilog\\fpu\\floatToInt.v")) u_float16_to_int (
    .in(A), .out(u_float16_to_int_out));
  int_to_float16 #(.applicationType("IVERILOG"), .CodeFile("D:\\Desktop\\fpga\\RemedyCpu\\verilog\\fpu\\intToFloat.v")) u_int_to_float16 (
    .in(A), .out(u_int_to_float16_out));
  fpu_normalize_pack #(.applicationType("IVERILOG"), .CodeFile("D:\\Desktop\\fpga\\RemedyCpu\\verilog\\fpu\\fpunormalize.v")) u_fpu_normalize_pack (
    .mantIn(u_fpu_operator_mantout), .expIn(u_fpu_align_commonexp), .signIn(u_fpu_operator_signout),
    .roundEn(1'b0), .result(u_fpu_normalize_pack_result));
  fpu_normalize_pack #(.applicationType("IVERILOG"), .CodeFile("D:\\Desktop\\fpga\\RemedyCpu\\verilog\\fpu\\fpunormalize.v")) u_fpu_normalize_pack_2 (
    .mantIn(u_fpu_mult_manstisa), .expIn(u_fpu_mult_exp), .signIn(u_fpu_mult_sign), .roundEn(1'b1),
    .result(u_fpu_normalize_pack_2_result));

  // Notes on the sheet:
  //   A: default 15360
  //   B: default 15360
endmodule
