// Digital circuit mini_quad.dig as structural Verilog
module mini_quad (
  input  [7:0] ui_in,
  input  clk,
  input  [7:0] uio_in,
  input  ena,
  input  rst_n,
  input  [15:0] in_10,
  input  [15:0] in_11,
  input  in_12,
  input  in_13,
  input  in_14,
  input  in_15,
  input  [15:0] in_16,
  input  [15:0] in_17,
  input  [15:0] in_18,
  input  in_19,
  input  in_20,
  input  in_21,
  input  in_22,
  input  in_23,
  output [7:0] uo_out,
  output [7:0] uio_out,
  output [7:0] uio_oe,
  output spimiso
);

  wire _1_addressable_register_1_dataout, abs, alu_1_carryout, alu_1_neg, alu_1_zero, and_1_out, and_2_out,
       and_3_out, and_4_out, and_8_out, and_9_out, and_10_out, and_11_out, Clk_in, comparator_1_eq,
       comparator_2_eq, comparator_3_gt, comparator_3_lt, controllogic_1_p17, controllogic_1_p18,
       controllogic_1_p28, controllogic_1_p29, data_done, execute_pulse, Fetch_done, interEnable, InterLock,
       intr, ioR, ioW, ld, multiplexer_5_out, multiplexer_6_out, multiplexer_7_out, multiplexer_8_out, muxA,
       not_1_out, not_3_out, or_2_out, pc_en, read_the_flags, Reti, rst, sf, spi_busy_ram, spi_clock_ram,
       spi_cs, spi_ld, spi_mosi_ram, spi_st, spi_target, spics_flash, spics_ram, st, store_the_flags, stPC,
       u_memory_mode_regs_cmd_flash_clear_qe, u_memory_mode_regs_cmd_flash_if_reset,
       u_memory_mode_regs_cmd_flash_set_qe, u_memory_mode_regs_cmd_ram_enter_qpi,
       u_memory_mode_regs_cmd_ram_exit_qpi, u_memory_mode_regs_cmd_ram_if_reset,
       u_memory_mode_regs_req_cont_fetch, u_memory_mode_regs_req_flash_quad_read,
       u_memory_mode_regs_req_ram_qpi, u_memory_wait_controller_spi_cont,
       u_memory_wait_controller_spi_stop_cont, u_spi_mem_bridge_sim_ram_ld, u_spi_mem_bridge_sim_ram_str, WE,
       xor_1_out;
  wire [1:0] and_12_out, iem;
  wire [2:0] br, FlagOut, muxB, u_muxEncoder_q;
  wire [5:0] aluOp;
  wire [6:0] multiplexer_1_out;
  wire [7:0] outputToOutsideEnable;
  wire [15:0] AddrOut, CurrentOpcode, DataOut, imreg_1_p5, inIntreg, inputReg_t, intEnD, intr_reg, iow_Din,
       mem_out, multiplexer_3_out, multiplexer_9_out, multiplexer_12_out, multiplexer_14_out, prog_d,
       programAddr, ram_d, register_1_q, register_2_q, registerblock_1_rdest, rngdat0, singextend_1__4d,
       singextend_1__4s, singextend_1__8sd, spi_addr, spi_data, spi_data_out, timerdat0,
       u_memory_mode_regs_memout, u_programCounter_nextpc, u_spi_mem_bridge_sim_ram_addr,
       u_spi_mem_bridge_sim_ram_din, u_spi_mem_bridge_sim_rom_addr;

  memory_mode_regs #(.applicationType("IVERILOG"), .CodeFile("C:\\Users\\Aer\\Desktop\\RemedyCpu\\verilog\\memory_mode_regs.v")) u_memory_mode_regs (
    .dOut(in_10), .Addr(in_11), .ioW(in_12), .ioR(in_13), .C(in_14), .rst(in_15), .memCtrlAddr(in_16),
    .memCmdAddr(in_17), .memStatusAddr(in_18), .mem_busy(in_19), .flash_qe_ok(in_20),
    .flash_quad_active(in_21), .ram_qpi_active(in_22), .mem_error(in_23), .MemOut(u_memory_mode_regs_memout),
    .req_flash_quad_read(u_memory_mode_regs_req_flash_quad_read),
    .req_cont_fetch(u_memory_mode_regs_req_cont_fetch), .req_ram_qpi(u_memory_mode_regs_req_ram_qpi),
    .cmd_flash_set_qe(u_memory_mode_regs_cmd_flash_set_qe),
    .cmd_flash_clear_qe(u_memory_mode_regs_cmd_flash_clear_qe),
    .cmd_ram_enter_qpi(u_memory_mode_regs_cmd_ram_enter_qpi),
    .cmd_ram_exit_qpi(u_memory_mode_regs_cmd_ram_exit_qpi),
    .cmd_flash_if_reset(u_memory_mode_regs_cmd_flash_if_reset),
    .cmd_ram_if_reset(u_memory_mode_regs_cmd_ram_if_reset));
  spi_mem_bridge_sim #(.applicationType("IVERILOG"), .CodeFile("C:\\Users\\Aer\\Desktop\\RemedyCpu\\verilog\\virtual_spi_memory_interface_cont.v")) u_spi_mem_bridge_sim (
    .clk(Clk_in), .rst(rst), .cs_flash(spics_flash), .cs_ram(spics_ram), .sclk(spi_clock_ram),
    .mosi(spi_mosi_ram), .rom_data(prog_d), .ram_data(ram_d), .miso(spimiso),
    .rom_addr(u_spi_mem_bridge_sim_rom_addr), .ram_addr(u_spi_mem_bridge_sim_ram_addr),
    .ram_din(u_spi_mem_bridge_sim_ram_din), .ram_ld(u_spi_mem_bridge_sim_ram_ld),
    .ram_str(u_spi_mem_bridge_sim_ram_str));  // open: rom_sel
  _1_addressable_register intEn (
    .Datain(DataOut), .ioW(ioW), .addrIn(AddrOut), .address(16'he), .clk(Clk_in), .ioR(ioR),
    .DataOut(interEnable), .Dataiow(intEnD));
  ROM #(.bigEndian("true"), .AddrBits(16), .isProgramMemory("true"), .Bits(16)) prog (
    .A(u_spi_mem_bridge_sim_rom_addr), .sel(1'b1), .D(prog_d));
  RAMDualPort #(.AddrBits(16), .Bits(16)) ram (
    .A(u_spi_mem_bridge_sim_ram_addr), .Din(u_spi_mem_bridge_sim_ram_din),
    .str(u_spi_mem_bridge_sim_ram_str), .C(Clk_in), .ld(u_spi_mem_bridge_sim_ram_ld), .D(ram_d));
  and and_1 (and_1_out, intr, execute_pulse, interEnable);
  and and_2 (and_2_out, interEnable, execute_pulse, Reti);
  and and_3 (and_3_out, abs, execute_pulse);
  Multiplexer #(.Bits(7)) multiplexer_1 (
    .sel(CurrentOpcode[15]), .in_0(CurrentOpcode[14:8]), .in_1({7{1'b0}}), .out(multiplexer_1_out));
  Multiplexer multiplexer_2 (.sel(ena), .in_0(1'b1), .in_1(clk), .out(Clk_in));
  and and_4 (and_4_out, xor_1_out, execute_pulse);
  // controllogic controllogic_1: pin names not known; wires that end beside it: multiplexer_1_out[6], multiplexer_1_out[5], multiplexer_1_out[4], multiplexer_1_out[3], multiplexer_1_out[2], multiplexer_1_out[1], multiplexer_1_out[0], muxB[2], muxB[1], muxB[0], aluOp[5], aluOp[4], aluOp[3], aluOp[2], aluOp[1], aluOp[0], controllogic_1_p17, controllogic_1_p18, iem[1], iem[0], br[2], br[1], br[0], muxA, ld, st, abs, controllogic_1_p28, controllogic_1_p29, stPC, Reti
  programCounter #(.applicationType("IVERILOG"), .CodeFile("C:\\Users\\Berkant\\Desktop\\fpga\\RemedyCpu\\verilog\\programCounter.v")) u_programCounter (
    .AluIn(AddrOut), .clk(Clk_in), .rst(rst), .pc_en(pc_en), .absJmp(and_3_out), .intr(and_1_out),
    .reti(and_2_out), .relJmp(and_4_out), .Nextpc(u_programCounter_nextpc), .PC(programAddr));
  memory_wait_controller #(.applicationType("IVERILOG"), .CodeFile("C:\\Users\\Aer\\Desktop\\RemedyCpu\\verilog\\main_memory_reader_cont_fix_cycler.v")) u_memory_wait_controller (
    .clk(Clk_in), .rst(rst), .ld_req(ld), .st_req(st), .fetch_addr(programAddr), .data_addr(AddrOut),
    .store_data(DataOut), .spi_data_out(spi_data), .spi_busy(spi_busy_ram), .mem_rdata(mem_out),
    .fetch_done(Fetch_done), .data_done(data_done), .spi_st(spi_st), .spi_ld(spi_ld), .spi_addr(spi_addr),
    .spi_data_in(spi_data_out), .spi_target(spi_target), .spi_cont(u_memory_wait_controller_spi_cont),
    .spi_stop_cont(u_memory_wait_controller_spi_stop_cont), .execute_now(execute_pulse), .pc_en(pc_en));
  spi_memory_interface #(.applicationType("IVERILOG"), .CodeFile("C:\\Users\\Aer\\Desktop\\RemedyCpu\\verilog\\spi_memory_cont.v")) u_spi_memory_interface (
    .clk(Clk_in), .spi_rst(rst), .st(spi_st), .ld(spi_ld), .addr(spi_addr), .data_in(spi_data_out),
    .is_continous(u_memory_wait_controller_spi_cont),
    .stop_continous(u_memory_wait_controller_spi_stop_cont), .spi_miso(spimiso), .data_out(spi_data),
    .spi_cs(spi_cs), .spi_clk(spi_clock_ram), .busy(spi_busy_ram), .spi_mosi(spi_mosi_ram));
  not not_1 (not_1_out, ld);
  and and_5 (sf, controllogic_1_p18, execute_pulse);
  and and_6 (ioW, controllogic_1_p28, execute_pulse);
  and and_7 (ioR, controllogic_1_p29, execute_pulse);
  and and_8 (and_8_out, not_1_out, execute_pulse, controllogic_1_p17);
  and and_9 (and_9_out, controllogic_1_p17, data_done, ld);
  not not_2 (rst, rst_n);
  or or_1 (WE, and_8_out, and_9_out);
  Multiplexer #(.Selector_Bits(3), .Bits(16)) multiplexer_3 (
    .sel(u_muxEncoder_q), .in_0(AddrOut), .in_1(mem_out), .in_2(iow_Din), .in_3(u_programCounter_nextpc),
    .in_4({16{1'b0}}), .in_5({16{1'b0}}), .in_6({{13{1'b0}}, FlagOut}), .in_7({16{1'b0}}),
    .out(multiplexer_3_out));
  Register #(.Bits(16)) register_1 (.D(mem_out), .C(Clk_in), .en(1'b1), .Q(register_1_q));
  muxEncoder #(.applicationType("IVERILOG"), .CodeFile("D:\\Desktop\\fpga\\RemedyCpu\\verilog\\multipleToMux.v")) u_muxEncoder (
    .a(1'b0), .b(ld), .c(ioR), .d(stPC), .e(1'b0), .f(1'b0), .g(read_the_flags), .h(1'b0), .Q(u_muxEncoder_q));
  xor xor_1 (xor_1_out, multiplexer_5_out, br[2]);
  Multiplexer #(.Bits(16)) multiplexer_4 (.sel(rst_n), .in_0({16{1'b0}}), .in_1(register_1_q), .out(CurrentOpcode));
  Multiplexer #(.Selector_Bits(2)) multiplexer_5 (
    .sel(br[1:0]), .in_0(1'b0), .in_1(FlagOut[0]), .in_2(FlagOut[1]), .in_3(FlagOut[2]),
    .out(multiplexer_5_out));
  register_1bit NegR (.D(multiplexer_6_out), .C(Clk_in), .en(sf), .rst(rst), .Q(FlagOut[2]));
  register_1bit ZeroR (.D(multiplexer_7_out), .C(Clk_in), .en(sf), .rst(rst), .Q(FlagOut[1]));
  register_1bit CarryR (.D(multiplexer_8_out), .C(Clk_in), .en(sf), .rst(rst), .Q(FlagOut[0]));
  RegisterBlock registerblock_1 (
    .DataIn(multiplexer_3_out), .WE(WE), .clk(Clk_in), .src(CurrentOpcode[3:0]), .Dest(CurrentOpcode[7:4]),
    .rst(rst), .RDest(registerblock_1_rdest), .Rsrc(DataOut));
  // ImReg imreg_1: pin names not known; wires that end beside it: CurrentOpcode[15], iem, Clk_in, CurrentOpcode, imreg_1_p5
  singExtend singextend_1 (
    .inst(CurrentOpcode), ._4S(singextend_1__4s), ._8SD(singextend_1__8sd), ._4D(singextend_1__4d));
  Multiplexer multiplexer_6 (.sel(store_the_flags), .in_0(alu_1_neg), .in_1(AddrOut[2]), .out(multiplexer_6_out));
  Multiplexer multiplexer_7 (.sel(store_the_flags), .in_0(alu_1_zero), .in_1(AddrOut[1]), .out(multiplexer_7_out));
  Multiplexer multiplexer_8 (.sel(store_the_flags), .in_0(alu_1_carryout), .in_1(AddrOut[0]), .out(multiplexer_8_out));
  Multiplexer #(.Bits(16)) multiplexer_9 (
    .sel(muxA), .in_0(registerblock_1_rdest), .in_1(DataOut), .out(multiplexer_9_out));
  Multiplexer multiplexer_10 (.sel(not_3_out), .in_0(1'b1), .in_1(spi_cs), .out(spics_flash));
  Multiplexer multiplexer_11 (.sel(spi_target), .in_0(1'b1), .in_1(spi_cs), .out(spics_ram));
  Multiplexer #(.Selector_Bits(3), .Bits(16)) multiplexer_12 (
    .sel(muxB), .in_0(DataOut), .in_1({16{1'b0}}), .in_2(imreg_1_p5), .in_3({16{1'b0}}), .in_4({16{1'b0}}),
    .in_5(singextend_1__4s), .in_6(singextend_1__8sd), .in_7(singextend_1__4d), .out(multiplexer_12_out));
  not not_3 (not_3_out, spi_target);
  Alu alu_1 (
    .A(multiplexer_9_out), .B(multiplexer_12_out), .carryIn(FlagOut[0]), .AluOp(aluOp), .Out(AddrOut),
    .Neg(alu_1_neg), .Zero(alu_1_zero), .CarryOut(alu_1_carryout));
  Multiplexer #(.Selector_Bits(4), .Bits(16)) multiplexer_13 (
    .sel(AddrOut[3:0]), .in_0({16{1'b0}}), .in_1(timerdat0), .in_2(timerdat0), .in_3(timerdat0),
    .in_4(timerdat0), .in_5(timerdat0), .in_6(timerdat0), .in_7(timerdat0), .in_8(timerdat0), .in_9(rngdat0),
    .in_10(rngdat0), .in_11({{8{1'b0}}, outputToOutsideEnable}), .in_12({{8{1'b0}}, uo_out}),
    .in_13(inputReg_t), .in_14(intr_reg), .in_15({16{1'b0}}), .out(iow_Din));
  lfsr_RandomNumberGen #(.applicationType("IVERILOG"), .CodeFile("D:\\Desktop\\fpga\\RemedyCpu\\verilog\\lfsr.v")) u_lfsr_RandomNumberGen (
    .adrrIn(AddrOut), .dataIn(DataOut), .ioW(ioW), .clk(Clk_in), .ioR(ioR), .SeedAdr(16'h9), .RngAdr(16'ha),
    .Out(rngdat0));
  Comparator #(.Signed("true"), .Bits(16)) comparator_1 (
    .a(AddrOut), .b(16'h10), .eq(comparator_1_eq));  // open: gt, lt
  timer #(.applicationType("IVERILOG"), .CodeFile("D:\\Desktop\\fpga\\RemedyCpu\\verilog\\timer_small.v")) u_timer (
    .dOut(DataOut), .Addr(AddrOut), .ioW(ioW), .ioR(ioR), .C(Clk_in), .InterLock(InterLock),
    .timerConfigAddr(16'h1), .timerTargetAddr(16'h2), .timerResetAddr(16'h3), .timerReadAddr(16'h4),
    .rst(rst), .TimerOut(timerdat0), .timer_interrupt(and_12_out[1]));
  Comparator #(.Signed("true"), .Bits(16)) comparator_2 (.a(AddrOut), .b(16'hf), .eq(comparator_2_eq));  // open: gt, lt
  and and_10 (and_10_out, comparator_1_eq, ioW);
  and and_11 (and_11_out, comparator_2_eq, ioW);
  _1_addressable_register _1_addressable_register_1 (
    .Datain(DataOut), .ioW(ioW), .addrIn(AddrOut), .address(16'hf), .clk(Clk_in), .ioR(ioR),
    .DataOut(_1_addressable_register_1_dataout), .Dataiow(inIntreg));
  interrupt_controller #(.applicationType("IVERILOG"), .CodeFile("D:\\Desktop\\fpga\\RemedyCpu\\verilog\\interrupt_controller.v")) u_interrupt_controller (
    .clk(Clk_in), .rst(rst), .irq_in({2'b00, and_12_out}), .imm(CurrentOpcode[15]), .reti(Reti),
    .pc_en(pc_en), .reg_we(ioW), .reg_addr(AddrOut[1:0]), .reg_wdata(DataOut), .reg_rdata(intr_reg),
    .intr(intr), .irq_lock(InterLock));
  register_8bit outputReg (.D(DataOut[7:0]), .C(Clk_in), .en(and_10_out), .rst(rst), .Q(outputToOutsideEnable));
  Multiplexer #(.Bits(16)) multiplexer_14 (
    .sel(InterLock), .in_0({{8{1'b0}}, ui_in}), .in_1(register_2_q), .out(multiplexer_14_out));
  Register #(.Bits(16)) register_2 (.D(multiplexer_14_out), .C(Clk_in), .en(or_2_out), .Q(register_2_q));
  register_8bit OutoutEnReg (.D(DataOut[7:0]), .C(Clk_in), .en(and_11_out), .rst(rst), .Q(uo_out));
  Comparator #(.Bits(16)) comparator_3 (
    .a(multiplexer_14_out), .b(register_2_q), .gt(comparator_3_gt), .lt(comparator_3_lt));  // open: eq
  or or_2 (or_2_out, comparator_3_gt, comparator_3_lt);
  and and_12 (and_12_out[0], or_2_out, _1_addressable_register_1_dataout);
  Multiplexer #(.Bits(16)) multiplexer_15 (
    .sel(_1_addressable_register_1_dataout), .in_0({{8{1'b0}}, ui_in}), .in_1(register_2_q), .out(inputReg_t));

  assign uio_oe = 8'h1e;
  assign uio_out = {8{1'b0}};

  // Other names for the same wires on the sheet: OPcode[7:0] = CurrentOpcode[15:8]; imm = CurrentOpcode[15];
  //   inputFromOutside[7:0] = ui_in; outEn[7:0] = uo_out; outputToOutside[7:0] = uo_out;
  //   outR[7:0] = outputToOutsideEnable; rest_n = rst_n; spi_miso = spimiso

  // Notes on the sheet:
  //   clk: Hz: 100
  //   ena: default 1
  //   in_17: default 1
  //   in_18: default 2
  //   prog loads testCompiler.bin
  //   Input/Output
  //   ControlLogic
  //   ProgramMemoryRead
  //   JumpLogic
  //   FlagStore
  //   PERIPHERAL ADDRESSES
  //   IO Addresses
  //   Write/Read Addresses
  //   RandomNumberGen
  //   PERIPHERAL BUS
  //   Timers
  //   Output
  //   Output_En
  //   input
  //   InterruptBus
  //   INTERRRRRUPT BUS
endmodule
