// Digital circuit minimal.dig as structural Verilog
module minimal (
  input  [7:0] ui_in,
  input  rst_n,
  input  clk,
  input  [7:0] uio_in,
  input  ena,
  output [7:0] uo_out,
  output [7:0] uio_out,
  output [7:0] uio_oe
);

  wire abs, alu_1_carryout, alu_1_neg, alu_1_zero, and_1_out, and_2_out, and_3_out, and_4_out, and_8_out,
       and_9_out, and_10_out, and_11_out, and_12_out, and_13_out, and_14_out, and_17_out, and_18_out,
       and_19_out, and_20_out, and_21_out, Clk_in, comparator_1_eq, comparator_2_eq, comparator_3_eq,
       comparator_4_gt, comparator_4_lt, controllogic_1_p17, controllogic_1_p18, controllogic_1_p28,
       controllogic_1_p29, d_ff_q, data_done, execut, execute_pulse, Fetch_done, fetch_request_pulse,
       InterLock, intr, ioR, ioW, ld, multiplexer_7_out, multiplexer_8_out, multiplexer_9_out,
       multiplexer_10_out, muxA, not_1_out, not_3_out, not_4_out, or_2_out, or_3_out, or_4_out, pc_en,
       read_the_flags, Reti, rst, sf, spi_busy_ram, spi_cs, spi_ld, spi_st, spi_target, st, store_the_flags,
       stPC, u_cpu_cycle_controller_wait_data, u_memory_wait_controller_mem_stall, WE, xor_1_out;
  wire [1:0] iem;
  wire [2:0] br, FlagOut, muxB, u_muxEncoder_q;
  wire [5:0] aluOp;
  wire [6:0] multiplexer_3_out;
  wire [7:0] outputToOutsideEnable;
  wire [15:0] AddrOut, CurrentOpcode, DataOut, imreg_1_p5, inputReg_t, iow_Din, mem_out, multiplexer_5_out,
       multiplexer_11_out, multiplexer_12_out, multiplexer_14_out, multiplexer_15_out, outEn, outR,
       programAddr, register_1_q, register_2_q, registerblock_1_rdest, singextend_1__4d, singextend_1__4s,
       singextend_1__8sd, spi_addr, spi_data, spi_data_out, u_programCounter_nextpc;

  Multiplexer multiplexer_1 (.sel(not_1_out), .in_0(1'b1), .in_1(spi_cs), .out(uio_out[1]));
  Multiplexer multiplexer_2 (.sel(spi_target), .in_0(1'b1), .in_1(spi_cs), .out(uio_out[0]));
  not not_1 (not_1_out, spi_target);
  and and_1 (and_1_out, intr, execute_pulse, 1'b1);
  and and_2 (and_2_out, 1'b1, execute_pulse, Reti);
  and and_3 (and_3_out, abs, execute_pulse);
  Multiplexer #(.Bits(7)) multiplexer_3 (
    .sel(CurrentOpcode[15]), .in_0(CurrentOpcode[14:8]), .in_1({7{1'b0}}), .out(multiplexer_3_out));
  Multiplexer multiplexer_4 (.sel(ena), .in_0(1'b1), .in_1(clk), .out(Clk_in));
  and and_4 (and_4_out, xor_1_out, execute_pulse);
  // controllogic controllogic_1: pin names not known; wires that end beside it: multiplexer_3_out[6], multiplexer_3_out[5], multiplexer_3_out[4], multiplexer_3_out[3], multiplexer_3_out[2], multiplexer_3_out[1], multiplexer_3_out[0], muxB[2], muxB[1], muxB[0], aluOp[5], aluOp[4], aluOp[3], aluOp[2], aluOp[1], aluOp[0], controllogic_1_p17, controllogic_1_p18, iem[1], iem[0], br[2], br[1], br[0], muxA, ld, st, abs, controllogic_1_p28, controllogic_1_p29, stPC, Reti
  not not_2 (rst, rst_n);
  programCounter #(.applicationType("IVERILOG"), .CodeFile("C:\\Users\\Berkant\\Desktop\\fpga\\RemedyCpu\\verilog\\programCounter.v")) u_programCounter (
    .AluIn(AddrOut), .clk(Clk_in), .rst(rst), .pc_en(pc_en), .absJmp(and_3_out), .intr(and_1_out),
    .reti(and_2_out), .relJmp(and_4_out), .Nextpc(u_programCounter_nextpc), .PC(programAddr));
  not not_3 (not_3_out, ld);
  and and_5 (sf, controllogic_1_p18, execute_pulse);
  and and_6 (ioW, controllogic_1_p28, execute_pulse);
  and and_7 (ioR, controllogic_1_p29, execute_pulse);
  and and_8 (and_8_out, not_3_out, execute_pulse, controllogic_1_p17);
  and and_9 (and_9_out, controllogic_1_p17, data_done, ld);
  or or_1 (WE, and_8_out, and_9_out);
  Multiplexer #(.Selector_Bits(3), .Bits(16)) multiplexer_5 (
    .sel(u_muxEncoder_q), .in_0(AddrOut), .in_1(mem_out), .in_2(iow_Din), .in_3(u_programCounter_nextpc),
    .in_4({16{1'b0}}), .in_5({16{1'b0}}), .in_6({{13{1'b0}}, FlagOut}), .in_7({16{1'b0}}),
    .out(multiplexer_5_out));
  Register #(.Bits(16)) register_1 (.D(mem_out), .C(Clk_in), .en(Fetch_done), .Q(register_1_q));
  muxEncoder #(.applicationType("IVERILOG"), .CodeFile("D:\\Desktop\\fpga\\RemedyCpu\\verilog\\multipleToMux.v")) u_muxEncoder (
    .a(1'b0), .b(ld), .c(ioR), .d(stPC), .e(1'b0), .f(1'b0), .g(read_the_flags), .h(1'b0), .Q(u_muxEncoder_q));
  xor xor_1 (xor_1_out, multiplexer_7_out, br[2]);
  and and_10 (and_10_out, ld, execute_pulse);
  and and_11 (and_11_out, execute_pulse, st);
  Multiplexer #(.Bits(16)) multiplexer_6 (.sel(rst_n), .in_0({16{1'b0}}), .in_1(register_1_q), .out(CurrentOpcode));
  Multiplexer #(.Selector_Bits(2)) multiplexer_7 (
    .sel(br[1:0]), .in_0(1'b0), .in_1(FlagOut[0]), .in_2(FlagOut[1]), .in_3(FlagOut[2]),
    .out(multiplexer_7_out));
  register_1bit NegR (.D(multiplexer_8_out), .C(Clk_in), .en(sf), .rst(rst), .Q(FlagOut[2]));
  register_1bit ZeroR (.D(multiplexer_9_out), .C(Clk_in), .en(sf), .rst(rst), .Q(FlagOut[1]));
  register_1bit CarryR (.D(multiplexer_10_out), .C(Clk_in), .en(sf), .rst(rst), .Q(FlagOut[0]));
  RegisterBlock registerblock_1 (
    .DataIn(multiplexer_5_out), .WE(WE), .clk(Clk_in), .src(CurrentOpcode[3:0]), .Dest(CurrentOpcode[7:4]),
    .rst(rst), .RDest(registerblock_1_rdest), .Rsrc(DataOut));
  // ImReg imreg_1: pin names not known; wires that end beside it: CurrentOpcode[15], iem, Clk_in, CurrentOpcode, imreg_1_p5
  singExtend singextend_1 (
    .inst(CurrentOpcode), ._4S(singextend_1__4s), ._8SD(singextend_1__8sd), ._4D(singextend_1__4d));
  memory_wait_controller #(.applicationType("IVERILOG"), .CodeFile("C:\\Users\\Berkant\\Desktop\\fpga\\RemedyCpu\\verilog\\memory_wait_controller.v")) u_memory_wait_controller (
    .clk(Clk_in), .rst(rst), .fetch_req(fetch_request_pulse), .ld_req(and_10_out), .st_req(and_11_out),
    .fetch_addr(programAddr), .data_addr(AddrOut), .store_data(DataOut), .spi_data_out(spi_data),
    .spi_busy(spi_busy_ram), .mem_rdata(mem_out), .fetch_done(Fetch_done), .data_done(data_done),
    .mem_stall(u_memory_wait_controller_mem_stall), .spi_st(spi_st), .spi_ld(spi_ld), .spi_addr(spi_addr),
    .spi_data_in(spi_data_out), .spi_target(spi_target));
  cpu_cycle_controller #(.applicationType("IVERILOG"), .CodeFile("C:\\Users\\Berkant\\Desktop\\fpga\\RemedyCpu\\verilog\\cpu_cycle_controller.v")) u_cpu_cycle_controller (
    .clk(Clk_in), .rst(rst), .fetch_done(Fetch_done), .data_done(data_done), .ld(ld), .st(st),
    .fetch_req(fetch_request_pulse), .execute_now(execut), .wait_data(u_cpu_cycle_controller_wait_data));
  spi_memory_interface #(.applicationType("IVERILOG"), .CodeFile("D:\\Desktop\\fpga\\RemedyCpu\\verilog\\spi_memory.v")) u_spi_memory_interface (
    .clk(Clk_in), .spi_rst(rst), .st(spi_st), .ld(spi_ld), .addr(spi_addr), .data_in(spi_data_out),
    .is_continous(1'b0), .spi_miso(uio_in[0]), .data_out(spi_data), .spi_cs(spi_cs), .spi_clk(uio_out[3]),
    .busy(spi_busy_ram), .spi_mosi(uio_out[2]));
  and and_12 (and_12_out, InterLock, ~Reti);  // And
  and and_13 (and_13_out, d_ff_q, ~Reti);  // And
  and and_14 (and_14_out, 1'b1, 1'b1);
  or or_2 (or_2_out, and_12_out, intr);
  or or_3 (or_3_out, and_13_out, and_14_out);
  Multiplexer multiplexer_8 (.sel(store_the_flags), .in_0(alu_1_neg), .in_1(AddrOut[2]), .out(multiplexer_8_out));
  Multiplexer multiplexer_9 (.sel(store_the_flags), .in_0(alu_1_zero), .in_1(AddrOut[1]), .out(multiplexer_9_out));
  Multiplexer multiplexer_10 (
    .sel(store_the_flags), .in_0(alu_1_carryout), .in_1(AddrOut[0]), .out(multiplexer_10_out));
  D_FF d_ff (.D(or_3_out), .C(~Clk_in), .Q(d_ff_q));  // open: nQ
  Multiplexer #(.Bits(16)) multiplexer_11 (
    .sel(muxA), .in_0(registerblock_1_rdest), .in_1(DataOut), .out(multiplexer_11_out));
  D_FF d_ff_2 (.D(or_2_out), .C(~Clk_in), .Q(InterLock));  // open: nQ
  Multiplexer #(.Selector_Bits(3), .Bits(16)) multiplexer_12 (
    .sel(muxB), .in_0(DataOut), .in_1({16{1'b0}}), .in_2(imreg_1_p5), .in_3({16{1'b0}}), .in_4({16{1'b0}}),
    .in_5(singextend_1__4s), .in_6(singextend_1__8sd), .in_7(singextend_1__4d), .out(multiplexer_12_out));
  and and_15 (intr, ~InterLock, ~CurrentOpcode[15], d_ff_q, ~1'b0);  // And
  not not_4 (not_4_out, u_memory_wait_controller_mem_stall);
  and and_16 (pc_en, not_4_out, execute_pulse);
  Alu alu_1 (
    .A(multiplexer_11_out), .B(multiplexer_12_out), .carryIn(FlagOut[0]), .AluOp(aluOp), .Out(AddrOut),
    .Neg(alu_1_neg), .Zero(alu_1_zero), .CarryOut(alu_1_carryout));
  pulse_on_rise #(.applicationType("IVERILOG"), .CodeFile("C:\\Users\\Berkant\\Desktop\\fpga\\RemedyCpu\\verilog\\pulse_on_rise.v")) u_pulse_on_rise (
    .clk(Clk_in), .rst(rst), .sig(execut), .pulse(execute_pulse));
  Multiplexer #(.Selector_Bits(5), .Bits(16)) multiplexer_13 (
    .sel(AddrOut[4:0]), .in_0({16{1'b0}}), .in_1({16{1'b0}}), .in_2({16{1'b0}}), .in_3({16{1'b0}}),
    .in_4({16{1'b0}}), .in_5({16{1'b0}}), .in_6({16{1'b0}}), .in_7({16{1'b0}}), .in_8({16{1'b0}}),
    .in_9({16{1'b0}}), .in_10({16{1'b0}}), .in_11({16{1'b0}}), .in_12({16{1'b0}}), .in_13({16{1'b0}}),
    .in_14({16{1'b0}}), .in_15(outR), .in_16(outEn), .in_17(inputReg_t), .in_18({16{1'b0}}),
    .in_19({16{1'b0}}), .in_20({16{1'b0}}), .in_21({16{1'b0}}), .in_22({16{1'b0}}), .in_23({16{1'b0}}),
    .in_24({16{1'b0}}), .in_25({16{1'b0}}), .in_26({16{1'b0}}), .in_27({16{1'b0}}), .in_28({16{1'b0}}),
    .in_29({16{1'b0}}), .in_30({16{1'b0}}), .in_31({16{1'b0}}), .out(iow_Din));
  Comparator #(.Signed("true"), .Bits(16)) comparator_1 (
    .a(AddrOut), .b(16'h10), .eq(comparator_1_eq));  // open: gt, lt
  Comparator #(.Signed("true"), .Bits(16)) comparator_2 (.a(AddrOut), .b(16'hf), .eq(comparator_2_eq));  // open: gt, lt
  Comparator #(.Signed("true"), .Bits(16)) comparator_3 (
    .a(AddrOut), .b(16'h11), .eq(comparator_3_eq));  // open: gt, lt
  and and_17 (and_17_out, comparator_1_eq, ioW);
  and and_18 (and_18_out, comparator_2_eq, ioW);
  and and_19 (and_19_out, comparator_3_eq, ioR);
  and and_20 (and_20_out, ioR, comparator_1_eq);
  register_8bit outputReg (.D(DataOut[7:0]), .C(Clk_in), .en(and_17_out), .rst(rst), .Q(outputToOutsideEnable));
  and and_21 (and_21_out, ioR, comparator_2_eq);
  Multiplexer #(.Bits(16)) multiplexer_14 (
    .sel(InterLock), .in_0({{8{1'b0}}, ui_in}), .in_1(register_2_q), .out(multiplexer_14_out));
  Register #(.Bits(16)) register_2 (.D(multiplexer_14_out), .C(Clk_in), .en(or_4_out), .Q(register_2_q));
  register_8bit OutoutEnReg (.D(DataOut[7:0]), .C(Clk_in), .en(and_18_out), .rst(rst), .Q(uo_out));
  Comparator #(.Bits(16)) comparator_4 (
    .a(multiplexer_14_out), .b(register_2_q), .gt(comparator_4_gt), .lt(comparator_4_lt));  // open: eq
  assign outEn = and_21_out ? {{8{1'b1}}, uo_out} : 16'bz;  // Driver driver_1
  or or_4 (or_4_out, comparator_4_gt, comparator_4_lt);
  assign outR = and_20_out ? {{8{1'b1}}, outputToOutsideEnable} : 16'bz;  // Driver driver_2
  Multiplexer #(.Bits(16)) multiplexer_15 (
    .sel(or_4_out), .in_0({{8{1'b0}}, ui_in}), .in_1(register_2_q), .out(multiplexer_15_out));
  assign inputReg_t = and_19_out ? multiplexer_15_out : 16'bz;  // Driver driver_3

  assign uio_oe = 8'hf;
  assign uio_out[7:4] = 4'b0000;

  // Other names for the same wires on the sheet: OPcode[7:0] = CurrentOpcode[15:8]; imm = CurrentOpcode[15];
  //   inputFromOutside[7:0] = ui_in; outputToOutside[7:0] = uo_out; rest_n = rst_n; spi_clock_ram = uio_out[3];
  //   spi_mosi_ram = uio_out[2]; spics_flash = uio_out[1]; spics_ram = uio_out[0]; spi_miso = uio_in[0]

  // Notes on the sheet:
  //   clk: Hz: 2147483647
  //   ena: default 1
  //   Input/Output
  //   ControlLogic
  //   JumpLogic
  //   FlagStore
  //   ProgramMemoryRead
  //   interrupt Logic
  //   PERIPHERAL ADDRESSES
  //   IO Addresses
  //   Write/Read Addresses
  //   PERIPHERAL BUS
  //   Timers
  //   Output
  //   Output_En
  //   input
  //   InterruptBus
endmodule
