// Digital circuit new program mwm.dig as structural Verilog
module new_program_mwm (
  input  in_3,
  input  in_4,
  input  [15:0] in_5,
  input  [15:0] in_6,
  input  in_7,
  input  in_8,
  input  [15:0] in_9,
  input  [15:0] in_10,
  input  clk,
  input  [15:0] in_12,
  input  in_13,
  input  in_14,
  input  in_15,
  input  in_16,
  input  in_17,
  output [15:0] out_1,
  output [15:0] out_2
);

  wire [15:0] programAddr, u_programCounter_nextpc;

  programCounter #(.applicationType("IVERILOG"), .CodeFile("C:\\Users\\Berkant\\Desktop\\fpga\\RemedyCpu\\verilog\\programCounter.v")) u_programCounter (
    .AluIn(in_12), .clk(clk), .rst(in_13), .absJmp(in_14), .intr(in_15), .reti(in_16), .relJmp(in_17),
    .Nextpc(u_programCounter_nextpc), .PC(programAddr));
  ROM #(.bigEndian("true"), .AddrBits(16), .isProgramMemory("true"), .Bits(16)) pgr (
    .A(programAddr), .sel(1'b1));  // open: D
  single_port_bram_16bit #(.applicationType("IVERILOG"), .CodeFile("D:\\Desktop\\fpga\\RemedyCpu\\verilog\\ram_2.v")) u_single_port_bram_16bit (
    .clk(clk), .we_1(in_3), .rld_1(in_4), .addr_1(in_5), .din_1(in_6), .we_2(in_7), .rld_2(in_8),
    .addr_2(in_9), .din_2(in_10), .dout_1(out_1), .dout_2(out_2));

  // Notes on the sheet:
  //   clk: Hz: 5
  //   pgr loads testCompiler.bin
endmodule
