// Digital circuit newCPUDesign.dig as structural Verilog
module newCPUDesign (
  input  [3:0] SW,
  input  [4:0] BTN,
  input  mclk,
  input  [15:0] a,
  input  sdfsdfz,
  input  [15:0] b,
  output [7:0] LED,
  output Deg2,
  output DataClockOut,
  output RealClockOut,
  output Deg4,
  output Deg1,
  output Deg3,
  output [15:0] dfdf,
  output [15:0] sdsd
);

  wire _16xprescaler_1_clockout, abs, Activate_Debug_out, alu2D, alut_1_carry, alut_1_neg, alut_1_zero,
       and_1_out, and_2_out, d_ff_2_q, DataSel, demultiplexer_1_out_1, dipswitch_1_out, dipswitch_2_out,
       dipswitch_3_out, dipswitch_4_out, flagread, flagStr, imm, inter, InterLock, intr, ioR, ioW, ld,
       multiplexer_5_out, multiplexer_7_out, multiplexer_8_out, multiplexer_9_out, muxA, not_1_out, or_1_out,
       or_2_out, RandomNUMSel, Reti, Sel3, sf, st, stPC, u_spi_master_busy, u_spi_master_mosi,
       u_spi_master_sclk, u_spi_master_ss_n, u_spi_slave_busy, u_spi_slave_miso, WE, xor_1_out;
  wire [1:0] iem;
  wire [2:0] br, muxB, WDmux;
  wire [3:0] FlagOut;
  wire [3:3] selectorformultplx_1_out;
  wire [4:0] aluOp;
  wire [7:0] OPcode, OpcodeDebug;
  wire [15:0] Addr, Din, Dout, imreg_1_p5, mem_d, multiplexer_2_out, multiplexer_3_out, multiplexer_4_out,
       PcDebug, pcte_1_nextpc, RandomNUM, registerblock_1_rdest, registerblock_1_rsrc, singextend_1__4d,
       singextend_1__4s, singextend_1__8sd;

  pcTe pcte_1 (
    .ALU(Addr), .C(RealClockOut), .abs(abs), .intr(intr), .reti(Reti), .rel(xor_1_out), .PC(PcDebug),
    .NextPC(pcte_1_nextpc));  // open: Reset, interruptEnable
  _16bit_paralel_serial _16bit_paralel_serial_1 (.Data(Dout), .Clk(DataClockOut), .Out(Deg4));
  _16bit_paralel_serial _16bit_paralel_serial_2 (.Data(Addr), .Clk(DataClockOut), .Out(Deg3));
  _16bit_paralel_serial _16bit_paralel_serial_3 (.Data(PcDebug), .Clk(DataClockOut), .Out(Deg2));
  _16bit_paralel_serial _16bit_paralel_serial_4 (.Data({OPcode, OpcodeDebug}), .Clk(DataClockOut), .Out(Deg1));
  Demultiplexer demultiplexer_1 (
    .sel(Activate_Debug_out), .in(mclk), .out_0(DataClockOut), .out_1(demultiplexer_1_out_1));
  DipSwitch Activate_Debug (.out(Activate_Debug_out));
  ROM #(.AddrBits(16), .isProgramMemory("true"), .Bits(16)) progMem (
    .A(PcDebug), .sel(1'b1), .D({OPcode, OpcodeDebug}));
  _16xPrescaler _16xprescaler_1 (.Clk(DataClockOut), .ClockOut(_16xprescaler_1_clockout));
  Multiplexer multiplexer_1 (
    .sel(Activate_Debug_out), .in_0(_16xprescaler_1_clockout), .in_1(demultiplexer_1_out_1),
    .out(RealClockOut));
  Multiplexer #(.Selector_Bits(3), .Bits(16)) multiplexer_2 (
    .sel(WDmux), .in_0(Addr), .in_1(mem_d), .in_2(Din), .in_3(pcte_1_nextpc), .in_4({{12{1'b0}}, FlagOut}),
    .in_5(RandomNUM), .in_6({16{1'b0}}), .in_7({16{1'b0}}), .out(multiplexer_2_out));
  OpDecoder opdecoder_1 (
    .OPcode(OPcode), .stPC(stPC), .WE(WE), .iem(iem), .absJmp(abs), .muxB(muxB), .muxA(muxA), .alu2D(alu2D),
    .aluOp(aluOp), .storeFlags(sf), .branch(br), .ramSt(st), .ramLd(ld), .ioW(ioW), .ioR(ioR), .RetI(Reti),
    .flagR(flagread), .flagST(flagStr), .imm(imm), .RandomSel(RandomNUMSel), .dataSel(DataSel));  // open: src2D, I2cSel
  SelectorForMultplx selectorformultplx_1 (
    .in1(ld), .in2(ioR), .in3(stPC), .in4(flagread), .in5(RandomNUMSel), .in6(1'b0), .in7(1'b0), .in8(1'b0),
    .in9(1'b0), .in10(1'b0), .in11(1'b0), .in12(1'b0), .in13(1'b0), .in14(1'b0), .in15(1'b0),
    .out({selectorformultplx_1_out[3], WDmux}));
  RegisterBlock registerblock_1 (
    .DataIn(multiplexer_2_out), .WE(WE), .clk(RealClockOut), .src(OpcodeDebug[3:0]), .Dest(OpcodeDebug[7:4]),
    .RDest(registerblock_1_rdest), .Rsrc(registerblock_1_rsrc));  // open: rst
  singExtend singextend_1 (
    .inst({OPcode, OpcodeDebug}), ._4S(singextend_1__4s), ._8SD(singextend_1__8sd), ._4D(singextend_1__4d));
  // ImReg imreg_1: pin names not known; wires that end beside it: imm, iem, RealClockOut, {OPcode, OpcodeDebug}, imreg_1_p5
  Multiplexer #(.Bits(16)) multiplexer_3 (
    .sel(muxA), .in_0(registerblock_1_rdest), .in_1(registerblock_1_rsrc), .out(multiplexer_3_out));
  Multiplexer #(.Selector_Bits(3), .Bits(16)) multiplexer_4 (
    .sel(muxB), .in_0(registerblock_1_rsrc), .in_1({16{1'b0}}), .in_2(imreg_1_p5), .in_3({16{1'b0}}),
    .in_4({16{1'b0}}), .in_5(singextend_1__4s), .in_6(singextend_1__8sd), .in_7(singextend_1__4d),
    .out(multiplexer_4_out));
  and and_1 (and_1_out, d_ff_2_q, ~Reti);  // And
  and and_2 (and_2_out, InterLock, ~Reti);  // And
  or or_1 (or_1_out, and_1_out, inter);
  // randomNumberGen randomnumbergen_1: pin names not known; wires that end beside it: RandomNUM, ioW, RandomNUMSel, Addr, Dout, RealClockOut
  xor xor_1 (xor_1_out, multiplexer_5_out, br[2]);
  or or_2 (or_2_out, and_2_out, intr);
  D_FF d_ff (.D(or_2_out), .C(~RealClockOut), .Q(InterLock));  // open: nQ
  D_FF d_ff_2 (.D(or_1_out), .C(~RealClockOut), .Q(d_ff_2_q));  // open: nQ
  Multiplexer #(.Selector_Bits(2)) multiplexer_5 (
    .sel(br[1:0]), .in_0(1'b0), .in_1(FlagOut[0]), .in_2(FlagOut[1]), .in_3(FlagOut[2]),
    .out(multiplexer_5_out));
  and and_3 (intr, ~InterLock, ~imm, d_ff_2_q, ~FlagOut[3]);  // And
  Multiplexer #(.Bits(16)) multiplexer_6 (
    .sel(DataSel), .in_0(registerblock_1_rsrc), .in_1(multiplexer_4_out), .out(Dout));
  Alut alut_1 (
    .A(multiplexer_3_out), .B(multiplexer_4_out), .Aluop(aluOp), .CarryIn(FlagOut[0]), .Zero(alut_1_zero),
    .Neg(alut_1_neg), .Carry(alut_1_carry), .DataOut(Addr));
  Register inter1 (.D(intr), .C(RealClockOut), .en(sf), .Q(FlagOut[3]));
  Register Neg (.D(multiplexer_7_out), .C(RealClockOut), .en(sf), .Q(FlagOut[2]));
  Register Zero (.D(multiplexer_8_out), .C(RealClockOut), .en(sf), .Q(FlagOut[1]));
  Register Carry (.D(multiplexer_9_out), .C(RealClockOut), .en(sf), .Q(FlagOut[0]));
  Multiplexer multiplexer_7 (.sel(flagStr), .in_0(alut_1_neg), .in_1(Dout[2]), .out(multiplexer_7_out));
  Multiplexer multiplexer_8 (.sel(flagStr), .in_0(alut_1_zero), .in_1(Dout[1]), .out(multiplexer_8_out));
  Multiplexer multiplexer_9 (.sel(flagStr), .in_0(alut_1_carry), .in_1(Dout[0]), .out(multiplexer_9_out));
  DipSwitch dipswitch_1 (.out(dipswitch_1_out));
  DipSwitch #(.dipDefault("true")) dipswitch_2 (.out(dipswitch_2_out));
  DipSwitch #(.dipDefault("true")) dipswitch_3 (.out(dipswitch_3_out));
  DipSwitch #(.dipDefault("true")) dipswitch_4 (.out(dipswitch_4_out));
  spi_master #(.applicationType("GHDL")) u_spi_master (
    .clk(sdfsdfz), .reset_n(dipswitch_4_out), .enable(dipswitch_3_out), .cpol(dipswitch_1_out),
    .cpha(dipswitch_2_out), .miso(u_spi_slave_miso), .tx(a), .sclk(u_spi_master_sclk),
    .ss_n(u_spi_master_ss_n), .mosi(u_spi_master_mosi), .busy(u_spi_master_busy), .rx(sdsd));
  RAMDualPort #(.AddrBits(10), .Bits(16), .Addr_Bits(10)) mem (
    .A(Addr[9:0]), .Din(Dout), .str(st), .C(RealClockOut), .ld(ld), .D(mem_d));
  spi_slave #(.applicationType("GHDL")) u_spi_slave (
    .reset_n(dipswitch_4_out), .cpol(dipswitch_1_out), .cpha(dipswitch_2_out), .sclk(u_spi_master_sclk),
    .ss_n(u_spi_master_ss_n), .mosi(u_spi_master_mosi), .rx_enable(dipswitch_3_out), .tx(b),
    .miso(u_spi_slave_miso), .rx(dfdf), .busy(u_spi_slave_busy));
  // GPO outputio: pin names not known; wires that end beside it: Dout, Addr, RealClockOut, ioW, LED[0], LED[1], LED[2], LED[3], LED[4], LED[5], LED[6], LED[7]
  GPI_HDL inputio (
    .A(Addr), .R(ioR), .In0(SW[0]), .In1(SW[1]), .In2(SW[2]), .In3(SW[3]), .In4(BTN[0]), .In5(BTN[1]),
    .In6(BTN[2]), .In7(BTN[3]), .In8(BTN[4]), .In9(1'b0), .In10(1'b0), .In11(1'b0), .In12(1'b0), .In13(1'b0),
    .In14(1'b0), .In15(1'b0), .clk(not_1_out), .inter_En(InterLock), .D(Din), .sel(Sel3), .Interrupt(inter));
  not not_1 (not_1_out, RealClockOut);

  // Other names for the same wires on the sheet: AddressDebug[15:0] = Addr; C = RealClockOut; Clk = RealClockOut;
  //   DoutDebug[15:0] = Dout; interEn = FlagOut[3]; OpcodeDebug[15:8] = OPcode

  // Notes on the sheet:
  //   mclk: Hz: 48
  //   sdfsdfz: Hz: 16
  //   Debugger
  //   contents of progMem (hex, n*v repeats v):
  //   a0f,3f30,4224,4223,8020,3e02,8020,4130,2087*0,1
  //   interrupt Logic
  //   RandomNumberGen
  //   FlagStore
endmodule

/* Code of spi_master:
LIBRARY ieee;
USE ieee.std_logic_1164.all;
USE ieee.std_logic_arith.all;
USE ieee.std_logic_unsigned.all;

ENTITY spi_master IS
  GENERIC(
    data_length : INTEGER := 16);     --data length in bits
  PORT(
    clk     : IN     STD_LOGIC;                             --system clock
    reset_n : IN     STD_LOGIC;                             --asynchronous active low reset
    enable  : IN     STD_LOGIC;                             --initiate communication
	 cpol    : IN     STD_LOGIC;  									--clock polarity mode
    cpha    : IN     STD_LOGIC;  									--clock phase mode
    miso    : IN     STD_LOGIC;                             --master in slave out
    sclk    : OUT    STD_LOGIC;                             --spi clock
    ss_n    : OUT    STD_LOGIC;                             --slave select
    mosi    : OUT    STD_LOGIC;                             --master out slave in
    busy    : OUT    STD_LOGIC;                             --master busy signal
    tx		: IN     STD_LOGIC_VECTOR(16-1 DOWNTO 0);  --data to transmit
    rx	   : OUT    STD_LOGIC_VECTOR(16-1 DOWNTO 0)); --data received
END spi_master;

ARCHITECTURE behavioural OF spi_master IS
  TYPE FSM IS(init, execute);                           		--state machine
  SIGNAL state       : FSM;                             
  SIGNAL receive_transmit : STD_LOGIC;                      --'1' for tx, '0' for rx 
  SIGNAL clk_toggles : INTEGER RANGE 0 TO data_length*2 + 1;    --clock toggle counter
  SIGNAL last_bit		: INTEGER RANGE 0 TO data_length*2;        --last bit indicator
  SIGNAL rxBuffer    : STD_LOGIC_VECTOR(data_length-1 DOWNTO 0) := (OTHERS => '0'); --receive data buffer
  SIGNAL txBuffer    : STD_LOGIC_VECTOR(data_length-1 DOWNTO 0) := (OTHERS => '0'); --transmit data buffer
  SIGNAL INT_ss_n    : STD_LOGIC;                            --Internal register for ss_n 
  SIGNAL INT_sclk    : STD_LOGIC;                            --Internal register for sclk 


BEGIN
	
  -- wire internal registers to outside	
  ss_n <= INT_ss_n;
  sclk <= INT_sclk;
  
  PROCESS(clk, reset_n)
  BEGIN

    IF(reset_n = '0') THEN        --reset everything
      busy <= '1';                
      INT_ss_n <= '1';            
      mosi <= 'Z';                
      rx <= (OTHERS => '0');      
      state <= init;              

    ELSIF(falling_edge(clk)) THEN
      CASE state IS               

        WHEN init =>					 -- bus is idle
          busy <= '0';             
          INT_ss_n <= '1'; 		  
          mosi <= 'Z';             
   
          IF(enable = '1') THEN       		--initiate communication
            busy <= '1';             
            INT_sclk <= cpol;        		--set spi clock polarity
            receive_transmit <= NOT cpha; --set spi clock phase
            txBuffer <= tx;    				--put data to buffer to transmit
            clk_toggles <= 0;        		--initiate clock toggle counter
            last_bit <= data_length*2 + conv_integer(cpha) - 1; --set last rx data bit
            state <= execute;        
          ELSE
            state <= init;          
          END IF;


        WHEN execute =>
          busy <= '1';               
          INT_ss_n <= '0';           						--pull the slave select signal down
			 receive_transmit <= NOT receive_transmit;   --change receive transmit mode
          
			 -- counter
			 IF(clk_toggles = data_length*2 + 1) THEN
				clk_toggles <= 0;               				--reset counter
          ELSE
				clk_toggles <= clk_toggles + 1; 				--increment counter
          END IF;
            
          -- toggle sclk
          IF(clk_toggles <= data_length*2 AND INT_ss_n = '0') THEN 
            INT_sclk <= NOT INT_sclk; --toggle spi clock
          END IF;
            
          --receive miso bit
          IF(receive_transmit = '0' AND clk_toggles < last_bit + 1 AND INT_ss_n = '0') THEN 
            rxBuffer <= rxBuffer(data_length-2 DOWNTO 0) & miso; 
          END IF;
            
          --transmit mosi bit
          IF(receive_transmit = '1' AND clk_toggles < last_bit) THEN 
            mosi <= txBuffer(data_length-1);                    
            txBuffer <= txBuffer(data_length-2 DOWNTO 0) & '0'; 
          END IF;
            
          -- Finish/ resume the communication
          IF(clk_toggles = data_length*2 + 1) THEN   
            busy <= '0';             
            INT_ss_n <= '1';         
            mosi <= 'Z';             
            rx <= rxBuffer;    
            state <= init;          
          ELSE                       
            state <= execute;        
          END IF;
      END CASE;
    END IF;
  END PROCESS; 
END behavioural;
*/

/* Code of spi_slave:
LIBRARY ieee;
USE ieee.std_logic_1164.all;
USE ieee.std_logic_arith.all;
--this is comment
ENTITY spi_slave IS
  PORT(
    reset_n      : IN     STD_LOGIC;  																	 --asynchronous active low reset
    cpol    	  : IN 	  STD_LOGIC;  																	 --clock polarity mode
    cpha    	  : IN 	  STD_LOGIC;  																	 --clock phase mode
    sclk         : IN     STD_LOGIC;  																	 --spi clk
    ss_n         : IN     STD_LOGIC;  																	 --slave select
    mosi         : IN     STD_LOGIC;  																	 --master out slave in
    miso         : OUT    STD_LOGIC;  																	 --master in slave out
    rx_enable    : IN     STD_LOGIC;  																	 --enable signal to wire rxBuffer to outside 
    tx		 : IN     STD_LOGIC_VECTOR(16-1 DOWNTO 0);  						 --data to transmit
    rx		 : OUT    STD_LOGIC_VECTOR(16-1 DOWNTO 0) := (OTHERS => '0');  --data received
    busy         : OUT    STD_LOGIC := '0');  														 --slave busy signal	 
END spi_slave;

ARCHITECTURE behavioural OF spi_slave IS
  SIGNAL mode    : STD_LOGIC;  																	  --according to CPOL and CPHA
  SIGNAL clk     : STD_LOGIC;  
  SIGNAL bit_counter : STD_LOGIC_VECTOR(16 DOWNTO 0); 						  --active bit indicator
  SIGNAL rxBuffer  : STD_LOGIC_VECTOR(16-1 DOWNTO 0) := (OTHERS => '0');  --receiver buffer
  SIGNAL txBuffer  : STD_LOGIC_VECTOR(16-1 DOWNTO 0) := (OTHERS => '0');  --transmit buffer
BEGIN
  busy <= NOT ss_n;  
  
  mode <= cpol XOR cpha;  

  PROCESS (mode, ss_n, sclk)
  BEGIN
  IF(ss_n = '1') then
     clk <= '0';
  ELSE
     IF (mode = '1') then
	     clk <= sclk;
	  ELSE
	     clk <= NOT sclk;
	  END IF;
  END IF;
  END PROCESS;

  --where is the active bit
  PROCESS(ss_n, clk)
  BEGIN
    IF(ss_n = '1' OR reset_n = '0') THEN                         
	   bit_counter <= (others => '0');
if cpha = '1' then
  bit_counter(0) <= '1';
else
  bit_counter(1) <= '1';
	end if; 
    ELSE                                                         
      IF(rising_edge(clk)) THEN                                  
        bit_counter <= bit_counter(16-1 DOWNTO 0) & '0';    --left shift active bit indicator
      END IF;
    END IF;
  END PROCESS;


  PROCESS(ss_n, clk, rx_enable, reset_n)
  BEGIN      
  
	 --receive mosi bit
    IF(cpha = '0') then
		 IF(reset_n = '0') THEN			--reset the buffer
			rxBuffer <= (OTHERS => '0');
		 ELSIF(bit_counter /= "00000000000000010" and falling_edge(clk)) THEN
			rxBuffer(16-1 DOWNTO 0) <= rxBuffer(16-2 DOWNTO 0) & mosi;  --shift in the received bit
		 END IF;
	 ELSE
		 IF(reset_n = '0') THEN       --reset the buffer
			rxBuffer <= (OTHERS => '0');
		 ELSIF(bit_counter /= "00000000000000001" and falling_edge(clk)) THEN
			rxBuffer(16-1 DOWNTO 0) <= rxBuffer(16-2 DOWNTO 0) & mosi;  --shift in the received bit
		 END IF;
	 END IF;

    --if user wants the received data output it
    IF(reset_n = '0') THEN
      rx <= (OTHERS => '0');
    ELSIF(ss_n = '1' AND rx_enable = '1') THEN  
      rx <= rxBuffer;
    END IF;

    --transmit registers
    IF(reset_n = '0') THEN
      txBuffer <= (OTHERS => '0');
    ELSIF(ss_n = '1') THEN  
      txBuffer <= tx;
    ELSIF(bit_counter(16) = '0' AND rising_edge(clk)) THEN
      txBuffer(16-1 DOWNTO 0) <= txBuffer(16-2 DOWNTO 0) & txBuffer(16-1);  --shift through tx data
    END IF;

    --transmit miso bit
    IF(ss_n = '1' OR reset_n = '0') THEN           
      miso <= 'Z';
    ELSIF(rising_edge(clk)) THEN
      miso <= txBuffer(16-1);               
    END IF;
    
  END PROCESS;
END behavioural;
*/
