// Digital circuit newDesign.dig as structural Verilog
module newDesign (
  input  [7:0] Input,
  input  rst_n,
  input  spiMiso,
  input  RX,
  input  clk_internal,
  input  in_14,
  input  in_15,
  input  in_20,
  output [3:0] debugOut,
  output spiClk,
  output spiMosi,
  output spiCSRam,
  output [7:0] Output,
  output TX,
  output spiCSProg,
  output [5:0] spiDeb,
  output busy,
  output done,
  output halt,
  output reset
);

  wire _1_addressable_register_1_dataout, abs, alu_1_carryout, alu_1_neg, alu_1_zero, and_1_out, and_2_out,
       and_3_out, and_4_out, and_5_out, and_6_out, and_8_out, and_9_out, and_10_out, and_11_out, and_12_out,
       and_13_out, comparator_1_eq, comparator_2_eq, comparator_3_eq, comparator_4_eq, comparator_5_gt,
       comparator_5_lt, comparator_6_gt, comparator_6_lt, counter_1_ovf, d_ff_q, Debug,
       demultiplexer_1_out_0, demultiplexer_1_out_1, Exevute, F_out, instDecode, instFetch, instRead, inter,
       interEn, interEnable, InterLock, intr, ioR, ioW, ld, multiplexer_6_out, multiplexer_8_out,
       multiplexer_9_out, multiplexer_10_out, muxA, or_1_out, or_2_out, or_3_out, or_4_out, or_5_out,
       or_6_out, or_7_out, R_out, read_the_flags, Reti, rst_n_t, sf, spi_busy_ram, st, store_the_flags, stPC,
       timer_Sel, u_pico_bus_if_rx_valid, u_pico_loader_ram_we, u_pico_loader_tx_valid,
       u_sim_pico_loader_pico_rd, u_sim_pico_loader_pico_reset_if, u_sim_pico_loader_pico_wr,
       u_spi_memory_interface_spi_clk, u_spi_memory_interface_spi_cs, u_spi_memory_interface_spi_cs_prog,
       u_spi_memory_interface_spi_mosi, uartblock_1_busy, V_out, WE, xor_1_out;
  wire [1:0] iem;
  wire [2:0] br, FlagOut, muxB, u_muxEncoder_q;
  wire [4:0] and_15_out;
  wire [5:0] aluOp;
  wire [6:0] multiplexer_3_out;
  wire [7:0] outputToOutsideEnable, u_pico_bus_if_pico_data_out, u_pico_bus_if_rx_byte,
       u_pico_loader_tx_byte, u_sim_pico_loader_pico_data_out;
  wire [15:0] AddrOut, CurrentOpcode, DataOut, din_bus, imreg_1_p5, inIntreg, inputReg_t, intEnD,
       interruptRegDat, iow_Din, multiplexer_1_out, multiplexer_4_out, multiplexer_7_out, multiplexer_11_out,
       multiplexer_12_out, multiplexer_14_out, multiplexer_15_out, multiplexer_16_out, outEn, outR, pgr_d,
       programAddr, programOpcode, register_1_q, register_2_q, registerblock_1_rdest, rngdat0,
       singextend_1__4d, singextend_1__4s, singextend_1__8sd, timerdat0, timerdat1, timerdat2,
       u_pico_loader_ram_addr, u_pico_loader_ram_din, u_programCounter_nextpc, u_sim_pico_loader_prog_addr,
       u_single_port_bram_16bit_dout_2, u_spi_memory_interface_data_out, uartDat0;
  wire [18:0] counter_1_out;

  _1_addressable_register intEn (
    .Datain(DataOut), .ioW(ioW), .addrIn(AddrOut), .address(16'h12), .clk(debugOut[3]), .ioR(ioR),
    .DataOut(interEnable), .Dataiow(intEnD));
  and and_1 (and_1_out, intr, interEnable);
  and and_2 (and_2_out, interEnable, Reti);
  programCounter #(.applicationType("IVERILOG"), .CodeFile("C:\\Users\\Berkant\\Desktop\\fpga\\RemedyCpu\\verilog\\programCounter.v")) u_programCounter (
    .AluIn(AddrOut), .clk(debugOut[3]), .rst(reset), .absJmp(abs), .intr(and_1_out), .reti(and_2_out),
    .relJmp(xor_1_out), .Nextpc(u_programCounter_nextpc), .PC(programAddr));
  pico_loader #(.applicationType("IVERILOG"), .CodeFile("D:\\Desktop\\fpga\\RemedyCpu\\verilog\\pico_loader.v")) u_pico_loader (
    .clk(debugOut[3]), .rst(u_sim_pico_loader_pico_reset_if), .rx_byte(u_pico_bus_if_rx_byte),
    .rx_valid(u_pico_bus_if_rx_valid), .ram_dout(u_single_port_bram_16bit_dout_2),
    .tx_byte(u_pico_loader_tx_byte), .tx_valid(u_pico_loader_tx_valid), .ram_we(u_pico_loader_ram_we),
    .ram_addr(u_pico_loader_ram_addr), .ram_din(u_pico_loader_ram_din), .cpu_halt(halt), .cpu_reset(reset));
  not not_1 (rst_n_t, reset);
  Button #(.activeLow("true")) V (.out(V_out));
  or or_1 (or_1_out, reset, V_out);
  and and_3 (and_3_out, clk_internal, or_1_out);
  pico_bus_if #(.applicationType("IVERILOG"), .CodeFile("D:\\Desktop\\fpga\\RemedyCpu\\verilog\\pico_bus_if_var.v")) u_pico_bus_if (
    .clk(debugOut[3]), .rst(u_sim_pico_loader_pico_reset_if), .pico_data_in(u_sim_pico_loader_pico_data_out),
    .pico_wr(u_sim_pico_loader_pico_wr), .pico_rd(u_sim_pico_loader_pico_rd),
    .tx_byte(u_pico_loader_tx_byte), .tx_valid(u_pico_loader_tx_valid), .rx_byte(u_pico_bus_if_rx_byte),
    .rx_valid(u_pico_bus_if_rx_valid), .pico_data_out(u_pico_bus_if_pico_data_out));
  Button F (.out(F_out));
  Multiplexer #(.Bits(16)) multiplexer_1 (
    .sel(halt), .in_0(programAddr), .in_1(u_pico_loader_ram_addr), .out(multiplexer_1_out));
  or or_2 (or_2_out, and_3_out, F_out);
  DipSwitch u_Debug (.out(Debug));
  Counter #(.Bits(19)) counter_1 (
    .en(1'b1), .C(or_2_out), .clr(counter_1_ovf), .out(counter_1_out), .ovf(counter_1_ovf));
  RAMDualPort #(.AddrBits(16), .Bits(16)) ramdualport_1 (
    .A(multiplexer_1_out), .Din(u_pico_loader_ram_din), .str(u_pico_loader_ram_we), .C(debugOut[3]),
    .ld(in_20));  // open: D
  single_port_bram_16bit #(.applicationType("IVERILOG"), .CodeFile("D:\\Desktop\\fpga\\RemedyCpu\\verilog\\ram_2.v")) u_single_port_bram_16bit (
    .clk(debugOut[3]), .we_1(st), .rld_1(ld), .addr_1(AddrOut), .din_1(DataOut), .we_2(u_pico_loader_ram_we),
    .rld_2(1'b1), .addr_2(multiplexer_1_out), .din_2(u_pico_loader_ram_din), .dout_1(din_bus),
    .dout_2(u_single_port_bram_16bit_dout_2));
  Multiplexer multiplexer_2 (.sel(Debug), .in_0(or_2_out), .in_1(or_2_out), .out(debugOut[3]));
  sim_pico_loader #(.applicationType("IVERILOG"), .CodeFile("D:\\Desktop\\fpga\\RemedyCpu\\verilog\\pico_sim.v")) u_sim_pico_loader (
    .clk(debugOut[3]), .rst(R_out), .start(in_14), .prog_data(pgr_d),
    .pico_data_in(u_pico_bus_if_pico_data_out), .pico_ready(in_15), .busy(busy), .done(done),
    .prog_addr(u_sim_pico_loader_prog_addr), .pico_data_out(u_sim_pico_loader_pico_data_out),
    .pico_wr(u_sim_pico_loader_pico_wr), .pico_rd(u_sim_pico_loader_pico_rd),
    .pico_reset_if(u_sim_pico_loader_pico_reset_if));
  ClockCont #(.applicationType("IVERILOG"), .CodeFile("D:\\Desktop\\fpga\\RemedyCpu\\verilog\\clockController.v")) u_ClockCont (
    .Clk(debugOut[3]), .Enable(spi_busy_ram), .rst(reset), .instRead(instRead), .instFetch(instFetch),
    .instDecode(instDecode), .instExecute(Exevute));
  Button R (.out(R_out));
  Multiplexer #(.Bits(7)) multiplexer_3 (
    .sel(CurrentOpcode[15]), .in_0(CurrentOpcode[14:8]), .in_1({7{1'b0}}), .out(multiplexer_3_out));
  ROM #(.bigEndian("true"), .AddrBits(16), .isProgramMemory("true"), .Bits(16)) pgr (
    .A(u_sim_pico_loader_prog_addr), .sel(1'b1), .D(pgr_d));
  controllogic controllogic_1 (
    .A(multiplexer_3_out[6]), .B(multiplexer_3_out[5]), .C(multiplexer_3_out[4]), .D(multiplexer_3_out[3]),
    .E(multiplexer_3_out[2]), .F(multiplexer_3_out[1]), .G(multiplexer_3_out[0]), .muxb0(muxB[2]),
    .muxb1(muxB[1]), .muxb2(muxB[0]), .aluop0(aluOp[5]), .aluop1(aluOp[4]), .aluop2(aluOp[3]),
    .aluop3(aluOp[2]), .aluop4(aluOp[1]), .aluop5(aluOp[0]), .WE(WE), .sf(sf), .iem0(iem[1]), .iem1(iem[0]),
    .br0(br[2]), .br1(br[1]), .br2(br[0]), .muxA(muxA), .ld(ld), .st(st), .abs(abs), .ioW(ioW), .ioR(ioR),
    .stPC(stPC), .Reti(Reti), .timerSel(timer_Sel), .read_flags(read_the_flags), .storeFlagI(store_the_flags));  // open: randomSel
  not not_2 (spiCSProg, demultiplexer_1_out_1);
  not not_3 (spiCSRam, demultiplexer_1_out_0);
  Demultiplexer demultiplexer_1 (
    .sel(instRead), .in(spi_busy_ram), .out_0(demultiplexer_1_out_0), .out_1(demultiplexer_1_out_1));
  Multiplexer #(.Selector_Bits(3), .Bits(16)) multiplexer_4 (
    .sel(u_muxEncoder_q), .in_0(AddrOut), .in_1(din_bus), .in_2(iow_Din), .in_3(u_programCounter_nextpc),
    .in_4({16{1'b0}}), .in_5({16{1'b0}}), .in_6({{13{1'b0}}, FlagOut}), .in_7({16{1'b0}}),
    .out(multiplexer_4_out));
  muxEncoder #(.applicationType("IVERILOG"), .CodeFile("D:\\Desktop\\fpga\\RemedyCpu\\verilog\\multipleToMux.v")) u_muxEncoder (
    .a(1'b0), .b(ld), .c(ioR), .d(stPC), .e(1'b0), .f(1'b0), .g(read_the_flags), .h(1'b0), .Q(u_muxEncoder_q));
  xor xor_1 (xor_1_out, multiplexer_6_out, br[2]);
  Multiplexer #(.Bits(16)) multiplexer_5 (
    .sel(rst_n_t), .in_0({16{1'b0}}), .in_1(u_single_port_bram_16bit_dout_2), .out(CurrentOpcode));
  Multiplexer #(.Selector_Bits(2)) multiplexer_6 (
    .sel(br[1:0]), .in_0(1'b0), .in_1(FlagOut[0]), .in_2(FlagOut[1]), .in_3(FlagOut[2]),
    .out(multiplexer_6_out));
  Multiplexer #(.Bits(16)) multiplexer_7 (
    .sel(instRead), .in_0({AddrOut[14:0], 1'b0}), .in_1({programAddr[14:0], 1'b0}), .out(multiplexer_7_out));
  register_1bit NegR (.D(multiplexer_8_out), .C(debugOut[3]), .en(sf), .rst(reset), .Q(FlagOut[2]));
  register_1bit ZeroR (.D(multiplexer_9_out), .C(debugOut[3]), .en(sf), .rst(reset), .Q(FlagOut[1]));
  register_1bit CarryR (.D(multiplexer_10_out), .C(debugOut[3]), .en(sf), .rst(reset), .Q(FlagOut[0]));
  RegisterBlock registerblock_1 (
    .DataIn(multiplexer_4_out), .WE(WE), .clk(debugOut[3]), .src(CurrentOpcode[3:0]),
    .Dest(CurrentOpcode[7:4]), .rst(reset), .RDest(registerblock_1_rdest), .Rsrc(DataOut));
  // ImReg imreg_1: pin names not known; wires that end beside it: CurrentOpcode[15], iem, debugOut[3], CurrentOpcode, imreg_1_p5
  singExtend singextend_1 (
    .inst(CurrentOpcode), ._4S(singextend_1__4s), ._8SD(singextend_1__8sd), ._4D(singextend_1__4d));
  and and_4 (and_4_out, InterLock, ~Reti);  // And
  and and_5 (and_5_out, d_ff_q, ~Reti);  // And
  and and_6 (and_6_out, inter, interEnable);
  or or_3 (or_3_out, and_4_out, intr);
  or or_4 (or_4_out, and_5_out, and_6_out);
  Multiplexer multiplexer_8 (.sel(store_the_flags), .in_0(alu_1_neg), .in_1(AddrOut[2]), .out(multiplexer_8_out));
  Multiplexer multiplexer_9 (.sel(store_the_flags), .in_0(alu_1_zero), .in_1(AddrOut[1]), .out(multiplexer_9_out));
  Multiplexer multiplexer_10 (
    .sel(store_the_flags), .in_0(alu_1_carryout), .in_1(AddrOut[0]), .out(multiplexer_10_out));
  spi_memory_interface #(.applicationType("IVERILOG"), .CodeFile("D:\\Desktop\\fpga\\RemedyCpu\\verilog\\spi.v")) u_spi_memory_interface (
    .clk(debugOut[3]), .spi_rst(reset), .st(st), .ld(st), .addr(multiplexer_7_out), .data_in(DataOut),
    .mem_sel(instRead), .spi_miso(spiMiso), .data_out(u_spi_memory_interface_data_out),
    .spi_cs(u_spi_memory_interface_spi_cs), .spi_cs_prog(u_spi_memory_interface_spi_cs_prog),
    .spi_clk(u_spi_memory_interface_spi_clk), .busy(spi_busy_ram), .spi_mosi(u_spi_memory_interface_spi_mosi));  // open: stateDeb
  D_FF d_ff (.D(or_4_out), .C(~debugOut[3]), .Q(d_ff_q));  // open: nQ
  Multiplexer #(.Bits(16)) multiplexer_11 (
    .sel(muxA), .in_0(registerblock_1_rdest), .in_1(DataOut), .out(multiplexer_11_out));
  D_FF d_ff_2 (.D(or_3_out), .C(~debugOut[3]), .Q(InterLock));  // open: nQ
  Multiplexer #(.Selector_Bits(3), .Bits(16)) multiplexer_12 (
    .sel(muxB), .in_0(DataOut), .in_1({16{1'b0}}), .in_2(imreg_1_p5), .in_3({16{1'b0}}), .in_4({16{1'b0}}),
    .in_5(singextend_1__4s), .in_6(singextend_1__8sd), .in_7(singextend_1__4d), .out(multiplexer_12_out));
  assign spiClk = spi_busy_ram ? u_spi_memory_interface_spi_clk : 1'bz;  // Driver driver_1
  assign spiDeb[2] = spi_busy_ram ? u_spi_memory_interface_spi_mosi : 1'bz;  // Driver driver_2
  and and_7 (intr, ~InterLock, ~CurrentOpcode[15], d_ff_q, ~1'b0);  // And
  Demultiplexer #(.Bits(16)) demultiplexer_2 (
    .sel(instRead), .in(u_spi_memory_interface_data_out), .out_0(programOpcode));  // open: out_1
  RAMDualPort #(.AddrBits(16), .Bits(16)) ramdualport_2 (
    .A(AddrOut), .Din(DataOut), .str(st), .C(debugOut[3]), .ld(ld));  // open: D
  Alu alu_1 (
    .A(multiplexer_11_out), .B(multiplexer_12_out), .carryIn(FlagOut[0]), .AluOp(aluOp), .Out(AddrOut),
    .Neg(alu_1_neg), .Zero(alu_1_zero), .CarryOut(alu_1_carryout));
  Multiplexer #(.Selector_Bits(5), .Bits(16)) multiplexer_13 (
    .sel(AddrOut[4:0]), .in_0({16{1'b0}}), .in_1(timerdat0), .in_2(timerdat0), .in_3(timerdat0),
    .in_4(timerdat0), .in_5(timerdat1), .in_6(timerdat1), .in_7(timerdat1), .in_8(timerdat1),
    .in_9(timerdat2), .in_10(timerdat2), .in_11(timerdat2), .in_12(timerdat2), .in_13(rngdat0),
    .in_14(rngdat0), .in_15(outR), .in_16(outEn), .in_17(inputReg_t), .in_18(intEnD), .in_19(inIntreg),
    .in_20(interruptRegDat), .in_21(uartDat0), .in_22(uartDat0), .in_23(uartDat0), .in_24({16{1'b0}}),
    .in_25({16{1'b0}}), .in_26({16{1'b0}}), .in_27({16{1'b0}}), .in_28({16{1'b0}}), .in_29({16{1'b0}}),
    .in_30({16{1'b0}}), .in_31({16{1'b0}}), .out(iow_Din));
  lfsr_RandomNumberGen lfsr_randomnumbergen_1 (
    .adrrIn(AddrOut), .dataIn(DataOut), .ioW(ioW), .clk(debugOut[3]), .ioR(ioR), .SeedAdr(16'hd),
    .RngAdr(16'he), .Out(rngdat0));
  UartBlock uartblock_1 (
    .rst(reset), .clk(debugOut[3]), .iow(ioW), .datain(DataOut), .ior(ioR), .addr(AddrOut),
    .interbusy(InterLock), .Rx(RX), .uartRegAdr(16'h16), .configRegAdr(16'h17), .statusRegAdr(16'h15),
    .tx(TX), .busy(uartblock_1_busy), .interrupt(and_15_out[4]), .dataout(uartDat0));
  Comparator #(.Signed("true"), .Bits(16)) comparator_1 (
    .a(AddrOut), .b(16'h10), .eq(comparator_1_eq));  // open: gt, lt
  timer timer0 (
    .dOut(DataOut), .Addr(AddrOut), .ioW(ioW), .ioR(ioR), .C(debugOut[3]), .InterLock(InterLock),
    .timerConfigAddr(16'h1), .timerTargetAddr(16'h2), .timerResetAddr(16'h3), .timerReadAddr(16'h4),
    .rst(reset), .TimerOut(timerdat0), .\timerİnterrupt (and_15_out[0]));
  timer timer1 (
    .dOut(DataOut), .Addr(AddrOut), .ioW(ioW), .ioR(ioR), .C(debugOut[3]), .InterLock(InterLock),
    .timerConfigAddr(16'h5), .timerTargetAddr(16'h6), .timerResetAddr(16'h7), .timerReadAddr(16'h8),
    .rst(reset), .TimerOut(timerdat1), .\timerİnterrupt (and_15_out[1]));
  timer timer2 (
    .dOut(DataOut), .Addr(AddrOut), .ioW(ioW), .ioR(ioR), .C(debugOut[3]), .InterLock(InterLock),
    .timerConfigAddr(16'h9), .timerTargetAddr(16'ha), .timerResetAddr(16'hb), .timerReadAddr(16'hc),
    .rst(reset), .TimerOut(timerdat2), .\timerİnterrupt (and_15_out[2]));
  Comparator #(.Signed("true"), .Bits(16)) comparator_2 (.a(AddrOut), .b(16'hf), .eq(comparator_2_eq));  // open: gt, lt
  Comparator #(.Signed("true"), .Bits(16)) comparator_3 (
    .a(AddrOut), .b(16'h11), .eq(comparator_3_eq));  // open: gt, lt
  and and_8 (and_8_out, comparator_1_eq, ioW);
  and and_9 (and_9_out, comparator_2_eq, ioW);
  and and_10 (and_10_out, comparator_3_eq, ioR);
  _1_addressable_register _1_addressable_register_1 (
    .Datain(DataOut), .ioW(ioW), .addrIn(AddrOut), .address(16'h13), .clk(debugOut[3]), .ioR(ioR),
    .DataOut(_1_addressable_register_1_dataout), .Dataiow(inIntreg));
  Comparator #(.Bits(16)) comparator_4 (.a(16'h14), .b(AddrOut), .eq(comparator_4_eq));  // open: gt, lt
  and and_11 (and_11_out, ioR, comparator_1_eq);
  register_8bit outputReg (.D(DataOut[7:0]), .C(debugOut[3]), .en(and_8_out), .rst(reset), .Q(outputToOutsideEnable));
  and and_12 (and_12_out, ioR, comparator_2_eq);
  Multiplexer #(.Bits(16)) multiplexer_14 (
    .sel(InterLock), .in_0({{8{1'b0}}, Input}), .in_1(register_1_q), .out(multiplexer_14_out));
  Register #(.Bits(16)) register_1 (.D(multiplexer_14_out), .C(debugOut[3]), .en(or_5_out), .Q(register_1_q));
  register_8bit OutoutEnReg (.D(DataOut[7:0]), .C(debugOut[3]), .en(and_9_out), .rst(reset), .Q(Output));
  Comparator #(.Bits(16)) comparator_5 (
    .a(multiplexer_14_out), .b(register_1_q), .gt(comparator_5_gt), .lt(comparator_5_lt));  // open: eq
  assign outEn = and_12_out ? {{8{1'b1}}, Output} : 16'bz;  // Driver driver_3
  or or_5 (or_5_out, comparator_5_gt, comparator_5_lt);
  and and_13 (and_13_out, ioW, comparator_4_eq);
  and and_14 (interEn, comparator_4_eq, ioR);
  assign outR = and_11_out ? {{8{1'b1}}, outputToOutsideEnable} : 16'bz;  // Driver driver_4
  and and_15 (and_15_out[3], or_5_out, _1_addressable_register_1_dataout);
  Multiplexer #(.Bits(16)) multiplexer_15 (
    .sel(and_13_out), .in_0({{11{1'b0}}, and_15_out}), .in_1(DataOut), .out(multiplexer_15_out));
  Register #(.Bits(16)) register_2 (.D(multiplexer_15_out), .C(debugOut[3]), .en(or_6_out), .Q(register_2_q));
  Multiplexer #(.Bits(16)) multiplexer_16 (
    .sel(_1_addressable_register_1_dataout), .in_0({{8{1'b0}}, Input}), .in_1(register_1_q),
    .out(multiplexer_16_out));
  assign inputReg_t = and_10_out ? multiplexer_16_out : 16'bz;  // Driver driver_5
  Comparator #(.Bits(16)) comparator_6 (
    .a(multiplexer_15_out), .b(register_2_q), .gt(comparator_6_gt), .lt(comparator_6_lt));  // open: eq
  assign interruptRegDat = interEn ? register_2_q : 16'bz;  // Driver driver_6
  or or_6 (or_6_out, comparator_6_gt, comparator_6_lt);
  and and_16 (inter, ~InterLock, or_7_out);  // And
  or or_7 (or_7_out, 1'b0, 1'b0, 1'b0, 1'b0, 1'b0, 1'b0, 1'b0, 1'b0, 1'b0, 1'b0, 1'b0, and_15_out[4], and_15_out[3], and_15_out[2], and_15_out[1], and_15_out[0]);

  assign debugOut[2:0] = {3{debugOut[3]}};
  assign {spiDeb[5:3], spiDeb[1:0]} = {spiCSRam, spiCSProg, spiClk, spiMiso, debugOut[3]};
  assign spiMosi = spiDeb[2];

  // Other names for the same wires on the sheet: OPcode[7:0] = CurrentOpcode[15:8]; imm = CurrentOpcode[15];
  //   inputFromOutside[7:0] = Input; outputToOutside[7:0] = Output; Clk_in = debugOut[3]; pcClock = debugOut[3];
  //   PeripheralClk_in = debugOut[3]; cpu_rst = reset; rst = reset; spi_clock_ram = spiClk; spi_miso = spiMiso;
  //   spi_mosi_ram = spiDeb[2]

  // Notes on the sheet:
  //   rst_n: default 1
  //   clk_internal: Hz: 80
  //   in_14: default 1
  //   in_15: default 1
  //   Input/Output
  //   ControlLogic
  //   MainClockController
  //   pgr loads testCompiler.bin
  //   JumpLogic
  //   FlagStore
  //   ProgramMemoryRead
  //   interrupt Logic
  //   PERIPHERAL ADDRESSES
  //   IO Addresses
  //   Write/Read Addresses
  //   RandomNumberGen
  //   PERIPHERAL BUS
  //   Timers
  //   Output
  //   Output_En
  //   input
  //   InterruptRegister
  //   InterruptBus
  //   INTERRRRRUPT BUS
endmodule
