// Digital circuit newSpi.dig as structural Verilog
module newSpi (
  input  [7:0] Input,
  input  rst_n,
  input  spiMiso,
  input  RX,
  input  clk_internal,
  output [3:0] debugOut,
  output spiClk,
  output spiMosi,
  output spiCSRam,
  output [7:0] Output,
  output TX,
  output spiCSProg
);

  wire _1_addressable_register_1_dataout, abs, add_1_c_o, and_1_out, and_2_out, and_3_out, and_5_out,
       and_6_out, and_7_out, and_8_out, and_9_out, and_10_out, and_11_out, and_12_out, and_13_out,
       and_17_out, and_18_out, and_22_out, comparator_1_eq, comparator_2_eq, comparator_3_eq,
       comparator_4_eq, comparator_5_eq, comparator_6_gt, comparator_6_lt, comparator_7_eq, comparator_8_eq,
       comparator_9_gt, comparator_9_lt, d_ff_as_1_nq, d_ff_as_1_q, d_ff_q, demultiplexer_1_out_0,
       demultiplexer_1_out_1, dipswitch_1_out, firstLoad_q, inputEn, inter, interEn, interEnable, InterLock,
       intr, ioR, ioW, jk_ff_2_q, ld, multiplexer_7_out, multiplexer_9_out, multiplexer_10_out,
       multiplexer_11_out, multiplexer_15_out, muxA, nor_1_out, nor_2_out, not_4_out, not_5_out, or_1_out,
       or_2_out, or_3_out, or_8_out, or_9_out, or_10_out, or_12_out, or_16_out, or_17_out, programClk,
       programRead, RandomNUMSel, read_the_flags, Reti, rst, sf, spi_busy_ram, SpiRam_spi_clk,
       SpiRam_spi_mosi, st, store_the_flags, stPC, sub_1_c_o, SysClock, timer0En, timer1En, timer2En, WE,
       xor_1_out, xor_2_out, xor_3_out, xor_5_out;
  wire [1:0] iem;
  wire [2:0] br, counter_1_out, FlagOut, muxB, or_7_out, or_13_out;
  wire [3:0] and_21_out;
  wire [4:0] aluOp;
  wire [6:0] multiplexer_2_out;
  wire [7:0] outputToOutsideEnable;
  wire [15:0] add_1_s, AddrOut, and_16_out, CurrentOpcode, DataOut, din_bus, divs_1_bolum, divs_1_kalan,
       imreg_1_p5, inputReg, interruptReg, iow_Din, mul_1_mul, multiplexer_1_out, multiplexer_3_out,
       multiplexer_5_out, multiplexer_8_out, multiplexer_12_out, multiplexer_13_out, multiplexer_17_out,
       multiplexer_18_out, multiplexer_19_out, neg_2_out, not_6_out, or_11_out, pgr_d, programAddr,
       programOpcode, RandomNUM, register_1_q, register_2_q, registerblock_1_rdest, seed_q, singextend_1__4d,
       singextend_1__4s, singextend_1__8sd, SpiRam_data_out, sub_1_s, time0In, time1In, time2In,
       u_programCounter_nextpc, xor_4_out;
  wire [15:15] and_15_out;
  wire [31:16] mul_1_mul_2;

  not not_1 (rst, rst_n);
  _1_addressable_register intEn (
    .Datain(DataOut), .ioW(ioW), .addrIn(AddrOut), .address(16'ha), .clk(clk_internal), .DataOut(interEnable));
  not not_2 (spiCSProg, demultiplexer_1_out_1);
  not not_3 (spiCSRam, demultiplexer_1_out_0);
  Demultiplexer demultiplexer_1 (
    .sel(programRead), .in(spi_busy_ram), .out_0(demultiplexer_1_out_0), .out_1(demultiplexer_1_out_1));
  and and_1 (and_1_out, intr, interEnable);
  and and_2 (and_2_out, interEnable, Reti);
  Multiplexer #(.Bits(16)) multiplexer_1 (
    .sel(programRead), .in_0({AddrOut[14:0], 1'b0}), .in_1({programAddr[14:0], 1'b0}), .out(multiplexer_1_out));
  or or_1 (or_1_out, st, st);
  or or_2 (or_2_out, ld, programRead);
  and and_3 (and_3_out, ~spi_busy_ram, firstLoad_q, clk_internal);  // And
  Register firstLoad (.D(spi_busy_ram), .C(clk_internal), .en(not_4_out), .Q(firstLoad_q));
  not not_4 (not_4_out, firstLoad_q);
  nor nor_1 (nor_1_out, or_1_out, or_2_out);
  programCounter #(.applicationType("IVERILOG"), .CodeFile("C:\\Users\\Berkant\\Desktop\\fpga\\RemedyCpu\\verilog\\programCounter.v")) u_programCounter (
    .AluIn(AddrOut), .clk(debugOut[3]), .rst(rst), .absJmp(abs), .intr(and_1_out), .reti(and_2_out),
    .relJmp(xor_1_out), .Nextpc(u_programCounter_nextpc), .PC(programAddr));
  Multiplexer #(.Bits(7)) multiplexer_2 (
    .sel(CurrentOpcode[15]), .in_0(CurrentOpcode[14:8]), .in_1({7{1'b0}}), .out(multiplexer_2_out));
  or or_3 (or_3_out, rst, nor_1_out);
  // controllogic controllogic_1: pin names not known; wires that end beside it: multiplexer_2_out[6], multiplexer_2_out[5], multiplexer_2_out[4], multiplexer_2_out[3], multiplexer_2_out[2], multiplexer_2_out[1], multiplexer_2_out[0], muxB[2], muxB[1], muxB[0], aluOp[4], aluOp[3], aluOp[2], aluOp[1], aluOp[0], WE, sf, iem[1], iem[0], br[2], br[1], br[0], muxA, ld, st, abs, ioW, ioR, stPC, Reti, RandomNUMSel
  spiden SpiRam (
    .spi_miso(spiMiso), .Address(multiplexer_1_out), .clk(clk_internal), .st(or_1_out), .DataIn(DataOut),
    .ld(or_2_out), .spi_rst(or_3_out), .spi_clk(SpiRam_spi_clk), .spi_mosi(SpiRam_spi_mosi),
    .Busy(spi_busy_ram), .data_out(SpiRam_data_out));
  JK_FF jk_ff_1 (.J(SysClock), .C(and_3_out), .K(SysClock), .Q(programClk));  // open: nQ
  Counter #(.Bits(3)) counter_1 (.en(1'b1), .C(and_3_out), .clr(and_10_out), .out(counter_1_out));  // open: ovf
  assign spiClk = spi_busy_ram ? SpiRam_spi_clk : 1'bz;  // Driver driver_1
  ROM #(.AddrBits(16), .isProgramMemory("true"), .Bits(16)) pgr (.A(programAddr), .sel(1'b1), .D(pgr_d));
  assign spiMosi = spi_busy_ram ? SpiRam_spi_mosi : 1'bz;  // Driver driver_2
  Demultiplexer #(.Bits(16)) demultiplexer_2 (
    .sel(nor_2_out), .in(SpiRam_data_out), .out_0(din_bus), .out_1(programOpcode));
  nor nor_2 (nor_2_out, st, ld);
  and and_4 (programRead, ~counter_1_out[2], ~counter_1_out[1], ~counter_1_out[0]);  // And
  Comparator #(.Signed("true"), .Bits(16)) comparator_1 (.a(AddrOut), .b(16'hd), .eq(comparator_1_eq));  // open: gt, lt
  or or_4 (or_7_out[2], 1'b0, RandomNUMSel, read_the_flags);
  Multiplexer #(.Selector_Bits(3), .Bits(16)) multiplexer_3 (
    .sel(or_7_out), .in_0(AddrOut), .in_1(din_bus), .in_2(iow_Din), .in_3(u_programCounter_nextpc),
    .in_4({16{1'b0}}), .in_5(RandomNUM), .in_6({{13{1'b0}}, FlagOut}), .in_7({16{1'b0}}),
    .out(multiplexer_3_out));
  or or_5 (or_7_out[1], ioR, stPC, read_the_flags);
  Multiplexer multiplexer_4 (.sel(dipswitch_1_out), .in_0(programClk), .in_1(clk_internal), .out(debugOut[3]));
  DipSwitch dipswitch_1 (.out(dipswitch_1_out));
  and and_5 (and_5_out, ~counter_1_out[2], counter_1_out[1], ~counter_1_out[0]);  // And
  or or_6 (SysClock, and_7_out, and_5_out);
  and and_6 (and_6_out, comparator_1_eq, ioW);
  Multiplexer #(.Bits(16)) multiplexer_5 (
    .sel(dipswitch_1_out), .in_0(programOpcode), .in_1(pgr_d), .out(multiplexer_5_out));
  and and_7 (and_7_out, ~counter_1_out[2], counter_1_out[1], counter_1_out[0]);  // And
  or or_7 (or_7_out[0], ld, stPC, RandomNUMSel);
  and and_8 (and_8_out, and_6_out, not_5_out);
  not not_5 (not_5_out, or_8_out);
  and and_9 (and_9_out, clk_internal, and_6_out);
  Multiplexer #(.Bits(16)) multiplexer_6 (
    .sel(SysClock), .in_0({16{1'b0}}), .in_1(multiplexer_5_out), .out(CurrentOpcode));
  xor xor_1 (xor_1_out, multiplexer_7_out, br[2]);
  and and_10 (and_10_out, counter_1_out[2], ~counter_1_out[1], ~counter_1_out[0]);  // And
  JK_FF jk_ff_2 (.J(or_8_out), .C(clk_internal), .K(or_8_out), .Q(jk_ff_2_q));  // open: nQ
  Multiplexer #(.Selector_Bits(2)) multiplexer_7 (
    .sel(br[1:0]), .in_0(1'b0), .in_1(FlagOut[0]), .in_2(FlagOut[1]), .in_3(FlagOut[2]),
    .out(multiplexer_7_out));
  D_FF_AS d_ff_as_1 (.Set(1'b0), .D(d_ff_as_1_nq), .C(and_9_out), .Clr(jk_ff_2_q), .Q(d_ff_as_1_q), .nQ(d_ff_as_1_nq));
  Register #(.Bits(16)) seed (.D(DataOut), .C(clk_internal), .en(and_6_out), .Q(seed_q));
  or or_8 (or_8_out, d_ff_as_1_q, jk_ff_2_q);
  Multiplexer #(.Bits(16)) multiplexer_8 (.sel(and_6_out), .in_0({16{1'b0}}), .in_1(seed_q), .out(multiplexer_8_out));
  register_1bit Neg (.D(multiplexer_11_out), .C(clk_internal), .en(sf), .rst(rst), .Q(FlagOut[2]));
  register_1bit Zero (.D(multiplexer_10_out), .C(clk_internal), .en(sf), .rst(rst), .Q(FlagOut[1]));
  register_1bit Carry (.D(multiplexer_9_out), .C(clk_internal), .en(sf), .rst(rst), .Q(FlagOut[0]));
  // Probe on RandomNUM
  RegisterBlock registerblock_1 (
    .DataIn(multiplexer_3_out), .WE(WE), .clk(debugOut[3]), .src(CurrentOpcode[3:0]),
    .Dest(CurrentOpcode[7:4]), .rst(rst), .RDest(registerblock_1_rdest), .Rsrc(DataOut));
  // ImReg imreg_1: pin names not known; wires that end beside it: CurrentOpcode[15], iem, debugOut[3], CurrentOpcode, imreg_1_p5
  singExtend singextend_1 (
    .inst(CurrentOpcode), ._4S(singextend_1__4s), ._8SD(singextend_1__8sd), ._4D(singextend_1__4d));
  and and_11 (and_11_out, d_ff_q, ~Reti);  // And
  and and_12 (and_12_out, inter, interEnable);
  Multiplexer multiplexer_9 (
    .sel(store_the_flags), .in_0(multiplexer_15_out), .in_1(multiplexer_12_out[4]), .out(multiplexer_9_out));
  Multiplexer multiplexer_10 (
    .sel(store_the_flags), .in_0(comparator_2_eq), .in_1(multiplexer_12_out[5]), .out(multiplexer_10_out));
  D_FF_AS d_ff_as_2 (
    .Set(multiplexer_8_out[0]), .D(xor_2_out), .C(clk_internal), .Clr(and_8_out), .Q(RandomNUM[0]));  // open: nQ
  and and_13 (and_13_out, InterLock, ~Reti);  // And
  Multiplexer multiplexer_11 (
    .sel(store_the_flags), .in_0(AddrOut[15]), .in_1(multiplexer_12_out[6]), .out(multiplexer_11_out));
  or or_9 (or_9_out, and_13_out, intr);
  or or_10 (or_10_out, and_11_out, and_12_out);
  D_FF_AS d_ff_as_3 (
    .Set(multiplexer_8_out[1]), .D(RandomNUM[0]), .C(clk_internal), .Clr(and_8_out), .Q(RandomNUM[1]));  // open: nQ
  D_FF d_ff (.D(or_10_out), .C(~clk_internal), .Q(d_ff_q));  // open: nQ
  Multiplexer #(.Bits(16)) multiplexer_12 (
    .sel(muxA), .in_0(registerblock_1_rdest), .in_1(DataOut),
    .out({multiplexer_12_out[11:8], multiplexer_12_out[15:12], multiplexer_12_out[3:0], multiplexer_12_out[7:4]}));
  Multiplexer #(.Selector_Bits(3), .Bits(16)) multiplexer_13 (
    .sel(muxB), .in_0(DataOut), .in_1({16{1'b0}}), .in_2(imreg_1_p5), .in_3({16{1'b0}}), .in_4({16{1'b0}}),
    .in_5(singextend_1__4s), .in_6(singextend_1__8sd), .in_7(singextend_1__4d), .out(multiplexer_13_out));
  D_FF_AS d_ff_as_4 (
    .Set(multiplexer_8_out[2]), .D(RandomNUM[1]), .C(clk_internal), .Clr(and_8_out), .Q(RandomNUM[2]));  // open: nQ
  D_FF d_ff_2 (.D(or_9_out), .C(~clk_internal), .Q(InterLock));  // open: nQ
  D_FF_AS d_ff_as_5 (
    .Set(multiplexer_8_out[3]), .D(RandomNUM[2]), .C(clk_internal), .Clr(and_8_out), .Q(RandomNUM[3]));  // open: nQ
  D_FF_AS d_ff_as_6 (
    .Set(multiplexer_8_out[4]), .D(RandomNUM[3]), .C(clk_internal), .Clr(and_8_out), .Q(RandomNUM[4]));  // open: nQ
  and and_14 (intr, ~InterLock, ~CurrentOpcode[15], d_ff_q, ~1'b0);  // And
  xor xor_2 (xor_2_out, RandomNUM[5], xor_3_out);
  D_FF_AS d_ff_as_7 (
    .Set(multiplexer_8_out[5]), .D(RandomNUM[4]), .C(clk_internal), .Clr(and_8_out), .Q(RandomNUM[5]));  // open: nQ
  D_FF_AS d_ff_as_8 (
    .Set(multiplexer_8_out[6]), .D(RandomNUM[5]), .C(clk_internal), .Clr(and_8_out), .Q(RandomNUM[6]));  // open: nQ
  and and_15 (and_15_out[15], aluOp[4], FlagOut[0]);
  D_FF_AS d_ff_as_9 (
    .Set(multiplexer_8_out[7]), .D(RandomNUM[6]), .C(clk_internal), .Clr(and_8_out), .Q(RandomNUM[7]));  // open: nQ
  D_FF_AS d_ff_as_10 (
    .Set(multiplexer_8_out[8]), .D(RandomNUM[7]), .C(clk_internal), .Clr(and_8_out), .Q(RandomNUM[8]));  // open: nQ
  Mul #(.Bits(16)) mul_1 (
    .a({multiplexer_12_out[11:8], multiplexer_12_out[15:12], multiplexer_12_out[3:0], multiplexer_12_out[7:4]}),
    .b(multiplexer_13_out), .mul({mul_1_mul_2, mul_1_mul}));
  divs divs_1 (
    .bolunen({multiplexer_12_out[11:8], multiplexer_12_out[15:12], multiplexer_12_out[3:0], multiplexer_12_out[7:4]}),
    .Bolen(multiplexer_13_out), .bolum(divs_1_bolum), .Kalan(divs_1_kalan));
  xor xor_3 (xor_3_out, RandomNUM[10], xor_5_out);
  D_FF_AS d_ff_as_11 (
    .Set(multiplexer_8_out[9]), .D(RandomNUM[8]), .C(clk_internal), .Clr(and_8_out), .Q(RandomNUM[9]));  // open: nQ
  Add #(.Bits(16)) add_1 (
    .a({multiplexer_12_out[11:8], multiplexer_12_out[15:12], multiplexer_12_out[3:0], multiplexer_12_out[7:4]}),
    .b(multiplexer_13_out), .c_i(and_15_out[15]), .s(add_1_s), .c_o(add_1_c_o));
  Sub #(.Bits(16)) sub_1 (
    .a({multiplexer_12_out[11:8], multiplexer_12_out[15:12], multiplexer_12_out[3:0], multiplexer_12_out[7:4]}),
    .b(multiplexer_13_out), .c_i(and_15_out[15]), .s(sub_1_s), .c_o(sub_1_c_o));
  assign and_16_out = {multiplexer_12_out[11:8], multiplexer_12_out[15:12], multiplexer_12_out[3:0], multiplexer_12_out[7:4]} & multiplexer_13_out;  // And and_16, 16 bits wide
  assign or_11_out = {multiplexer_12_out[11:8], multiplexer_12_out[15:12], multiplexer_12_out[3:0], multiplexer_12_out[7:4]} | multiplexer_13_out;  // Or or_11, 16 bits wide
  assign xor_4_out = {multiplexer_12_out[11:8], multiplexer_12_out[15:12], multiplexer_12_out[3:0], multiplexer_12_out[7:4]} ^ multiplexer_13_out;  // XOr xor_4, 16 bits wide
  assign not_6_out = ~{multiplexer_12_out[11:8], multiplexer_12_out[15:12], multiplexer_12_out[3:0], multiplexer_12_out[7:4]};  // Not not_6, 16 bits wide
  Neg #(.Bits(16)) neg_2 (
    .in({multiplexer_12_out[11:8], multiplexer_12_out[15:12], multiplexer_12_out[3:0], multiplexer_12_out[7:4]}),
    .out(neg_2_out));
  D_FF_AS d_ff_as_12 (
    .Set(multiplexer_8_out[10]), .D(RandomNUM[9]), .C(clk_internal), .Clr(and_8_out), .Q(RandomNUM[10]));  // open: nQ
  D_FF_AS d_ff_as_13 (
    .Set(multiplexer_8_out[11]), .D(RandomNUM[10]), .C(clk_internal), .Clr(and_8_out), .Q(RandomNUM[11]));  // open: nQ
  xor xor_5 (xor_5_out, RandomNUM[12], RandomNUM[14]);
  D_FF_AS d_ff_as_14 (
    .Set(multiplexer_8_out[12]), .D(RandomNUM[11]), .C(clk_internal), .Clr(and_8_out), .Q(RandomNUM[12]));  // open: nQ
  D_FF_AS d_ff_as_15 (
    .Set(multiplexer_8_out[13]), .D(RandomNUM[12]), .C(clk_internal), .Clr(and_8_out), .Q(RandomNUM[13]));  // open: nQ
  D_FF_AS d_ff_as_16 (
    .Set(multiplexer_8_out[14]), .D(RandomNUM[13]), .C(clk_internal), .Clr(and_8_out), .Q(RandomNUM[14]));  // open: nQ
  Multiplexer #(.Selector_Bits(4), .Bits(16)) multiplexer_14 (
    .sel(aluOp[3:0]), .in_0(multiplexer_13_out), .in_1(add_1_s), .in_2(sub_1_s), .in_3(and_16_out),
    .in_4(or_11_out), .in_5(xor_4_out), .in_6(not_6_out), .in_7(neg_2_out),
    .in_8({multiplexer_12_out[10:8], multiplexer_12_out[15:12], multiplexer_12_out[3:0], multiplexer_12_out[7:4], and_15_out[15]}),
    .in_9({and_15_out[15], multiplexer_12_out[11:8], multiplexer_12_out[15:12], multiplexer_12_out[3:0], multiplexer_12_out[7:5]}),
    .in_10({{2{multiplexer_12_out[11]}}, multiplexer_12_out[10:8], multiplexer_12_out[15:12], multiplexer_12_out[3:0], multiplexer_12_out[7:5]}),
    .in_11({multiplexer_12_out[3:0], multiplexer_12_out[7:4], multiplexer_12_out[11:8], multiplexer_12_out[15:12]}),
    .in_12(multiplexer_12_out), .in_13(mul_1_mul), .in_14(divs_1_bolum), .in_15(divs_1_kalan), .out(AddrOut));
  Multiplexer #(.Selector_Bits(4)) multiplexer_15 (
    .sel(aluOp[3:0]), .in_0(1'b0), .in_1(add_1_c_o), .in_2(sub_1_c_o), .in_3(1'b0), .in_4(1'b0), .in_5(1'b0),
    .in_6(1'b0), .in_7(1'b0), .in_8(multiplexer_12_out[11]), .in_9(multiplexer_12_out[4]),
    .in_10(multiplexer_12_out[4]), .in_11(1'b0), .in_12(1'b0), .in_13(1'b0), .in_14(1'b0), .in_15(1'b0),
    .out(multiplexer_15_out));
  D_FF_AS d_ff_as_17 (
    .Set(multiplexer_8_out[15]), .D(RandomNUM[14]), .C(clk_internal), .Clr(and_8_out), .Q(RandomNUM[15]));  // open: nQ
  Comparator #(.Signed("true"), .Bits(16)) comparator_2 (
    .a(AddrOut), .b({16{1'b0}}), .eq(comparator_2_eq));  // open: gt, lt
  timer timer0 (
    .dOut(DataOut), .Addr(AddrOut), .ioW(ioW), .ioR(ioR), .C(debugOut[3]), .InterLock(InterLock),
    .timerConfigAddr(16'h1), .timerTargetAddr(16'h2), .timerResetAddr(16'h3), .timerReadAddr(16'h1),
    .rst(rst), .TimerOut(time0In), .\timerİnterrupt (and_21_out[0]), .TimerEn(timer0En));
  timer timer1 (
    .dOut(DataOut), .Addr(AddrOut), .ioW(ioW), .ioR(ioR), .C(debugOut[3]), .InterLock(InterLock),
    .timerConfigAddr(16'h4), .timerTargetAddr(16'h5), .timerResetAddr(16'h6), .timerReadAddr(16'h2),
    .rst(rst), .TimerOut(time1In), .\timerİnterrupt (and_21_out[1]), .TimerEn(timer1En));
  timer timer2 (
    .dOut(DataOut), .Addr(AddrOut), .ioW(ioW), .ioR(ioR), .C(debugOut[3]), .InterLock(InterLock),
    .timerConfigAddr(16'h7), .timerTargetAddr(16'h8), .timerResetAddr(16'h9), .timerReadAddr(16'h3),
    .rst(rst), .TimerOut(time2In), .\timerİnterrupt (and_21_out[2]), .TimerEn(timer2En));
  Comparator #(.Signed("true"), .Bits(16)) comparator_3 (.a(AddrOut), .b(16'hc), .eq(comparator_3_eq));  // open: gt, lt
  Comparator #(.Signed("true"), .Bits(16)) comparator_4 (.a(AddrOut), .b(16'hb), .eq(comparator_4_eq));  // open: gt, lt
  Comparator #(.Signed("true"), .Bits(16)) comparator_5 (.a(AddrOut), .b(16'hb), .eq(comparator_5_eq));  // open: gt, lt
  and and_17 (and_17_out, comparator_3_eq, ioW);
  and and_18 (and_18_out, comparator_4_eq, ioW);
  and and_19 (inputEn, comparator_5_eq, ioR);
  _1_addressable_register _1_addressable_register_1 (
    .Datain(DataOut), .ioW(ioW), .addrIn(AddrOut), .address(16'he), .clk(debugOut[3]),
    .DataOut(_1_addressable_register_1_dataout));
  Multiplexer #(.Selector_Bits(3), .Bits(16)) multiplexer_16 (
    .sel(or_13_out), .in_0({16{1'b0}}), .in_1(interruptReg), .in_2(inputReg), .in_3(time0In), .in_4(time1In),
    .in_5(time2In), .in_6({16{1'b0}}), .in_7({16{1'b0}}), .out(iow_Din));
  register_8bit outputReg (.D(DataOut[7:0]), .C(debugOut[3]), .en(and_17_out), .rst(rst), .Q(outputToOutsideEnable));
  Multiplexer #(.Bits(16)) multiplexer_17 (
    .sel(InterLock), .in_0({{8{1'b0}}, Input}), .in_1(register_1_q), .out(multiplexer_17_out));
  Register #(.Bits(16)) register_1 (.D(multiplexer_17_out), .C(debugOut[3]), .en(or_12_out), .Q(register_1_q));
  uartBlock uartblock_1 (
    .TX(TX), .RX(RX), .clk(debugOut[3]), .localclk(clk_internal), .rst(rst), .dataIn(DataOut),
    .Addr(AddrOut), .ioW(ioW), .ioR(ioR), .transmitAddr(16'h10), .ReceiveAddr(16'h5));  // open: DataOut
  register_8bit OutoutEnReg (.D(DataOut[7:0]), .C(debugOut[3]), .en(and_18_out), .rst(rst), .Q(Output));
  Comparator #(.Bits(16)) comparator_6 (
    .a(multiplexer_17_out), .b(register_1_q), .gt(comparator_6_gt), .lt(comparator_6_lt));  // open: eq
  Comparator #(.Bits(16)) comparator_7 (.a(16'h4), .b(AddrOut), .eq(comparator_7_eq));  // open: gt, lt
  or or_12 (or_12_out, comparator_6_gt, comparator_6_lt);
  or or_13 (or_13_out[2], timer1En, timer2En, 1'b0);
  or or_14 (or_13_out[1], inputEn, timer0En, 1'b0);
  or or_15 (or_13_out[0], interEn, timer0En, timer2En);
  Comparator #(.Bits(16)) comparator_8 (.a(16'ha), .b(AddrOut), .eq(comparator_8_eq));  // open: gt, lt
  and and_20 (interEn, comparator_7_eq, ioR);
  and and_21 (and_21_out[3], or_12_out, _1_addressable_register_1_dataout);
  Multiplexer #(.Bits(16)) multiplexer_18 (
    .sel(and_22_out), .in_0({{12{1'b0}}, and_21_out}), .in_1(DataOut), .out(multiplexer_18_out));
  and and_22 (and_22_out, comparator_8_eq, ioW);
  Register #(.Bits(16)) register_2 (.D(multiplexer_18_out), .C(debugOut[3]), .en(or_16_out), .Q(register_2_q));
  Multiplexer #(.Bits(16)) multiplexer_19 (
    .sel(_1_addressable_register_1_dataout), .in_0({{8{1'b0}}, Input}), .in_1(register_1_q),
    .out(multiplexer_19_out));
  assign inputReg = inputEn ? multiplexer_19_out : 16'bz;  // Driver driver_3
  Comparator #(.Bits(16)) comparator_9 (
    .a(multiplexer_18_out), .b(register_2_q), .gt(comparator_9_gt), .lt(comparator_9_lt));  // open: eq
  assign interruptReg = interEn ? register_2_q : 16'bz;  // Driver driver_4
  or or_16 (or_16_out, comparator_9_gt, comparator_9_lt);
  and and_23 (inter, ~InterLock, or_17_out);  // And
  or or_17 (or_17_out, 1'b0, 1'b0, 1'b0, 1'b0, 1'b0, 1'b0, 1'b0, 1'b0, 1'b0, 1'b0, 1'b0, 1'b0, and_21_out[3], and_21_out[2], and_21_out[1], and_21_out[0]);

  assign debugOut[2:0] = {3{debugOut[3]}};

  // Other names for the same wires on the sheet: sel[3:0] = aluOp[3:0]; OPcode[7:0] = CurrentOpcode[15:8];
  //   imm = CurrentOpcode[15]; inputFromOutside[7:0] = Input; outputToOutside[7:0] = Output; pcClock = debugOut[3];
  //   Clk_in = clk_internal; PeripheralClk_in = clk_internal; spi_clock_ram = spiClk; spi_miso = spiMiso;
  //   spi_mosi_ram = spiMosi; uart_rx = RX; uart_tx = TX

  // Notes on the sheet:
  //   rst_n: default 1
  //   clk_internal: Hz: 1000
  //   Input/Output
  //   ProgramMemoryRead
  //   ControlLogic
  //   RandomNumberGen
  //   pgr loads int.hex
  //   JumpLogic
  //   FlagStore
  //   interrupt Logic
  //   ALU
  //   IO Addresses
  //   logical shift left
  //   logical shift right
  //   arithmetic shift right
  //   swapBytes
  //   swapNibbles
  //   Write Addresses
  //   Read Addresses
  //   IO BUS
  //   Timers
  //   Output
  //   Output_En
  //   input
  //   inputBus
  //   InterruptRegister
  //   InterruptBus
endmodule
