// Digital circuit newcp.dig as structural Verilog
module newcp (
  input  [15:0] in_1,
  input  clk
);

  wire dipswitch_1_out, dipswitch_2_out, dipswitch_3_out, dipswitch_4_out, rst;
  wire [15:0] register_16bit_1_q, rom_1_d, u_programCounter_nextpc, u_programCounter_pc;

  programCounter #(.applicationType("IVERILOG"), .CodeFile("C:\\Users\\Berkant\\Desktop\\fpga\\RemedyCpu\\verilog\\programCounter.v")) u_programCounter (
    .AluIn(in_1), .clk(clk), .rst(rst), .absJmp(dipswitch_1_out), .intr(dipswitch_2_out),
    .reti(dipswitch_3_out), .relJmp(dipswitch_4_out), .Nextpc(u_programCounter_nextpc),
    .PC(u_programCounter_pc));
  DipSwitch dipswitch_1 (.out(dipswitch_1_out));
  DipSwitch dipswitch_2 (.out(dipswitch_2_out));
  DipSwitch dipswitch_3 (.out(dipswitch_3_out));
  DipSwitch dipswitch_4 (.out(dipswitch_4_out));
  DipSwitch dipswitch_5 (.out(rst));
  ROM #(.AddrBits(16), .Bits(16)) rom_1 (.A(u_programCounter_pc), .sel(1'b1), .D(rom_1_d));
  register_16bit register_16bit_1 (.D(rom_1_d), .C(clk), .en(1'b1), .rst(rst), .Q(register_16bit_1_q));

  // Notes on the sheet:
  //   contents of rom_1 (hex, n*v repeats v):
  //   0,1,2,3,4,5,6,7,8,9
endmodule
