// Digital circuit pc.dig as structural Verilog
module pc (
  input  [15:0] Alu,
  input  clk,
  input  rst,
  input  abs,
  input  intr,
  input  reti,
  input  Rel,
  output [15:0] Next,
  output [15:0] PcOut
);

  wire and_1_out, and_2_out, not_1_out;
  wire [15:0] add_2_s, multiplexer_1_out, multiplexer_2_out, multiplexer_3_out, multiplexer_4_out,
       register_1_q;

  not not_1 (not_1_out, clk);
  register_16bit PC (.D(multiplexer_4_out), .C(not_1_out), .en(1'b1), .rst(rst), .Q(PcOut));
  Add #(.Bits(16)) add_1 (.a(PcOut), .b(16'h1), .c_i(1'b0), .s(Next));  // open: c_o
  Add #(.Bits(16)) add_2 (.a(Next), .b(Alu), .c_i(1'b0), .s(add_2_s));  // open: c_o
  Multiplexer #(.Bits(16)) multiplexer_1 (.sel(Rel), .in_0(Next), .in_1(add_2_s), .out(multiplexer_1_out));
  Multiplexer #(.Bits(16)) multiplexer_2 (.sel(abs), .in_0(multiplexer_1_out), .in_1(Alu), .out(multiplexer_2_out));
  Register #(.Bits(16)) register_1 (.D(multiplexer_2_out), .C(~clk), .en(and_1_out), .Q(register_1_q));
  Multiplexer #(.Bits(16)) multiplexer_3 (
    .sel(and_1_out), .in_0(multiplexer_2_out), .in_1(16'h2), .out(multiplexer_3_out));
  and and_1 (and_1_out, intr, intr);
  Multiplexer #(.Bits(16)) multiplexer_4 (
    .sel(and_2_out), .in_0(multiplexer_3_out), .in_1(register_1_q), .out(multiplexer_4_out));
  and and_2 (and_2_out, reti, reti);
endmodule
