// Digital circuit ram.dig as structural Verilog
module ram (
  input  in_1,
  input  [15:0] in_2,
  input  [15:0] in_3,
  input  clk,
  output [15:0] out_4
);

  single_port_bram_16bit #(.applicationType("IVERILOG"), .CodeFile("D:\\Desktop\\fpga\\RemedyCpu\\verilog\\ram.v")) u_single_port_bram_16bit (
    .clk(clk), .we(in_1), .addr(in_2), .din(in_3), .dout(out_4));
endmodule
