// Digital circuit singExtend.dig as structural Verilog
module singExtend (
  input  [15:0] inst,
  output [15:0] _4S,
  output [15:0] _8SD,
  output [15:0] _4D
);


  assign _4D = {{12{1'b0}}, inst[7:4]};
  assign _4S = {{12{1'b0}}, inst[3:0]};
  assign _8SD = {{9{inst[7]}}, inst[6:0]};

  // Notes on the sheet:
  //   inst: instruction word
  //   {{de Das Befehlswort}}
  //   _4S: The four bits taken from Rs.
  //   {{de Die vier Bit aus Rs}}
  //   _8SD: The eight bits taken from Rs,Rd with sign extension.
  //   {{de Die neun Bit aus Rs,Rd mit Vorzeichenerweiterung}}
  //   _4D: The four bits taken from Rd.
  //   {{de Die vier Bit aus Rd}}
endmodule
