// Digital circuit smallScpu.dig as structural Verilog
module smallScpu (
  input  [7:0] ui_in,
  input  [7:0] uio_in,
  input  ena,
  input  clk,
  input  rst_n,
  output [7:0] uo_out,
  output [7:0] uio_out,
  output [7:0] uio_oe
);

  wire abs, addr_p5, alu2D, and_1_out, and_2_out, and_4_out, and_5_out, and_6_out, and_8_out, and_9_out,
       and_10_out, asr_1_p2, C, comparator_1_eq, comparator_2_eq, comparator_3_eq, comparator_4_eq,
       d_ff_as_1_nq, d_ff_as_1_q, imm, ioR, ioW, jk_ff_1_q, ld, lsl_1_p4, lsr_1_p4, multiplexer_7_out,
       multiplexer_9_out, muxA, not_1_out, not_3_out, or_4_out, RandomNUMSel, sf, src2D, st, stPC, subbr_p5,
       u_DIG_Counter_ovf, WE, xor_1_out, xor_3_out, xor_4_out, xor_5_out;
  wire [1:0] iem, u_DIG_Counter_p_out, WDmux;
  wire [2:0] br, FlagOut, muxB;
  wire [3:0] register_2_q, register_2_q_2;
  wire [4:0] aluOp;
  wire [6:0] multiplexer_3_out, OPcode;
  wire [11:0] adder12_1_p4, adder12_2_p4, multiplexer_1_out, multiplexer_2_out;
  wire [15:0] Addr, addr_p4, and_7_out, asr_1_p3, Dout, imreg_1_p5, lsl_1_p3, lsr_1_p3, mem_d,
       multiplexer_4_out, multiplexer_5_out, multiplexer_6_out, multiplexer_10_out, neg_2_out, not_2_out,
       or_3_out, RandomNUM, registerblock_1_rdest, seed_q, singextend_1__4d, singextend_1__4s,
       singextend_1__8sd, subbr_p4, swap_1_p2, swapn_1_p2, xor_2_out;

  Register #(.Bits(12), .isProgramCounter("true")) PC (
    .D(multiplexer_2_out), .C(~C), .en(1'b1), .Q({uio_out[3:0], uo_out}));
  // adder12 adder12_1: pin names not known; wires that end beside it: {uio_out[3:0], uo_out}, 12'h1, 1'b0, adder12_1_p4
  // adder12 adder12_2: pin names not known; wires that end beside it: adder12_1_p4, Addr[11:0], 1'b0, adder12_2_p4
  Multiplexer #(.Bits(12)) multiplexer_1 (
    .sel(xor_1_out), .in_0(adder12_1_p4), .in_1(adder12_2_p4), .out(multiplexer_1_out));
  Multiplexer #(.Bits(12)) multiplexer_2 (
    .sel(abs), .in_0(multiplexer_1_out), .in_1(Addr[11:0]), .out(multiplexer_2_out));
  DIG_Counter #(.applicationType("GHDL")) u_DIG_Counter (
    .en(1'b1), .C(clk), .clr(rst_n), .p_out(u_DIG_Counter_p_out), .ovf(u_DIG_Counter_ovf));
  Multiplexer #(.Bits(7)) multiplexer_3 (.sel(imm), .in_0(OPcode), .in_1({7{1'b0}}), .out(multiplexer_3_out));
  not not_1 (not_1_out, clk);
  and and_1 (and_1_out, u_DIG_Counter_p_out[0], ~u_DIG_Counter_p_out[1]);  // And
  and and_2 (and_2_out, ~u_DIG_Counter_p_out[0], u_DIG_Counter_p_out[1]);  // And
  and and_3 (C, u_DIG_Counter_p_out[0], u_DIG_Counter_p_out[1]);
  // controllogic controllogic_1: pin names not known; wires that end beside it: multiplexer_3_out[6], multiplexer_3_out[5], multiplexer_3_out[4], multiplexer_3_out[3], multiplexer_3_out[2], multiplexer_3_out[1], multiplexer_3_out[0], muxB[2], muxB[1], muxB[0], src2D, aluOp[4], aluOp[3], aluOp[2], aluOp[1], aluOp[0], WE, sf, alu2D, iem[1], iem[0], br[2], br[1], br[0], muxA, ld, st, abs, ioW, ioR, stPC
  Register #(.Bits(8)) register_1 (.D(ui_in), .C(not_1_out), .en(and_1_out), .Q({imm, OPcode}));
  Register #(.Bits(8)) register_2 (.D(ui_in), .C(not_1_out), .en(and_2_out), .Q({register_2_q_2, register_2_q}));
  or or_1 (WDmux[0], stPC, ld, RandomNUMSel);
  or or_2 (WDmux[1], ioR, stPC);
  Multiplexer #(.Selector_Bits(3), .Bits(16)) multiplexer_4 (
    .sel({RandomNUMSel, WDmux}), .in_0(Addr), .in_1(mem_d), .in_2({{8{1'b0}}, uio_in}),
    .in_3({4'b0000, adder12_1_p4}), .in_4({16{1'b0}}), .in_5(RandomNUM), .in_6({16{1'b0}}),
    .in_7({16{1'b0}}), .out(multiplexer_4_out));
  RegisterBlock registerblock_1 (
    .DataIn(multiplexer_4_out), .WE(WE), .clk(C), .src(register_2_q), .Dest(register_2_q_2),
    .RDest(registerblock_1_rdest), .Rsrc(Dout));  // open: rst
  singExtend singextend_1 (
    .inst({imm, OPcode, register_2_q_2, register_2_q}), ._4S(singextend_1__4s), ._8SD(singextend_1__8sd),
    ._4D(singextend_1__4d));
  // ImReg imreg_1: pin names not known; wires that end beside it: imm, iem, C, {imm, OPcode, register_2_q_2, register_2_q}, imreg_1_p5
  Multiplexer #(.Bits(16)) multiplexer_5 (
    .sel(muxA), .in_0(registerblock_1_rdest), .in_1(Dout), .out(multiplexer_5_out));
  Multiplexer #(.Selector_Bits(3), .Bits(16)) multiplexer_6 (
    .sel(muxB), .in_0(Dout), .in_1({16{1'b0}}), .in_2(imreg_1_p5), .in_3({16{1'b0}}), .in_4({16{1'b0}}),
    .in_5(singextend_1__4s), .in_6(singextend_1__8sd), .in_7(singextend_1__4d), .out(multiplexer_6_out));
  xor xor_1 (xor_1_out, multiplexer_7_out, br[2]);
  Multiplexer #(.Selector_Bits(2)) multiplexer_7 (
    .sel(br[1:0]), .in_0(1'b0), .in_1(FlagOut[0]), .in_2(FlagOut[1]), .in_3(FlagOut[2]),
    .out(multiplexer_7_out));
  Register Neg (.D(Addr[15]), .C(C), .en(sf), .Q(FlagOut[2]));
  Register Zero (.D(comparator_3_eq), .C(C), .en(sf), .Q(FlagOut[1]));
  Register Carry (.D(multiplexer_9_out), .C(C), .en(sf), .Q(FlagOut[0]));
  Comparator #(.Signed("true"), .Bits(16)) comparator_1 (.a(Addr), .b(16'h6), .eq(comparator_1_eq));  // open: gt, lt
  Comparator #(.Signed("true"), .Bits(16)) comparator_2 (.a(Addr), .b(16'h5), .eq(comparator_2_eq));  // open: gt, lt
  and and_4 (and_4_out, comparator_1_eq, ioW);
  and and_5 (and_5_out, comparator_2_eq, ioW);
  Register #(.Bits(4)) register_3 (.D(Dout[3:0]), .C(C), .en(and_4_out), .Q(uio_oe[7:4]));
  Register #(.Bits(4)) register_4 (.D(Dout[3:0]), .C(C), .en(and_5_out), .Q(uio_out[7:4]));
  and and_6 (and_6_out, aluOp[4], FlagOut[0]);
  // adder16 addr: pin names not known; wires that end beside it: multiplexer_5_out, multiplexer_6_out, and_6_out, addr_p4, addr_p5
  // subber16 subbr: pin names not known; wires that end beside it: multiplexer_5_out, multiplexer_6_out, and_6_out, subbr_p4, subbr_p5, {16{1'b0}}
  assign and_7_out = multiplexer_5_out & multiplexer_6_out;  // And and_7, 16 bits wide
  assign or_3_out = multiplexer_5_out | multiplexer_6_out;  // Or or_3, 16 bits wide
  assign xor_2_out = multiplexer_5_out ^ multiplexer_6_out;  // XOr xor_2, 16 bits wide
  assign not_2_out = ~multiplexer_5_out;  // Not not_2, 16 bits wide
  Neg #(.Bits(16)) neg_2 (.in(multiplexer_5_out), .out(neg_2_out));
  // LSL lsl_1: pin names not known; wires that end beside it: multiplexer_5_out, and_6_out, lsl_1_p3, lsl_1_p4
  // LSR lsr_1: pin names not known; wires that end beside it: multiplexer_5_out, and_6_out, lsr_1_p3, lsr_1_p4
  // ASR asr_1: pin names not known; wires that end beside it: multiplexer_5_out, asr_1_p2, asr_1_p3
  // SWAP swap_1: pin names not known; wires that end beside it: multiplexer_5_out, swap_1_p2
  // SWAPN swapn_1: pin names not known; wires that end beside it: multiplexer_5_out, swapn_1_p2
  Multiplexer #(.Selector_Bits(4), .Bits(16)) multiplexer_8 (
    .sel(aluOp[3:0]), .in_0(multiplexer_6_out), .in_1(addr_p4), .in_2(subbr_p4), .in_3(and_7_out),
    .in_4(or_3_out), .in_5(xor_2_out), .in_6(not_2_out), .in_7(neg_2_out), .in_8(lsl_1_p3), .in_9(lsr_1_p3),
    .in_10(asr_1_p3), .in_11(swap_1_p2), .in_12(swapn_1_p2), .in_13({16{1'b0}}), .in_14({16{1'b0}}),
    .in_15({16{1'b0}}), .out(Addr));
  Multiplexer #(.Selector_Bits(4)) multiplexer_9 (
    .sel(aluOp[3:0]), .in_0(1'b0), .in_1(addr_p5), .in_2(subbr_p5), .in_3(1'b0), .in_4(1'b0), .in_5(1'b0),
    .in_6(1'b0), .in_7(1'b0), .in_8(lsl_1_p4), .in_9(lsr_1_p4), .in_10(asr_1_p2), .in_11(1'b0), .in_12(1'b0),
    .in_13(1'b0), .in_14(1'b0), .in_15(1'b0), .out(multiplexer_9_out));
  Comparator #(.Signed("true"), .Bits(16)) comparator_3 (
    .a(Addr), .b({16{1'b0}}), .eq(comparator_3_eq));  // open: gt, lt
  Comparator #(.Signed("true"), .Bits(16)) comparator_4 (.a(Addr), .b(16'h8), .eq(comparator_4_eq));  // open: gt, lt
  and and_8 (and_8_out, comparator_4_eq, ioW);
  not not_3 (not_3_out, or_4_out);
  and and_9 (and_9_out, C, and_8_out);
  and and_10 (and_10_out, and_8_out, not_3_out);
  JK_FF jk_ff_1 (.J(or_4_out), .C(C), .K(or_4_out), .Q(jk_ff_1_q));  // open: nQ
  D_FF_AS d_ff_as_1 (.Set(1'b0), .D(d_ff_as_1_nq), .C(and_9_out), .Clr(jk_ff_1_q), .Q(d_ff_as_1_q), .nQ(d_ff_as_1_nq));
  Register #(.Bits(16)) seed (.D(Dout), .C(C), .en(and_8_out), .Q(seed_q));
  or or_4 (or_4_out, d_ff_as_1_q, jk_ff_1_q);
  Multiplexer #(.Bits(16)) multiplexer_10 (.sel(and_8_out), .in_0({16{1'b0}}), .in_1(seed_q), .out(multiplexer_10_out));
  // Probe on RandomNUM
  D_FF_AS d_ff_as_2 (
    .Set(multiplexer_10_out[0]), .D(xor_3_out), .C(C), .Clr(and_10_out), .Q(RandomNUM[0]));  // open: nQ
  D_FF_AS d_ff_as_3 (
    .Set(multiplexer_10_out[1]), .D(RandomNUM[0]), .C(C), .Clr(and_10_out), .Q(RandomNUM[1]));  // open: nQ
  D_FF_AS d_ff_as_4 (
    .Set(multiplexer_10_out[2]), .D(RandomNUM[1]), .C(C), .Clr(and_10_out), .Q(RandomNUM[2]));  // open: nQ
  D_FF_AS d_ff_as_5 (
    .Set(multiplexer_10_out[3]), .D(RandomNUM[2]), .C(C), .Clr(and_10_out), .Q(RandomNUM[3]));  // open: nQ
  D_FF_AS d_ff_as_6 (
    .Set(multiplexer_10_out[4]), .D(RandomNUM[3]), .C(C), .Clr(and_10_out), .Q(RandomNUM[4]));  // open: nQ
  xor xor_3 (xor_3_out, RandomNUM[5], xor_4_out);
  D_FF_AS d_ff_as_7 (
    .Set(multiplexer_10_out[5]), .D(RandomNUM[4]), .C(C), .Clr(and_10_out), .Q(RandomNUM[5]));  // open: nQ
  RAMDualPort #(.AddrBits(5), .Bits(16), .Addr_Bits(10)) mem (
    .A(Addr[4:0]), .Din(Dout), .str(st), .C(C), .ld(ld), .D(mem_d));
  D_FF_AS d_ff_as_8 (
    .Set(multiplexer_10_out[6]), .D(RandomNUM[5]), .C(C), .Clr(and_10_out), .Q(RandomNUM[6]));  // open: nQ
  D_FF_AS d_ff_as_9 (
    .Set(multiplexer_10_out[7]), .D(RandomNUM[6]), .C(C), .Clr(and_10_out), .Q(RandomNUM[7]));  // open: nQ
  D_FF_AS d_ff_as_10 (
    .Set(multiplexer_10_out[8]), .D(RandomNUM[7]), .C(C), .Clr(and_10_out), .Q(RandomNUM[8]));  // open: nQ
  xor xor_4 (xor_4_out, RandomNUM[10], xor_5_out);
  D_FF_AS d_ff_as_11 (
    .Set(multiplexer_10_out[9]), .D(RandomNUM[8]), .C(C), .Clr(and_10_out), .Q(RandomNUM[9]));  // open: nQ
  D_FF_AS d_ff_as_12 (
    .Set(multiplexer_10_out[10]), .D(RandomNUM[9]), .C(C), .Clr(and_10_out), .Q(RandomNUM[10]));  // open: nQ
  D_FF_AS d_ff_as_13 (
    .Set(multiplexer_10_out[11]), .D(RandomNUM[10]), .C(C), .Clr(and_10_out), .Q(RandomNUM[11]));  // open: nQ
  D_FF_AS d_ff_as_14 (
    .Set(multiplexer_10_out[12]), .D(RandomNUM[11]), .C(C), .Clr(and_10_out), .Q(RandomNUM[12]));  // open: nQ
  xor xor_5 (xor_5_out, RandomNUM[12], RandomNUM[14]);
  D_FF_AS d_ff_as_15 (
    .Set(multiplexer_10_out[13]), .D(RandomNUM[12]), .C(C), .Clr(and_10_out), .Q(RandomNUM[13]));  // open: nQ
  D_FF_AS d_ff_as_16 (
    .Set(multiplexer_10_out[14]), .D(RandomNUM[13]), .C(C), .Clr(and_10_out), .Q(RandomNUM[14]));  // open: nQ
  D_FF_AS d_ff_as_17 (
    .Set(multiplexer_10_out[15]), .D(RandomNUM[14]), .C(C), .Clr(and_10_out), .Q(RandomNUM[15]));  // open: nQ

  assign uio_oe[3:0] = 4'b0000;

  // Other names for the same wires on the sheet: OPcode[7] = imm; sel[3:0] = aluOp[3:0]; AddressDebug[15:0] = Addr;
  //   Clk_in = clk; Clk_t = C; DoutDebug[15:0] = Dout; enable = ena; Din[7:0] = uio_in;
  //   inputFromOutside[7:0] = uio_in; opcode_in[7:0] = ui_in; outputToOutside[3:0] = uio_out[7:4];
  //   outputToOutsideEnable[3:0] = uio_oe[7:4]; pcOut[11:0] = {uio_out[3:0], uo_out}; WDmux[2] = RandomNUMSel

  // Notes on the sheet:
  //   clk: Hz: 1000
  //   PC
  //   FlagStore
  //   input
  //   Output_En
  //   Output
  //   ALU
  //   RandomNumberGen
endmodule

/* Code of DIG_Counter:
LIBRARY ieee;
USE ieee.std_logic_1164.all;
USE ieee.numeric_std.all;

entity DIG_Counter is
  port (
    p_out: out std_logic_vector((2-1) downto 0);
    ovf: out std_logic;
    C: in std_logic;
    en: in std_logic;
    clr: in std_logic );
end DIG_Counter;

architecture Behavioral of DIG_Counter is
   signal count : std_logic_vector((2-1) downto 0) := (others => '0');
begin
    process (C, clr, en)
    begin
      if rising_edge(C) then
        if clr='1' then
          count <= (others => '0');
        elsif en='1' then
          count <=  std_logic_vector(unsigned(count) + 1);
        end if;
      end if;
    end process;

    p_out <= count;
    ovf <= en when unsigned(count) = ((2**2)-1) else '0';
end Behavioral;
*/
