// Digital circuit spi_sim.dig as structural Verilog
module spi_sim (
  output spimiso
);

  wire Clk_in, rst, spi_clock_ram, spi_mosi_ram, u_spi_mem_bridge_sim_ram_ld, u_spi_mem_bridge_sim_ram_str;
  wire [15:0] prog_d, ram_d, u_spi_mem_bridge_sim_ram_addr, u_spi_mem_bridge_sim_ram_din,
       u_spi_mem_bridge_sim_rom_addr;

  spi_mem_bridge_sim #(.applicationType("IVERILOG"), .CodeFile("C:\\Users\\Berkant\\Desktop\\fpga\\RemedyCpu\\verilog\\virtual_spi_memory_interface.v")) u_spi_mem_bridge_sim (
    .clk(Clk_in), .rst(rst), .sclk(spi_clock_ram), .mosi(spi_mosi_ram), .rom_data(prog_d), .ram_data(ram_d),
    .miso(spimiso), .rom_addr(u_spi_mem_bridge_sim_rom_addr), .ram_addr(u_spi_mem_bridge_sim_ram_addr),
    .ram_din(u_spi_mem_bridge_sim_ram_din), .ram_ld(u_spi_mem_bridge_sim_ram_ld),
    .ram_str(u_spi_mem_bridge_sim_ram_str));  // open: cs_flash, cs_ram, rom_sel
  ROM #(.bigEndian("true"), .AddrBits(16), .isProgramMemory("true"), .Bits(16)) prog (
    .A(u_spi_mem_bridge_sim_rom_addr), .sel(1'b1), .D(prog_d));
  RAMDualPort #(.AddrBits(16), .Bits(16)) ram (
    .A(u_spi_mem_bridge_sim_ram_addr), .Din(u_spi_mem_bridge_sim_ram_din),
    .str(u_spi_mem_bridge_sim_ram_str), .C(Clk_in), .ld(u_spi_mem_bridge_sim_ram_ld), .D(ram_d));

  // Other names for the same wires on the sheet: spi_miso = spimiso

  // Notes on the sheet:
  //   prog loads testCompiler.bin
endmodule
