// Digital circuit spiram.dig as structural Verilog
module spiram (
  input  clk,
  input  in_2,
  input  in_3,
  input  [15:0] in_4,
  input  [15:0] in_5,
  input  in_6,
  input  in_7,
  input  in_8,
  output [15:0] dataout,
  output cs,
  output clk_2,
  output busy,
  output mosi,
  output [4:0] dataout_2
);

  wire u_spi_memory_interface_spi_clk, u_spi_memory_interface_spi_mosi;

  spi_memory_interface #(.applicationType("IVERILOG"), .CodeFile("D:\\Desktop\\fpga\\RemedyCpu\\verilog\\spi_memory.v")) u_spi_memory_interface (
    .clk(clk), .spi_rst(in_8), .st(in_7), .ld(in_6), .addr(in_5), .data_in(in_4), .is_continous(in_3),
    .spi_miso(in_2), .data_out(dataout), .spi_cs(cs), .spi_clk(u_spi_memory_interface_spi_clk), .busy(busy),
    .spi_mosi(u_spi_memory_interface_spi_mosi), .stateDeb(dataout_2));
  assign clk_2 = busy ? u_spi_memory_interface_spi_clk : 1'bz;  // Driver driver_1
  assign mosi = busy ? u_spi_memory_interface_spi_mosi : 1'bz;  // Driver driver_2
endmodule
