// Digital circuit spiverilog.dig as structural Verilog
module spiverilog (
  input  [15:0] in_1,
  input  [15:0] in_2,
  input  in_3,
  input  in_4,
  input  in_5,
  input  clk,
  input  in_7,
  input  in_12,
  output mosi,
  output clk_2,
  output cs,
  output [15:0] out_11,
  output cs2
);

  wire u_spi_memory_interface_busy;
  wire [4:0] u_spi_memory_interface_statedeb;

  spi_memory_interface #(.applicationType("IVERILOG"), .CodeFile("D:\\Desktop\\fpga\\RemedyCpu\\verilog\\spi.v")) u_spi_memory_interface (
    .clk(clk), .spi_rst(in_5), .st(in_4), .ld(in_3), .addr(in_1), .data_in(in_2), .mem_sel(in_12),
    .spi_miso(in_7), .data_out(out_11), .busy(u_spi_memory_interface_busy), .spi_cs(cs), .spi_cs_prog(cs2),
    .spi_clk(clk_2), .spi_mosi(mosi), .stateDeb(u_spi_memory_interface_statedeb));

  // Notes on the sheet:
  //   in_1: default 30804
  //   in_2: default 5412
  //   in_12: default 5412
endmodule
