// Digital circuit sub_multplex.dig as structural Verilog
module sub_multplex (
  input  a,
  input  b,
  input  bi,
  input  os,
  output bo,
  output d
);

  wire and_1_out, and_2_out, sub_1_s;

  Sub sub_1 (.a(a), .b(b), .c_i(bi), .s(sub_1_s), .c_o(bo));
  and and_1 (and_1_out, a, os);
  and and_2 (and_2_out, sub_1_s, ~os);  // And
  or or_1 (d, and_1_out, and_2_out);
endmodule
