// Digital circuit tristate.dig as structural Verilog
module tristate (
  input  Enable,
  input  A,
  output Out
);

  wire nand_1_out, nor_1_out, not_1_out;

  nand nand_1 (nand_1_out, A, Enable);
  not not_1 (not_1_out, Enable);
  nor nor_1 (nor_1_out, not_1_out, A);
  FGPFET fgpfet_1 (.G(nand_1_out), .S(1'b1), .D(Out));
  NFET nfet_1 (.G(nor_1_out), .D(Out), .S(1'b0));
endmodule
