// Digital circuit tt_um_remedy_cpu_flash_simulation.dig as structural Verilog
module tt_um_remedy_cpu_flash_simulation (
  input  [7:0] ui_in,
  input  clk,
  input  [7:0] uio_in,
  input  ena,
  input  rst_n,
  output [7:0] uo_out,
  output [7:0] uio_out,
  output [7:0] uio_oe,
  output spimiso
);

  wire abs, alu_1_carryout, alu_1_neg, alu_1_zero, and_1_out, and_2_out, and_3_out, and_4_out, and_8_out,
       and_9_out, and_10_out, and_11_out, and_12_out, and_13_out, and_14_out, and_16_out, and_17_out,
       and_18_out, and_19_out, and_20_out, and_21_out, and_22_out, and_23_out, and_24_out, CarryR_q, Clk_in,
       comparator_1_eq, data_done, execute_pulse, Fetch_done, fetch_request_pulse, flash_req, i2c_inter,
       imem_ior, imem_iow, imm, InterLock, intr, ld, multiplexer_4_out, muxA, NegR_q, not_1_out, not_2_out,
       not_3_out, not_4_out, not_5_out, not_6_out, not_7_out, not_8_out, or_1_out, or_2_out, or_4_out, pc_en,
       Reti, sf, spi_busy_ram, spi_cs, spi_ld, spi_st, spi_target, st, stPC,
       u_memory_wait_controller_mem_stall, u_opcode_microcode_rom_ior, u_opcode_microcode_rom_iow,
       u_opcode_microcode_rom_sf, u_opcode_microcode_rom_we, u_spi_mem_bridge_sim_ram_ld,
       u_spi_mem_bridge_sim_ram_str, WE, xor_1_out, ZeroR_q;
  wire [1:0] iem, u_muxEncoder_q;
  wire [2:0] br, muxB, or_7_out, u_timer_tiny_timer_interrupt;
  wire [5:0] aluOp;
  wire [6:0] multiplexer_1_out, OPcode;
  wire [7:0] register_1_q;
  wire [15:0] AddrOut, DataOut, i2cDat, ImmReg, intr_reg, iow_Din, mem_out, multiplexer_3_out,
       multiplexer_5_out, multiplexer_6_out, multiplexer_10_out, prog_d, programAddr, ram_d, register_2_q,
       rngdat0, singextend_1_p2, singextend_1_p3, singextend_1_p4, spi_addr, spi_data, spi_data_out,
       timerdat1, timerdat2, u_programCounter_nextpc, u_RegisterBlock_rdest, u_spi_mem_bridge_sim_ram_addr,
       u_spi_mem_bridge_sim_ram_din, u_spi_mem_bridge_sim_rom_addr;

  spi_mem_bridge_sim #(.applicationType("IVERILOG"), .CodeFile("C:\\Users\\Berkant\\Desktop\\fpga\\RemedyCpu\\verilog\\virtual_spi_memory_interface.v")) u_spi_mem_bridge_sim (
    .clk(Clk_in), .rst_n(rst_n), .cs_flash(uio_out[2]), .cs_ram(uio_out[1]), .sclk(uio_out[4]),
    .mosi(uio_out[3]), .rom_data(prog_d), .ram_data(ram_d), .miso(spimiso),
    .rom_addr(u_spi_mem_bridge_sim_rom_addr), .ram_addr(u_spi_mem_bridge_sim_ram_addr),
    .ram_din(u_spi_mem_bridge_sim_ram_din), .ram_ld(u_spi_mem_bridge_sim_ram_ld),
    .ram_str(u_spi_mem_bridge_sim_ram_str));  // open: rom_sel
  and and_1 (and_1_out, intr, execute_pulse);
  and and_2 (and_2_out, execute_pulse, Reti);
  ROM #(.bigEndian("true"), .AddrBits(16), .isProgramMemory("true"), .Bits(16)) prog (
    .A(u_spi_mem_bridge_sim_rom_addr), .sel(1'b1), .D(prog_d));
  RAMDualPort #(.AddrBits(16), .Bits(16)) ram (
    .A(u_spi_mem_bridge_sim_ram_addr), .Din(u_spi_mem_bridge_sim_ram_din),
    .str(u_spi_mem_bridge_sim_ram_str), .C(Clk_in), .ld(u_spi_mem_bridge_sim_ram_ld), .D(ram_d));
  and and_3 (and_3_out, abs, execute_pulse);
  Multiplexer #(.Bits(7)) multiplexer_1 (.sel(imm), .in_0(OPcode), .in_1({7{1'b0}}), .out(multiplexer_1_out));
  Multiplexer multiplexer_2 (.sel(ena), .in_0(1'b1), .in_1(clk), .out(Clk_in));
  and and_4 (and_4_out, xor_1_out, execute_pulse);
  opcode_microcode_rom #(.applicationType("IVERILOG"), .CodeFile("D:\\Desktop\\fpga\\RemedyCpu\\verilog\\opcode_microcode_rom.v")) u_opcode_microcode_rom (
    .opcode(multiplexer_1_out), .muxb0(muxB[2]), .muxb1(muxB[1]), .muxb2(muxB[0]), .aluop0(aluOp[5]),
    .aluop1(aluOp[4]), .aluop2(aluOp[3]), .aluop3(aluOp[2]), .aluop4(aluOp[1]), .aluop5(aluOp[0]),
    .WE(u_opcode_microcode_rom_we), .sf(u_opcode_microcode_rom_sf), .iem0(iem[1]), .iem1(iem[0]),
    .br0(br[2]), .br1(br[1]), .br2(br[0]), .muxA(muxA), .ld(ld), .st(st), .abs(abs),
    .ioW(u_opcode_microcode_rom_iow), .ioR(u_opcode_microcode_rom_ior), .stPC(stPC), .Reti(Reti),
    .flash_req(flash_req));
  programCounter #(.applicationType("IVERILOG"), .CodeFile("C:\\Users\\Berkant\\Desktop\\fpga\\RemedyCpu\\verilog\\programCounter.v")) u_programCounter (
    .AluIn(AddrOut), .clk(Clk_in), .rst_n(rst_n), .pc_en(pc_en), .absJmp(and_3_out), .intr(and_1_out),
    .reti(and_2_out), .relJmp(and_4_out), .Nextpc(u_programCounter_nextpc), .PC(programAddr));
  not not_1 (not_1_out, flash_req);
  not not_2 (not_2_out, ld);
  and and_5 (sf, u_opcode_microcode_rom_sf, execute_pulse);
  and and_6 (imem_iow, u_opcode_microcode_rom_iow, execute_pulse);
  and and_7 (imem_ior, u_opcode_microcode_rom_ior, execute_pulse);
  or or_1 (or_1_out, not_1_out, not_2_out);
  or or_2 (or_2_out, flash_req, ld);
  and and_8 (and_8_out, or_1_out, execute_pulse, u_opcode_microcode_rom_we);
  and and_9 (and_9_out, u_opcode_microcode_rom_we, data_done, or_2_out);
  Multiplexer #(.Selector_Bits(2), .Bits(16)) multiplexer_3 (
    .sel(u_muxEncoder_q), .in_0(AddrOut), .in_1(mem_out), .in_2(iow_Din), .in_3(u_programCounter_nextpc),
    .out(multiplexer_3_out));
  or or_3 (WE, and_8_out, and_9_out);
  or or_4 (or_4_out, flash_req, ld);
  muxEncoder #(.applicationType("IVERILOG"), .CodeFile("D:\\Desktop\\fpga\\RemedyCpu\\verilog\\multipleToMux-4.v")) u_muxEncoder (
    .a(1'b0), .b(or_4_out), .c(imem_ior), .d(stPC), .Q(u_muxEncoder_q));
  Register #(.Bits(16)) register_1 (.D(mem_out), .C(Clk_in), .en(Fetch_done), .Q({imm, OPcode, register_1_q}));
  and and_10 (and_10_out, ld, execute_pulse);
  and and_11 (and_11_out, execute_pulse, st);
  and and_12 (and_12_out, execute_pulse, flash_req);
  xor xor_1 (xor_1_out, multiplexer_4_out, br[2]);
  Multiplexer #(.Selector_Bits(2)) multiplexer_4 (
    .sel(br[1:0]), .in_0(1'b0), .in_1(CarryR_q), .in_2(ZeroR_q), .in_3(NegR_q), .out(multiplexer_4_out));
  register_1bit NegR (.D(alu_1_neg), .C(Clk_in), .en(sf), .rst(rst_n), .Q(NegR_q));
  register_1bit ZeroR (.D(alu_1_zero), .C(Clk_in), .en(sf), .rst(rst_n), .Q(ZeroR_q));
  register_1bit CarryR (.D(alu_1_carryout), .C(Clk_in), .en(sf), .rst(rst_n), .Q(CarryR_q));
  RegisterBlock #(.applicationType("IVERILOG"), .CodeFile("D:\\Desktop\\fpga\\RemedyCpu\\verilog\\reg16x16.v")) u_RegisterBlock (
    .DataIn(multiplexer_3_out), .WE(WE), .clk(Clk_in), .src(register_1_q[3:0]), .Dest(register_1_q[7:4]),
    .RDest(u_RegisterBlock_rdest), .Rsrc(DataOut));
  memory_wait_controller #(.applicationType("IVERILOG"), .CodeFile("D:\\Desktop\\fpga\\RemedyCpu\\verilog\\memory_wait_controller.v")) u_memory_wait_controller (
    .clk(Clk_in), .rst_n(rst_n), .fetch_req(fetch_request_pulse), .ld_req(and_10_out), .st_req(and_11_out),
    .flash_req(and_12_out), .fetch_addr(programAddr), .data_addr(AddrOut), .store_data(DataOut),
    .spi_data_out(spi_data), .spi_busy(spi_busy_ram), .mem_rdata(mem_out), .fetch_done(Fetch_done),
    .data_done(data_done), .mem_stall(u_memory_wait_controller_mem_stall), .spi_st(spi_st), .spi_ld(spi_ld),
    .spi_addr(spi_addr), .spi_data_in(spi_data_out), .spi_target(spi_target));  // open: spi_fast, spi_seq
  cpu_cycle_controller #(.applicationType("IVERILOG"), .CodeFile("C:\\Users\\Berkant\\Desktop\\fpga\\RemedyCpu\\verilog\\cpu_cycle_controller.v")) u_cpu_cycle_controller (
    .clk(Clk_in), .rst_n(rst_n), .fetch_done(Fetch_done), .data_done(data_done), .ld(ld), .st(st),
    .flash_ld(flash_req), .fetch_req(fetch_request_pulse), .execute_now_pulse(execute_pulse));
  // ImReg imreg_1: pin names not known; wires that end beside it: imm, iem, Clk_in, {imm, OPcode, register_1_q}, ImmReg
  // singExtend singextend_1: pin names not known; wires that end beside it: register_1_q, singextend_1_p2, singextend_1_p3, singextend_1_p4
  spi_memory_interface #(.applicationType("IVERILOG"), .CodeFile("D:\\Desktop\\fpga\\RemedyCpu\\verilog\\spi_memory.v")) u_spi_memory_interface (
    .clk(Clk_in), .spi_rst_n(rst_n), .st(spi_st), .ld(spi_ld), .addr(spi_addr), .data_in(spi_data_out),
    .is_continous(1'b0), .spi_miso(spimiso), .data_out(spi_data), .spi_cs(spi_cs), .spi_clk(uio_out[4]),
    .busy(spi_busy_ram), .spi_mosi(uio_out[3]));
  Multiplexer #(.Bits(16)) multiplexer_5 (
    .sel(muxA), .in_0(u_RegisterBlock_rdest), .in_1(DataOut), .out(multiplexer_5_out));
  Multiplexer #(.Selector_Bits(3), .Bits(16)) multiplexer_6 (
    .sel(muxB), .in_0(DataOut), .in_1({16{1'b0}}), .in_2(ImmReg), .in_3({16{1'b0}}), .in_4({16{1'b0}}),
    .in_5(singextend_1_p2), .in_6(singextend_1_p3), .in_7(singextend_1_p4), .out(multiplexer_6_out));
  and and_13 (and_13_out, AddrOut[2], AddrOut[1]);
  not not_3 (not_3_out, u_memory_wait_controller_mem_stall);
  and and_14 (and_14_out, AddrOut[3], not_7_out, not_8_out);
  and and_15 (pc_en, not_3_out, execute_pulse);
  and and_16 (and_16_out, AddrOut[3], not_8_out, AddrOut[0]);
  or or_5 (or_7_out[0], and_17_out, and_16_out, and_14_out, and_13_out);
  Alu alu_1 (
    .A(multiplexer_5_out), .B(multiplexer_6_out), .carryIn(CarryR_q), .AluOp(aluOp), .Out(AddrOut),
    .Neg(alu_1_neg), .Zero(alu_1_zero), .CarryOut(alu_1_carryout));
  and and_17 (and_17_out, not_5_out, not_7_out, not_8_out, AddrOut[0]);
  Multiplexer multiplexer_7 (.sel(not_4_out), .in_0(1'b1), .in_1(spi_cs), .out(uio_out[2]));
  Multiplexer multiplexer_8 (.sel(spi_target), .in_0(1'b1), .in_1(spi_cs), .out(uio_out[1]));
  and and_18 (and_18_out, AddrOut[3], not_7_out, not_8_out);
  Multiplexer #(.Selector_Bits(3), .Bits(16)) multiplexer_9 (
    .sel(or_7_out), .in_0({{8{1'b0}}, ui_in}), .in_1({{8{1'b0}}, uo_out}), .in_2(timerdat1),
    .in_3(timerdat2), .in_4(rngdat0), .in_5(intr_reg), .in_6(i2cDat), .in_7(i2cDat), .out(iow_Din));
  not not_4 (not_4_out, spi_target);
  and and_19 (and_19_out, not_6_out, AddrOut[2]);
  and and_20 (and_20_out, not_6_out, AddrOut[1]);
  or or_6 (or_7_out[1], AddrOut[4], and_20_out, and_19_out, and_18_out);
  and and_21 (and_21_out, AddrOut[3], AddrOut[2]);
  and and_22 (and_22_out, AddrOut[3], AddrOut[1], AddrOut[0]);
  or or_7 (or_7_out[2], AddrOut[4], and_22_out, and_21_out);
  not not_5 (not_5_out, AddrOut[4]);
  not not_6 (not_6_out, AddrOut[3]);
  not not_7 (not_7_out, AddrOut[2]);
  not not_8 (not_8_out, AddrOut[1]);
  lfsr_RandomNumberGen #(.applicationType("IVERILOG"), .CodeFile("D:\\Desktop\\fpga\\RemedyCpu\\verilog\\lfsr.v")) u_lfsr_RandomNumberGen (
    .adrrIn(AddrOut), .dataIn(DataOut[7:0]), .ioW(imem_iow), .clk(Clk_in), .SeedAdr(16'hb), .RngAdr(16'hc),
    .Out(rngdat0));
  Comparator #(.Signed("true"), .Bits(16)) comparator_1 (.a(AddrOut), .b(16'h1), .eq(comparator_1_eq));  // open: gt, lt
  and and_23 (and_23_out, AddrOut[4], imem_iow);
  // Probe dout on DataOut[8:0]
  timer #(.applicationType("IVERILOG"), .CodeFile("D:\\Desktop\\fpga\\RemedyCpu\\verilog\\timer_small.v")) u_timer (
    .dOut(DataOut), .Addr(AddrOut), .ioW(imem_iow), .C(Clk_in), .InterLock(InterLock),
    .timerConfigAddr(16'h2), .timerTargetAddr(16'h3), .timerResetAddr(16'h4), .timerReadAddr(16'h5),
    .timerSyncStartAddr(16'ha), .rst_n(rst_n), .TimerOut(timerdat1),
    .timer_interrupt(u_timer_tiny_timer_interrupt[1]));
  timer_tiny #(.applicationType("IVERILOG"), .CodeFile("D:\\Desktop\\fpga\\RemedyCpu\\verilog\\timer_tiny.v")) u_timer_tiny (
    .dOut(DataOut[8:0]), .Addr(AddrOut), .ioW(imem_iow), .C(Clk_in), .InterLock(InterLock),
    .timerConfigAddr(16'h6), .timerTargetAddr(16'h7), .timerResetAddr(16'h8), .timerReadAddr(16'h9),
    .timerSyncStartAddr(16'ha), .rst_n(rst_n), .TimerOut(timerdat2),
    .timer_interrupt(u_timer_tiny_timer_interrupt[2]));
  and and_24 (and_24_out, comparator_1_eq, imem_iow);
  interrupt_controller_small #(.applicationType("IVERILOG"), .CodeFile("D:\\Desktop\\fpga\\RemedyCpu\\verilog\\interrupt_controller.v")) u_interrupt_controller_small (
    .dOut(DataOut[3:0]), .Addr(AddrOut), .ioW(imem_iow), .C(Clk_in), .rst_n(rst_n),
    .irq_in({i2c_inter, u_timer_tiny_timer_interrupt}), .imm(imm), .reti(Reti), .pc_en(pc_en),
    .CPUInterruptEnableAddr(16'hd), .inputInterruptAddr(16'he), .interruptRegAddr(16'hf),
    .InterruptOut(intr_reg), .intr(intr), .irq_lock(InterLock));
  register_8bit outputReg (.D(DataOut[7:0]), .C(Clk_in), .en(and_24_out), .rst(rst_n), .Q(uo_out));
  i2c_master_ctrl #(.applicationType("IVERILOG"), .CodeFile("D:\\Desktop\\fpga\\RemedyCpu\\verilog\\i2c_master_ctrl.v")) u_i2c_master_ctrl (
    .clk(Clk_in), .rst_n(rst_n), .wr_en(and_23_out), .reg_addr(AddrOut[3:0]), .cpu_din(DataOut),
    .sda_in(uio_in[5]), .scl_in(uio_in[6]), .cpu_dout(i2cDat), .sda_out(uio_out[5]), .scl_out(uio_out[6]),
    .sda_oe(uio_oe[5]), .scl_oe(uio_oe[6]), .interrupt(i2c_inter));
  Multiplexer #(.Bits(16)) multiplexer_10 (
    .sel(InterLock), .in_0({{8{1'b0}}, ui_in}), .in_1(register_2_q), .out(multiplexer_10_out));
  Register #(.Bits(16)) register_2 (
    .D(multiplexer_10_out), .C(Clk_in), .en(u_timer_tiny_timer_interrupt[0]), .Q(register_2_q));
  is_different #(.applicationType("IVERILOG"), .CodeFile("D:\\Desktop\\fpga\\RemedyCpu\\verilog\\is_different.v")) u_is_different (
    .in1(multiplexer_10_out), .in2(register_2_q), .different(u_timer_tiny_timer_interrupt[0]));

  assign {uio_oe[7], uio_oe[4:0]} = 6'b011110;
  assign {uio_out[7], uio_out[0]} = 2'b00;

  // Other names for the same wires on the sheet: OPcode[7] = imm; imem_clk = Clk_in; inputFromOutside[7:0] = ui_in;
  //   inputReg[7:0] = ui_in; io_addr[15:0] = AddrOut; io_data[15:0] = DataOut; ioR = imem_ior; ioW = imem_iow;
  //   outputToOutside[7:0] = uo_out; outR[7:0] = uo_out; rst = rst_n; scl_o = uio_out[6]; scl_oe = uio_oe[6];
  //   sda_o = uio_out[5]; sda_oe = uio_oe[5]; spi_clock_ram = uio_out[4]; spi_miso = spimiso;
  //   spi_mosi_ram = uio_out[3]; spics_flash = uio_out[2]; spics_ram = uio_out[1]; sda_in = uio_in[5];
  //   scl_in = uio_in[6]

  // Notes on the sheet:
  //   clk: Hz: 200
  //   ena: default 1
  //   Input/Output
  //   prog loads flashread.bin
  //   ControlLogic
  //   ProgramMemoryRead
  //   JumpLogic
  //   FlagStore
  //   PERIPHERAL ADDRESSES
  //   IO Addresses
  //   Write/Read Addresses
  //   RandomNumberGen
  //   PERIPHERAL BUS
  //   Timers
  //   Output
  //   input
  //   InterruptBus
  //   INTERRRRRUPT BUS
endmodule
