// Digital circuit tt_um_smallcpuVivado.dig as structural Verilog
module tt_um_smallcpuVivado (
  input  [7:0] ui_in,
  input  ena,
  input  clk,
  input  rst_n,
  output [7:0] uo_out,
  output uio_out0,
  output uio_out1,
  output uio_out2,
  output uio_out3,
  output uio_out4,
  output uio_out5,
  output uio_out6,
  output uio_out7
);

  wire abs, add_3_c_o, alu2D, and_1_out, and_2_out, and_3_out, and_4_out, and_5_out, and_7_out, and_8_out,
       and_9_out, and_11_out, and_12_out, and_13_out, and_14_out, and_15_out, and_16_out, and_17_out,
       and_18_out, and_19_out, and_21_out, and_22_out, and_24_out, and_25_out, and_27_out, and_28_out,
       and_29_out, and_30_out, and_31_out, and_32_out, and_33_out, C, comparator_1_eq, comparator_2_eq,
       comparator_3_eq, comparator_4_eq, comparator_5_eq, comparator_6_eq, comparator_7_eq, comparator_8_eq,
       comparator_9_eq, comparator_9_gt, comparator_10_eq, comparator_11_eq, comparator_12_eq, counter_1_ovf,
       d_ff_2_q, d_ff_as_1_nq, d_ff_as_1_q, dipswitch_1_out, imm, inter, interEnable, InterLock, intr, ioR,
       ioW, jk_ff_1_q, ld, multiplexer_1_out, multiplexer_11_out, multiplexer_12_out, multiplexer_15_out,
       multiplexer_17_out, muxA, not_1_out, not_3_out, or_4_out, or_5_out, or_6_out, or_8_out, or_9_out,
       RandomNUMSel, Reload_q, Reset_q, Reti, sf, src2D, st, stPC, sub_1_c_o, timer_Sel, WE, xor_1_out,
       xor_3_out, xor_4_out, xor_5_out;
  wire [1:0] counter_1_out, iem;
  wire [2:0] br, FlagOut, multiplexer_13_out, muxB, or_3_out, prescaler_q;
  wire [3:0] outputToOutside, outputToOutsideEnable, register_3_q, register_3_q_2;
  wire [4:0] aluOp;
  wire [6:0] multiplexer_7_out, OPcode;
  wire [7:0] counter_2_out, Din;
  wire [9:2] undriven;
  wire [11:0] add_1_s, add_2_s, multiplexer_2_out, multiplexer_3_out, multiplexer_4_out, multiplexer_5_out,
       multiplexer_6_out, register_1_q;
  wire [11:8] pcOut;
  wire [15:0] add_3_s, Addr, and_23_out, Dout, imreg_1_p5, mem_2_d, mem_d, multiplexer_8_out,
       multiplexer_9_out, multiplexer_10_out, multiplexer_14_out, multiplexer_18_out, multiplexer_19_out,
       neg_2_out, not_2_out, or_7_out, RandomNUM, registerblock_1_rdest, seed_q, singextend_1__4d,
       singextend_1__4s, singextend_1__8sd, sub_1_s, target_q, timer_in, xor_2_out;
  wire [15:1] intEn_q;
  wire [15:15] and_20_out;

  Multiplexer multiplexer_1 (.sel(rst_n), .in_0(clk), .in_1(C), .out(multiplexer_1_out));
  // PinControl pincontrol_1: pin names not known; wires that end beside it: uio_out0, Din[0], 1'b1, pcOut[8]
  // PinControl pincontrol_2: pin names not known; wires that end beside it: uio_out1, Din[1], 1'b1, pcOut[9]
  // PinControl pincontrol_3: pin names not known; wires that end beside it: uio_out2, Din[2], 1'b1, pcOut[10]
  // PinControl pincontrol_4: pin names not known; wires that end beside it: uio_out3, Din[3], 1'b1, pcOut[11]
  // PinControl pincontrol_5: pin names not known; wires that end beside it: uio_out4, Din[4], outputToOutsideEnable[0], outputToOutside[0]
  // PinControl pincontrol_6: pin names not known; wires that end beside it: uio_out5, Din[5], outputToOutsideEnable[1], outputToOutside[1]
  // PinControl pincontrol_7: pin names not known; wires that end beside it: uio_out6, Din[6], outputToOutsideEnable[2], outputToOutside[2]
  // PinControl pincontrol_8: pin names not known; wires that end beside it: uio_out7, Din[7], outputToOutsideEnable[3], outputToOutside[3]
  Multiplexer #(.Bits(12)) multiplexer_2 (
    .sel(rst_n), .in_0({12{1'b0}}), .in_1(multiplexer_6_out), .out(multiplexer_2_out));
  Register #(.Bits(12), .isProgramCounter("true")) PC (
    .D(multiplexer_2_out), .C(~multiplexer_1_out), .en(1'b1), .Q({pcOut, uo_out}));
  Add #(.Bits(12)) add_1 (.a({pcOut, uo_out}), .b(12'h1), .c_i(1'b0), .s(add_1_s));  // open: c_o
  Add #(.Bits(12)) add_2 (.a(add_1_s), .b(Addr[11:0]), .c_i(1'b0), .s(add_2_s));  // open: c_o
  Multiplexer #(.Bits(12)) multiplexer_3 (.sel(xor_1_out), .in_0(add_1_s), .in_1(add_2_s), .out(multiplexer_3_out));
  Multiplexer #(.Bits(12)) multiplexer_4 (
    .sel(abs), .in_0(multiplexer_3_out), .in_1(Addr[11:0]), .out(multiplexer_4_out));
  Comparator #(.Bits(16)) comparator_1 (.a(Addr), .b(16'h7), .eq(comparator_1_eq));  // open: gt, lt
  Register #(.Bits(12)) register_1 (.D(multiplexer_4_out), .C(~C), .en(and_2_out), .Q(register_1_q));
  and and_1 (and_1_out, comparator_1_eq, ioW);
  Multiplexer #(.Bits(12)) multiplexer_5 (
    .sel(and_2_out), .in_0(multiplexer_4_out), .in_1(12'h2), .out(multiplexer_5_out));
  and and_2 (and_2_out, intr, interEnable);
  Multiplexer #(.Bits(12)) multiplexer_6 (
    .sel(and_3_out), .in_0(multiplexer_5_out), .in_1(register_1_q), .out(multiplexer_6_out));
  and and_3 (and_3_out, interEnable, Reti);
  Register #(.Bits(16)) intEn (.D(Dout), .C(C), .en(and_1_out), .Q({intEn_q, interEnable}));
  Counter #(.Bits(2)) counter_1 (.en(1'b1), .C(clk), .clr(~rst_n), .out(counter_1_out), .ovf(counter_1_ovf));
  Multiplexer #(.Bits(7)) multiplexer_7 (.sel(imm), .in_0(OPcode), .in_1({7{1'b0}}), .out(multiplexer_7_out));
  not not_1 (not_1_out, clk);
  and and_4 (and_4_out, counter_1_out[0], ~counter_1_out[1]);  // And
  and and_5 (and_5_out, ~counter_1_out[0], counter_1_out[1]);  // And
  and and_6 (C, counter_1_out[0], counter_1_out[1]);
  // controllogic controllogic_1: pin names not known; wires that end beside it: multiplexer_7_out[6], multiplexer_7_out[5], multiplexer_7_out[4], multiplexer_7_out[3], multiplexer_7_out[2], multiplexer_7_out[1], multiplexer_7_out[0], muxB[2], muxB[1], muxB[0], src2D, aluOp[4], aluOp[3], aluOp[2], aluOp[1], aluOp[0], WE, sf, alu2D, iem[1], iem[0], br[2], br[1], br[0], muxA, ld, st, abs, ioW, ioR, stPC
  Register #(.Bits(8)) register_2 (.D(ui_in), .C(not_1_out), .en(and_4_out), .Q({imm, OPcode}));
  Register #(.Bits(8)) register_3 (.D(ui_in), .C(not_1_out), .en(and_5_out), .Q({register_3_q_2, register_3_q}));
  or or_1 (or_3_out[2], timer_Sel, RandomNUMSel);
  Multiplexer #(.Selector_Bits(3), .Bits(16)) multiplexer_8 (
    .sel(or_3_out), .in_0(Addr), .in_1(multiplexer_19_out), .in_2({{8{1'b0}}, Din}),
    .in_3({4'b0000, add_1_s}), .in_4(timer_in), .in_5(RandomNUM), .in_6({16{1'b0}}), .in_7({16{1'b0}}),
    .out(multiplexer_8_out));
  or or_2 (or_3_out[1], ioR, stPC);
  or or_3 (or_3_out[0], stPC, ld, RandomNUMSel);
  RegisterBlock registerblock_1 (
    .DataIn(multiplexer_8_out), .WE(WE), .clk(C), .src(register_3_q), .Dest(register_3_q_2),
    .RDest(registerblock_1_rdest), .Rsrc(Dout));  // open: rst
  singExtend singextend_1 (
    .inst({imm, OPcode, register_3_q_2, register_3_q}), ._4S(singextend_1__4s), ._8SD(singextend_1__8sd),
    ._4D(singextend_1__4d));
  // ImReg imreg_1: pin names not known; wires that end beside it: imm, iem, C, {imm, OPcode, register_3_q_2, register_3_q}, imreg_1_p5
  Multiplexer #(.Bits(16)) multiplexer_9 (
    .sel(muxA), .in_0(registerblock_1_rdest), .in_1(Dout),
    .out({multiplexer_9_out[11:8], multiplexer_9_out[15:12], multiplexer_9_out[3:0], multiplexer_9_out[7:4]}));
  Multiplexer #(.Selector_Bits(3), .Bits(16)) multiplexer_10 (
    .sel(muxB), .in_0(Dout), .in_1({16{1'b0}}), .in_2(imreg_1_p5), .in_3({16{1'b0}}), .in_4({16{1'b0}}),
    .in_5(singextend_1__4s), .in_6(singextend_1__8sd), .in_7(singextend_1__4d), .out(multiplexer_10_out));
  xor xor_1 (xor_1_out, multiplexer_11_out, br[2]);
  Multiplexer #(.Selector_Bits(2)) multiplexer_11 (
    .sel(br[1:0]), .in_0(1'b0), .in_1(FlagOut[0]), .in_2(FlagOut[1]), .in_3(FlagOut[2]),
    .out(multiplexer_11_out));
  and and_7 (and_7_out, d_ff_2_q, ~Reti);  // And
  and and_8 (and_8_out, inter, interEnable);
  and and_9 (and_9_out, InterLock, ~Reti);  // And
  or or_4 (or_4_out, and_7_out, and_8_out);
  or or_5 (or_5_out, and_9_out, intr);
  Register Neg (.D(Addr[15]), .C(C), .en(sf), .Q(FlagOut[2]));
  Register Zero (.D(comparator_11_eq), .C(C), .en(sf), .Q(FlagOut[1]));
  Register Carry (.D(multiplexer_17_out), .C(C), .en(sf), .Q(FlagOut[0]));
  D_FF d_ff (.D(or_5_out), .C(~C), .Q(InterLock));  // open: nQ
  D_FF d_ff_2 (.D(or_4_out), .C(~C), .Q(d_ff_2_q));  // open: nQ
  and and_10 (intr, ~InterLock, ~imm, d_ff_2_q, ~1'b0);  // And
  Comparator #(.Signed("true"), .Bits(16)) comparator_2 (.a(Addr), .b(16'h5), .eq(comparator_2_eq));  // open: gt, lt
  Comparator #(.Signed("true"), .Bits(16)) comparator_3 (.a(Addr), .b(16'h3), .eq(comparator_3_eq));  // open: gt, lt
  Comparator #(.Signed("true"), .Bits(16)) comparator_4 (.a(Addr), .b(16'h6), .eq(comparator_4_eq));  // open: gt, lt
  Comparator #(.Signed("true"), .Bits(16)) comparator_5 (.a(Addr), .b(16'h1), .eq(comparator_5_eq));  // open: gt, lt
  Comparator #(.Signed("true"), .Bits(16)) comparator_6 (.a(Addr), .b(16'h2), .eq(comparator_6_eq));  // open: gt, lt
  Comparator #(.Signed("true"), .Bits(16)) comparator_7 (.a(Addr), .b(16'h9), .eq(comparator_7_eq));  // open: gt, lt
  Comparator #(.Signed("true"), .Bits(16)) comparator_8 (.a(Addr), .b(16'h8), .eq(comparator_8_eq));  // open: gt, lt
  and and_11 (and_11_out, comparator_2_eq, ioW);
  and and_12 (and_12_out, comparator_3_eq, ioW);
  and and_13 (and_13_out, comparator_4_eq, ioW);
  and and_14 (and_14_out, comparator_5_eq, ioW);
  and and_15 (and_15_out, comparator_6_eq, ioW);
  and and_16 (and_16_out, comparator_7_eq, ioW);
  and and_17 (and_17_out, comparator_8_eq, ioW);
  and and_18 (and_18_out, Dout[0], and_13_out);
  Register timer_is_active (.D(Dout[0]), .C(C), .en(and_14_out));  // open: Q
  Register Reload (.D(Dout[0]), .C(C), .en(and_11_out), .Q(Reload_q));
  Register #(.Bits(16)) target (.D(Dout), .C(C), .en(and_12_out), .Q(target_q));
  Register #(.Bits(3)) prescaler (.D(Dout[2:0]), .C(C), .en(and_15_out), .Q(prescaler_q));
  Register #(.Bits(4)) register_4 (.D(Dout[3:0]), .C(C), .en(and_16_out), .Q(outputToOutsideEnable));
  Register #(.Bits(4)) register_5 (.D(Dout[3:0]), .C(C), .en(and_17_out), .Q(outputToOutside));
  JK_FF Reset (.J(and_18_out), .C(C), .K(1'b1), .Q(Reset_q));  // open: nQ
  DipSwitch dipswitch_1 (.out(dipswitch_1_out));
  and and_19 (and_19_out, comparator_10_eq, Reload_q);
  and and_20 (and_20_out[15], aluOp[4], FlagOut[0]);
  and and_21 (and_21_out, comparator_10_eq, ~comparator_9_eq);  // And
  or or_6 (or_6_out, and_19_out, Reset_q);
  Comparator #(.Bits(16)) comparator_9 (
    .a(target_q), .b({16{1'b0}}), .gt(comparator_9_gt), .eq(comparator_9_eq));  // open: lt
  Counter #(.Bits(8)) counter_2 (.en(dipswitch_1_out), .C(C), .clr(1'b0), .out(counter_2_out));  // open: ovf
  and and_22 (and_22_out, ~comparator_9_eq, or_6_out);  // And
  Multiplexer #(.Selector_Bits(3)) multiplexer_12 (
    .sel(multiplexer_13_out), .in_0(counter_2_out[0]), .in_1(counter_2_out[1]), .in_2(counter_2_out[2]),
    .in_3(counter_2_out[3]), .in_4(counter_2_out[4]), .in_5(counter_2_out[5]), .in_6(counter_2_out[6]),
    .in_7(counter_2_out[7]), .out(multiplexer_12_out));
  Multiplexer #(.Bits(3)) multiplexer_13 (
    .sel(and_22_out), .in_0(prescaler_q), .in_1(3'b000), .out(multiplexer_13_out));
  Add #(.Bits(16)) add_3 (
    .a({multiplexer_9_out[11:8], multiplexer_9_out[15:12], multiplexer_9_out[3:0], multiplexer_9_out[7:4]}),
    .b(multiplexer_10_out), .c_i(and_20_out[15]), .s(add_3_s), .c_o(add_3_c_o));
  Sub #(.Bits(16)) sub_1 (
    .a({multiplexer_9_out[11:8], multiplexer_9_out[15:12], multiplexer_9_out[3:0], multiplexer_9_out[7:4]}),
    .b(multiplexer_10_out), .c_i(and_20_out[15]), .s(sub_1_s), .c_o(sub_1_c_o));
  assign and_23_out = {multiplexer_9_out[11:8], multiplexer_9_out[15:12], multiplexer_9_out[3:0], multiplexer_9_out[7:4]} & multiplexer_10_out;  // And and_23, 16 bits wide
  assign or_7_out = {multiplexer_9_out[11:8], multiplexer_9_out[15:12], multiplexer_9_out[3:0], multiplexer_9_out[7:4]} | multiplexer_10_out;  // Or or_7, 16 bits wide
  assign xor_2_out = {multiplexer_9_out[11:8], multiplexer_9_out[15:12], multiplexer_9_out[3:0], multiplexer_9_out[7:4]} ^ multiplexer_10_out;  // XOr xor_2, 16 bits wide
  assign not_2_out = ~{multiplexer_9_out[11:8], multiplexer_9_out[15:12], multiplexer_9_out[3:0], multiplexer_9_out[7:4]};  // Not not_2, 16 bits wide
  Neg #(.Bits(16)) neg_2 (
    .in({multiplexer_9_out[11:8], multiplexer_9_out[15:12], multiplexer_9_out[3:0], multiplexer_9_out[7:4]}),
    .out(neg_2_out));
  Multiplexer #(.Bits(16)) multiplexer_14 (
    .sel(comparator_9_gt), .in_0({16{1'b0}}), .in_1(target_q), .out(multiplexer_14_out));
  and and_24 (and_24_out, and_21_out, ~and_22_out);  // And
  or or_8 (or_8_out, InterLock, and_24_out);
  Multiplexer multiplexer_15 (.sel(or_8_out), .in_0(multiplexer_12_out), .in_1(1'b1), .out(multiplexer_15_out));
  CounterPreset #(.Bits(16)) counterpreset_1 (
    .en(dipswitch_1_out), .C(multiplexer_15_out), .dir(1'b0), .in({16{1'b0}}), .ld(and_22_out), .clr(1'b0),
    .out(timer_in));  // open: ovf
  Multiplexer #(.Selector_Bits(4), .Bits(16)) multiplexer_16 (
    .sel(aluOp[3:0]), .in_0(multiplexer_10_out), .in_1(add_3_s), .in_2(sub_1_s), .in_3(and_23_out),
    .in_4(or_7_out), .in_5(xor_2_out), .in_6(not_2_out), .in_7(neg_2_out),
    .in_8({multiplexer_9_out[10:8], multiplexer_9_out[15:12], multiplexer_9_out[3:0], multiplexer_9_out[7:4], and_20_out[15]}),
    .in_9({and_20_out[15], multiplexer_9_out[11:8], multiplexer_9_out[15:12], multiplexer_9_out[3:0], multiplexer_9_out[7:5]}),
    .in_10({{2{multiplexer_9_out[11]}}, multiplexer_9_out[10:8], multiplexer_9_out[15:12], multiplexer_9_out[3:0], multiplexer_9_out[7:5]}),
    .in_11({multiplexer_9_out[3:0], multiplexer_9_out[7:4], multiplexer_9_out[11:8], multiplexer_9_out[15:12]}),
    .in_12(multiplexer_9_out), .in_13({16{1'b0}}), .in_14({16{1'b0}}), .in_15({16{1'b0}}), .out(Addr));
  Multiplexer #(.Selector_Bits(4)) multiplexer_17 (
    .sel(aluOp[3:0]), .in_0(1'b0), .in_1(add_3_c_o), .in_2(sub_1_c_o), .in_3(1'b0), .in_4(1'b0), .in_5(1'b0),
    .in_6(1'b0), .in_7(1'b0), .in_8(multiplexer_9_out[11]), .in_9(multiplexer_9_out[4]),
    .in_10(multiplexer_9_out[4]), .in_11(1'b0), .in_12(1'b0), .in_13(1'b0), .in_14(1'b0), .in_15(1'b0),
    .out(multiplexer_17_out));
  Comparator #(.Bits(16)) comparator_10 (.a(multiplexer_14_out), .b(timer_in), .eq(comparator_10_eq));  // open: gt, lt
  and and_25 (and_25_out, ~comparator_9_eq, comparator_10_eq);  // And
  Comparator #(.Signed("true"), .Bits(16)) comparator_11 (
    .a(Addr), .b({16{1'b0}}), .eq(comparator_11_eq));  // open: gt, lt
  Comparator #(.Signed("true"), .Bits(16)) comparator_12 (.a(Addr), .b(16'h8), .eq(comparator_12_eq));  // open: gt, lt
  and and_26 (inter, ~InterLock, and_25_out);  // And
  and and_27 (and_27_out, comparator_12_eq, ioW);
  not not_3 (not_3_out, or_9_out);
  and and_28 (and_28_out, C, and_27_out);
  and and_29 (and_29_out, and_27_out, not_3_out);
  JK_FF jk_ff_1 (.J(or_9_out), .C(C), .K(or_9_out), .Q(jk_ff_1_q));  // open: nQ
  D_FF_AS d_ff_as_1 (.Set(1'b0), .D(d_ff_as_1_nq), .C(and_28_out), .Clr(jk_ff_1_q), .Q(d_ff_as_1_q), .nQ(d_ff_as_1_nq));
  Register #(.Bits(16)) seed (.D(Dout), .C(C), .en(and_27_out), .Q(seed_q));
  or or_9 (or_9_out, d_ff_as_1_q, jk_ff_1_q);
  Multiplexer #(.Bits(16)) multiplexer_18 (
    .sel(and_27_out), .in_0({16{1'b0}}), .in_1(seed_q), .out(multiplexer_18_out));
  // Probe on RandomNUM
  D_FF_AS d_ff_as_2 (
    .Set(multiplexer_18_out[0]), .D(xor_3_out), .C(C), .Clr(and_29_out), .Q(RandomNUM[0]));  // open: nQ
  and and_30 (and_30_out, Addr[5], st);
  and and_31 (and_31_out, Addr[5], ld);
  D_FF_AS d_ff_as_3 (
    .Set(multiplexer_18_out[1]), .D(RandomNUM[0]), .C(C), .Clr(and_29_out), .Q(RandomNUM[1]));  // open: nQ
  D_FF_AS d_ff_as_4 (
    .Set(multiplexer_18_out[2]), .D(RandomNUM[1]), .C(C), .Clr(and_29_out), .Q(RandomNUM[2]));  // open: nQ
  and and_32 (and_32_out, st, ~Addr[5]);  // And
  and and_33 (and_33_out, ld, ~Addr[5]);  // And
  RAMDualPort #(.Bits(16), .Addr_Bits(10)) mem (
    .A({undriven, Addr[1:0]}), .Din(Dout), .str(and_30_out), .C(C), .ld(and_31_out), .D(mem_d));
  D_FF_AS d_ff_as_5 (
    .Set(multiplexer_18_out[3]), .D(RandomNUM[2]), .C(C), .Clr(and_29_out), .Q(RandomNUM[3]));  // open: nQ
  D_FF_AS d_ff_as_6 (
    .Set(multiplexer_18_out[4]), .D(RandomNUM[3]), .C(C), .Clr(and_29_out), .Q(RandomNUM[4]));  // open: nQ
  xor xor_3 (xor_3_out, RandomNUM[5], xor_4_out);
  D_FF_AS d_ff_as_7 (
    .Set(multiplexer_18_out[5]), .D(RandomNUM[4]), .C(C), .Clr(and_29_out), .Q(RandomNUM[5]));  // open: nQ
  RAMDualPort #(.AddrBits(5), .Bits(16), .Addr_Bits(10)) mem_2 (
    .A(Addr[4:0]), .Din(Dout), .str(and_32_out), .C(C), .ld(and_33_out), .D(mem_2_d));
  D_FF_AS d_ff_as_8 (
    .Set(multiplexer_18_out[6]), .D(RandomNUM[5]), .C(C), .Clr(and_29_out), .Q(RandomNUM[6]));  // open: nQ
  Multiplexer #(.Bits(16)) multiplexer_19 (.sel(Addr[5]), .in_0(mem_2_d), .in_1(mem_d), .out(multiplexer_19_out));
  D_FF_AS d_ff_as_9 (
    .Set(multiplexer_18_out[7]), .D(RandomNUM[6]), .C(C), .Clr(and_29_out), .Q(RandomNUM[7]));  // open: nQ
  D_FF_AS d_ff_as_10 (
    .Set(multiplexer_18_out[8]), .D(RandomNUM[7]), .C(C), .Clr(and_29_out), .Q(RandomNUM[8]));  // open: nQ
  xor xor_4 (xor_4_out, RandomNUM[10], xor_5_out);
  D_FF_AS d_ff_as_11 (
    .Set(multiplexer_18_out[9]), .D(RandomNUM[8]), .C(C), .Clr(and_29_out), .Q(RandomNUM[9]));  // open: nQ
  D_FF_AS d_ff_as_12 (
    .Set(multiplexer_18_out[10]), .D(RandomNUM[9]), .C(C), .Clr(and_29_out), .Q(RandomNUM[10]));  // open: nQ
  D_FF_AS d_ff_as_13 (
    .Set(multiplexer_18_out[11]), .D(RandomNUM[10]), .C(C), .Clr(and_29_out), .Q(RandomNUM[11]));  // open: nQ
  D_FF_AS d_ff_as_14 (
    .Set(multiplexer_18_out[12]), .D(RandomNUM[11]), .C(C), .Clr(and_29_out), .Q(RandomNUM[12]));  // open: nQ
  xor xor_5 (xor_5_out, RandomNUM[12], RandomNUM[14]);
  D_FF_AS d_ff_as_15 (
    .Set(multiplexer_18_out[13]), .D(RandomNUM[12]), .C(C), .Clr(and_29_out), .Q(RandomNUM[13]));  // open: nQ
  D_FF_AS d_ff_as_16 (
    .Set(multiplexer_18_out[14]), .D(RandomNUM[13]), .C(C), .Clr(and_29_out), .Q(RandomNUM[14]));  // open: nQ
  D_FF_AS d_ff_as_17 (
    .Set(multiplexer_18_out[15]), .D(RandomNUM[14]), .C(C), .Clr(and_29_out), .Q(RandomNUM[15]));  // open: nQ
  // Pins of 2 and 10 bits meet at {undriven, Addr[1:0]}

  // Other names for the same wires on the sheet: OPcode[7] = imm; sel[3:0] = aluOp[3:0]; inputFromOutside[7:0] = Din;
  //   AddressDebug[15:0] = Addr; Clk_in = clk; DoutDebug[15:0] = Dout; enable = ena; opcode_in[7:0] = ui_in;
  //   pcOut[7:0] = uo_out

  // Notes on the sheet:
  //   clk: Hz: 1000
  //   rst_n: default 1
  //   PC
  //   FlagStore
  //   interrupt Logic
  //   Timer
  //   input
  //   Output_En
  //   Output
  //   ALU
  //   logical shift left
  //   logival shift right
  //   arithmetic shift right
  //   swapBytes
  //   swapNibbles
  //   RandomNumberGen
endmodule
