// Digital circuit tt_um_smallcpu_spi.dig as structural Verilog
module tt_um_smallcpu_spi (
  input  [7:0] Input,
  input  rst_n,
  input  clk_internal,
  input  [15:0] in_6,
  output [3:0] debugOut,
  output [7:0] Output
);

  wire _1_addressable_register_1_dataout, abs, add_1_c_o, and_1_out, and_2_out, and_3_out, and_4_out,
       and_5_out, and_6_out, and_7_out, and_8_out, and_12_out, and_13_out, and_17_out, comparator_1_eq,
       comparator_2_eq, comparator_3_eq, comparator_4_eq, comparator_5_eq, comparator_6_gt, comparator_6_lt,
       comparator_7_eq, comparator_8_eq, comparator_9_gt, comparator_9_lt, d_ff_as_1_nq, d_ff_as_1_q, d_ff_q,
       inputEn, inter, interEn, interEnable, InterLock, intr, ioR, ioW, jk_ff_1_q, ld, multiplexer_3_out,
       multiplexer_5_out, multiplexer_6_out, multiplexer_7_out, multiplexer_11_out, muxA, not_2_out,
       or_4_out, or_5_out, or_6_out, or_8_out, or_9_out, or_10_out, RandomNUMSel, read_the_flags, Reti, rst,
       sf, st, store_the_flags, stPC, sub_1_c_o, WE, xor_1_out, xor_2_out, xor_3_out, xor_5_out;
  wire [1:0] iem;
  wire [2:0] br, FlagOut, muxB, or_3_out;
  wire [3:0] and_16_out;
  wire [4:0] aluOp;
  wire [6:0] multiplexer_1_out;
  wire [7:0] outputToOutsideEnable;
  wire [15:0] add_1_s, AddrOut, and_11_out, DataOut, divs_1_bolum, divs_1_kalan, imreg_1_p5, inputReg,
       interruptReg, iow_Din, mul_1_mul, multiplexer_2_out, multiplexer_4_out, multiplexer_8_out,
       multiplexer_9_out, multiplexer_13_out, multiplexer_14_out, multiplexer_15_out, neg_2_out, not_3_out,
       or_7_out, RandomNUM, register_1_q, register_2_q, registerblock_1_rdest, seed_q, singextend_1__4d,
       singextend_1__4s, singextend_1__8sd, sub_1_s, time0In, time1In, time2In, u_programCounter_nextpc,
       xor_4_out;
  wire [15:15] and_10_out;
  wire [31:16] mul_1_mul_2;

  not not_1 (rst, rst_n);
  _1_addressable_register intEn (
    .Datain(DataOut), .ioW(ioW), .addrIn(AddrOut), .address(16'ha), .clk(clk_internal), .ioR(ioW),
    .DataOut(interEnable));  // open: Dataiow
  and and_1 (and_1_out, intr, interEnable);
  and and_2 (and_2_out, interEnable, Reti);
  programCounter #(.applicationType("IVERILOG"), .CodeFile("C:\\Users\\Berkant\\Desktop\\fpga\\RemedyCpu\\verilog\\programCounter.v")) u_programCounter (
    .AluIn(AddrOut), .clk(clk_internal), .rst(rst), .absJmp(abs), .intr(and_1_out), .reti(and_2_out),
    .relJmp(xor_1_out), .Nextpc(u_programCounter_nextpc));  // open: PC
  Multiplexer #(.Bits(7)) multiplexer_1 (.sel(in_6[15]), .in_0(in_6[14:8]), .in_1({7{1'b0}}), .out(multiplexer_1_out));
  // controllogic controllogic_1: pin names not known; wires that end beside it: multiplexer_1_out[6], multiplexer_1_out[5], multiplexer_1_out[4], multiplexer_1_out[3], multiplexer_1_out[2], multiplexer_1_out[1], multiplexer_1_out[0], muxB[2], muxB[1], muxB[0], aluOp[4], aluOp[3], aluOp[2], aluOp[1], aluOp[0], WE, sf, iem[1], iem[0], br[2], br[1], br[0], muxA, ld, st, abs, ioW, ioR, stPC, Reti, RandomNUMSel
  Comparator #(.Signed("true"), .Bits(16)) comparator_1 (.a(AddrOut), .b(16'hd), .eq(comparator_1_eq));  // open: gt, lt
  or or_1 (or_3_out[2], 1'b0, RandomNUMSel, read_the_flags);
  Multiplexer #(.Selector_Bits(3), .Bits(16)) multiplexer_2 (
    .sel(or_3_out), .in_0(AddrOut), .in_1(AddrOut), .in_2(iow_Din), .in_3(u_programCounter_nextpc),
    .in_4({16{1'b0}}), .in_5(RandomNUM), .in_6({{13{1'b0}}, FlagOut}), .in_7({16{1'b0}}),
    .out(multiplexer_2_out));
  or or_2 (or_3_out[1], ioR, stPC, read_the_flags);
  and and_3 (and_3_out, comparator_1_eq, ioW);
  or or_3 (or_3_out[0], ld, stPC, RandomNUMSel);
  and and_4 (and_4_out, and_3_out, not_2_out);
  not not_2 (not_2_out, or_4_out);
  and and_5 (and_5_out, clk_internal, and_3_out);
  xor xor_1 (xor_1_out, multiplexer_3_out, br[2]);
  JK_FF jk_ff_1 (.J(or_4_out), .C(clk_internal), .K(or_4_out), .Q(jk_ff_1_q));  // open: nQ
  Multiplexer #(.Selector_Bits(2)) multiplexer_3 (
    .sel(br[1:0]), .in_0(1'b0), .in_1(FlagOut[0]), .in_2(FlagOut[1]), .in_3(FlagOut[2]),
    .out(multiplexer_3_out));
  D_FF_AS d_ff_as_1 (.Set(1'b0), .D(d_ff_as_1_nq), .C(and_5_out), .Clr(jk_ff_1_q), .Q(d_ff_as_1_q), .nQ(d_ff_as_1_nq));
  Register #(.Bits(16)) seed (.D(DataOut), .C(clk_internal), .en(and_3_out), .Q(seed_q));
  or or_4 (or_4_out, d_ff_as_1_q, jk_ff_1_q);
  Multiplexer #(.Bits(16)) multiplexer_4 (.sel(and_3_out), .in_0({16{1'b0}}), .in_1(seed_q), .out(multiplexer_4_out));
  register_1bit Neg (.D(multiplexer_7_out), .C(clk_internal), .en(sf), .rst(rst), .Q(FlagOut[2]));
  register_1bit Zero (.D(multiplexer_6_out), .C(clk_internal), .en(sf), .rst(rst), .Q(FlagOut[1]));
  register_1bit Carry (.D(multiplexer_5_out), .C(clk_internal), .en(sf), .rst(rst), .Q(FlagOut[0]));
  // Probe on RandomNUM
  RegisterBlock registerblock_1 (
    .DataIn(multiplexer_2_out), .WE(WE), .clk(clk_internal), .src(in_6[3:0]), .Dest(in_6[7:4]), .rst(rst),
    .RDest(registerblock_1_rdest), .Rsrc(DataOut));
  // ImReg imreg_1: pin names not known; wires that end beside it: in_6[15], iem, clk_internal, in_6, imreg_1_p5
  singExtend singextend_1 (.inst(in_6), ._4S(singextend_1__4s), ._8SD(singextend_1__8sd), ._4D(singextend_1__4d));
  and and_6 (and_6_out, d_ff_q, ~Reti);  // And
  and and_7 (and_7_out, inter, interEnable);
  Multiplexer multiplexer_5 (
    .sel(store_the_flags), .in_0(multiplexer_11_out), .in_1(multiplexer_8_out[4]), .out(multiplexer_5_out));
  Multiplexer multiplexer_6 (
    .sel(store_the_flags), .in_0(comparator_2_eq), .in_1(multiplexer_8_out[5]), .out(multiplexer_6_out));
  D_FF_AS d_ff_as_2 (
    .Set(multiplexer_4_out[0]), .D(xor_2_out), .C(clk_internal), .Clr(and_4_out), .Q(RandomNUM[0]));  // open: nQ
  and and_8 (and_8_out, InterLock, ~Reti);  // And
  Multiplexer multiplexer_7 (
    .sel(store_the_flags), .in_0(AddrOut[15]), .in_1(multiplexer_8_out[6]), .out(multiplexer_7_out));
  or or_5 (or_5_out, and_8_out, intr);
  or or_6 (or_6_out, and_6_out, and_7_out);
  D_FF_AS d_ff_as_3 (
    .Set(multiplexer_4_out[1]), .D(RandomNUM[0]), .C(clk_internal), .Clr(and_4_out), .Q(RandomNUM[1]));  // open: nQ
  D_FF d_ff (.D(or_6_out), .C(~clk_internal), .Q(d_ff_q));  // open: nQ
  Multiplexer #(.Bits(16)) multiplexer_8 (
    .sel(muxA), .in_0(registerblock_1_rdest), .in_1(DataOut),
    .out({multiplexer_8_out[11:8], multiplexer_8_out[15:12], multiplexer_8_out[3:0], multiplexer_8_out[7:4]}));
  Multiplexer #(.Selector_Bits(3), .Bits(16)) multiplexer_9 (
    .sel(muxB), .in_0(DataOut), .in_1({16{1'b0}}), .in_2(imreg_1_p5), .in_3({16{1'b0}}), .in_4({16{1'b0}}),
    .in_5(singextend_1__4s), .in_6(singextend_1__8sd), .in_7(singextend_1__4d), .out(multiplexer_9_out));
  D_FF_AS d_ff_as_4 (
    .Set(multiplexer_4_out[2]), .D(RandomNUM[1]), .C(clk_internal), .Clr(and_4_out), .Q(RandomNUM[2]));  // open: nQ
  D_FF d_ff_2 (.D(or_5_out), .C(~clk_internal), .Q(InterLock));  // open: nQ
  D_FF_AS d_ff_as_5 (
    .Set(multiplexer_4_out[3]), .D(RandomNUM[2]), .C(clk_internal), .Clr(and_4_out), .Q(RandomNUM[3]));  // open: nQ
  D_FF_AS d_ff_as_6 (
    .Set(multiplexer_4_out[4]), .D(RandomNUM[3]), .C(clk_internal), .Clr(and_4_out), .Q(RandomNUM[4]));  // open: nQ
  and and_9 (intr, ~InterLock, ~in_6[15], d_ff_q, ~1'b0);  // And
  xor xor_2 (xor_2_out, RandomNUM[5], xor_3_out);
  D_FF_AS d_ff_as_7 (
    .Set(multiplexer_4_out[5]), .D(RandomNUM[4]), .C(clk_internal), .Clr(and_4_out), .Q(RandomNUM[5]));  // open: nQ
  D_FF_AS d_ff_as_8 (
    .Set(multiplexer_4_out[6]), .D(RandomNUM[5]), .C(clk_internal), .Clr(and_4_out), .Q(RandomNUM[6]));  // open: nQ
  and and_10 (and_10_out[15], aluOp[4], FlagOut[0]);
  D_FF_AS d_ff_as_9 (
    .Set(multiplexer_4_out[7]), .D(RandomNUM[6]), .C(clk_internal), .Clr(and_4_out), .Q(RandomNUM[7]));  // open: nQ
  D_FF_AS d_ff_as_10 (
    .Set(multiplexer_4_out[8]), .D(RandomNUM[7]), .C(clk_internal), .Clr(and_4_out), .Q(RandomNUM[8]));  // open: nQ
  Mul #(.Bits(16)) mul_1 (
    .a({multiplexer_8_out[11:8], multiplexer_8_out[15:12], multiplexer_8_out[3:0], multiplexer_8_out[7:4]}),
    .b(multiplexer_9_out), .mul({mul_1_mul_2, mul_1_mul}));
  divs divs_1 (
    .bolunen({multiplexer_8_out[11:8], multiplexer_8_out[15:12], multiplexer_8_out[3:0], multiplexer_8_out[7:4]}),
    .Bolen(multiplexer_9_out), .bolum(divs_1_bolum), .Kalan(divs_1_kalan));
  xor xor_3 (xor_3_out, RandomNUM[10], xor_5_out);
  D_FF_AS d_ff_as_11 (
    .Set(multiplexer_4_out[9]), .D(RandomNUM[8]), .C(clk_internal), .Clr(and_4_out), .Q(RandomNUM[9]));  // open: nQ
  Add #(.Bits(16)) add_1 (
    .a({multiplexer_8_out[11:8], multiplexer_8_out[15:12], multiplexer_8_out[3:0], multiplexer_8_out[7:4]}),
    .b(multiplexer_9_out), .c_i(and_10_out[15]), .s(add_1_s), .c_o(add_1_c_o));
  Sub #(.Bits(16)) sub_1 (
    .a({multiplexer_8_out[11:8], multiplexer_8_out[15:12], multiplexer_8_out[3:0], multiplexer_8_out[7:4]}),
    .b(multiplexer_9_out), .c_i(and_10_out[15]), .s(sub_1_s), .c_o(sub_1_c_o));
  assign and_11_out = {multiplexer_8_out[11:8], multiplexer_8_out[15:12], multiplexer_8_out[3:0], multiplexer_8_out[7:4]} & multiplexer_9_out;  // And and_11, 16 bits wide
  assign or_7_out = {multiplexer_8_out[11:8], multiplexer_8_out[15:12], multiplexer_8_out[3:0], multiplexer_8_out[7:4]} | multiplexer_9_out;  // Or or_7, 16 bits wide
  assign xor_4_out = {multiplexer_8_out[11:8], multiplexer_8_out[15:12], multiplexer_8_out[3:0], multiplexer_8_out[7:4]} ^ multiplexer_9_out;  // XOr xor_4, 16 bits wide
  assign not_3_out = ~{multiplexer_8_out[11:8], multiplexer_8_out[15:12], multiplexer_8_out[3:0], multiplexer_8_out[7:4]};  // Not not_3, 16 bits wide
  Neg #(.Bits(16)) neg_2 (
    .in({multiplexer_8_out[11:8], multiplexer_8_out[15:12], multiplexer_8_out[3:0], multiplexer_8_out[7:4]}),
    .out(neg_2_out));
  D_FF_AS d_ff_as_12 (
    .Set(multiplexer_4_out[10]), .D(RandomNUM[9]), .C(clk_internal), .Clr(and_4_out), .Q(RandomNUM[10]));  // open: nQ
  D_FF_AS d_ff_as_13 (
    .Set(multiplexer_4_out[11]), .D(RandomNUM[10]), .C(clk_internal), .Clr(and_4_out), .Q(RandomNUM[11]));  // open: nQ
  xor xor_5 (xor_5_out, RandomNUM[12], RandomNUM[14]);
  D_FF_AS d_ff_as_14 (
    .Set(multiplexer_4_out[12]), .D(RandomNUM[11]), .C(clk_internal), .Clr(and_4_out), .Q(RandomNUM[12]));  // open: nQ
  D_FF_AS d_ff_as_15 (
    .Set(multiplexer_4_out[13]), .D(RandomNUM[12]), .C(clk_internal), .Clr(and_4_out), .Q(RandomNUM[13]));  // open: nQ
  D_FF_AS d_ff_as_16 (
    .Set(multiplexer_4_out[14]), .D(RandomNUM[13]), .C(clk_internal), .Clr(and_4_out), .Q(RandomNUM[14]));  // open: nQ
  Multiplexer #(.Selector_Bits(4), .Bits(16)) multiplexer_10 (
    .sel(aluOp[3:0]), .in_0(multiplexer_9_out), .in_1(add_1_s), .in_2(sub_1_s), .in_3(and_11_out),
    .in_4(or_7_out), .in_5(xor_4_out), .in_6(not_3_out), .in_7(neg_2_out),
    .in_8({multiplexer_8_out[10:8], multiplexer_8_out[15:12], multiplexer_8_out[3:0], multiplexer_8_out[7:4], and_10_out[15]}),
    .in_9({and_10_out[15], multiplexer_8_out[11:8], multiplexer_8_out[15:12], multiplexer_8_out[3:0], multiplexer_8_out[7:5]}),
    .in_10({{2{multiplexer_8_out[11]}}, multiplexer_8_out[10:8], multiplexer_8_out[15:12], multiplexer_8_out[3:0], multiplexer_8_out[7:5]}),
    .in_11({multiplexer_8_out[3:0], multiplexer_8_out[7:4], multiplexer_8_out[11:8], multiplexer_8_out[15:12]}),
    .in_12(multiplexer_8_out), .in_13(mul_1_mul), .in_14(divs_1_bolum), .in_15(divs_1_kalan), .out(AddrOut));
  Multiplexer #(.Selector_Bits(4)) multiplexer_11 (
    .sel(aluOp[3:0]), .in_0(1'b0), .in_1(add_1_c_o), .in_2(sub_1_c_o), .in_3(1'b0), .in_4(1'b0), .in_5(1'b0),
    .in_6(1'b0), .in_7(1'b0), .in_8(multiplexer_8_out[11]), .in_9(multiplexer_8_out[4]),
    .in_10(multiplexer_8_out[4]), .in_11(1'b0), .in_12(1'b0), .in_13(1'b0), .in_14(1'b0), .in_15(1'b0),
    .out(multiplexer_11_out));
  D_FF_AS d_ff_as_17 (
    .Set(multiplexer_4_out[15]), .D(RandomNUM[14]), .C(clk_internal), .Clr(and_4_out), .Q(RandomNUM[15]));  // open: nQ
  Comparator #(.Signed("true"), .Bits(16)) comparator_2 (
    .a(AddrOut), .b({16{1'b0}}), .eq(comparator_2_eq));  // open: gt, lt
  timer timer0 (
    .dOut(DataOut), .Addr(AddrOut), .ioW(ioW), .ioR(ioR), .C(clk_internal), .InterLock(InterLock),
    .timerConfigAddr(16'h1), .timerTargetAddr(16'h2), .timerResetAddr(16'h3), .timerReadAddr(16'h1),
    .rst(rst), .TimerOut(time0In), .\timerİnterrupt (and_16_out[0]));
  timer timer1 (
    .dOut(DataOut), .Addr(AddrOut), .ioW(ioW), .ioR(ioR), .C(clk_internal), .InterLock(InterLock),
    .timerConfigAddr(16'h4), .timerTargetAddr(16'h5), .timerResetAddr(16'h6), .timerReadAddr(16'h2),
    .rst(rst), .TimerOut(time1In), .\timerİnterrupt (and_16_out[1]));
  timer timer2 (
    .dOut(DataOut), .Addr(AddrOut), .ioW(ioW), .ioR(ioR), .C(clk_internal), .InterLock(InterLock),
    .timerConfigAddr(16'h7), .timerTargetAddr(16'h8), .timerResetAddr(16'h9), .timerReadAddr(16'h3),
    .rst(rst), .TimerOut(time2In), .\timerİnterrupt (and_16_out[2]));
  Comparator #(.Signed("true"), .Bits(16)) comparator_3 (.a(AddrOut), .b(16'hc), .eq(comparator_3_eq));  // open: gt, lt
  Comparator #(.Signed("true"), .Bits(16)) comparator_4 (.a(AddrOut), .b(16'hb), .eq(comparator_4_eq));  // open: gt, lt
  Comparator #(.Signed("true"), .Bits(16)) comparator_5 (.a(AddrOut), .b(16'hb), .eq(comparator_5_eq));  // open: gt, lt
  and and_12 (and_12_out, comparator_3_eq, ioW);
  and and_13 (and_13_out, comparator_4_eq, ioW);
  and and_14 (inputEn, comparator_5_eq, ioR);
  _1_addressable_register _1_addressable_register_1 (
    .Datain(DataOut), .ioW(ioW), .addrIn(AddrOut), .address(16'he), .clk(clk_internal), .ioR(ioW),
    .DataOut(_1_addressable_register_1_dataout));  // open: Dataiow
  Multiplexer #(.Selector_Bits(3), .Bits(16)) multiplexer_12 (
    .sel(3'b111), .in_0({16{1'b0}}), .in_1(interruptReg), .in_2(inputReg), .in_3(time0In), .in_4(time1In),
    .in_5(time2In), .in_6({16{1'b0}}), .in_7({16{1'b0}}), .out(iow_Din));
  register_8bit outputReg (.D(DataOut[7:0]), .C(clk_internal), .en(and_12_out), .rst(rst), .Q(outputToOutsideEnable));
  Multiplexer #(.Bits(16)) multiplexer_13 (
    .sel(InterLock), .in_0({{8{1'b0}}, Input}), .in_1(register_1_q), .out(multiplexer_13_out));
  Register #(.Bits(16)) register_1 (.D(multiplexer_13_out), .C(clk_internal), .en(or_8_out), .Q(register_1_q));
  register_8bit OutoutEnReg (.D(DataOut[7:0]), .C(clk_internal), .en(and_13_out), .rst(rst), .Q(Output));
  Comparator #(.Bits(16)) comparator_6 (
    .a(multiplexer_13_out), .b(register_1_q), .gt(comparator_6_gt), .lt(comparator_6_lt));  // open: eq
  Comparator #(.Bits(16)) comparator_7 (.a(16'h4), .b(AddrOut), .eq(comparator_7_eq));  // open: gt, lt
  or or_8 (or_8_out, comparator_6_gt, comparator_6_lt);
  Comparator #(.Bits(16)) comparator_8 (.a(16'ha), .b(AddrOut), .eq(comparator_8_eq));  // open: gt, lt
  and and_15 (interEn, comparator_7_eq, ioR);
  and and_16 (and_16_out[3], or_8_out, _1_addressable_register_1_dataout);
  Multiplexer #(.Bits(16)) multiplexer_14 (
    .sel(and_17_out), .in_0({{12{1'b0}}, and_16_out}), .in_1(DataOut), .out(multiplexer_14_out));
  and and_17 (and_17_out, comparator_8_eq, ioW);
  Register #(.Bits(16)) register_2 (.D(multiplexer_14_out), .C(clk_internal), .en(or_9_out), .Q(register_2_q));
  Multiplexer #(.Bits(16)) multiplexer_15 (
    .sel(_1_addressable_register_1_dataout), .in_0({{8{1'b0}}, Input}), .in_1(register_1_q),
    .out(multiplexer_15_out));
  assign inputReg = inputEn ? multiplexer_15_out : 16'bz;  // Driver driver_1
  Comparator #(.Bits(16)) comparator_9 (
    .a(multiplexer_14_out), .b(register_2_q), .gt(comparator_9_gt), .lt(comparator_9_lt));  // open: eq
  assign interruptReg = interEn ? register_2_q : 16'bz;  // Driver driver_2
  or or_9 (or_9_out, comparator_9_gt, comparator_9_lt);
  and and_18 (inter, ~InterLock, or_10_out);  // And
  or or_10 (or_10_out, 1'b0, 1'b0, 1'b0, 1'b0, 1'b0, 1'b0, 1'b0, 1'b0, 1'b0, 1'b0, 1'b0, 1'b0, and_16_out[3], and_16_out[2], and_16_out[1], and_16_out[0]);

  assign debugOut = {4{clk_internal}};

  // Other names for the same wires on the sheet: sel[3:0] = aluOp[3:0]; CurrentOpcode[15:0] = in_6;
  //   OPcode[7:0] = in_6[15:8]; imm = in_6[15]; inputFromOutside[7:0] = Input; outputToOutside[7:0] = Output;
  //   Clk_in = clk_internal; pcClock = clk_internal; PeripheralClk_in = clk_internal

  // Notes on the sheet:
  //   rst_n: default 1
  //   clk_internal: Hz: 1000
  //   Input/Output
  //   ControlLogic
  //   RandomNumberGen
  //   JumpLogic
  //   FlagStore
  //   interrupt Logic
  //   ALU
  //   IO Addresses
  //   logical shift left
  //   logical shift right
  //   arithmetic shift right
  //   swapBytes
  //   swapNibbles
  //   Write Addresses
  //   Read Addresses
  //   IO BUS
  //   Timers
  //   Output
  //   Output_En
  //   input
  //   inputBus
  //   InterruptRegister
  //   InterruptBus
endmodule
