// Digital circuit tt_um_smallcpu_spi_backup.dig as structural Verilog
module tt_um_smallcpu_spi_backup (
  input  [7:0] Input,
  input  clk,
  input  rst_n,
  input  instruction,
  input  [15:0] in_12,
  output [3:0] debugOut,
  output spiClk,
  output spiMosi,
  output spiCS,
  output PCOut,
  output [3:0] spiDeg,
  output [7:0] Output
);

  wire abs, add_3_c_o, alu2D, and_1_out, and_2_out, and_3_out, and_4_out, and_5_out, and_6_out, and_8_out,
       and_9_out, and_10_out, and_13_out, and_14_out, button_1_out, comparator_1_eq, comparator_2_eq,
       comparator_3_eq, comparator_4_eq, comparator_5_eq, d_ff_2_q, d_ff_as_1_nq, d_ff_as_1_q,
       dipswitch_1_out, dipswitch_2_out, dipswitch_3_out, dipswitch_4_out, dipswitch_5_out, inter,
       interEnable, InterLock, intr, ioR, ioW, jk_ff_1_q, ld, multiplexer_5_out, multiplexer_8_out,
       multiplexer_13_out, muxA, not_1_out, not_4_out, not_5_out, or_1_out, or_2_out, or_6_out, RandomNUMSel,
       Reti, rst, sf, spi_busy_ram, SpiRam_spi_clk, SpiRam_spi_mosi, src2D, st, stPC, sub_1_c_o, timer_Sel,
       WE, xor_1_out, xor_2_out, xor_4_out, xor_5_out;
  wire [1:0] iem;
  wire [2:0] br, FlagOut, muxB, or_5_out;
  wire [4:0] aluOp;
  wire [6:0] multiplexer_7_out;
  wire [7:0] outputToOutsideEnable;
  wire [15:0] add_1_s, add_2_s, add_3_s, AddrOut, and_12_out, CurrentOpcode, DataOut, din_bus, imreg_1_p5,
       mul_1_mul, multiplexer_1_out, multiplexer_2_out, multiplexer_3_out, multiplexer_4_out,
       multiplexer_6_out, multiplexer_9_out, multiplexer_10_out, multiplexer_11_out, neg_2_out, not_6_out,
       or_7_out, pc_1_next, pc_1_pcout, pcOut_t, RandomNUM, register_1_q, registerblock_1_rdest, seed_q,
       singextend_1__4d, singextend_1__4s, singextend_1__8sd, sub_1_s, timer_in, xor_3_out;
  wire [15:1] intEn_q;
  wire [15:15] and_11_out;
  wire [31:16] mul_1_mul_2;

  Button button_1 (.out(button_1_out));
  DipSwitch dipswitch_1 (.out(dipswitch_1_out));
  DipSwitch dipswitch_2 (.out(dipswitch_2_out));
  DipSwitch dipswitch_3 (.out(dipswitch_3_out));
  DipSwitch dipswitch_4 (.out(dipswitch_4_out));
  DipSwitch dipswitch_5 (.out(dipswitch_5_out));
  pc pc_1 (
    .Alu(in_12), .clk(button_1_out), .rst(dipswitch_1_out), .abs(dipswitch_2_out), .intr(dipswitch_3_out),
    .reti(dipswitch_4_out), .Rel(dipswitch_5_out), .Next(pc_1_next), .PcOut(pc_1_pcout));
  not not_1 (not_1_out, debugOut[3]);
  register_16bit PC_2 (.D(multiplexer_4_out), .C(not_1_out), .en(1'b1), .rst(rst), .Q(pcOut_t));
  Comparator #(.Bits(16)) comparator_1 (.a(AddrOut), .b(16'h6), .eq(comparator_1_eq));  // open: gt, lt
  and and_1 (and_1_out, comparator_1_eq, ioW);
  Add #(.Bits(16)) add_1 (.a(pcOut_t), .b(16'h1), .c_i(1'b0), .s(add_1_s));  // open: c_o
  Register #(.Bits(16)) intEn (.D(DataOut), .C(clk), .en(and_1_out), .Q({intEn_q, interEnable}));
  Add #(.Bits(16)) add_2 (.a(add_1_s), .b(AddrOut), .c_i(1'b0), .s(add_2_s));  // open: c_o
  Multiplexer #(.Bits(16)) multiplexer_1 (.sel(xor_1_out), .in_0(add_1_s), .in_1(add_2_s), .out(multiplexer_1_out));
  not not_2 (spiCS, spi_busy_ram);
  Multiplexer #(.Bits(16)) multiplexer_2 (.sel(abs), .in_0(multiplexer_1_out), .in_1(AddrOut), .out(multiplexer_2_out));
  Register #(.Bits(16)) register_1 (.D(multiplexer_2_out), .C(~clk), .en(and_2_out), .Q(register_1_q));
  programCounter #(.applicationType("IVERILOG"), .CodeFile("C:\\Users\\Berkant\\Desktop\\fpga\\RemedyCpu\\verilog\\programCounter.v")) u_programCounter ();  // open: AluIn, clk, rst, absJmp, intr, reti, relJmp, Nextpc, PC
  Multiplexer #(.Bits(16)) multiplexer_3 (
    .sel(and_2_out), .in_0(multiplexer_2_out), .in_1(16'h2), .out(multiplexer_3_out));
  and and_2 (and_2_out, intr, interEnable);
  Multiplexer #(.Bits(16)) multiplexer_4 (
    .sel(and_3_out), .in_0(multiplexer_3_out), .in_1(register_1_q), .out(multiplexer_4_out));
  and and_3 (and_3_out, interEnable, Reti);
  not not_3 (rst, rst_n);
  and and_4 (and_4_out, d_ff_2_q, ~Reti);  // And
  and and_5 (and_5_out, inter, interEnable);
  and and_6 (and_6_out, InterLock, ~Reti);  // And
  or or_1 (or_1_out, and_4_out, and_5_out);
  or or_2 (or_2_out, and_6_out, intr);
  D_FF d_ff (.D(or_2_out), .C(~clk), .Q(InterLock));  // open: nQ
  D_FF d_ff_2 (.D(or_1_out), .C(~clk), .Q(d_ff_2_q));  // open: nQ
  and and_7 (intr, ~InterLock, ~CurrentOpcode[15], d_ff_2_q, ~1'b0);  // And
  Multiplexer multiplexer_5 (.sel(spi_busy_ram), .in_0(clk), .in_1(1'b1), .out(multiplexer_5_out));
  not not_4 (not_4_out, rst_n);
  OpCode #(.applicationType("IVERILOG"), .CodeFile("C:\\Users\\Berkant\\Desktop\\fpga\\RemedyCpu\\verilog\\opcode.v")) u_OpCode (
    .clk(multiplexer_5_out), .rst(not_4_out), .instructionInput(instruction), .ProgramCounter(pcOut_t),
    .opcoder(CurrentOpcode), .PcClock(debugOut[3]), .PcShifter(PCOut));
  or or_3 (or_5_out[2], timer_Sel, RandomNUMSel);
  Multiplexer #(.Selector_Bits(3), .Bits(16)) multiplexer_6 (
    .sel(or_5_out), .in_0(AddrOut), .in_1(din_bus), .in_2({{8{1'b0}}, Input}), .in_3(add_1_s),
    .in_4(timer_in), .in_5(RandomNUM), .in_6({16{1'b0}}), .in_7({16{1'b0}}), .out(multiplexer_6_out));
  or or_4 (or_5_out[1], ioR, stPC);
  or or_5 (or_5_out[0], stPC, ld, RandomNUMSel);
  Multiplexer #(.Bits(7)) multiplexer_7 (
    .sel(CurrentOpcode[15]), .in_0(CurrentOpcode[14:8]), .in_1({7{1'b0}}), .out(multiplexer_7_out));
  // controllogic controllogic_1: pin names not known; wires that end beside it: multiplexer_7_out[6], multiplexer_7_out[5], multiplexer_7_out[4], multiplexer_7_out[3], multiplexer_7_out[2], multiplexer_7_out[1], multiplexer_7_out[0], muxB[2], muxB[1], muxB[0], src2D, aluOp[4], aluOp[3], aluOp[2], aluOp[1], aluOp[0], WE, sf, alu2D, iem[1], iem[0], br[2], br[1], br[0], muxA, ld, st, abs, ioW, ioR, stPC
  Comparator #(.Signed("true"), .Bits(16)) comparator_2 (.a(AddrOut), .b(16'h9), .eq(comparator_2_eq));  // open: gt, lt
  and and_8 (and_8_out, comparator_2_eq, ioW);
  xor xor_1 (xor_1_out, multiplexer_8_out, br[2]);
  Multiplexer #(.Selector_Bits(2)) multiplexer_8 (
    .sel(br[1:0]), .in_0(1'b0), .in_1(FlagOut[0]), .in_2(FlagOut[1]), .in_3(FlagOut[2]),
    .out(multiplexer_8_out));
  and and_9 (and_9_out, clk, and_8_out);
  and and_10 (and_10_out, and_8_out, not_5_out);
  not not_5 (not_5_out, or_6_out);
  JK_FF jk_ff_1 (.J(or_6_out), .C(clk), .K(or_6_out), .Q(jk_ff_1_q));  // open: nQ
  D_FF_AS d_ff_as_1 (.Set(1'b0), .D(d_ff_as_1_nq), .C(and_9_out), .Clr(jk_ff_1_q), .Q(d_ff_as_1_q), .nQ(d_ff_as_1_nq));
  Register #(.Bits(16)) seed (.D(DataOut), .C(clk), .en(and_8_out), .Q(seed_q));
  Multiplexer #(.Bits(16)) multiplexer_9 (.sel(and_8_out), .in_0({16{1'b0}}), .in_1(seed_q), .out(multiplexer_9_out));
  RegisterBlock registerblock_1 (
    .DataIn(multiplexer_6_out), .WE(WE), .clk(debugOut[3]), .src(CurrentOpcode[3:0]),
    .Dest(CurrentOpcode[7:4]), .rst(rst), .RDest(registerblock_1_rdest), .Rsrc(DataOut));
  // ImReg imreg_1: pin names not known; wires that end beside it: CurrentOpcode[15], iem, debugOut[3], CurrentOpcode, imreg_1_p5
  or or_6 (or_6_out, d_ff_as_1_q, jk_ff_1_q);
  singExtend singextend_1 (
    .inst(CurrentOpcode), ._4S(singextend_1__4s), ._8SD(singextend_1__8sd), ._4D(singextend_1__4d));
  register_1bit Neg (.D(AddrOut[15]), .C(clk), .en(sf), .rst(rst), .Q(FlagOut[2]));
  register_1bit Zero (.D(comparator_3_eq), .C(clk), .en(sf), .rst(rst), .Q(FlagOut[1]));
  register_1bit Carry (.D(multiplexer_13_out), .C(clk), .en(sf), .rst(rst), .Q(FlagOut[0]));
  // Probe on RandomNUM
  D_FF_AS d_ff_as_2 (
    .Set(multiplexer_9_out[0]), .D(xor_2_out), .C(clk), .Clr(and_10_out), .Q(RandomNUM[0]));  // open: nQ
  Multiplexer #(.Bits(16)) multiplexer_10 (
    .sel(muxA), .in_0(registerblock_1_rdest), .in_1(DataOut),
    .out({multiplexer_10_out[11:8], multiplexer_10_out[15:12], multiplexer_10_out[3:0], multiplexer_10_out[7:4]}));
  Multiplexer #(.Selector_Bits(3), .Bits(16)) multiplexer_11 (
    .sel(muxB), .in_0(DataOut), .in_1({16{1'b0}}), .in_2(imreg_1_p5), .in_3({16{1'b0}}), .in_4({16{1'b0}}),
    .in_5(singextend_1__4s), .in_6(singextend_1__8sd), .in_7(singextend_1__4d), .out(multiplexer_11_out));
  D_FF_AS d_ff_as_3 (
    .Set(multiplexer_9_out[1]), .D(RandomNUM[0]), .C(clk), .Clr(and_10_out), .Q(RandomNUM[1]));  // open: nQ
  D_FF_AS d_ff_as_4 (
    .Set(multiplexer_9_out[2]), .D(RandomNUM[1]), .C(clk), .Clr(and_10_out), .Q(RandomNUM[2]));  // open: nQ
  D_FF_AS d_ff_as_5 (
    .Set(multiplexer_9_out[3]), .D(RandomNUM[2]), .C(clk), .Clr(and_10_out), .Q(RandomNUM[3]));  // open: nQ
  D_FF_AS d_ff_as_6 (
    .Set(multiplexer_9_out[4]), .D(RandomNUM[3]), .C(clk), .Clr(and_10_out), .Q(RandomNUM[4]));  // open: nQ
  xor xor_2 (xor_2_out, RandomNUM[5], xor_4_out);
  D_FF_AS d_ff_as_7 (
    .Set(multiplexer_9_out[5]), .D(RandomNUM[4]), .C(clk), .Clr(and_10_out), .Q(RandomNUM[5]));  // open: nQ
  and and_11 (and_11_out[15], aluOp[4], FlagOut[0]);
  D_FF_AS d_ff_as_8 (
    .Set(multiplexer_9_out[6]), .D(RandomNUM[5]), .C(clk), .Clr(and_10_out), .Q(RandomNUM[6]));  // open: nQ
  D_FF_AS d_ff_as_9 (
    .Set(multiplexer_9_out[7]), .D(RandomNUM[6]), .C(clk), .Clr(and_10_out), .Q(RandomNUM[7]));  // open: nQ
  Add #(.Bits(16)) add_3 (
    .a({multiplexer_10_out[11:8], multiplexer_10_out[15:12], multiplexer_10_out[3:0], multiplexer_10_out[7:4]}),
    .b(multiplexer_11_out), .c_i(and_11_out[15]), .s(add_3_s), .c_o(add_3_c_o));
  Sub #(.Bits(16)) sub_1 (
    .a({multiplexer_10_out[11:8], multiplexer_10_out[15:12], multiplexer_10_out[3:0], multiplexer_10_out[7:4]}),
    .b(multiplexer_11_out), .c_i(and_11_out[15]), .s(sub_1_s), .c_o(sub_1_c_o));
  assign and_12_out = {multiplexer_10_out[11:8], multiplexer_10_out[15:12], multiplexer_10_out[3:0], multiplexer_10_out[7:4]} & multiplexer_11_out;  // And and_12, 16 bits wide
  assign or_7_out = {multiplexer_10_out[11:8], multiplexer_10_out[15:12], multiplexer_10_out[3:0], multiplexer_10_out[7:4]} | multiplexer_11_out;  // Or or_7, 16 bits wide
  assign xor_3_out = {multiplexer_10_out[11:8], multiplexer_10_out[15:12], multiplexer_10_out[3:0], multiplexer_10_out[7:4]} ^ multiplexer_11_out;  // XOr xor_3, 16 bits wide
  assign not_6_out = ~{multiplexer_10_out[11:8], multiplexer_10_out[15:12], multiplexer_10_out[3:0], multiplexer_10_out[7:4]};  // Not not_6, 16 bits wide
  Neg #(.Bits(16)) neg_2 (
    .in({multiplexer_10_out[11:8], multiplexer_10_out[15:12], multiplexer_10_out[3:0], multiplexer_10_out[7:4]}),
    .out(neg_2_out));
  Mul #(.Bits(16)) mul_1 (
    .a({multiplexer_10_out[11:8], multiplexer_10_out[15:12], multiplexer_10_out[3:0], multiplexer_10_out[7:4]}),
    .b(multiplexer_11_out), .mul({mul_1_mul_2, mul_1_mul}));
  D_FF_AS d_ff_as_10 (
    .Set(multiplexer_9_out[8]), .D(RandomNUM[7]), .C(clk), .Clr(and_10_out), .Q(RandomNUM[8]));  // open: nQ
  spiden SpiRam (
    .spi_miso(Input[0]), .Address({AddrOut[14:0], 1'b0}), .clk(clk), .st(1'b0), .DataIn(DataOut), .ld(1'b0),
    .spi_clk(SpiRam_spi_clk), .spi_mosi(SpiRam_spi_mosi), .Busy(spi_busy_ram), .data_out(din_bus));  // open: spi_rst
  xor xor_4 (xor_4_out, RandomNUM[10], xor_5_out);
  D_FF_AS d_ff_as_11 (
    .Set(multiplexer_9_out[9]), .D(RandomNUM[8]), .C(clk), .Clr(and_10_out), .Q(RandomNUM[9]));  // open: nQ
  D_FF_AS d_ff_as_12 (
    .Set(multiplexer_9_out[10]), .D(RandomNUM[9]), .C(clk), .Clr(and_10_out), .Q(RandomNUM[10]));  // open: nQ
  D_FF_AS d_ff_as_13 (
    .Set(multiplexer_9_out[11]), .D(RandomNUM[10]), .C(clk), .Clr(and_10_out), .Q(RandomNUM[11]));  // open: nQ
  assign spiClk = spi_busy_ram ? SpiRam_spi_clk : 1'bz;  // Driver driver_1
  assign spiMosi = spi_busy_ram ? SpiRam_spi_mosi : 1'bz;  // Driver driver_2
  xor xor_5 (xor_5_out, RandomNUM[12], RandomNUM[14]);
  D_FF_AS d_ff_as_14 (
    .Set(multiplexer_9_out[12]), .D(RandomNUM[11]), .C(clk), .Clr(and_10_out), .Q(RandomNUM[12]));  // open: nQ
  Multiplexer #(.Selector_Bits(4), .Bits(16)) multiplexer_12 (
    .sel(aluOp[3:0]), .in_0(multiplexer_11_out), .in_1(add_3_s), .in_2(sub_1_s), .in_3(and_12_out),
    .in_4(or_7_out), .in_5(xor_3_out), .in_6(not_6_out), .in_7(neg_2_out),
    .in_8({multiplexer_10_out[10:8], multiplexer_10_out[15:12], multiplexer_10_out[3:0], multiplexer_10_out[7:4], and_11_out[15]}),
    .in_9({and_11_out[15], multiplexer_10_out[11:8], multiplexer_10_out[15:12], multiplexer_10_out[3:0], multiplexer_10_out[7:5]}),
    .in_10({{2{multiplexer_10_out[11]}}, multiplexer_10_out[10:8], multiplexer_10_out[15:12], multiplexer_10_out[3:0], multiplexer_10_out[7:5]}),
    .in_11({multiplexer_10_out[3:0], multiplexer_10_out[7:4], multiplexer_10_out[11:8], multiplexer_10_out[15:12]}),
    .in_12(multiplexer_10_out), .in_13(mul_1_mul), .in_14({16{1'b0}}), .in_15({16{1'b0}}), .out(AddrOut));
  Multiplexer #(.Selector_Bits(4)) multiplexer_13 (
    .sel(aluOp[3:0]), .in_0(1'b0), .in_1(add_3_c_o), .in_2(sub_1_c_o), .in_3(1'b0), .in_4(1'b0), .in_5(1'b0),
    .in_6(1'b0), .in_7(1'b0), .in_8(multiplexer_10_out[11]), .in_9(multiplexer_10_out[4]),
    .in_10(multiplexer_10_out[4]), .in_11(1'b0), .in_12(1'b0), .in_13(1'b0), .in_14(1'b0), .in_15(1'b0),
    .out(multiplexer_13_out));
  D_FF_AS d_ff_as_15 (
    .Set(multiplexer_9_out[13]), .D(RandomNUM[12]), .C(clk), .Clr(and_10_out), .Q(RandomNUM[13]));  // open: nQ
  D_FF_AS d_ff_as_16 (
    .Set(multiplexer_9_out[14]), .D(RandomNUM[13]), .C(clk), .Clr(and_10_out), .Q(RandomNUM[14]));  // open: nQ
  Comparator #(.Signed("true"), .Bits(16)) comparator_3 (
    .a(AddrOut), .b({16{1'b0}}), .eq(comparator_3_eq));  // open: gt, lt
  D_FF_AS d_ff_as_17 (
    .Set(multiplexer_9_out[15]), .D(RandomNUM[14]), .C(clk), .Clr(and_10_out), .Q(RandomNUM[15]));  // open: nQ
  Comparator #(.Signed("true"), .Bits(16)) comparator_4 (.a(AddrOut), .b(16'h8), .eq(comparator_4_eq));  // open: gt, lt
  Comparator #(.Signed("true"), .Bits(16)) comparator_5 (.a(AddrOut), .b(16'h7), .eq(comparator_5_eq));  // open: gt, lt
  timer timer_1 (
    .dOut(DataOut), .Addr(AddrOut), .ioW(ioW), .ioR(ioR), .C(clk), .InterLock(InterLock),
    .timerConfigAddr(16'h1), .timerTargetAddr(16'h2), .timerResetAddr(16'h3), .timerReadAddr(16'h1),
    .rst(rst), .TimerOut(timer_in), .\timerİnterrupt (inter));  // open: TimerEn
  and and_13 (and_13_out, comparator_4_eq, ioW);
  and and_14 (and_14_out, comparator_5_eq, ioW);
  register_8bit outputReg (.D(DataOut[7:0]), .C(clk), .en(and_13_out), .rst(rst), .Q(outputToOutsideEnable));
  register_8bit OutoutEnReg (.D(DataOut[7:0]), .C(clk), .en(and_14_out), .rst(rst), .Q(Output));

  assign debugOut[2:0] = {3{debugOut[3]}};
  assign spiDeg = {PCOut, clk, rst_n, instruction};

  // Other names for the same wires on the sheet: sel[3:0] = aluOp[3:0]; C = clk; Clk_in = clk;
  //   OPcode[7:0] = CurrentOpcode[15:8]; imm = CurrentOpcode[15]; inputFromOutside[7:0] = Input; iow_Din[7:0] = Input;
  //   spi_miso = Input[0]; intsin = instruction; outputToOutside[7:0] = Output; pcClock = debugOut[3];
  //   pcShift = PCOut; spi_clock_ram = spiClk; spi_mosi_ram = spiMosi

  // Notes on the sheet:
  //   clk: Hz: 1000
  //   rst_n: default 1
  //   PC
  //   interrupt Logic
  //   RandomNumberGen
  //   JumpLogic
  //   FlagStore
  //   ALU
  //   logical shift left
  //   logival shift right
  //   arithmetic shift right
  //   swapBytes
  //   swapNibbles
  //   Timer
  //   Output_En
  //   Output
  //   input
endmodule
