// Digital circuit tt_um_smallcpu_spiram.dig as structural Verilog
module tt_um_smallcpu_spiram (
  input  [7:0] ui_in,
  input  ena,
  input  clk,
  input  rst_n,
  output [3:0] uo_out,
  output uio_out0,
  output uio_out1,
  output uio_out2,
  output uio_out3,
  output uio_out4,
  output uio_out5,
  output uio_out6,
  output uio_out7,
  output [3:0] debugOut,
  output [5:0] spiDeg
);

  wire abs, add_3_c_o, alu2D, and_1_out, and_2_out, and_3_out, and_4_out, and_5_out, and_6_out, and_8_out,
       and_9_out, and_12_out, and_13_out, and_14_out, comparator_1_eq, comparator_2_eq, comparator_3_eq,
       comparator_4_eq, comparator_5_eq, d_ff_2_q, d_ff_as_1_nq, d_ff_as_1_q, imm, inter, interEnable,
       InterLock, intr, ioR, ioW, jk_ff_1_q, ld, multiplexer_1_out, multiplexer_13_out, multiplexer_15_out,
       muxA, not_4_out, or_1_out, or_5_out, or_6_out, or_8_out, RandomNUMSel, Reti, sf, spi_busy_ram,
       spi_clock_ram, spi_mosi_ram, SpiRam_spi_clk, SpiRam_spi_mosi, src2D, st, stPC, sub_1_c_o, timer_Sel,
       WE, xor_1_out, xor_3_out, xor_4_out, xor_5_out;
  wire [1:0] iem;
  wire [2:0] br, FlagOut, muxB, or_4_out;
  wire [3:0] outputToOutsideEnable, ProgMem_d, ProgMem_d_2;
  wire [4:0] aluOp;
  wire [6:0] multiplexer_10_out, OPcode;
  wire [7:0] inputFromOutside, outputToOutside;
  wire [15:0] add_1_s, add_2_s, add_3_s, Addr, and_11_out, din_bus, Dout, imreg_1_p5, mul_1_mul,
       multiplexer_2_out, multiplexer_3_out, multiplexer_4_out, multiplexer_5_out, multiplexer_6_out,
       multiplexer_9_out, multiplexer_11_out, multiplexer_12_out, multiplexer_16_out, neg_2_out, not_3_out,
       or_7_out, RandomNUM, register_1_q, registerblock_1_rdest, seed_q, singextend_1__4d, singextend_1__4s,
       singextend_1__8sd, sub_1_s, timer_in, xor_2_out;
  wire [15:1] intEn_q;
  wire [15:3] pcOut;
  wire [15:15] and_10_out;
  wire [31:16] mul_1_mul_2;

  Multiplexer multiplexer_1 (.sel(or_1_out), .in_0(clk), .in_1(1'b1), .out(multiplexer_1_out));
  or or_1 (or_1_out, spi_busy_ram, spi_busy_ram);
  Multiplexer #(.Bits(16)) multiplexer_2 (
    .sel(rst_n), .in_0({16{1'b0}}), .in_1(multiplexer_6_out), .out(multiplexer_2_out));
  Register #(.Bits(16), .isProgramCounter("true")) PC (
    .D(multiplexer_2_out), .C(~multiplexer_1_out), .en(1'b1), .Q({pcOut, debugOut[3:1]}));
  Comparator #(.Bits(16)) comparator_1 (.a(Addr), .b(16'h6), .eq(comparator_1_eq));  // open: gt, lt
  and and_1 (and_1_out, comparator_1_eq, ioW);
  Add #(.Bits(16)) add_1 (.a({pcOut, debugOut[3:1]}), .b(16'h1), .c_i(1'b0), .s(add_1_s));  // open: c_o
  Register #(.Bits(16)) intEn (.D(Dout), .C(clk), .en(and_1_out), .Q({intEn_q, interEnable}));
  Add #(.Bits(16)) add_2 (.a(add_1_s), .b(Addr), .c_i(1'b0), .s(add_2_s));  // open: c_o
  Multiplexer #(.Bits(16)) multiplexer_3 (.sel(xor_1_out), .in_0(add_1_s), .in_1(add_2_s), .out(multiplexer_3_out));
  Multiplexer #(.Bits(16)) multiplexer_4 (.sel(abs), .in_0(multiplexer_3_out), .in_1(Addr), .out(multiplexer_4_out));
  Register #(.Bits(16)) register_1 (.D(multiplexer_4_out), .C(~clk), .en(and_2_out), .Q(register_1_q));
  Multiplexer #(.Bits(16)) multiplexer_5 (
    .sel(and_2_out), .in_0(multiplexer_4_out), .in_1(16'h2), .out(multiplexer_5_out));
  and and_2 (and_2_out, intr, interEnable);
  // PinControl pincontrol_1: pin names not known; wires that end beside it: uio_out0, inputFromOutside[0], 1'b1, outputToOutside[0]
  // PinControl pincontrol_2: pin names not known; wires that end beside it: uio_out1, inputFromOutside[1], 1'b1, outputToOutside[1]
  // PinControl pincontrol_3: pin names not known; wires that end beside it: uio_out2, inputFromOutside[2], 1'b1, outputToOutside[2]
  // PinControl pincontrol_4: pin names not known; wires that end beside it: uio_out3, inputFromOutside[3], 1'b1, outputToOutside[3]
  // PinControl pincontrol_5: pin names not known; wires that end beside it: uio_out4, inputFromOutside[4], 1'b1, outputToOutside[4]
  // PinControl pincontrol_6: pin names not known; wires that end beside it: uio_out5, inputFromOutside[5], 1'b1, outputToOutside[5]
  // PinControl pincontrol_7: pin names not known; wires that end beside it: uio_out6, inputFromOutside[6], 1'b1, outputToOutside[6]
  // PinControl pincontrol_8: pin names not known; wires that end beside it: uio_out7, inputFromOutside[7], 1'b1, outputToOutside[7]
  Multiplexer #(.Bits(16)) multiplexer_6 (
    .sel(and_3_out), .in_0(multiplexer_5_out), .in_1(register_1_q), .out(multiplexer_6_out));
  and and_3 (and_3_out, interEnable, Reti);
  ROM #(.AddrBits(16), .isProgramMemory("true"), .Bits(16)) ProgMem (
    .A({pcOut, debugOut[3:1]}), .sel(1'b1), .D({imm, OPcode, ProgMem_d_2, ProgMem_d}));
  not not_1 (spiDeg[2], spi_busy_ram);
  not not_2 (spiDeg[3], spi_busy_ram);
  Multiplexer multiplexer_7 (.sel(spi_busy_ram), .in_0(spi_clock_ram), .in_1(spi_clock_ram), .out(spiDeg[0]));
  Multiplexer multiplexer_8 (.sel(spi_busy_ram), .in_0(spi_mosi_ram), .in_1(spi_mosi_ram), .out(spiDeg[1]));
  or or_2 (or_4_out[2], timer_Sel, RandomNUMSel);
  Multiplexer #(.Selector_Bits(3), .Bits(16)) multiplexer_9 (
    .sel(or_4_out), .in_0(Addr), .in_1(din_bus), .in_2({{8{1'b0}}, inputFromOutside}), .in_3(add_1_s),
    .in_4(timer_in), .in_5(RandomNUM), .in_6({16{1'b0}}), .in_7({16{1'b0}}), .out(multiplexer_9_out));
  or or_3 (or_4_out[1], ioR, stPC);
  Multiplexer #(.Bits(7)) multiplexer_10 (.sel(imm), .in_0(OPcode), .in_1({7{1'b0}}), .out(multiplexer_10_out));
  or or_4 (or_4_out[0], stPC, ld, RandomNUMSel);
  RegisterBlock registerblock_1 (
    .DataIn(multiplexer_9_out), .WE(WE), .clk(clk), .src(ProgMem_d), .Dest(ProgMem_d_2),
    .RDest(registerblock_1_rdest), .Rsrc(Dout));  // open: rst
  // ImReg imreg_1: pin names not known; wires that end beside it: imm, iem, clk, {imm, OPcode, ProgMem_d_2, ProgMem_d}, imreg_1_p5
  singExtend singextend_1 (
    .inst({imm, OPcode, ProgMem_d_2, ProgMem_d}), ._4S(singextend_1__4s), ._8SD(singextend_1__8sd),
    ._4D(singextend_1__4d));
  and and_4 (and_4_out, InterLock, ~Reti);  // And
  and and_5 (and_5_out, d_ff_2_q, ~Reti);  // And
  and and_6 (and_6_out, inter, interEnable);
  // controllogic controllogic_1: pin names not known; wires that end beside it: multiplexer_10_out[6], multiplexer_10_out[5], multiplexer_10_out[4], multiplexer_10_out[3], multiplexer_10_out[2], multiplexer_10_out[1], multiplexer_10_out[0], muxB[2], muxB[1], muxB[0], src2D, aluOp[4], aluOp[3], aluOp[2], aluOp[1], aluOp[0], WE, sf, alu2D, iem[1], iem[0], br[2], br[1], br[0], muxA, ld, st, abs, ioW, ioR, stPC
  or or_5 (or_5_out, and_5_out, and_6_out);
  or or_6 (or_6_out, and_4_out, intr);
  D_FF d_ff (.D(or_6_out), .C(~clk), .Q(InterLock));  // open: nQ
  D_FF d_ff_2 (.D(or_5_out), .C(~clk), .Q(d_ff_2_q));  // open: nQ
  Multiplexer #(.Bits(16)) multiplexer_11 (
    .sel(muxA), .in_0(registerblock_1_rdest), .in_1(Dout),
    .out({multiplexer_11_out[11:8], multiplexer_11_out[15:12], multiplexer_11_out[3:0], multiplexer_11_out[7:4]}));
  Multiplexer #(.Selector_Bits(3), .Bits(16)) multiplexer_12 (
    .sel(muxB), .in_0(Dout), .in_1({16{1'b0}}), .in_2(imreg_1_p5), .in_3({16{1'b0}}), .in_4({16{1'b0}}),
    .in_5(singextend_1__4s), .in_6(singextend_1__8sd), .in_7(singextend_1__4d), .out(multiplexer_12_out));
  and and_7 (intr, ~InterLock, ~imm, d_ff_2_q, ~1'b0);  // And
  xor xor_1 (xor_1_out, multiplexer_13_out, br[2]);
  Multiplexer #(.Selector_Bits(2)) multiplexer_13 (
    .sel(br[1:0]), .in_0(1'b0), .in_1(FlagOut[0]), .in_2(FlagOut[1]), .in_3(FlagOut[2]),
    .out(multiplexer_13_out));
  Register Neg (.D(Addr[15]), .C(clk), .en(sf), .Q(FlagOut[2]));
  Register Zero (.D(comparator_4_eq), .C(clk), .en(sf), .Q(FlagOut[1]));
  Register Carry (.D(multiplexer_15_out), .C(clk), .en(sf), .Q(FlagOut[0]));
  Comparator #(.Signed("true"), .Bits(16)) comparator_2 (.a(Addr), .b(16'h8), .eq(comparator_2_eq));  // open: gt, lt
  Comparator #(.Signed("true"), .Bits(16)) comparator_3 (.a(Addr), .b(16'h7), .eq(comparator_3_eq));  // open: gt, lt
  timer timer_1 (
    .dOut(Dout), .Addr(Addr), .ioW(ioW), .ioR(ioR), .C(clk), .InterLock(InterLock), .timerConfigAddr(16'h1),
    .timerTargetAddr(16'h2), .timerResetAddr(16'h3), .timerReadAddr(16'h1), .TimerOut(timer_in),
    .\timerİnterrupt (inter));  // open: rst, TimerEn
  and and_8 (and_8_out, comparator_2_eq, ioW);
  and and_9 (and_9_out, comparator_3_eq, ioW);
  Register #(.Bits(4)) register_2 (.D(Dout[3:0]), .C(clk), .en(and_8_out), .Q(outputToOutsideEnable));
  Register #(.Bits(8)) register_3 (.D(Dout[7:0]), .C(clk), .en(and_9_out), .Q(outputToOutside));
  and and_10 (and_10_out[15], aluOp[4], FlagOut[0]);
  Add #(.Bits(16)) add_3 (
    .a({multiplexer_11_out[11:8], multiplexer_11_out[15:12], multiplexer_11_out[3:0], multiplexer_11_out[7:4]}),
    .b(multiplexer_12_out), .c_i(and_10_out[15]), .s(add_3_s), .c_o(add_3_c_o));
  Sub #(.Bits(16)) sub_1 (
    .a({multiplexer_11_out[11:8], multiplexer_11_out[15:12], multiplexer_11_out[3:0], multiplexer_11_out[7:4]}),
    .b(multiplexer_12_out), .c_i(and_10_out[15]), .s(sub_1_s), .c_o(sub_1_c_o));
  assign and_11_out = {multiplexer_11_out[11:8], multiplexer_11_out[15:12], multiplexer_11_out[3:0], multiplexer_11_out[7:4]} & multiplexer_12_out;  // And and_11, 16 bits wide
  assign or_7_out = {multiplexer_11_out[11:8], multiplexer_11_out[15:12], multiplexer_11_out[3:0], multiplexer_11_out[7:4]} | multiplexer_12_out;  // Or or_7, 16 bits wide
  assign xor_2_out = {multiplexer_11_out[11:8], multiplexer_11_out[15:12], multiplexer_11_out[3:0], multiplexer_11_out[7:4]} ^ multiplexer_12_out;  // XOr xor_2, 16 bits wide
  assign not_3_out = ~{multiplexer_11_out[11:8], multiplexer_11_out[15:12], multiplexer_11_out[3:0], multiplexer_11_out[7:4]};  // Not not_3, 16 bits wide
  Neg #(.Bits(16)) neg_2 (
    .in({multiplexer_11_out[11:8], multiplexer_11_out[15:12], multiplexer_11_out[3:0], multiplexer_11_out[7:4]}),
    .out(neg_2_out));
  Mul #(.Bits(16)) mul_1 (
    .a({multiplexer_11_out[11:8], multiplexer_11_out[15:12], multiplexer_11_out[3:0], multiplexer_11_out[7:4]}),
    .b(multiplexer_12_out), .mul({mul_1_mul_2, mul_1_mul}));
  Multiplexer #(.Selector_Bits(4), .Bits(16)) multiplexer_14 (
    .sel(aluOp[3:0]), .in_0(multiplexer_12_out), .in_1(add_3_s), .in_2(sub_1_s), .in_3(and_11_out),
    .in_4(or_7_out), .in_5(xor_2_out), .in_6(not_3_out), .in_7(neg_2_out),
    .in_8({multiplexer_11_out[10:8], multiplexer_11_out[15:12], multiplexer_11_out[3:0], multiplexer_11_out[7:4], and_10_out[15]}),
    .in_9({and_10_out[15], multiplexer_11_out[11:8], multiplexer_11_out[15:12], multiplexer_11_out[3:0], multiplexer_11_out[7:5]}),
    .in_10({{2{multiplexer_11_out[11]}}, multiplexer_11_out[10:8], multiplexer_11_out[15:12], multiplexer_11_out[3:0], multiplexer_11_out[7:5]}),
    .in_11({multiplexer_11_out[3:0], multiplexer_11_out[7:4], multiplexer_11_out[11:8], multiplexer_11_out[15:12]}),
    .in_12(multiplexer_11_out), .in_13(mul_1_mul), .in_14({16{1'b0}}), .in_15({16{1'b0}}), .out(Addr));
  Multiplexer #(.Selector_Bits(4)) multiplexer_15 (
    .sel(aluOp[3:0]), .in_0(1'b0), .in_1(add_3_c_o), .in_2(sub_1_c_o), .in_3(1'b0), .in_4(1'b0), .in_5(1'b0),
    .in_6(1'b0), .in_7(1'b0), .in_8(multiplexer_11_out[11]), .in_9(multiplexer_11_out[4]),
    .in_10(multiplexer_11_out[4]), .in_11(1'b0), .in_12(1'b0), .in_13(1'b0), .in_14(1'b0), .in_15(1'b0),
    .out(multiplexer_15_out));
  Comparator #(.Signed("true"), .Bits(16)) comparator_4 (
    .a(Addr), .b({16{1'b0}}), .eq(comparator_4_eq));  // open: gt, lt
  Comparator #(.Signed("true"), .Bits(16)) comparator_5 (.a(Addr), .b(16'h9), .eq(comparator_5_eq));  // open: gt, lt
  and and_12 (and_12_out, comparator_5_eq, ioW);
  not not_4 (not_4_out, or_8_out);
  and and_13 (and_13_out, clk, and_12_out);
  and and_14 (and_14_out, and_12_out, not_4_out);
  spiden SpiRam (
    .spi_miso(ui_in[0]), .Address({Addr[14:0], 1'b0}), .clk(clk), .st(st), .DataIn(Dout), .ld(ld),
    .spi_clk(SpiRam_spi_clk), .spi_mosi(SpiRam_spi_mosi), .Busy(spi_busy_ram), .data_out(din_bus));  // open: spi_rst
  JK_FF jk_ff_1 (.J(or_8_out), .C(clk), .K(or_8_out), .Q(jk_ff_1_q));  // open: nQ
  D_FF_AS d_ff_as_1 (.Set(1'b0), .D(d_ff_as_1_nq), .C(and_13_out), .Clr(jk_ff_1_q), .Q(d_ff_as_1_q), .nQ(d_ff_as_1_nq));
  Register #(.Bits(16)) seed (.D(Dout), .C(clk), .en(and_12_out), .Q(seed_q));
  or or_8 (or_8_out, d_ff_as_1_q, jk_ff_1_q);
  Multiplexer #(.Bits(16)) multiplexer_16 (
    .sel(and_12_out), .in_0({16{1'b0}}), .in_1(seed_q), .out(multiplexer_16_out));
  assign spi_clock_ram = spi_busy_ram ? SpiRam_spi_clk : 1'bz;  // Driver driver_1
  assign spi_mosi_ram = spi_busy_ram ? SpiRam_spi_mosi : 1'bz;  // Driver driver_2
  // Probe on RandomNUM
  D_FF_AS d_ff_as_2 (
    .Set(multiplexer_16_out[0]), .D(xor_3_out), .C(clk), .Clr(and_14_out), .Q(RandomNUM[0]));  // open: nQ
  D_FF_AS d_ff_as_3 (
    .Set(multiplexer_16_out[1]), .D(RandomNUM[0]), .C(clk), .Clr(and_14_out), .Q(RandomNUM[1]));  // open: nQ
  D_FF_AS d_ff_as_4 (
    .Set(multiplexer_16_out[2]), .D(RandomNUM[1]), .C(clk), .Clr(and_14_out), .Q(RandomNUM[2]));  // open: nQ
  D_FF_AS d_ff_as_5 (
    .Set(multiplexer_16_out[3]), .D(RandomNUM[2]), .C(clk), .Clr(and_14_out), .Q(RandomNUM[3]));  // open: nQ
  D_FF_AS d_ff_as_6 (
    .Set(multiplexer_16_out[4]), .D(RandomNUM[3]), .C(clk), .Clr(and_14_out), .Q(RandomNUM[4]));  // open: nQ
  xor xor_3 (xor_3_out, RandomNUM[5], xor_4_out);
  D_FF_AS d_ff_as_7 (
    .Set(multiplexer_16_out[5]), .D(RandomNUM[4]), .C(clk), .Clr(and_14_out), .Q(RandomNUM[5]));  // open: nQ
  D_FF_AS d_ff_as_8 (
    .Set(multiplexer_16_out[6]), .D(RandomNUM[5]), .C(clk), .Clr(and_14_out), .Q(RandomNUM[6]));  // open: nQ
  D_FF_AS d_ff_as_9 (
    .Set(multiplexer_16_out[7]), .D(RandomNUM[6]), .C(clk), .Clr(and_14_out), .Q(RandomNUM[7]));  // open: nQ
  D_FF_AS d_ff_as_10 (
    .Set(multiplexer_16_out[8]), .D(RandomNUM[7]), .C(clk), .Clr(and_14_out), .Q(RandomNUM[8]));  // open: nQ
  xor xor_4 (xor_4_out, RandomNUM[10], xor_5_out);
  D_FF_AS d_ff_as_11 (
    .Set(multiplexer_16_out[9]), .D(RandomNUM[8]), .C(clk), .Clr(and_14_out), .Q(RandomNUM[9]));  // open: nQ
  D_FF_AS d_ff_as_12 (
    .Set(multiplexer_16_out[10]), .D(RandomNUM[9]), .C(clk), .Clr(and_14_out), .Q(RandomNUM[10]));  // open: nQ
  D_FF_AS d_ff_as_13 (
    .Set(multiplexer_16_out[11]), .D(RandomNUM[10]), .C(clk), .Clr(and_14_out), .Q(RandomNUM[11]));  // open: nQ
  D_FF_AS d_ff_as_14 (
    .Set(multiplexer_16_out[12]), .D(RandomNUM[11]), .C(clk), .Clr(and_14_out), .Q(RandomNUM[12]));  // open: nQ
  xor xor_5 (xor_5_out, RandomNUM[12], RandomNUM[14]);
  D_FF_AS d_ff_as_15 (
    .Set(multiplexer_16_out[13]), .D(RandomNUM[12]), .C(clk), .Clr(and_14_out), .Q(RandomNUM[13]));  // open: nQ
  D_FF_AS d_ff_as_16 (
    .Set(multiplexer_16_out[14]), .D(RandomNUM[13]), .C(clk), .Clr(and_14_out), .Q(RandomNUM[14]));  // open: nQ
  D_FF_AS d_ff_as_17 (
    .Set(multiplexer_16_out[15]), .D(RandomNUM[14]), .C(clk), .Clr(and_14_out), .Q(RandomNUM[15]));  // open: nQ

  assign debugOut[0] = clk;
  assign spiDeg[5:4] = {ui_in[0], ui_in[1]};
  assign uo_out = spiDeg[3:0];

  // Other names for the same wires on the sheet: sel[3:0] = aluOp[3:0]; OPcode[7] = imm;
  //   iow_Din[7:0] = inputFromOutside; AddressDebug[15:0] = Addr; C = clk; Clk_in = clk; DoutDebug[15:0] = Dout;
  //   enable = ena; pcOut[2:0] = debugOut[3:1]; spi_miso = ui_in[0]; spi_miso_pgm = ui_in[1]

  // Notes on the sheet:
  //   clk: Hz: 1000
  //   rst_n: default 1
  //   PC
  //   ProgMem loads testbench2.hex
  //   interrupt Logic
  //   JumpLogic
  //   FlagStore
  //   Timer
  //   Output_En
  //   Output
  //   ALU
  //   logical shift left
  //   logival shift right
  //   arithmetic shift right
  //   swapBytes
  //   swapNibbles
  //   input
  //   RandomNumberGen
endmodule
