// Digital circuit vga-test.dig as structural Verilog
module vga_test (
);

  wire PC, undriven, undriven_2;
  wire [1:0] undriven_3, undriven_4, undriven_5;

  VGA vga_1 (.R(undriven_3), .G(undriven_4), .B(undriven_5), .H(undriven), .V(undriven_2), .C(PC));
endmodule
