// Digital circuit yedek.dig as structural Verilog
module yedek (
  input  clk,
  input  rst_n,
  input  [7:0] ui_in,
  input  [7:0] uio_in,
  input  ena,
  output [7:0] uo_out,
  output [7:0] uio_out,
  output [7:0] uio_oe
);

  wire abs, add_1_c_o, and_1_out, and_2_out, and_3_out, and_4_out, and_5_out, and_6_out, and_8_out,
       and_9_out, and_10_out, and_11_out, and_14_out, and_15_out, comparator_1_eq, comparator_2_eq,
       comparator_3_eq, comparator_4_eq, comparator_5_eq, d_ff_2_q, d_ff_as_1_nq, d_ff_as_1_q, inter,
       interEnable, InterLock, intr, ioR, ioW, jk_ff_1_q, ld, multiplexer_4_out, multiplexer_5_out,
       multiplexer_6_out, multiplexer_7_out, multiplexer_12_out, muxA, nor_1_out, not_2_out, not_4_out,
       not_6_out, or_1_out, or_2_out, or_6_out, pcClock, RandomNUMSel, read_the_flags, Reti, rst, sf,
       spi_busy_ram, spiyedek_1_p9, spiyedek_1_p10, st, store_the_flags, stPC, sub_1_c_o, timer0_p13,
       timer1_p14, timer2_p14, timer_Sel, u_OpCode_pcclock, WE, xor_1_out, xor_2_out, xor_4_out, xor_5_out;
  wire [1:0] iem, timer2_p12;
  wire [2:0] br, FlagOut, muxB, or_5_out;
  wire [4:0] aluOp;
  wire [6:0] multiplexer_1_out;
  wire [15:0] add_1_s, AddrOut, and_13_out, CurrentOpcode, DataOut, din_bus, imreg_1_p5, mul_1_mul,
       multiplexer_3_out, multiplexer_8_out, multiplexer_9_out, multiplexer_10_out, neg_2_out, not_5_out,
       or_7_out, RandomNUM, registerblock_1_rdest, seed_q, singextend_1__4d, singextend_1__4s,
       singextend_1__8sd, sub_1_s, timer_in, timerout0, timerout1, timerout2, u_OpCode_opcoder,
       u_programCounter_nextpc, u_programCounter_pc, xor_3_out;
  wire [15:1] intEn_q;
  wire [15:15] and_12_out;
  wire [31:16] mul_1_mul_2;

  Comparator #(.Bits(16)) comparator_1 (.a(AddrOut), .b(16'ha), .eq(comparator_1_eq));  // open: gt, lt
  and and_1 (and_1_out, comparator_1_eq, ioW);
  Register #(.Bits(16)) intEn (.D(DataOut), .C(clk), .en(and_1_out), .Q({intEn_q, interEnable}));
  not not_1 (uo_out[3], spi_busy_ram);
  and and_2 (and_2_out, d_ff_2_q, ~Reti);  // And
  and and_3 (and_3_out, inter, interEnable);
  and and_4 (and_4_out, intr, interEnable);
  and and_5 (and_5_out, interEnable, Reti);
  and and_6 (and_6_out, InterLock, ~Reti);  // And
  or or_1 (or_1_out, and_2_out, and_3_out);
  or or_2 (or_2_out, and_6_out, intr);
  D_FF d_ff (.D(or_2_out), .C(~clk), .Q(InterLock));  // open: nQ
  D_FF d_ff_2 (.D(or_1_out), .C(~clk), .Q(d_ff_2_q));  // open: nQ
  programCounter #(.applicationType("IVERILOG"), .CodeFile("C:\\Users\\Berkant\\Desktop\\fpga\\RemedyCpu\\verilog\\programCounter.v")) u_programCounter (
    .AluIn(AddrOut), .clk(pcClock), .rst(rst), .absJmp(abs), .intr(and_4_out), .reti(and_5_out),
    .relJmp(xor_1_out), .Nextpc(u_programCounter_nextpc), .PC(u_programCounter_pc));
  and and_7 (intr, ~InterLock, ~CurrentOpcode[15], d_ff_2_q, ~1'b0);  // And
  Multiplexer #(.Bits(7)) multiplexer_1 (
    .sel(CurrentOpcode[15]), .in_0(CurrentOpcode[14:8]), .in_1({7{1'b0}}), .out(multiplexer_1_out));
  Multiplexer multiplexer_2 (.sel(spi_busy_ram), .in_0(clk), .in_1(1'b1), .out(pcClock));
  // controllogic controllogic_1: pin names not known; wires that end beside it: multiplexer_1_out[6], multiplexer_1_out[5], multiplexer_1_out[4], multiplexer_1_out[3], multiplexer_1_out[2], multiplexer_1_out[1], multiplexer_1_out[0], muxB[2], muxB[1], muxB[0], aluOp[4], aluOp[3], aluOp[2], aluOp[1], aluOp[0], WE, sf, iem[1], iem[0], br[2], br[1], br[0], muxA, ld, st, abs, ioW, ioR, stPC, Reti, RandomNUMSel
  not not_2 (not_2_out, rst_n);
  not not_3 (rst, rst_n);
  OpCode #(.applicationType("IVERILOG"), .CodeFile("C:\\Users\\Berkant\\Desktop\\fpga\\RemedyCpu\\verilog\\opcode.v")) u_OpCode (
    .clk(pcClock), .rst(not_2_out), .instructionInput(ui_in[1]), .ProgramCounter(u_programCounter_pc),
    .opcoder(u_OpCode_opcoder), .PcClock(u_OpCode_pcclock), .PcShifter(uo_out[0]));
  ROM #(.AddrBits(16), .isProgramMemory("true"), .Bits(16)) pgr (
    .A(u_programCounter_pc), .sel(1'b1), .D(CurrentOpcode));
  or or_3 (or_5_out[2], timer_Sel, read_the_flags, RandomNUMSel);
  Multiplexer #(.Selector_Bits(3), .Bits(16)) multiplexer_3 (
    .sel(or_5_out), .in_0(AddrOut), .in_1(din_bus), .in_2({{8{1'b0}}, uio_in}),
    .in_3(u_programCounter_nextpc), .in_4(timer_in), .in_5(RandomNUM), .in_6({{13{1'b0}}, FlagOut}),
    .in_7({16{1'b0}}), .out(multiplexer_3_out));
  and and_8 (and_8_out, ioR, ~timer_Sel);  // And
  or or_4 (or_5_out[1], and_8_out, read_the_flags, stPC);
  or or_5 (or_5_out[0], stPC, ld, RandomNUMSel);
  xor xor_1 (xor_1_out, multiplexer_4_out, br[2]);
  Multiplexer #(.Selector_Bits(2)) multiplexer_4 (
    .sel(br[1:0]), .in_0(1'b0), .in_1(FlagOut[0]), .in_2(FlagOut[1]), .in_3(FlagOut[2]),
    .out(multiplexer_4_out));
  Comparator #(.Signed("true"), .Bits(16)) comparator_2 (.a(AddrOut), .b(16'hd), .eq(comparator_2_eq));  // open: gt, lt
  and and_9 (and_9_out, comparator_2_eq, ioW);
  register_1bit Neg (.D(multiplexer_7_out), .C(clk), .en(sf), .rst(rst), .Q(FlagOut[2]));
  register_1bit Zero (.D(multiplexer_6_out), .C(clk), .en(sf), .rst(rst), .Q(FlagOut[1]));
  register_1bit Carry (.D(multiplexer_5_out), .C(clk), .en(sf), .rst(rst), .Q(FlagOut[0]));
  not not_4 (not_4_out, or_6_out);
  and and_10 (and_10_out, clk, and_9_out);
  RegisterBlock registerblock_1 (
    .DataIn(multiplexer_3_out), .WE(WE), .clk(pcClock), .src(CurrentOpcode[3:0]), .Dest(CurrentOpcode[7:4]),
    .rst(rst), .RDest(registerblock_1_rdest), .Rsrc(DataOut));
  // ImReg imreg_1: pin names not known; wires that end beside it: CurrentOpcode[15], iem, pcClock, CurrentOpcode, imreg_1_p5
  and and_11 (and_11_out, and_9_out, not_4_out);
  singExtend singextend_1 (
    .inst(CurrentOpcode), ._4S(singextend_1__4s), ._8SD(singextend_1__8sd), ._4D(singextend_1__4d));
  Multiplexer multiplexer_5 (
    .sel(store_the_flags), .in_0(multiplexer_12_out), .in_1(multiplexer_9_out[4]), .out(multiplexer_5_out));
  JK_FF jk_ff_1 (.J(or_6_out), .C(clk), .K(or_6_out), .Q(jk_ff_1_q));  // open: nQ
  D_FF_AS d_ff_as_1 (.Set(1'b0), .D(d_ff_as_1_nq), .C(and_10_out), .Clr(jk_ff_1_q), .Q(d_ff_as_1_q), .nQ(d_ff_as_1_nq));
  Register #(.Bits(16)) seed (.D(DataOut), .C(clk), .en(and_9_out), .Q(seed_q));
  Multiplexer multiplexer_6 (
    .sel(store_the_flags), .in_0(comparator_3_eq), .in_1(multiplexer_9_out[5]), .out(multiplexer_6_out));
  Multiplexer multiplexer_7 (
    .sel(store_the_flags), .in_0(AddrOut[15]), .in_1(multiplexer_9_out[6]), .out(multiplexer_7_out));
  or or_6 (or_6_out, d_ff_as_1_q, jk_ff_1_q);
  Multiplexer #(.Bits(16)) multiplexer_8 (.sel(and_9_out), .in_0({16{1'b0}}), .in_1(seed_q), .out(multiplexer_8_out));
  Multiplexer #(.Bits(16)) multiplexer_9 (
    .sel(muxA), .in_0(registerblock_1_rdest), .in_1(DataOut),
    .out({multiplexer_9_out[11:8], multiplexer_9_out[15:12], multiplexer_9_out[3:0], multiplexer_9_out[7:4]}));
  Multiplexer #(.Selector_Bits(3), .Bits(16)) multiplexer_10 (
    .sel(muxB), .in_0(DataOut), .in_1({16{1'b0}}), .in_2(imreg_1_p5), .in_3({16{1'b0}}), .in_4({16{1'b0}}),
    .in_5(singextend_1__4s), .in_6(singextend_1__8sd), .in_7(singextend_1__4d), .out(multiplexer_10_out));
  // Probe on RandomNUM
  D_FF_AS d_ff_as_2 (
    .Set(multiplexer_8_out[0]), .D(xor_2_out), .C(clk), .Clr(and_11_out), .Q(RandomNUM[0]));  // open: nQ
  D_FF_AS d_ff_as_3 (
    .Set(multiplexer_8_out[1]), .D(RandomNUM[0]), .C(clk), .Clr(and_11_out), .Q(RandomNUM[1]));  // open: nQ
  D_FF_AS d_ff_as_4 (
    .Set(multiplexer_8_out[2]), .D(RandomNUM[1]), .C(clk), .Clr(and_11_out), .Q(RandomNUM[2]));  // open: nQ
  D_FF_AS d_ff_as_5 (
    .Set(multiplexer_8_out[3]), .D(RandomNUM[2]), .C(clk), .Clr(and_11_out), .Q(RandomNUM[3]));  // open: nQ
  and and_12 (and_12_out[15], aluOp[4], FlagOut[0]);
  D_FF_AS d_ff_as_6 (
    .Set(multiplexer_8_out[4]), .D(RandomNUM[3]), .C(clk), .Clr(and_11_out), .Q(RandomNUM[4]));  // open: nQ
  xor xor_2 (xor_2_out, RandomNUM[5], xor_4_out);
  D_FF_AS d_ff_as_7 (
    .Set(multiplexer_8_out[5]), .D(RandomNUM[4]), .C(clk), .Clr(and_11_out), .Q(RandomNUM[5]));  // open: nQ
  Add #(.Bits(16)) add_1 (
    .a({multiplexer_9_out[11:8], multiplexer_9_out[15:12], multiplexer_9_out[3:0], multiplexer_9_out[7:4]}),
    .b(multiplexer_10_out), .c_i(and_12_out[15]), .s(add_1_s), .c_o(add_1_c_o));
  Sub #(.Bits(16)) sub_1 (
    .a({multiplexer_9_out[11:8], multiplexer_9_out[15:12], multiplexer_9_out[3:0], multiplexer_9_out[7:4]}),
    .b(multiplexer_10_out), .c_i(and_12_out[15]), .s(sub_1_s), .c_o(sub_1_c_o));
  assign and_13_out = {multiplexer_9_out[11:8], multiplexer_9_out[15:12], multiplexer_9_out[3:0], multiplexer_9_out[7:4]} & multiplexer_10_out;  // And and_13, 16 bits wide
  assign or_7_out = {multiplexer_9_out[11:8], multiplexer_9_out[15:12], multiplexer_9_out[3:0], multiplexer_9_out[7:4]} | multiplexer_10_out;  // Or or_7, 16 bits wide
  assign xor_3_out = {multiplexer_9_out[11:8], multiplexer_9_out[15:12], multiplexer_9_out[3:0], multiplexer_9_out[7:4]} ^ multiplexer_10_out;  // XOr xor_3, 16 bits wide
  assign not_5_out = ~{multiplexer_9_out[11:8], multiplexer_9_out[15:12], multiplexer_9_out[3:0], multiplexer_9_out[7:4]};  // Not not_5, 16 bits wide
  Neg #(.Bits(16)) neg_2 (
    .in({multiplexer_9_out[11:8], multiplexer_9_out[15:12], multiplexer_9_out[3:0], multiplexer_9_out[7:4]}),
    .out(neg_2_out));
  Mul #(.Bits(16)) mul_1 (
    .a({multiplexer_9_out[11:8], multiplexer_9_out[15:12], multiplexer_9_out[3:0], multiplexer_9_out[7:4]}),
    .b(multiplexer_10_out), .mul({mul_1_mul_2, mul_1_mul}));
  D_FF_AS d_ff_as_8 (
    .Set(multiplexer_8_out[6]), .D(RandomNUM[5]), .C(clk), .Clr(and_11_out), .Q(RandomNUM[6]));  // open: nQ
  D_FF_AS d_ff_as_9 (
    .Set(multiplexer_8_out[7]), .D(RandomNUM[6]), .C(clk), .Clr(and_11_out), .Q(RandomNUM[7]));  // open: nQ
  D_FF_AS d_ff_as_10 (
    .Set(multiplexer_8_out[8]), .D(RandomNUM[7]), .C(clk), .Clr(and_11_out), .Q(RandomNUM[8]));  // open: nQ
  xor xor_4 (xor_4_out, RandomNUM[10], xor_5_out);
  D_FF_AS d_ff_as_11 (
    .Set(multiplexer_8_out[9]), .D(RandomNUM[8]), .C(clk), .Clr(and_11_out), .Q(RandomNUM[9]));  // open: nQ
  D_FF_AS d_ff_as_12 (
    .Set(multiplexer_8_out[10]), .D(RandomNUM[9]), .C(clk), .Clr(and_11_out), .Q(RandomNUM[10]));  // open: nQ
  Multiplexer #(.Selector_Bits(4), .Bits(16)) multiplexer_11 (
    .sel(aluOp[3:0]), .in_0(multiplexer_10_out), .in_1(add_1_s), .in_2(sub_1_s), .in_3(and_13_out),
    .in_4(or_7_out), .in_5(xor_3_out), .in_6(not_5_out), .in_7(neg_2_out),
    .in_8({multiplexer_9_out[10:8], multiplexer_9_out[15:12], multiplexer_9_out[3:0], multiplexer_9_out[7:4], and_12_out[15]}),
    .in_9({and_12_out[15], multiplexer_9_out[11:8], multiplexer_9_out[15:12], multiplexer_9_out[3:0], multiplexer_9_out[7:5]}),
    .in_10({{2{multiplexer_9_out[11]}}, multiplexer_9_out[10:8], multiplexer_9_out[15:12], multiplexer_9_out[3:0], multiplexer_9_out[7:5]}),
    .in_11({multiplexer_9_out[3:0], multiplexer_9_out[7:4], multiplexer_9_out[11:8], multiplexer_9_out[15:12]}),
    .in_12(multiplexer_9_out), .in_13(mul_1_mul), .in_14({16{1'b0}}), .in_15({16{1'b0}}), .out(AddrOut));
  Multiplexer #(.Selector_Bits(4)) multiplexer_12 (
    .sel(aluOp[3:0]), .in_0(1'b0), .in_1(add_1_c_o), .in_2(sub_1_c_o), .in_3(1'b0), .in_4(1'b0), .in_5(1'b0),
    .in_6(1'b0), .in_7(1'b0), .in_8(multiplexer_9_out[11]), .in_9(multiplexer_9_out[4]),
    .in_10(multiplexer_9_out[4]), .in_11(1'b0), .in_12(1'b0), .in_13(1'b0), .in_14(1'b0), .in_15(1'b0),
    .out(multiplexer_12_out));
  D_FF_AS d_ff_as_13 (
    .Set(multiplexer_8_out[11]), .D(RandomNUM[10]), .C(clk), .Clr(and_11_out), .Q(RandomNUM[11]));  // open: nQ
  D_FF_AS d_ff_as_14 (
    .Set(multiplexer_8_out[12]), .D(RandomNUM[11]), .C(clk), .Clr(and_11_out), .Q(RandomNUM[12]));  // open: nQ
  Comparator #(.Signed("true"), .Bits(16)) comparator_3 (
    .a(AddrOut), .b({16{1'b0}}), .eq(comparator_3_eq));  // open: gt, lt
  xor xor_5 (xor_5_out, RandomNUM[12], RandomNUM[14]);
  D_FF_AS d_ff_as_15 (
    .Set(multiplexer_8_out[13]), .D(RandomNUM[12]), .C(clk), .Clr(and_11_out), .Q(RandomNUM[13]));  // open: nQ
  D_FF_AS d_ff_as_16 (
    .Set(multiplexer_8_out[14]), .D(RandomNUM[13]), .C(clk), .Clr(and_11_out), .Q(RandomNUM[14]));  // open: nQ
  D_FF_AS d_ff_as_17 (
    .Set(multiplexer_8_out[15]), .D(RandomNUM[14]), .C(clk), .Clr(and_11_out), .Q(RandomNUM[15]));  // open: nQ
  not not_6 (not_6_out, clk);
  Comparator #(.Signed("true"), .Bits(16)) comparator_4 (.a(AddrOut), .b(16'hc), .eq(comparator_4_eq));  // open: gt, lt
  Comparator #(.Signed("true"), .Bits(16)) comparator_5 (.a(AddrOut), .b(16'hb), .eq(comparator_5_eq));  // open: gt, lt
  nor nor_1 (nor_1_out, st, ld);
  and and_14 (and_14_out, comparator_4_eq, ioW);
  and and_15 (and_15_out, comparator_5_eq, ioW);
  // timer timer0: pin names not known; wires that end beside it: DataOut, AddrOut, ioW, ioR, clk, InterLock, 16'h1, 16'h2, 16'h3, 16'h1, rst, timerout0, timer0_p13
  // timer timer1: pin names not known; wires that end beside it: DataOut, AddrOut, ioW, ioR, clk, InterLock, 16'h4, 16'h5, 16'h6, 16'h2, rst, timer2_p12[0], timerout1, timer1_p14
  // timer timer2: pin names not known; wires that end beside it: DataOut, AddrOut, ioW, ioR, clk, InterLock, 16'h7, 16'h8, 16'h9, 16'h3, rst, timer2_p12[1], timerout2, timer2_p14
  // spiYedek spiyedek_1: pin names not known; wires that end beside it: AddrOut[15], ui_in[0], {AddrOut[14:0], 1'b0}, clk, st, DataOut, ld, nor_1_out, spiyedek_1_p9, spiyedek_1_p10, spi_busy_ram, din_bus
  register_8bit outputReg (.D(DataOut[7:0]), .C(clk), .en(and_14_out), .rst(rst), .Q(uio_oe));
  register_8bit OutoutEnReg (.D(DataOut[7:0]), .C(clk), .en(and_15_out), .rst(rst), .Q(uio_out));
  assign uo_out[1] = spi_busy_ram ? spiyedek_1_p9 : 1'bz;  // Driver driver_1
  assign uo_out[2] = spi_busy_ram ? spiyedek_1_p10 : 1'bz;  // Driver driver_2
  or or_8 (inter, timer0_p13, timer1_p14, timer2_p14);
  Multiplexer #(.Selector_Bits(2), .Bits(16)) multiplexer_13 (
    .sel(timer2_p12), .in_0(timerout0), .in_1(timerout1), .in_2(timerout2), .in_3(timerout2), .out(timer_in));

  assign uo_out[7:4] = 4'b0000;

  // Other names for the same wires on the sheet: sel[3:0] = aluOp[3:0]; C = clk; Clk_in = clk;
  //   OPcode[7:0] = CurrentOpcode[15:8]; imm = CurrentOpcode[15]; inputFromOutside[7:0] = uio_in;
  //   iow_Din[7:0] = uio_in; outputToOutside[7:0] = uio_out; outputToOutsideEnable[7:0] = uio_oe; pcShift = uo_out[0];
  //   spi_clock_ram = uo_out[1]; spi_mosi_ram = uo_out[2]; spi_miso = ui_in[0]; intsin = ui_in[1]

  // Notes on the sheet:
  //   clk: Hz: 1000
  //   rst_n: default 1
  //   interrupt Logic
  //   pgr loads simple.hex
  //   JumpLogic
  //   FlagStore
  //   RandomNumberGen
  //   ALU
  //   logical shift left
  //   logival shift right
  //   arithmetic shift right
  //   swapBytes
  //   swapNibbles
  //   Timer
  //   Output_En
  //   Output
  //   input
endmodule
